// Logisim project 实验1-CS2008-15533-徐瑞达.circ as structural Verilog: 5 circuits, main circuit 一位二进制半加器
module \一位二进制半加器  (
  input  A,
  input  B,
  output S,
  output C
);

  xor xor_1 (S, A, B);
  and and_1 (C, A, B);
endmodule

module \一位二进制全加器  (
  input  A,
  input  B,
  input  Ci,
  output S,
  output Co
);

  wire nand_1_out, nand_3_out, xor_1_out;

  xor xor_1 (xor_1_out, A, B);
  xor xor_2 (S, xor_1_out, Ci);
  nand nand_1 (nand_1_out, xor_1_out, Ci);
  nand nand_2 (Co, nand_1_out, nand_3_out);
  nand nand_3 (nand_3_out, A, B);
endmodule

module \串行进位的四位二进制并行加法器  (
  input  A0,
  input  B0,
  input  C0,
  input  A1,
  input  B1,
  input  A2,
  input  B2,
  input  A3,
  input  B3,
  output S0,
  output S1,
  output S2,
  output S3,
  output C4
);

  wire \一位二进制全加器_1_co , \一位二进制全加器_2_co , \一位二进制全加器_3_co ;

  \一位二进制全加器  \u_一位二进制全加器_1  (.A(A0), .B(B0), .Ci(C0), .S(S0), .Co(\一位二进制全加器_1_co ));
  \一位二进制全加器  \u_一位二进制全加器_2  (.A(A1), .B(B1), .Ci(\一位二进制全加器_1_co ), .S(S1), .Co(\一位二进制全加器_2_co ));
  \一位二进制全加器  \u_一位二进制全加器_3  (.A(A2), .B(B2), .Ci(\一位二进制全加器_2_co ), .S(S2), .Co(\一位二进制全加器_3_co ));
  \一位二进制全加器  \u_一位二进制全加器_4  (.A(A3), .B(B3), .Ci(\一位二进制全加器_3_co ), .S(S3), .Co(C4));
endmodule

module \先行进位的四位二进制并行加法器  (
  input  A3,
  input  B3,
  input  A2,
  input  B2,
  input  A1,
  input  B1,
  input  A0,
  input  B0,
  input  C0,
  output C4,
  output S3,
  output S2,
  output S1,
  output S0
);

  wire and_1_out, and_2_out, and_3_out, and_4_out, and_5_out, and_6_out, and_7_out, and_8_out, and_9_out,
       and_10_out, C1_out, C2_out, C3_out, G0_out, G1_out, G2_out, G3_out, P0_out, P1_out, P2_out, P3_out;

  and G3 (G3_out, A3, B3);
  or P3 (P3_out, A3, B3);
  and G2 (G2_out, A2, B2);
  or P2 (P2_out, A2, B2);
  and G1 (G1_out, A1, B1);
  or P1 (P1_out, A1, B1);
  and G0 (G0_out, A0, B0);
  or P0 (P0_out, A0, B0);
  and and_1 (and_1_out, G2_out, P3_out);
  and and_2 (and_2_out, G1_out, P2_out, P3_out);
  and and_3 (and_3_out, G0_out, P1_out, P2_out, P3_out);
  and and_4 (and_4_out, P3_out, P2_out, P1_out, P0_out, C0);
  and and_5 (and_5_out, G1_out, P2_out);
  and and_6 (and_6_out, P1_out, P2_out, G0_out);
  and and_7 (and_7_out, P2_out, P1_out, P0_out, C0);
  and and_8 (and_8_out, P1_out, G0_out);
  and and_9 (and_9_out, P1_out, P0_out, C0);
  and and_10 (and_10_out, P0_out, C0);
  or u_C4 (C4, G3_out, and_1_out, and_2_out, and_3_out, and_4_out);
  or C3 (C3_out, G2_out, and_5_out, and_6_out, and_7_out);
  or C2 (C2_out, G1_out, and_8_out, and_9_out);
  or C1 (C1_out, G0_out, and_10_out);
  xor xor_1 (S3, A3, B3, C3_out);
  xor xor_2 (S2, A2, B2, C2_out);
  xor xor_3 (S1, A1, B1, C1_out);
  xor xor_4 (S0, A0, B0, C0);
endmodule

module \先行进位的四位二进制并行加法器测试电路  (
  input  C0,
  input  A3,
  input  A2,
  input  A1,
  input  A0,
  input  B3,
  input  B2,
  input  B1,
  input  B0,
  output C4,
  output S3,
  output S2,
  output S1,
  output S0
);

  \先行进位的四位二进制并行加法器  \u_先行进位的四位二进制并行加法器_1  (
    .A3(A3), .B3(B3), .A2(A2), .B2(B2), .A1(A1), .B1(B1), .A0(A0), .B0(B0), .C0(C0), .C4(C4), .S3(S3),
    .S2(S2), .S1(S1), .S0(S0));
endmodule
