// Logisim project 实验2-CS2008-15533-徐瑞达.circ as structural Verilog: 12 circuits, main circuit 四位可逆二进制计数器
module \四位可逆二进制计数器  (
  input  CPD,
  input  A,
  input  CLR,
  input  B,
  input  LD,
  input  CPU,
  input  C,
  input  D,
  output QA,
  output QB,
  output QC,
  output QD
);

  wire and_1_out, and_2_out, and_3_out, and_4_out, and_5_out, and_6_out, C1_out, multiplexer_1_out,
       multiplexer_2_out, multiplexer_3_out, multiplexer_4_out, multiplexer_5_out, multiplexer_6_out,
       multiplexer_7_out, multiplexer_8_out, not_1_out, not_2_out, not_3_out, not_4_out, not_5_out,
       not_6_out, not_7_out, not_8_out, not_9_out, not_10_out, not_11_out, not_12_out, not_13_out,
       not_14_out, not_15_out, or_1_out, or_2_out, or_3_out;

  not not_1 (not_1_out, QA);
  not not_2 (not_2_out, QB);
  not not_3 (not_3_out, QC);
  or C1 (C1_out, CPD, CPU);
  not not_4 (not_4_out, A);
  not not_5 (not_5_out, not_1_out);
  and and_1 (and_1_out, QA, CPU);
  and and_2 (and_2_out, not_1_out, CPD);
  and and_3 (and_3_out, QA, QB, CPU);
  and and_4 (and_4_out, not_1_out, not_2_out, CPD);
  and and_5 (and_5_out, QA, QB, QC, CPU);
  and and_6 (and_6_out, not_2_out, not_1_out, not_3_out, CPD);
  Multiplexer #(.select(1), .width(1), .disabled("Z"), .enable("false")) multiplexer_1 (
    .in0(not_15_out), .in1(C1_out), .out(multiplexer_1_out), .sel(LD));
  not not_6 (not_6_out, multiplexer_2_out);
  Multiplexer #(.select(1), .width(1), .disabled("Z"), .enable("false")) multiplexer_2 (
    .in0(not_4_out), .in1(not_5_out), .out(multiplexer_2_out), .sel(LD));
  Multiplexer #(.select(1), .width(1), .disabled("Z"), .enable("false")) multiplexer_3 (
    .in0(not_15_out), .in1(or_1_out), .out(multiplexer_3_out), .sel(LD));
  or or_1 (or_1_out, and_1_out, and_2_out);
  not not_7 (not_7_out, B);
  not not_8 (not_8_out, not_2_out);
  or or_2 (or_2_out, and_3_out, and_4_out);
  Multiplexer #(.select(1), .width(1), .disabled("Z"), .enable("false")) multiplexer_4 (
    .in0(not_15_out), .in1(or_2_out), .out(multiplexer_4_out), .sel(LD));
  not not_9 (not_9_out, C);
  not not_10 (not_10_out, not_3_out);
  Multiplexer #(.select(1), .width(1), .disabled("Z"), .enable("false")) multiplexer_5 (
    .in0(not_15_out), .in1(or_3_out), .out(multiplexer_5_out), .sel(LD));
  or or_3 (or_3_out, and_5_out, and_6_out);
  not not_11 (not_11_out, D);
  D_Flip_Flop #(.trigger("falling"), .Pre_Clr_Positions("ABOVE_BELOW"), .NegatePresetClear("false"), .enable("false"), .NewFFLayout("true")) d_ff_1 (
    .clk(multiplexer_1_out), .D(not_6_out), .Q(QA), .reset(CLR));  // open: Qn, preset
  not not_12 (not_12_out, multiplexer_6_out);
  Multiplexer #(.select(1), .width(1), .disabled("Z"), .enable("false")) multiplexer_6 (
    .in0(not_7_out), .in1(not_8_out), .out(multiplexer_6_out), .sel(LD));
  not not_13 (not_13_out, multiplexer_7_out);
  Multiplexer #(.select(1), .width(1), .disabled("Z"), .enable("false")) multiplexer_7 (
    .in0(not_9_out), .in1(not_10_out), .out(multiplexer_7_out), .sel(LD));
  not not_14 (not_14_out, multiplexer_8_out);
  Multiplexer #(.select(1), .width(1), .disabled("Z"), .enable("false")) multiplexer_8 (
    .in0(not_11_out), .in1(QD), .out(multiplexer_8_out), .sel(LD));
  D_Flip_Flop #(.trigger("falling"), .Pre_Clr_Positions("ABOVE_BELOW"), .NegatePresetClear("false"), .enable("false"), .NewFFLayout("true")) d_ff_2 (
    .clk(multiplexer_3_out), .D(not_12_out), .Q(QB), .reset(CLR));  // open: Qn, preset
  D_Flip_Flop #(.trigger("falling"), .Pre_Clr_Positions("ABOVE_BELOW"), .NegatePresetClear("false"), .enable("false"), .NewFFLayout("true")) d_ff_3 (
    .clk(multiplexer_4_out), .D(not_13_out), .Q(QC), .reset(CLR));  // open: Qn, preset
  D_Flip_Flop #(.trigger("falling"), .Pre_Clr_Positions("ABOVE_BELOW"), .NegatePresetClear("false"), .enable("false"), .NewFFLayout("true")) d_ff_4 (
    .clk(multiplexer_5_out), .D(not_14_out), .Q(QD), .reset(CLR));  // open: Qn, preset
  not not_15 (not_15_out, LD);
endmodule

module \四位二进制可逆计数器含进位  (
  input  CPD,
  input  A,
  input  CLR,
  input  LD,
  input  B,
  input  CPU,
  input  C,
  input  D,
  output QA,
  output QB,
  output QC,
  output QD,
  output QJ
);

  wire and_1_out, and_2_out, and_3_out, and_4_out, and_5_out, and_6_out, and_7_out, and_8_out, d_ff_5_qn,
       multiplexer_1_out, multiplexer_2_out, multiplexer_3_out, multiplexer_4_out, multiplexer_5_out,
       multiplexer_6_out, multiplexer_7_out, multiplexer_8_out, not_1_out, not_2_out, not_3_out, not_4_out,
       not_5_out, not_6_out, not_7_out, not_8_out, not_9_out, not_10_out, not_11_out, not_12_out, not_13_out,
       or_1_out, or_2_out, or_3_out, or_4_out, or_5_out;

  not not_1 (not_1_out, QA);
  not not_2 (not_2_out, QB);
  not not_3 (not_3_out, QC);
  not not_4 (not_4_out, QD);
  or or_1 (or_1_out, CPD, CPU);
  and and_1 (and_1_out, QA, CPU);
  or or_2 (or_2_out, and_1_out, and_2_out);
  and and_2 (and_2_out, not_1_out, CPD);
  and and_3 (and_3_out, QB, QA, CPU);
  or or_3 (or_3_out, and_3_out, and_4_out);
  and and_4 (and_4_out, not_2_out, not_1_out, CPD);
  and and_5 (and_5_out, QA, QC, CPU, QB);
  or or_4 (or_4_out, and_5_out, and_6_out);
  and and_6 (and_6_out, not_1_out, not_3_out, CPD, not_2_out);
  and and_7 (and_7_out, QB, QD, QA, CPU, QC);
  or or_5 (or_5_out, and_7_out, and_8_out);
  and and_8 (and_8_out, not_1_out, not_4_out, not_2_out, CPD, not_3_out);
  Multiplexer #(.select(1), .width(1), .disabled("Z"), .enable("false")) multiplexer_1 (
    .in0(not_13_out), .in1(or_1_out), .out(multiplexer_1_out), .sel(LD));
  not not_5 (not_5_out, A);
  Multiplexer #(.select(1), .width(1), .disabled("Z"), .enable("false")) multiplexer_2 (
    .in0(not_13_out), .in1(or_2_out), .out(multiplexer_2_out), .sel(LD));
  not not_6 (not_6_out, B);
  Multiplexer #(.select(1), .width(1), .disabled("Z"), .enable("false")) multiplexer_3 (
    .in0(not_13_out), .in1(or_3_out), .out(multiplexer_3_out), .sel(LD));
  not not_7 (not_7_out, C);
  Multiplexer #(.select(1), .width(1), .disabled("Z"), .enable("false")) multiplexer_4 (
    .in0(not_13_out), .in1(or_4_out), .out(multiplexer_4_out), .sel(LD));
  not not_8 (not_8_out, D);
  Multiplexer #(.select(1), .width(1), .disabled("Z"), .enable("false")) multiplexer_5 (
    .in0(not_5_out), .in1(QA), .out(multiplexer_5_out), .sel(LD));
  not not_9 (not_9_out, multiplexer_5_out);
  not not_10 (not_10_out, multiplexer_6_out);
  Multiplexer #(.select(1), .width(1), .disabled("Z"), .enable("false")) multiplexer_6 (
    .in0(not_6_out), .in1(QB), .out(multiplexer_6_out), .sel(LD));
  not not_11 (not_11_out, multiplexer_7_out);
  Multiplexer #(.select(1), .width(1), .disabled("Z"), .enable("false")) multiplexer_7 (
    .in0(not_7_out), .in1(QC), .out(multiplexer_7_out), .sel(LD));
  Multiplexer #(.select(1), .width(1), .disabled("Z"), .enable("false")) multiplexer_8 (
    .in0(not_8_out), .in1(QD), .out(multiplexer_8_out), .sel(LD));
  not not_12 (not_12_out, multiplexer_8_out);
  D_Flip_Flop #(.trigger("falling"), .Pre_Clr_Positions("ABOVE_BELOW"), .NegatePresetClear("false"), .enable("false"), .NewFFLayout("true")) d_ff_1 (
    .clk(multiplexer_1_out), .D(not_9_out), .Q(QA), .reset(CLR));  // open: Qn, preset
  D_Flip_Flop #(.trigger("falling"), .Pre_Clr_Positions("ABOVE_BELOW"), .NegatePresetClear("false"), .enable("false"), .NewFFLayout("true")) d_ff_2 (
    .clk(multiplexer_2_out), .D(not_10_out), .Q(QB), .reset(CLR));  // open: Qn, preset
  D_Flip_Flop #(.trigger("falling"), .Pre_Clr_Positions("ABOVE_BELOW"), .NegatePresetClear("false"), .enable("false"), .NewFFLayout("true")) d_ff_3 (
    .clk(multiplexer_3_out), .D(not_11_out), .Q(QC), .reset(CLR));  // open: Qn, preset
  D_Flip_Flop #(.trigger("falling"), .Pre_Clr_Positions("ABOVE_BELOW"), .NegatePresetClear("false"), .enable("false"), .NewFFLayout("true")) d_ff_4 (
    .clk(multiplexer_4_out), .D(not_12_out), .Q(QD), .reset(CLR));  // open: Qn, preset
  D_Flip_Flop #(.trigger("falling"), .Pre_Clr_Positions("ABOVE_BELOW"), .NegatePresetClear("false"), .enable("false"), .NewFFLayout("true")) d_ff_5 (
    .clk(or_5_out), .D(d_ff_5_qn), .Q(QJ), .Qn(d_ff_5_qn), .reset(CLR));  // open: preset
  not not_13 (not_13_out, LD);
endmodule

module \四位可逆二进制计数器测试电路  (
  input  CPU,
  input  CLR,
  input  CPD,
  input  D,
  input  C,
  input  B,
  input  A,
  input  LD,
  output QD,
  output QC,
  output QB,
  output QA
);

  \四位可逆二进制计数器  \u_四位可逆二进制计数器_1  (
    .CPD(CPD), .CLR(CLR), .CPU(CPU), .QA(QA), .QB(QB), .QC(QC), .QD(QD), .A(A), .LD(LD), .B(B), .C(C), .D(D));
endmodule

module \先行进位的四位二进制并行加法器  (
  input  A3,
  input  B3,
  input  A2,
  input  B2,
  input  A1,
  input  B1,
  input  A0,
  input  B0,
  input  C0,
  output C4,
  output S3,
  output S2,
  output S1,
  output S0
);

  wire and_1_out, and_2_out, and_3_out, and_4_out, and_5_out, and_6_out, and_7_out, and_8_out, and_9_out,
       and_10_out, C1_out, C2_out, C3_out, G0_out, G1_out, G2_out, G3_out, P0_out, P1_out, P2_out, P3_out;

  and G3 (G3_out, A3, B3);
  and G2 (G2_out, A2, B2);
  or P2 (P2_out, A2, B2);
  and G1 (G1_out, A1, B1);
  or P1 (P1_out, A1, B1);
  and G0 (G0_out, A0, B0);
  or P0 (P0_out, A0, B0);
  or P3 (P3_out, A3, B3);
  and and_1 (and_1_out, G2_out, P3_out);
  and and_2 (and_2_out, G1_out, P2_out, P3_out);
  and and_3 (and_3_out, G0_out, P1_out, P2_out, P3_out);
  and and_4 (and_4_out, P3_out, P2_out, P1_out, P0_out, C0);
  and and_5 (and_5_out, G1_out, P2_out);
  and and_6 (and_6_out, P1_out, P2_out, G0_out);
  and and_7 (and_7_out, P2_out, P1_out, P0_out, C0);
  and and_8 (and_8_out, P1_out, G0_out);
  and and_9 (and_9_out, P1_out, P0_out, C0);
  and and_10 (and_10_out, P0_out, C0);
  or u_C4 (C4, G3_out, and_1_out, and_2_out, and_3_out, and_4_out);
  or C3 (C3_out, G2_out, and_5_out, and_6_out, and_7_out);
  or C2 (C2_out, G1_out, and_8_out, and_9_out);
  or C1 (C1_out, G0_out, and_10_out);
  xor xor_1 (S3, A3, B3, C3_out);
  xor xor_2 (S2, A2, B2, C2_out);
  xor xor_3 (S1, A1, B1, C1_out);
  xor xor_4 (S0, A0, B0, C0);
endmodule

module \二进制转8421BCD码  (
  input  C0,
  input  A3,
  input  A2,
  input  A1,
  input  A0,
  output S7,
  output S6,
  output S5,
  output S4,
  output S3,
  output S2,
  output S1,
  output S0
);

  wire and_1_out, or_1_out;

  \先行进位的四位二进制并行加法器  \u_先行进位的四位二进制并行加法器_1  (
    .A3(A3), .B3(1'b0), .A2(A2), .B2(and_1_out), .A1(A1), .B1(and_1_out), .A0(A0), .B0(1'b0), .C0(C0),
    .C4(S4), .S3(S3), .S2(S2), .S1(S1), .S0(S0));
  and and_1 (and_1_out, A3, or_1_out);
  or or_1 (or_1_out, A1, A2);

  assign S5 = 1'b0;
  assign S6 = 1'b0;
  assign S7 = 1'b0;
endmodule

module \二进制转8421_封装  (
  input  C0,
  input  A3,
  input  A2,
  input  A1,
  input  A0,
  output S7,
  output S6,
  output S5,
  output S4,
  output S3,
  output S2,
  output S1,
  output S0
);

  \二进制转8421BCD码  \u_二进制转8421bcd码_1  (
    .S3(S3), .S2(S2), .S1(S1), .S0(S0), .A3(A3), .A2(A2), .A1(A1), .A0(A0), .S4(S4), .C0(C0), .S5(S5),
    .S6(S6), .S7(S7));
endmodule

module \七段译码器  (
  input  A3,
  input  A2,
  input  A1,
  input  A0,
  output a,
  output b,
  output c,
  output d,
  output e,
  output f,
  output g
);

  wire and_1_out, and_2_out, and_3_out, and_4_out, and_5_out, and_6_out, and_7_out, and_8_out, and_9_out,
       and_10_out, and_11_out, and_12_out, and_13_out, and_14_out, and_15_out, and_16_out, and_17_out,
       and_18_out, and_19_out, and_20_out, and_21_out, and_22_out, and_23_out, and_24_out, and_25_out,
       and_26_out, not_1_out, not_2_out, not_3_out, not_4_out, not_5_out, not_6_out, not_7_out, not_8_out,
       not_9_out, not_10_out, not_11_out, not_12_out, not_13_out, not_14_out, not_15_out, not_16_out,
       not_17_out, not_18_out, not_19_out, not_20_out, not_21_out, not_22_out, not_23_out, not_24_out,
       not_25_out, not_26_out, not_27_out, not_28_out, not_29_out, not_30_out, not_31_out, not_32_out,
       not_33_out, not_34_out, not_35_out, not_36_out, not_37_out;

  not not_1 (not_1_out, A3);
  not not_2 (not_2_out, A2);
  and and_1 (and_1_out, not_1_out, not_2_out, not_3_out);
  not not_3 (not_3_out, A0);
  not not_4 (not_4_out, A3);
  and and_2 (and_2_out, not_4_out, not_5_out, A1);
  not not_5 (not_5_out, A2);
  not not_6 (not_6_out, A3);
  and and_3 (and_3_out, not_6_out, A2, A0);
  not not_7 (not_7_out, A2);
  and and_4 (and_4_out, A3, not_7_out, not_8_out);
  not not_8 (not_8_out, A1);
  and and_5 (and_5_out, A3, not_9_out, A0);
  not not_9 (not_9_out, A1);
  not not_10 (not_10_out, A3);
  and and_6 (and_6_out, not_10_out, not_11_out);
  not not_11 (not_11_out, A2);
  not not_12 (not_12_out, A2);
  and and_7 (and_7_out, not_12_out, not_13_out);
  not not_13 (not_13_out, A1);
  not not_14 (not_14_out, A1);
  and and_8 (and_8_out, not_14_out, not_15_out);
  not not_15 (not_15_out, A0);
  not not_16 (not_16_out, A3);
  and and_9 (and_9_out, not_16_out, A1, A0);
  not not_17 (not_17_out, A2);
  and and_10 (and_10_out, not_17_out, not_18_out);
  not not_18 (not_18_out, A1);
  not not_19 (not_19_out, A2);
  and and_11 (and_11_out, not_19_out, A0);
  not not_20 (not_20_out, A3);
  and and_12 (and_12_out, not_20_out, A2);
  not not_21 (not_21_out, A2);
  and and_13 (and_13_out, not_21_out, not_22_out);
  not not_22 (not_22_out, A0);
  not not_23 (not_23_out, A2);
  and and_14 (and_14_out, not_23_out, A1);
  and and_15 (and_15_out, A1, not_24_out);
  not not_24 (not_24_out, A0);
  and and_16 (and_16_out, A2, not_25_out, A0);
  not not_25 (not_25_out, A1);
  not not_26 (not_26_out, A2);
  and and_17 (and_17_out, not_26_out, not_27_out);
  not not_27 (not_27_out, A0);
  and and_18 (and_18_out, A1, not_28_out);
  not not_28 (not_28_out, A0);
  not not_29 (not_29_out, A1);
  and and_19 (and_19_out, not_29_out, not_30_out);
  not not_30 (not_30_out, A0);
  and and_20 (and_20_out, A2, not_31_out);
  not not_31 (not_31_out, A1);
  and and_21 (and_21_out, A2, not_32_out);
  not not_32 (not_32_out, A0);
  and and_22 (and_22_out, A3, not_33_out);
  not not_33 (not_33_out, A1);
  not not_34 (not_34_out, A2);
  and and_23 (and_23_out, not_34_out, A1);
  and and_24 (and_24_out, A2, not_35_out);
  not not_35 (not_35_out, A1);
  and and_25 (and_25_out, A2, not_36_out);
  not not_36 (not_36_out, A0);
  and and_26 (and_26_out, A3, not_37_out);
  not not_37 (not_37_out, A2);
  or or_1 (a, and_1_out, and_2_out, and_3_out, and_4_out, and_5_out);
  or or_2 (b, and_6_out, and_7_out, and_8_out, and_9_out);
  or or_3 (c, and_10_out, and_11_out, and_12_out);
  or or_4 (d, and_13_out, and_14_out, and_15_out, and_16_out);
  or or_5 (e, and_17_out, and_18_out);
  or or_6 (f, and_19_out, and_20_out, and_21_out, and_22_out);
  or or_7 (g, and_23_out, and_24_out, and_25_out, and_26_out);
endmodule

module \七段译码器封装  (
  input  A3,
  input  A2,
  input  A1,
  input  A0
);

  wire \七段译码器_1_a , \七段译码器_1_b , \七段译码器_1_c , \七段译码器_1_d , \七段译码器_1_e , \七段译码器_1_f , \七段译码器_1_g ;

  \七段译码器  \u_七段译码器_1  (
    .A3(A3), .A2(A2), .A1(A1), .A0(A0), .g(\七段译码器_1_g ), .f(\七段译码器_1_f ), .e(\七段译码器_1_e ), .d(\七段译码器_1_d ),
    .c(\七段译码器_1_c ), .b(\七段译码器_1_b ), .a(\七段译码器_1_a ));
  _7_Segment_Display #(.active("true")) u_7_segment_display_1 (
    .g(\七段译码器_1_g ), .f(\七段译码器_1_f ), .a(\七段译码器_1_a ), .b(\七段译码器_1_b ), .e(\七段译码器_1_e ), .d(\七段译码器_1_d ),
    .c(\七段译码器_1_c ));  // open: dp
endmodule

module \报警电路  (
  input  CPU,
  input  CLR,
  input  CPD,
  input  D,
  input  C,
  input  B,
  input  A,
  input  LD,
  output \报警 ,
  output QD,
  output QC,
  output QB,
  output QA
);

  wire and_2_out, and_3_out, and_4_out, not_1_out, or_1_out;

  and and_1 (\报警 , and_2_out, CPU);
  // Buzzer #(.freq_measure("Hz"), .vol_width(7)) buzzer_1: pin names not known; wires that end beside it: 14'h250, \报警 , 7'b0001000
  or or_1 (or_1_out, QA, QB, QC, QD);
  and and_2 (and_2_out, QA, QB, QC, QD);
  not not_1 (not_1_out, and_2_out);
  and and_3 (and_3_out, CPU, not_1_out);
  and and_4 (and_4_out, or_1_out, CPD);
  \四位可逆二进制计数器  \u_四位可逆二进制计数器_1  (
    .CPD(and_4_out), .CLR(CLR), .CPU(and_3_out), .QA(QA), .QB(QB), .QC(QC), .QD(QD), .A(A), .LD(LD), .B(B),
    .C(C), .D(D));
endmodule

module \报警电路封装  (
  input  CPU,
  input  CLR,
  input  CPD,
  input  D,
  input  C,
  input  B,
  input  A,
  input  LD,
  output QD,
  output QC,
  output QB,
  output QA,
  output \报警 
);

  \报警电路  \u_报警电路_1  (
    .QD(QD), .QC(QC), .QB(QB), .QA(QA), .CPU(CPU), .CLR(CLR), .CPD(CPD), .\报警 (\报警 ), .D(D), .C(C), .B(B),
    .A(A), .LD(LD));
endmodule

module \门禁系统  (
  input  CPU,
  input  CLR,
  input  CPD,
  input  D,
  input  C,
  input  B,
  input  A,
  input  LD,
  output f1,
  output g1,
  output c1,
  output b1,
  output a1,
  output d1,
  output e1,
  output a_2,
  output b_2,
  output e,
  output d_2,
  output c_2,
  output f,
  output g,
  output \报警 
);

  wire \二进制转8421bcd码_1_s0 , \二进制转8421bcd码_1_s1 , \二进制转8421bcd码_1_s2 , \二进制转8421bcd码_1_s3 ,
       \二进制转8421bcd码_1_s4 , \二进制转8421bcd码_1_s5 , \二进制转8421bcd码_1_s6 , \二进制转8421bcd码_1_s7 , \报警电路_1_qa ,
       \报警电路_1_qb , \报警电路_1_qc , \报警电路_1_qd ;

  \七段译码器  \u_七段译码器_1  (
    .A3(\二进制转8421bcd码_1_s7 ), .A2(\二进制转8421bcd码_1_s6 ), .A1(\二进制转8421bcd码_1_s5 ), .A0(\二进制转8421bcd码_1_s4 ),
    .g(g1), .f(f1), .e(e1), .d(d1), .c(c1), .b(b1), .a(a1));
  \二进制转8421BCD码  \u_二进制转8421bcd码_1  (
    .S3(\二进制转8421bcd码_1_s3 ), .S2(\二进制转8421bcd码_1_s2 ), .S1(\二进制转8421bcd码_1_s1 ), .S0(\二进制转8421bcd码_1_s0 ),
    .A3(\报警电路_1_qd ), .A2(\报警电路_1_qc ), .A1(\报警电路_1_qb ), .A0(\报警电路_1_qa ), .S4(\二进制转8421bcd码_1_s4 ),
    .C0(1'b0), .S5(\二进制转8421bcd码_1_s5 ), .S6(\二进制转8421bcd码_1_s6 ), .S7(\二进制转8421bcd码_1_s7 ));
  \报警电路  \u_报警电路_1  (
    .QD(\报警电路_1_qd ), .QC(\报警电路_1_qc ), .QB(\报警电路_1_qb ), .QA(\报警电路_1_qa ), .CPU(CPU), .CLR(CLR), .CPD(CPD),
    .\报警 (\报警 ), .D(D), .C(C), .B(B), .A(A), .LD(LD));
  \七段译码器  \u_七段译码器_2  (
    .A3(\二进制转8421bcd码_1_s3 ), .A2(\二进制转8421bcd码_1_s2 ), .A1(\二进制转8421bcd码_1_s1 ), .A0(\二进制转8421bcd码_1_s0 ),
    .g(g), .f(f), .e(e), .d(d_2), .c(c_2), .b(b_2), .a(a_2));
endmodule

module \门禁系统测试  (
  input  CPU,
  input  CLR,
  input  CPD,
  input  D,
  input  C,
  input  B,
  input  A,
  input  LD,
  output \报警 
);

  wire \门禁系统_1_a1 , \门禁系统_1_a_2 , \门禁系统_1_b1 , \门禁系统_1_b_2 , \门禁系统_1_c1 , \门禁系统_1_c_2 , \门禁系统_1_d1 ,
       \门禁系统_1_d_2 , \门禁系统_1_e , \门禁系统_1_e1 , \门禁系统_1_f , \门禁系统_1_f1 , \门禁系统_1_g , \门禁系统_1_g1 ;

  _7_Segment_Display #(.active("true")) u_7_segment_display_1 (
    .g(\门禁系统_1_g1 ), .f(\门禁系统_1_f1 ), .a(\门禁系统_1_a1 ), .b(\门禁系统_1_b1 ), .e(\门禁系统_1_e1 ), .d(\门禁系统_1_d1 ),
    .c(\门禁系统_1_c1 ));  // open: dp
  _7_Segment_Display #(.active("true")) u_7_segment_display_2 (
    .g(\门禁系统_1_g ), .f(\门禁系统_1_f ), .a(\门禁系统_1_a_2 ), .b(\门禁系统_1_b_2 ), .e(\门禁系统_1_e ), .d(\门禁系统_1_d_2 ),
    .c(\门禁系统_1_c_2 ));  // open: dp
  \门禁系统  \u_门禁系统_1  (
    .CPU(CPU), .CLR(CLR), .\报警 (\报警 ), .CPD(CPD), .a_2(\门禁系统_1_a_2 ), .b_2(\门禁系统_1_b_2 ), .e(\门禁系统_1_e ),
    .d_2(\门禁系统_1_d_2 ), .c_2(\门禁系统_1_c_2 ), .g(\门禁系统_1_g ), .f(\门禁系统_1_f ), .a1(\门禁系统_1_a1 ),
    .b1(\门禁系统_1_b1 ), .d1(\门禁系统_1_d1 ), .e1(\门禁系统_1_e1 ), .c1(\门禁系统_1_c1 ), .f1(\门禁系统_1_f1 ),
    .g1(\门禁系统_1_g1 ), .D(D), .C(C), .B(B), .A(A), .LD(LD));
endmodule
