// Logisim project 实验4-CS2008-15533-徐瑞达.circ as structural Verilog: 4 circuits, main circuit 四位除法器
module \四位除法器  (
  input  [3:0] A,
  input  [3:0] B,
  output [3:0] rem,
  output [3:0] quot
);

  wire comparator_1_eq, comparator_1_lt, comparator_2_eq, comparator_2_lt, comparator_3_eq, comparator_3_lt,
       comparator_4_eq, comparator_4_lt, or_1_out, or_2_out, or_3_out, or_4_out;
  wire [3:0] adder_1_out, adder_3_out, adder_5_out, adder_7_out, bitselector_1_out, bitselector_2_out,
       bitselector_3_out, bitselector_4_out, bitselector_5_out, bitselector_6_out, bitselector_7_out,
       bitselector_8_out, multiplexer_1_out, multiplexer_2_out, multiplexer_3_out, multiplexer_4_out,
       multiplexer_5_out, multiplexer_6_out, subtractor_1_out, subtractor_2_out, subtractor_3_out,
       subtractor_4_out;
  wire [7:0] adder_2_out, adder_4_out, adder_6_out, bit_extender_1_out, bit_extender_2_out,
       bit_extender_3_out, bit_extender_4_out, bit_extender_5_out, bit_extender_6_out, bit_extender_7_out,
       shifter_1_out, shifter_2_out, shifter_3_out, shifter_4_out, shifter_5_out, shifter_6_out,
       shifter_7_out;

  assign bit_extender_1_out = {{4{1'b0}}, A};  // Bit_Extender bit_extender_1
  Shifter #(.width(8), .shift("ll")) shifter_1 (.in(bit_extender_1_out), .\dist (3'b001), .out(shifter_1_out));
  BitSelector #(.width(8), .group(4)) bitselector_1 (.in(shifter_1_out), .out(bitselector_1_out), .sel(1'b0));
  BitSelector #(.width(8), .group(4)) bitselector_2 (.in(shifter_1_out), .out(bitselector_2_out), .sel(1'b1));
  Adder #(.width(4)) adder_1 (.a(4'b0001), .b(bitselector_1_out), .out(adder_1_out));  // open: cin, cout
  Subtractor #(.width(4)) subtractor_1 (.a(bitselector_2_out), .b(B), .out(subtractor_1_out));  // open: bin, bout
  Comparator #(.width(4), .mode("unsigned")) comparator_1 (
    .a(B), .b(bitselector_2_out), .eq(comparator_1_eq), .lt(comparator_1_lt));  // open: gt
  Multiplexer #(.select(1), .width(4), .disabled("Z"), .enable("false")) multiplexer_1 (
    .in0(bitselector_2_out), .in1(subtractor_1_out), .out(multiplexer_1_out), .sel(or_1_out));
  or or_1 (or_1_out, comparator_1_eq, comparator_1_lt);
  assign bit_extender_2_out = {{4{1'b0}}, multiplexer_1_out};  // Bit_Extender bit_extender_2
  Multiplexer #(.select(1), .width(4), .disabled("Z"), .enable("false")) multiplexer_2 (
    .in0(bitselector_1_out), .in1(adder_1_out), .out(multiplexer_2_out), .sel(or_1_out));
  assign bit_extender_3_out = {{4{1'b0}}, multiplexer_2_out};  // Bit_Extender bit_extender_3
  Shifter #(.width(8), .shift("ll")) shifter_2 (.in(bit_extender_2_out), .\dist (3'b100), .out(shifter_2_out));
  Adder #(.width(8)) adder_2 (.a(bit_extender_3_out), .b(shifter_2_out), .out(adder_2_out));  // open: cin, cout
  Shifter #(.width(8), .shift("ll")) shifter_3 (.in(adder_2_out), .\dist (3'b001), .out(shifter_3_out));
  Adder #(.width(4)) adder_3 (.a(4'b0001), .b(bitselector_3_out), .out(adder_3_out));  // open: cin, cout
  BitSelector #(.width(8), .group(4)) bitselector_3 (.in(shifter_3_out), .out(bitselector_3_out), .sel(1'b0));
  BitSelector #(.width(8), .group(4)) bitselector_4 (.in(shifter_3_out), .out(bitselector_4_out), .sel(1'b1));
  Subtractor #(.width(4)) subtractor_2 (.a(bitselector_4_out), .b(B), .out(subtractor_2_out));  // open: bin, bout
  Comparator #(.width(4), .mode("unsigned")) comparator_2 (
    .a(B), .b(bitselector_4_out), .eq(comparator_2_eq), .lt(comparator_2_lt));  // open: gt
  or or_2 (or_2_out, comparator_2_eq, comparator_2_lt);
  Multiplexer #(.select(1), .width(4), .disabled("Z"), .enable("false")) multiplexer_3 (
    .in0(bitselector_4_out), .in1(subtractor_2_out), .out(multiplexer_3_out), .sel(or_2_out));
  assign bit_extender_4_out = {{4{1'b0}}, multiplexer_3_out};  // Bit_Extender bit_extender_4
  Multiplexer #(.select(1), .width(4), .disabled("Z"), .enable("false")) multiplexer_4 (
    .in0(bitselector_3_out), .in1(adder_3_out), .out(multiplexer_4_out), .sel(or_2_out));
  assign bit_extender_5_out = {{4{1'b0}}, multiplexer_4_out};  // Bit_Extender bit_extender_5
  Shifter #(.width(8), .shift("ll")) shifter_4 (.in(bit_extender_4_out), .\dist (3'b100), .out(shifter_4_out));
  Adder #(.width(8)) adder_4 (.a(bit_extender_5_out), .b(shifter_4_out), .out(adder_4_out));  // open: cin, cout
  Shifter #(.width(8), .shift("ll")) shifter_5 (.in(adder_4_out), .\dist (3'b001), .out(shifter_5_out));
  Adder #(.width(4)) adder_5 (.a(4'b0001), .b(bitselector_5_out), .out(adder_5_out));  // open: cin, cout
  BitSelector #(.width(8), .group(4)) bitselector_5 (.in(shifter_5_out), .out(bitselector_5_out), .sel(1'b0));
  BitSelector #(.width(8), .group(4)) bitselector_6 (.in(shifter_5_out), .out(bitselector_6_out), .sel(1'b1));
  Subtractor #(.width(4)) subtractor_3 (.a(bitselector_6_out), .b(B), .out(subtractor_3_out));  // open: bin, bout
  Comparator #(.width(4), .mode("unsigned")) comparator_3 (
    .a(B), .b(bitselector_6_out), .eq(comparator_3_eq), .lt(comparator_3_lt));  // open: gt
  or or_3 (or_3_out, comparator_3_eq, comparator_3_lt);
  Multiplexer #(.select(1), .width(4), .disabled("Z"), .enable("false")) multiplexer_5 (
    .in0(bitselector_6_out), .in1(subtractor_3_out), .out(multiplexer_5_out), .sel(or_3_out));
  assign bit_extender_6_out = {{4{1'b0}}, multiplexer_5_out};  // Bit_Extender bit_extender_6
  Multiplexer #(.select(1), .width(4), .disabled("Z"), .enable("false")) multiplexer_6 (
    .in0(bitselector_5_out), .in1(adder_5_out), .out(multiplexer_6_out), .sel(or_3_out));
  assign bit_extender_7_out = {{4{1'b0}}, multiplexer_6_out};  // Bit_Extender bit_extender_7
  Shifter #(.width(8), .shift("ll")) shifter_6 (.in(bit_extender_6_out), .\dist (3'b100), .out(shifter_6_out));
  Adder #(.width(8)) adder_6 (.a(bit_extender_7_out), .b(shifter_6_out), .out(adder_6_out));  // open: cin, cout
  Shifter #(.width(8), .shift("ll")) shifter_7 (.in(adder_6_out), .\dist (3'b001), .out(shifter_7_out));
  Adder #(.width(4)) adder_7 (.a(4'b0001), .b(bitselector_7_out), .out(adder_7_out));  // open: cin, cout
  BitSelector #(.width(8), .group(4)) bitselector_7 (.in(shifter_7_out), .out(bitselector_7_out), .sel(1'b0));
  BitSelector #(.width(8), .group(4)) bitselector_8 (.in(shifter_7_out), .out(bitselector_8_out), .sel(1'b1));
  Subtractor #(.width(4)) subtractor_4 (.a(bitselector_8_out), .b(B), .out(subtractor_4_out));  // open: bin, bout
  Comparator #(.width(4), .mode("unsigned")) comparator_4 (
    .a(B), .b(bitselector_8_out), .eq(comparator_4_eq), .lt(comparator_4_lt));  // open: gt
  or or_4 (or_4_out, comparator_4_eq, comparator_4_lt);
  Multiplexer #(.select(1), .width(4), .disabled("Z"), .enable("false")) multiplexer_7 (
    .in0(bitselector_8_out), .in1(subtractor_4_out), .out(rem), .sel(or_4_out));
  Multiplexer #(.select(1), .width(4), .disabled("Z"), .enable("false")) multiplexer_8 (
    .in0(bitselector_7_out), .in1(adder_7_out), .out(quot), .sel(or_4_out));
endmodule

// 四位除法器
module \四位除法器测试电路  (
  input  [3:0] A,
  input  [3:0] B,
  output [3:0] rem,
  output [3:0] quot
);

  \四位除法器  \u_四位除法器_1  (.A(A), .B(B), .rem(rem), .quot(quot));
endmodule

module \_32位除法器  (
  input  [31:0] A,
  input  [31:0] B,
  output [31:0] quot,
  output [31:0] rem
);

  wire bitselector_1_out, bitselector_2_out, bitselector_3_out, bitselector_4_out, bitselector_5_out,
       bitselector_6_out, bitselector_7_out, bitselector_8_out, bitselector_9_out, bitselector_10_out,
       bitselector_11_out, bitselector_12_out, bitselector_13_out, bitselector_14_out, bitselector_15_out,
       bitselector_16_out, bitselector_17_out, bitselector_18_out, bitselector_19_out, bitselector_20_out,
       bitselector_21_out, bitselector_22_out, bitselector_23_out, bitselector_24_out, bitselector_25_out,
       bitselector_26_out, bitselector_27_out, bitselector_28_out, bitselector_29_out, bitselector_30_out,
       bitselector_31_out, bitselector_32_out, comparator_1_eq, comparator_1_gt, comparator_2_eq,
       comparator_2_gt, comparator_3_eq, comparator_3_gt, comparator_4_eq, comparator_4_gt, comparator_5_eq,
       comparator_5_gt, comparator_6_eq, comparator_6_gt, comparator_7_eq, comparator_7_gt, comparator_8_eq,
       comparator_8_gt, comparator_9_eq, comparator_9_gt, comparator_10_eq, comparator_10_gt,
       comparator_11_eq, comparator_11_gt, comparator_12_eq, comparator_12_gt, comparator_13_eq,
       comparator_13_gt, comparator_14_eq, comparator_14_gt, comparator_15_eq, comparator_15_gt,
       comparator_16_eq, comparator_16_gt, comparator_17_eq, comparator_17_gt, comparator_18_eq,
       comparator_18_gt, comparator_19_eq, comparator_19_gt, comparator_20_eq, comparator_20_gt,
       comparator_21_eq, comparator_21_gt, comparator_22_eq, comparator_22_gt, comparator_23_eq,
       comparator_23_gt, comparator_24_eq, comparator_24_gt, comparator_25_eq, comparator_25_gt,
       comparator_26_eq, comparator_26_gt, comparator_27_eq, comparator_27_gt, comparator_28_eq,
       comparator_28_gt, comparator_29_eq, comparator_29_gt, comparator_30_eq, comparator_30_gt,
       comparator_31_eq, comparator_31_gt, comparator_32_eq, comparator_32_gt, or_1_out, or_2_out, or_3_out,
       or_4_out, or_5_out, or_6_out, or_7_out, or_8_out, or_9_out, or_10_out, or_11_out, or_12_out,
       or_13_out, or_14_out, or_15_out, or_16_out, or_17_out, or_18_out, or_19_out, or_20_out, or_21_out,
       or_22_out, or_23_out, or_24_out, or_25_out, or_26_out, or_27_out, or_28_out, or_29_out, or_30_out,
       or_31_out, or_32_out;
  wire [31:0] adder_1_out, adder_2_out, adder_3_out, adder_4_out, adder_5_out, adder_6_out, adder_7_out,
       adder_8_out, adder_9_out, adder_10_out, adder_11_out, adder_12_out, adder_13_out, adder_14_out,
       adder_15_out, adder_16_out, adder_17_out, adder_18_out, adder_19_out, adder_20_out, adder_21_out,
       adder_22_out, adder_23_out, adder_24_out, adder_25_out, adder_26_out, adder_27_out, adder_28_out,
       adder_29_out, adder_30_out, adder_31_out, adder_32_out, adder_33_out, adder_34_out, adder_35_out,
       adder_36_out, adder_37_out, adder_38_out, adder_39_out, adder_40_out, adder_41_out, adder_42_out,
       adder_43_out, adder_44_out, adder_45_out, adder_46_out, adder_47_out, adder_48_out, adder_49_out,
       adder_50_out, adder_51_out, adder_52_out, adder_53_out, adder_54_out, adder_55_out, adder_56_out,
       adder_57_out, adder_58_out, adder_59_out, adder_60_out, adder_61_out, adder_62_out, adder_63_out,
       bit_extender_1_out, bit_extender_2_out, bit_extender_3_out, bit_extender_4_out, bit_extender_5_out,
       bit_extender_6_out, bit_extender_7_out, bit_extender_8_out, bit_extender_9_out, bit_extender_10_out,
       bit_extender_11_out, bit_extender_12_out, bit_extender_13_out, bit_extender_14_out,
       bit_extender_15_out, bit_extender_16_out, bit_extender_17_out, bit_extender_18_out,
       bit_extender_19_out, bit_extender_20_out, bit_extender_21_out, bit_extender_22_out,
       bit_extender_23_out, bit_extender_24_out, bit_extender_25_out, bit_extender_26_out,
       bit_extender_27_out, bit_extender_28_out, bit_extender_29_out, bit_extender_30_out,
       bit_extender_31_out, bit_extender_32_out, multiplexer_1_out, multiplexer_2_out, multiplexer_3_out,
       multiplexer_4_out, multiplexer_5_out, multiplexer_6_out, multiplexer_7_out, multiplexer_8_out,
       multiplexer_9_out, multiplexer_10_out, multiplexer_11_out, multiplexer_12_out, multiplexer_13_out,
       multiplexer_14_out, multiplexer_15_out, multiplexer_16_out, multiplexer_17_out, multiplexer_18_out,
       multiplexer_19_out, multiplexer_20_out, multiplexer_21_out, multiplexer_22_out, multiplexer_23_out,
       multiplexer_24_out, multiplexer_25_out, multiplexer_26_out, multiplexer_27_out, multiplexer_28_out,
       multiplexer_29_out, multiplexer_30_out, multiplexer_31_out, multiplexer_32_out, multiplexer_33_out,
       multiplexer_34_out, multiplexer_35_out, multiplexer_36_out, multiplexer_37_out, multiplexer_38_out,
       multiplexer_39_out, multiplexer_40_out, multiplexer_41_out, multiplexer_42_out, multiplexer_43_out,
       multiplexer_44_out, multiplexer_45_out, multiplexer_46_out, multiplexer_47_out, multiplexer_48_out,
       multiplexer_49_out, multiplexer_50_out, multiplexer_51_out, multiplexer_52_out, multiplexer_53_out,
       multiplexer_54_out, multiplexer_55_out, multiplexer_56_out, multiplexer_57_out, multiplexer_58_out,
       multiplexer_59_out, multiplexer_60_out, multiplexer_61_out, multiplexer_62_out, shifter_1_out,
       shifter_2_out, shifter_3_out, shifter_4_out, shifter_5_out, shifter_6_out, shifter_7_out,
       shifter_8_out, shifter_9_out, shifter_10_out, shifter_11_out, shifter_12_out, shifter_13_out,
       shifter_14_out, shifter_15_out, shifter_16_out, shifter_17_out, shifter_18_out, shifter_19_out,
       shifter_20_out, shifter_21_out, shifter_22_out, shifter_23_out, shifter_24_out, shifter_25_out,
       shifter_26_out, shifter_27_out, shifter_28_out, shifter_29_out, shifter_30_out, shifter_31_out,
       shifter_32_out, shifter_33_out, shifter_34_out, shifter_35_out, shifter_36_out, shifter_37_out,
       shifter_38_out, shifter_39_out, shifter_40_out, shifter_41_out, shifter_42_out, shifter_43_out,
       shifter_44_out, shifter_45_out, shifter_46_out, shifter_47_out, shifter_48_out, shifter_49_out,
       shifter_50_out, shifter_51_out, shifter_52_out, shifter_53_out, shifter_54_out, shifter_55_out,
       shifter_56_out, shifter_57_out, shifter_58_out, shifter_59_out, shifter_60_out, shifter_61_out,
       shifter_62_out, shifter_63_out, subtractor_1_out, subtractor_2_out, subtractor_3_out,
       subtractor_4_out, subtractor_5_out, subtractor_6_out, subtractor_7_out, subtractor_8_out,
       subtractor_9_out, subtractor_10_out, subtractor_11_out, subtractor_12_out, subtractor_13_out,
       subtractor_14_out, subtractor_15_out, subtractor_16_out, subtractor_17_out, subtractor_18_out,
       subtractor_19_out, subtractor_20_out, subtractor_21_out, subtractor_22_out, subtractor_23_out,
       subtractor_24_out, subtractor_25_out, subtractor_26_out, subtractor_27_out, subtractor_28_out,
       subtractor_29_out, subtractor_30_out, subtractor_31_out, subtractor_32_out;

  BitSelector #(.width(32), .group(1)) bitselector_1 (.in(A), .out(bitselector_1_out), .sel({5{1'b1}}));
  Shifter #(.width(32), .shift("ll")) shifter_1 (.in(A), .\dist (5'b00001), .out(shifter_1_out));
  assign bit_extender_1_out = {{31{1'b0}}, bitselector_1_out};  // Bit_Extender bit_extender_1
  Comparator #(.width(32), .mode("unsigned")) comparator_1 (
    .a(bit_extender_1_out), .b(B), .gt(comparator_1_gt), .eq(comparator_1_eq));  // open: lt
  Adder #(.width(32)) adder_1 (.a(shifter_1_out), .b(32'h1), .out(adder_1_out));  // open: cin, cout
  Subtractor #(.width(32)) subtractor_1 (.a(bit_extender_1_out), .b(B), .out(subtractor_1_out));  // open: bin, bout
  or or_1 (or_1_out, comparator_1_gt, comparator_1_eq);
  Multiplexer #(.select(1), .width(32), .disabled("Z"), .enable("false")) multiplexer_1 (
    .in0(shifter_1_out), .in1(adder_1_out), .out(multiplexer_1_out), .sel(or_1_out));
  Multiplexer #(.select(1), .width(32), .disabled("Z"), .enable("false")) multiplexer_2 (
    .in0(bit_extender_1_out), .in1(subtractor_1_out), .out(multiplexer_2_out), .sel(or_1_out));
  Shifter #(.width(32), .shift("ll")) shifter_2 (.in(multiplexer_1_out), .\dist (5'b00001), .out(shifter_2_out));
  BitSelector #(.width(32), .group(1)) bitselector_2 (.in(multiplexer_1_out), .out(bitselector_2_out), .sel({5{1'b1}}));
  Shifter #(.width(32), .shift("ll")) shifter_3 (.in(multiplexer_2_out), .\dist (5'b00001), .out(shifter_3_out));
  assign bit_extender_2_out = {{31{1'b0}}, bitselector_2_out};  // Bit_Extender bit_extender_2
  Adder #(.width(32)) adder_2 (.a(shifter_2_out), .b(32'h1), .out(adder_2_out));  // open: cin, cout
  Adder #(.width(32)) adder_3 (.a(bit_extender_2_out), .b(shifter_3_out), .out(adder_3_out));  // open: cin, cout
  Subtractor #(.width(32)) subtractor_2 (.a(adder_3_out), .b(B), .out(subtractor_2_out));  // open: bin, bout
  Comparator #(.width(32), .mode("unsigned")) comparator_2 (
    .a(adder_3_out), .b(B), .gt(comparator_2_gt), .eq(comparator_2_eq));  // open: lt
  or or_2 (or_2_out, comparator_2_gt, comparator_2_eq);
  Multiplexer #(.select(1), .width(32), .disabled("Z"), .enable("false")) multiplexer_3 (
    .in0(shifter_2_out), .in1(adder_2_out), .out(multiplexer_3_out), .sel(or_2_out));
  Multiplexer #(.select(1), .width(32), .disabled("Z"), .enable("false")) multiplexer_4 (
    .in0(adder_3_out), .in1(subtractor_2_out), .out(multiplexer_4_out), .sel(or_2_out));
  BitSelector #(.width(32), .group(1)) bitselector_3 (.in(multiplexer_3_out), .out(bitselector_3_out), .sel({5{1'b1}}));
  Shifter #(.width(32), .shift("ll")) shifter_4 (.in(multiplexer_3_out), .\dist (5'b00001), .out(shifter_4_out));
  assign bit_extender_3_out = {{31{1'b0}}, bitselector_3_out};  // Bit_Extender bit_extender_3
  Shifter #(.width(32), .shift("ll")) shifter_5 (.in(multiplexer_4_out), .\dist (5'b00001), .out(shifter_5_out));
  Adder #(.width(32)) adder_4 (.a(shifter_4_out), .b(32'h1), .out(adder_4_out));  // open: cin, cout
  Adder #(.width(32)) adder_5 (.a(bit_extender_3_out), .b(shifter_5_out), .out(adder_5_out));  // open: cin, cout
  Subtractor #(.width(32)) subtractor_3 (.a(adder_5_out), .b(B), .out(subtractor_3_out));  // open: bin, bout
  Comparator #(.width(32), .mode("unsigned")) comparator_3 (
    .a(adder_5_out), .b(B), .gt(comparator_3_gt), .eq(comparator_3_eq));  // open: lt
  Multiplexer #(.select(1), .width(32), .disabled("Z"), .enable("false")) multiplexer_5 (
    .in0(adder_5_out), .in1(subtractor_3_out), .out(multiplexer_5_out), .sel(or_3_out));
  or or_3 (or_3_out, comparator_3_gt, comparator_3_eq);
  Multiplexer #(.select(1), .width(32), .disabled("Z"), .enable("false")) multiplexer_6 (
    .in0(shifter_4_out), .in1(adder_4_out), .out(multiplexer_6_out), .sel(or_3_out));
  Shifter #(.width(32), .shift("ll")) shifter_6 (.in(multiplexer_6_out), .\dist (5'b00001), .out(shifter_6_out));
  BitSelector #(.width(32), .group(1)) bitselector_4 (.in(multiplexer_6_out), .out(bitselector_4_out), .sel({5{1'b1}}));
  Shifter #(.width(32), .shift("ll")) shifter_7 (.in(multiplexer_5_out), .\dist (5'b00001), .out(shifter_7_out));
  assign bit_extender_4_out = {{31{1'b0}}, bitselector_4_out};  // Bit_Extender bit_extender_4
  Adder #(.width(32)) adder_6 (.a(shifter_6_out), .b(32'h1), .out(adder_6_out));  // open: cin, cout
  Adder #(.width(32)) adder_7 (.a(bit_extender_4_out), .b(shifter_7_out), .out(adder_7_out));  // open: cin, cout
  Comparator #(.width(32), .mode("unsigned")) comparator_4 (
    .a(adder_7_out), .b(B), .gt(comparator_4_gt), .eq(comparator_4_eq));  // open: lt
  Subtractor #(.width(32)) subtractor_4 (.a(adder_7_out), .b(B), .out(subtractor_4_out));  // open: bin, bout
  or or_4 (or_4_out, comparator_4_gt, comparator_4_eq);
  Multiplexer #(.select(1), .width(32), .disabled("Z"), .enable("false")) multiplexer_7 (
    .in0(adder_7_out), .in1(subtractor_4_out), .out(multiplexer_7_out), .sel(or_4_out));
  Multiplexer #(.select(1), .width(32), .disabled("Z"), .enable("false")) multiplexer_8 (
    .in0(shifter_6_out), .in1(adder_6_out), .out(multiplexer_8_out), .sel(or_4_out));
  Shifter #(.width(32), .shift("ll")) shifter_8 (.in(multiplexer_8_out), .\dist (5'b00001), .out(shifter_8_out));
  BitSelector #(.width(32), .group(1)) bitselector_5 (.in(multiplexer_8_out), .out(bitselector_5_out), .sel({5{1'b1}}));
  Shifter #(.width(32), .shift("ll")) shifter_9 (.in(multiplexer_7_out), .\dist (5'b00001), .out(shifter_9_out));
  Adder #(.width(32)) adder_8 (.a(shifter_8_out), .b(32'h1), .out(adder_8_out));  // open: cin, cout
  assign bit_extender_5_out = {{31{1'b0}}, bitselector_5_out};  // Bit_Extender bit_extender_5
  Adder #(.width(32)) adder_9 (.a(bit_extender_5_out), .b(shifter_9_out), .out(adder_9_out));  // open: cin, cout
  Comparator #(.width(32), .mode("unsigned")) comparator_5 (
    .a(adder_9_out), .b(B), .gt(comparator_5_gt), .eq(comparator_5_eq));  // open: lt
  Subtractor #(.width(32)) subtractor_5 (.a(adder_9_out), .b(B), .out(subtractor_5_out));  // open: bin, bout
  or or_5 (or_5_out, comparator_5_gt, comparator_5_eq);
  Multiplexer #(.select(1), .width(32), .disabled("Z"), .enable("false")) multiplexer_9 (
    .in0(shifter_8_out), .in1(adder_8_out), .out(multiplexer_9_out), .sel(or_5_out));
  Multiplexer #(.select(1), .width(32), .disabled("Z"), .enable("false")) multiplexer_10 (
    .in0(adder_9_out), .in1(subtractor_5_out), .out(multiplexer_10_out), .sel(or_5_out));
  BitSelector #(.width(32), .group(1)) bitselector_6 (.in(multiplexer_9_out), .out(bitselector_6_out), .sel({5{1'b1}}));
  Shifter #(.width(32), .shift("ll")) shifter_10 (.in(multiplexer_9_out), .\dist (5'b00001), .out(shifter_10_out));
  assign bit_extender_6_out = {{31{1'b0}}, bitselector_6_out};  // Bit_Extender bit_extender_6
  Shifter #(.width(32), .shift("ll")) shifter_11 (.in(multiplexer_10_out), .\dist (5'b00001), .out(shifter_11_out));
  Adder #(.width(32)) adder_10 (.a(shifter_10_out), .b(32'h1), .out(adder_10_out));  // open: cin, cout
  Adder #(.width(32)) adder_11 (.a(bit_extender_6_out), .b(shifter_11_out), .out(adder_11_out));  // open: cin, cout
  Subtractor #(.width(32)) subtractor_6 (.a(adder_11_out), .b(B), .out(subtractor_6_out));  // open: bin, bout
  or or_6 (or_6_out, comparator_6_gt, comparator_6_eq);
  Comparator #(.width(32), .mode("unsigned")) comparator_6 (
    .a(adder_11_out), .b(B), .gt(comparator_6_gt), .eq(comparator_6_eq));  // open: lt
  Multiplexer #(.select(1), .width(32), .disabled("Z"), .enable("false")) multiplexer_11 (
    .in0(adder_11_out), .in1(subtractor_6_out), .out(multiplexer_11_out), .sel(or_6_out));
  Multiplexer #(.select(1), .width(32), .disabled("Z"), .enable("false")) multiplexer_12 (
    .in0(shifter_10_out), .in1(adder_10_out), .out(multiplexer_12_out), .sel(or_6_out));
  Shifter #(.width(32), .shift("ll")) shifter_12 (.in(multiplexer_12_out), .\dist (5'b00001), .out(shifter_12_out));
  BitSelector #(.width(32), .group(1)) bitselector_7 (
    .in(multiplexer_12_out), .out(bitselector_7_out), .sel({5{1'b1}}));
  Shifter #(.width(32), .shift("ll")) shifter_13 (.in(multiplexer_11_out), .\dist (5'b00001), .out(shifter_13_out));
  assign bit_extender_7_out = {{31{1'b0}}, bitselector_7_out};  // Bit_Extender bit_extender_7
  Adder #(.width(32)) adder_12 (.a(shifter_12_out), .b(32'h1), .out(adder_12_out));  // open: cin, cout
  Adder #(.width(32)) adder_13 (.a(bit_extender_7_out), .b(shifter_13_out), .out(adder_13_out));  // open: cin, cout
  Comparator #(.width(32), .mode("unsigned")) comparator_7 (
    .a(adder_13_out), .b(B), .gt(comparator_7_gt), .eq(comparator_7_eq));  // open: lt
  Subtractor #(.width(32)) subtractor_7 (.a(adder_13_out), .b(B), .out(subtractor_7_out));  // open: bin, bout
  or or_7 (or_7_out, comparator_7_gt, comparator_7_eq);
  Multiplexer #(.select(1), .width(32), .disabled("Z"), .enable("false")) multiplexer_13 (
    .in0(shifter_12_out), .in1(adder_12_out), .out(multiplexer_13_out), .sel(or_7_out));
  Multiplexer #(.select(1), .width(32), .disabled("Z"), .enable("false")) multiplexer_14 (
    .in0(adder_13_out), .in1(subtractor_7_out), .out(multiplexer_14_out), .sel(or_7_out));
  Shifter #(.width(32), .shift("ll")) shifter_14 (.in(multiplexer_13_out), .\dist (5'b00001), .out(shifter_14_out));
  BitSelector #(.width(32), .group(1)) bitselector_8 (
    .in(multiplexer_13_out), .out(bitselector_8_out), .sel({5{1'b1}}));
  Shifter #(.width(32), .shift("ll")) shifter_15 (.in(multiplexer_14_out), .\dist (5'b00001), .out(shifter_15_out));
  Adder #(.width(32)) adder_14 (.a(shifter_14_out), .b(32'h1), .out(adder_14_out));  // open: cin, cout
  assign bit_extender_8_out = {{31{1'b0}}, bitselector_8_out};  // Bit_Extender bit_extender_8
  Adder #(.width(32)) adder_15 (.a(bit_extender_8_out), .b(shifter_15_out), .out(adder_15_out));  // open: cin, cout
  Subtractor #(.width(32)) subtractor_8 (.a(adder_15_out), .b(B), .out(subtractor_8_out));  // open: bin, bout
  Comparator #(.width(32), .mode("unsigned")) comparator_8 (
    .a(adder_15_out), .b(B), .gt(comparator_8_gt), .eq(comparator_8_eq));  // open: lt
  Multiplexer #(.select(1), .width(32), .disabled("Z"), .enable("false")) multiplexer_15 (
    .in0(adder_15_out), .in1(subtractor_8_out), .out(multiplexer_15_out), .sel(or_8_out));
  or or_8 (or_8_out, comparator_8_gt, comparator_8_eq);
  Multiplexer #(.select(1), .width(32), .disabled("Z"), .enable("false")) multiplexer_16 (
    .in0(shifter_14_out), .in1(adder_14_out), .out(multiplexer_16_out), .sel(or_8_out));
  Shifter #(.width(32), .shift("ll")) shifter_16 (.in(multiplexer_16_out), .\dist (5'b00001), .out(shifter_16_out));
  BitSelector #(.width(32), .group(1)) bitselector_9 (
    .in(multiplexer_16_out), .out(bitselector_9_out), .sel({5{1'b1}}));
  assign bit_extender_9_out = {{31{1'b0}}, bitselector_9_out};  // Bit_Extender bit_extender_9
  Shifter #(.width(32), .shift("ll")) shifter_17 (.in(multiplexer_15_out), .\dist (5'b00001), .out(shifter_17_out));
  Adder #(.width(32)) adder_16 (.a(shifter_16_out), .b(32'h1), .out(adder_16_out));  // open: cin, cout
  Adder #(.width(32)) adder_17 (.a(bit_extender_9_out), .b(shifter_17_out), .out(adder_17_out));  // open: cin, cout
  Subtractor #(.width(32)) subtractor_9 (.a(adder_17_out), .b(B), .out(subtractor_9_out));  // open: bin, bout
  Comparator #(.width(32), .mode("unsigned")) comparator_9 (
    .a(adder_17_out), .b(B), .gt(comparator_9_gt), .eq(comparator_9_eq));  // open: lt
  or or_9 (or_9_out, comparator_9_gt, comparator_9_eq);
  Multiplexer #(.select(1), .width(32), .disabled("Z"), .enable("false")) multiplexer_17 (
    .in0(adder_17_out), .in1(subtractor_9_out), .out(multiplexer_17_out), .sel(or_9_out));
  Multiplexer #(.select(1), .width(32), .disabled("Z"), .enable("false")) multiplexer_18 (
    .in0(shifter_16_out), .in1(adder_16_out), .out(multiplexer_18_out), .sel(or_9_out));
  Shifter #(.width(32), .shift("ll")) shifter_18 (.in(multiplexer_18_out), .\dist (5'b00001), .out(shifter_18_out));
  BitSelector #(.width(32), .group(1)) bitselector_10 (
    .in(multiplexer_18_out), .out(bitselector_10_out), .sel({5{1'b1}}));
  Shifter #(.width(32), .shift("ll")) shifter_19 (.in(multiplexer_17_out), .\dist (5'b00001), .out(shifter_19_out));
  Adder #(.width(32)) adder_18 (.a(shifter_18_out), .b(32'h1), .out(adder_18_out));  // open: cin, cout
  assign bit_extender_10_out = {{31{1'b0}}, bitselector_10_out};  // Bit_Extender bit_extender_10
  Adder #(.width(32)) adder_19 (.a(bit_extender_10_out), .b(shifter_19_out), .out(adder_19_out));  // open: cin, cout
  Comparator #(.width(32), .mode("unsigned")) comparator_10 (
    .a(adder_19_out), .b(B), .gt(comparator_10_gt), .eq(comparator_10_eq));  // open: lt
  Subtractor #(.width(32)) subtractor_10 (.a(adder_19_out), .b(B), .out(subtractor_10_out));  // open: bin, bout
  or or_10 (or_10_out, comparator_10_gt, comparator_10_eq);
  Multiplexer #(.select(1), .width(32), .disabled("Z"), .enable("false")) multiplexer_19 (
    .in0(shifter_18_out), .in1(adder_18_out), .out(multiplexer_19_out), .sel(or_10_out));
  Multiplexer #(.select(1), .width(32), .disabled("Z"), .enable("false")) multiplexer_20 (
    .in0(adder_19_out), .in1(subtractor_10_out), .out(multiplexer_20_out), .sel(or_10_out));
  BitSelector #(.width(32), .group(1)) bitselector_11 (
    .in(multiplexer_19_out), .out(bitselector_11_out), .sel({5{1'b1}}));
  Shifter #(.width(32), .shift("ll")) shifter_20 (.in(multiplexer_19_out), .\dist (5'b00001), .out(shifter_20_out));
  assign bit_extender_11_out = {{31{1'b0}}, bitselector_11_out};  // Bit_Extender bit_extender_11
  Shifter #(.width(32), .shift("ll")) shifter_21 (.in(multiplexer_20_out), .\dist (5'b00001), .out(shifter_21_out));
  Adder #(.width(32)) adder_20 (.a(shifter_20_out), .b(32'h1), .out(adder_20_out));  // open: cin, cout
  Adder #(.width(32)) adder_21 (.a(bit_extender_11_out), .b(shifter_21_out), .out(adder_21_out));  // open: cin, cout
  Subtractor #(.width(32)) subtractor_11 (.a(adder_21_out), .b(B), .out(subtractor_11_out));  // open: bin, bout
  Comparator #(.width(32), .mode("unsigned")) comparator_11 (
    .a(adder_21_out), .b(B), .gt(comparator_11_gt), .eq(comparator_11_eq));  // open: lt
  Multiplexer #(.select(1), .width(32), .disabled("Z"), .enable("false")) multiplexer_21 (
    .in0(adder_21_out), .in1(subtractor_11_out), .out(multiplexer_21_out), .sel(or_11_out));
  or or_11 (or_11_out, comparator_11_gt, comparator_11_eq);
  Multiplexer #(.select(1), .width(32), .disabled("Z"), .enable("false")) multiplexer_22 (
    .in0(shifter_20_out), .in1(adder_20_out), .out(multiplexer_22_out), .sel(or_11_out));
  Shifter #(.width(32), .shift("ll")) shifter_22 (.in(multiplexer_22_out), .\dist (5'b00001), .out(shifter_22_out));
  BitSelector #(.width(32), .group(1)) bitselector_12 (
    .in(multiplexer_22_out), .out(bitselector_12_out), .sel({5{1'b1}}));
  Shifter #(.width(32), .shift("ll")) shifter_23 (.in(multiplexer_21_out), .\dist (5'b00001), .out(shifter_23_out));
  assign bit_extender_12_out = {{31{1'b0}}, bitselector_12_out};  // Bit_Extender bit_extender_12
  Adder #(.width(32)) adder_22 (.a(shifter_22_out), .b(32'h1), .out(adder_22_out));  // open: cin, cout
  Adder #(.width(32)) adder_23 (.a(bit_extender_12_out), .b(shifter_23_out), .out(adder_23_out));  // open: cin, cout
  Comparator #(.width(32), .mode("unsigned")) comparator_12 (
    .a(adder_23_out), .b(B), .gt(comparator_12_gt), .eq(comparator_12_eq));  // open: lt
  Subtractor #(.width(32)) subtractor_12 (.a(adder_23_out), .b(B), .out(subtractor_12_out));  // open: bin, bout
  or or_12 (or_12_out, comparator_12_gt, comparator_12_eq);
  Multiplexer #(.select(1), .width(32), .disabled("Z"), .enable("false")) multiplexer_23 (
    .in0(adder_23_out), .in1(subtractor_12_out), .out(multiplexer_23_out), .sel(or_12_out));
  Multiplexer #(.select(1), .width(32), .disabled("Z"), .enable("false")) multiplexer_24 (
    .in0(shifter_22_out), .in1(adder_22_out), .out(multiplexer_24_out), .sel(or_12_out));
  Shifter #(.width(32), .shift("ll")) shifter_24 (.in(multiplexer_24_out), .\dist (5'b00001), .out(shifter_24_out));
  BitSelector #(.width(32), .group(1)) bitselector_13 (
    .in(multiplexer_24_out), .out(bitselector_13_out), .sel({5{1'b1}}));
  Shifter #(.width(32), .shift("ll")) shifter_25 (.in(multiplexer_23_out), .\dist (5'b00001), .out(shifter_25_out));
  Adder #(.width(32)) adder_24 (.a(shifter_24_out), .b(32'h1), .out(adder_24_out));  // open: cin, cout
  assign bit_extender_13_out = {{31{1'b0}}, bitselector_13_out};  // Bit_Extender bit_extender_13
  Adder #(.width(32)) adder_25 (.a(bit_extender_13_out), .b(shifter_25_out), .out(adder_25_out));  // open: cin, cout
  Comparator #(.width(32), .mode("unsigned")) comparator_13 (
    .a(adder_25_out), .b(B), .gt(comparator_13_gt), .eq(comparator_13_eq));  // open: lt
  Subtractor #(.width(32)) subtractor_13 (.a(adder_25_out), .b(B), .out(subtractor_13_out));  // open: bin, bout
  or or_13 (or_13_out, comparator_13_gt, comparator_13_eq);
  Multiplexer #(.select(1), .width(32), .disabled("Z"), .enable("false")) multiplexer_25 (
    .in0(shifter_24_out), .in1(adder_24_out), .out(multiplexer_25_out), .sel(or_13_out));
  Multiplexer #(.select(1), .width(32), .disabled("Z"), .enable("false")) multiplexer_26 (
    .in0(adder_25_out), .in1(subtractor_13_out), .out(multiplexer_26_out), .sel(or_13_out));
  BitSelector #(.width(32), .group(1)) bitselector_14 (
    .in(multiplexer_25_out), .out(bitselector_14_out), .sel({5{1'b1}}));
  Shifter #(.width(32), .shift("ll")) shifter_26 (.in(multiplexer_25_out), .\dist (5'b00001), .out(shifter_26_out));
  assign bit_extender_14_out = {{31{1'b0}}, bitselector_14_out};  // Bit_Extender bit_extender_14
  Shifter #(.width(32), .shift("ll")) shifter_27 (.in(multiplexer_26_out), .\dist (5'b00001), .out(shifter_27_out));
  Adder #(.width(32)) adder_26 (.a(shifter_26_out), .b(32'h1), .out(adder_26_out));  // open: cin, cout
  Adder #(.width(32)) adder_27 (.a(bit_extender_14_out), .b(shifter_27_out), .out(adder_27_out));  // open: cin, cout
  Subtractor #(.width(32)) subtractor_14 (.a(adder_27_out), .b(B), .out(subtractor_14_out));  // open: bin, bout
  or or_14 (or_14_out, comparator_14_gt, comparator_14_eq);
  Comparator #(.width(32), .mode("unsigned")) comparator_14 (
    .a(adder_27_out), .b(B), .gt(comparator_14_gt), .eq(comparator_14_eq));  // open: lt
  Multiplexer #(.select(1), .width(32), .disabled("Z"), .enable("false")) multiplexer_27 (
    .in0(adder_27_out), .in1(subtractor_14_out), .out(multiplexer_27_out), .sel(or_14_out));
  Multiplexer #(.select(1), .width(32), .disabled("Z"), .enable("false")) multiplexer_28 (
    .in0(shifter_26_out), .in1(adder_26_out), .out(multiplexer_28_out), .sel(or_14_out));
  Shifter #(.width(32), .shift("ll")) shifter_28 (.in(multiplexer_28_out), .\dist (5'b00001), .out(shifter_28_out));
  BitSelector #(.width(32), .group(1)) bitselector_15 (
    .in(multiplexer_28_out), .out(bitselector_15_out), .sel({5{1'b1}}));
  Shifter #(.width(32), .shift("ll")) shifter_29 (.in(multiplexer_27_out), .\dist (5'b00001), .out(shifter_29_out));
  assign bit_extender_15_out = {{31{1'b0}}, bitselector_15_out};  // Bit_Extender bit_extender_15
  Adder #(.width(32)) adder_28 (.a(shifter_28_out), .b(32'h1), .out(adder_28_out));  // open: cin, cout
  Adder #(.width(32)) adder_29 (.a(bit_extender_15_out), .b(shifter_29_out), .out(adder_29_out));  // open: cin, cout
  Comparator #(.width(32), .mode("unsigned")) comparator_15 (
    .a(adder_29_out), .b(B), .gt(comparator_15_gt), .eq(comparator_15_eq));  // open: lt
  Subtractor #(.width(32)) subtractor_15 (.a(adder_29_out), .b(B), .out(subtractor_15_out));  // open: bin, bout
  or or_15 (or_15_out, comparator_15_gt, comparator_15_eq);
  Multiplexer #(.select(1), .width(32), .disabled("Z"), .enable("false")) multiplexer_29 (
    .in0(shifter_28_out), .in1(adder_28_out), .out(multiplexer_29_out), .sel(or_15_out));
  Multiplexer #(.select(1), .width(32), .disabled("Z"), .enable("false")) multiplexer_30 (
    .in0(adder_29_out), .in1(subtractor_15_out), .out(multiplexer_30_out), .sel(or_15_out));
  Shifter #(.width(32), .shift("ll")) shifter_30 (.in(multiplexer_29_out), .\dist (5'b00001), .out(shifter_30_out));
  BitSelector #(.width(32), .group(1)) bitselector_16 (
    .in(multiplexer_29_out), .out(bitselector_16_out), .sel({5{1'b1}}));
  Shifter #(.width(32), .shift("ll")) shifter_31 (.in(multiplexer_30_out), .\dist (5'b00001), .out(shifter_31_out));
  Adder #(.width(32)) adder_30 (.a(shifter_30_out), .b(32'h1), .out(adder_30_out));  // open: cin, cout
  assign bit_extender_16_out = {{31{1'b0}}, bitselector_16_out};  // Bit_Extender bit_extender_16
  Adder #(.width(32)) adder_31 (.a(bit_extender_16_out), .b(shifter_31_out), .out(adder_31_out));  // open: cin, cout
  Subtractor #(.width(32)) subtractor_16 (.a(adder_31_out), .b(B), .out(subtractor_16_out));  // open: bin, bout
  Comparator #(.width(32), .mode("unsigned")) comparator_16 (
    .a(adder_31_out), .b(B), .gt(comparator_16_gt), .eq(comparator_16_eq));  // open: lt
  Multiplexer #(.select(1), .width(32), .disabled("Z"), .enable("false")) multiplexer_31 (
    .in0(adder_31_out), .in1(subtractor_16_out), .out(multiplexer_31_out), .sel(or_16_out));
  or or_16 (or_16_out, comparator_16_gt, comparator_16_eq);
  Multiplexer #(.select(1), .width(32), .disabled("Z"), .enable("false")) multiplexer_32 (
    .in0(shifter_30_out), .in1(adder_30_out), .out(multiplexer_32_out), .sel(or_16_out));
  Shifter #(.width(32), .shift("ll")) shifter_32 (.in(multiplexer_32_out), .\dist (5'b00001), .out(shifter_32_out));
  BitSelector #(.width(32), .group(1)) bitselector_17 (
    .in(multiplexer_32_out), .out(bitselector_17_out), .sel({5{1'b1}}));
  assign bit_extender_17_out = {{31{1'b0}}, bitselector_17_out};  // Bit_Extender bit_extender_17
  Shifter #(.width(32), .shift("ll")) shifter_33 (.in(multiplexer_31_out), .\dist (5'b00001), .out(shifter_33_out));
  Adder #(.width(32)) adder_32 (.a(shifter_32_out), .b(32'h1), .out(adder_32_out));  // open: cin, cout
  Adder #(.width(32)) adder_33 (.a(bit_extender_17_out), .b(shifter_33_out), .out(adder_33_out));  // open: cin, cout
  Subtractor #(.width(32)) subtractor_17 (.a(adder_33_out), .b(B), .out(subtractor_17_out));  // open: bin, bout
  Comparator #(.width(32), .mode("unsigned")) comparator_17 (
    .a(adder_33_out), .b(B), .gt(comparator_17_gt), .eq(comparator_17_eq));  // open: lt
  or or_17 (or_17_out, comparator_17_gt, comparator_17_eq);
  Multiplexer #(.select(1), .width(32), .disabled("Z"), .enable("false")) multiplexer_33 (
    .in0(adder_33_out), .in1(subtractor_17_out), .out(multiplexer_33_out), .sel(or_17_out));
  Multiplexer #(.select(1), .width(32), .disabled("Z"), .enable("false")) multiplexer_34 (
    .in0(shifter_32_out), .in1(adder_32_out), .out(multiplexer_34_out), .sel(or_17_out));
  Shifter #(.width(32), .shift("ll")) shifter_34 (.in(multiplexer_34_out), .\dist (5'b00001), .out(shifter_34_out));
  BitSelector #(.width(32), .group(1)) bitselector_18 (
    .in(multiplexer_34_out), .out(bitselector_18_out), .sel({5{1'b1}}));
  Shifter #(.width(32), .shift("ll")) shifter_35 (.in(multiplexer_33_out), .\dist (5'b00001), .out(shifter_35_out));
  Adder #(.width(32)) adder_34 (.a(shifter_34_out), .b(32'h1), .out(adder_34_out));  // open: cin, cout
  assign bit_extender_18_out = {{31{1'b0}}, bitselector_18_out};  // Bit_Extender bit_extender_18
  Adder #(.width(32)) adder_35 (.a(bit_extender_18_out), .b(shifter_35_out), .out(adder_35_out));  // open: cin, cout
  Comparator #(.width(32), .mode("unsigned")) comparator_18 (
    .a(adder_35_out), .b(B), .gt(comparator_18_gt), .eq(comparator_18_eq));  // open: lt
  Subtractor #(.width(32)) subtractor_18 (.a(adder_35_out), .b(B), .out(subtractor_18_out));  // open: bin, bout
  or or_18 (or_18_out, comparator_18_gt, comparator_18_eq);
  Multiplexer #(.select(1), .width(32), .disabled("Z"), .enable("false")) multiplexer_35 (
    .in0(shifter_34_out), .in1(adder_34_out), .out(multiplexer_35_out), .sel(or_18_out));
  Multiplexer #(.select(1), .width(32), .disabled("Z"), .enable("false")) multiplexer_36 (
    .in0(adder_35_out), .in1(subtractor_18_out), .out(multiplexer_36_out), .sel(or_18_out));
  BitSelector #(.width(32), .group(1)) bitselector_19 (
    .in(multiplexer_35_out), .out(bitselector_19_out), .sel({5{1'b1}}));
  Shifter #(.width(32), .shift("ll")) shifter_36 (.in(multiplexer_35_out), .\dist (5'b00001), .out(shifter_36_out));
  assign bit_extender_19_out = {{31{1'b0}}, bitselector_19_out};  // Bit_Extender bit_extender_19
  Shifter #(.width(32), .shift("ll")) shifter_37 (.in(multiplexer_36_out), .\dist (5'b00001), .out(shifter_37_out));
  Adder #(.width(32)) adder_36 (.a(shifter_36_out), .b(32'h1), .out(adder_36_out));  // open: cin, cout
  Adder #(.width(32)) adder_37 (.a(bit_extender_19_out), .b(shifter_37_out), .out(adder_37_out));  // open: cin, cout
  Subtractor #(.width(32)) subtractor_19 (.a(adder_37_out), .b(B), .out(subtractor_19_out));  // open: bin, bout
  Comparator #(.width(32), .mode("unsigned")) comparator_19 (
    .a(adder_37_out), .b(B), .gt(comparator_19_gt), .eq(comparator_19_eq));  // open: lt
  Multiplexer #(.select(1), .width(32), .disabled("Z"), .enable("false")) multiplexer_37 (
    .in0(adder_37_out), .in1(subtractor_19_out), .out(multiplexer_37_out), .sel(or_19_out));
  or or_19 (or_19_out, comparator_19_gt, comparator_19_eq);
  Multiplexer #(.select(1), .width(32), .disabled("Z"), .enable("false")) multiplexer_38 (
    .in0(shifter_36_out), .in1(adder_36_out), .out(multiplexer_38_out), .sel(or_19_out));
  Shifter #(.width(32), .shift("ll")) shifter_38 (.in(multiplexer_38_out), .\dist (5'b00001), .out(shifter_38_out));
  BitSelector #(.width(32), .group(1)) bitselector_20 (
    .in(multiplexer_38_out), .out(bitselector_20_out), .sel({5{1'b1}}));
  Shifter #(.width(32), .shift("ll")) shifter_39 (.in(multiplexer_37_out), .\dist (5'b00001), .out(shifter_39_out));
  assign bit_extender_20_out = {{31{1'b0}}, bitselector_20_out};  // Bit_Extender bit_extender_20
  Adder #(.width(32)) adder_38 (.a(shifter_38_out), .b(32'h1), .out(adder_38_out));  // open: cin, cout
  Adder #(.width(32)) adder_39 (.a(bit_extender_20_out), .b(shifter_39_out), .out(adder_39_out));  // open: cin, cout
  Comparator #(.width(32), .mode("unsigned")) comparator_20 (
    .a(adder_39_out), .b(B), .gt(comparator_20_gt), .eq(comparator_20_eq));  // open: lt
  Subtractor #(.width(32)) subtractor_20 (.a(adder_39_out), .b(B), .out(subtractor_20_out));  // open: bin, bout
  or or_20 (or_20_out, comparator_20_gt, comparator_20_eq);
  Multiplexer #(.select(1), .width(32), .disabled("Z"), .enable("false")) multiplexer_39 (
    .in0(adder_39_out), .in1(subtractor_20_out), .out(multiplexer_39_out), .sel(or_20_out));
  Multiplexer #(.select(1), .width(32), .disabled("Z"), .enable("false")) multiplexer_40 (
    .in0(shifter_38_out), .in1(adder_38_out), .out(multiplexer_40_out), .sel(or_20_out));
  Shifter #(.width(32), .shift("ll")) shifter_40 (.in(multiplexer_40_out), .\dist (5'b00001), .out(shifter_40_out));
  BitSelector #(.width(32), .group(1)) bitselector_21 (
    .in(multiplexer_40_out), .out(bitselector_21_out), .sel({5{1'b1}}));
  Shifter #(.width(32), .shift("ll")) shifter_41 (.in(multiplexer_39_out), .\dist (5'b00001), .out(shifter_41_out));
  Adder #(.width(32)) adder_40 (.a(shifter_40_out), .b(32'h1), .out(adder_40_out));  // open: cin, cout
  assign bit_extender_21_out = {{31{1'b0}}, bitselector_21_out};  // Bit_Extender bit_extender_21
  Adder #(.width(32)) adder_41 (.a(bit_extender_21_out), .b(shifter_41_out), .out(adder_41_out));  // open: cin, cout
  Comparator #(.width(32), .mode("unsigned")) comparator_21 (
    .a(adder_41_out), .b(B), .gt(comparator_21_gt), .eq(comparator_21_eq));  // open: lt
  Subtractor #(.width(32)) subtractor_21 (.a(adder_41_out), .b(B), .out(subtractor_21_out));  // open: bin, bout
  or or_21 (or_21_out, comparator_21_gt, comparator_21_eq);
  Multiplexer #(.select(1), .width(32), .disabled("Z"), .enable("false")) multiplexer_41 (
    .in0(shifter_40_out), .in1(adder_40_out), .out(multiplexer_41_out), .sel(or_21_out));
  Multiplexer #(.select(1), .width(32), .disabled("Z"), .enable("false")) multiplexer_42 (
    .in0(adder_41_out), .in1(subtractor_21_out), .out(multiplexer_42_out), .sel(or_21_out));
  BitSelector #(.width(32), .group(1)) bitselector_22 (
    .in(multiplexer_41_out), .out(bitselector_22_out), .sel({5{1'b1}}));
  Shifter #(.width(32), .shift("ll")) shifter_42 (.in(multiplexer_41_out), .\dist (5'b00001), .out(shifter_42_out));
  assign bit_extender_22_out = {{31{1'b0}}, bitselector_22_out};  // Bit_Extender bit_extender_22
  Shifter #(.width(32), .shift("ll")) shifter_43 (.in(multiplexer_42_out), .\dist (5'b00001), .out(shifter_43_out));
  Adder #(.width(32)) adder_42 (.a(shifter_42_out), .b(32'h1), .out(adder_42_out));  // open: cin, cout
  Adder #(.width(32)) adder_43 (.a(bit_extender_22_out), .b(shifter_43_out), .out(adder_43_out));  // open: cin, cout
  Subtractor #(.width(32)) subtractor_22 (.a(adder_43_out), .b(B), .out(subtractor_22_out));  // open: bin, bout
  or or_22 (or_22_out, comparator_22_gt, comparator_22_eq);
  Comparator #(.width(32), .mode("unsigned")) comparator_22 (
    .a(adder_43_out), .b(B), .gt(comparator_22_gt), .eq(comparator_22_eq));  // open: lt
  Multiplexer #(.select(1), .width(32), .disabled("Z"), .enable("false")) multiplexer_43 (
    .in0(adder_43_out), .in1(subtractor_22_out), .out(multiplexer_43_out), .sel(or_22_out));
  Multiplexer #(.select(1), .width(32), .disabled("Z"), .enable("false")) multiplexer_44 (
    .in0(shifter_42_out), .in1(adder_42_out), .out(multiplexer_44_out), .sel(or_22_out));
  Shifter #(.width(32), .shift("ll")) shifter_44 (.in(multiplexer_44_out), .\dist (5'b00001), .out(shifter_44_out));
  BitSelector #(.width(32), .group(1)) bitselector_23 (
    .in(multiplexer_44_out), .out(bitselector_23_out), .sel({5{1'b1}}));
  Shifter #(.width(32), .shift("ll")) shifter_45 (.in(multiplexer_43_out), .\dist (5'b00001), .out(shifter_45_out));
  assign bit_extender_23_out = {{31{1'b0}}, bitselector_23_out};  // Bit_Extender bit_extender_23
  Adder #(.width(32)) adder_44 (.a(shifter_44_out), .b(32'h1), .out(adder_44_out));  // open: cin, cout
  Adder #(.width(32)) adder_45 (.a(bit_extender_23_out), .b(shifter_45_out), .out(adder_45_out));  // open: cin, cout
  Comparator #(.width(32), .mode("unsigned")) comparator_23 (
    .a(adder_45_out), .b(B), .gt(comparator_23_gt), .eq(comparator_23_eq));  // open: lt
  Subtractor #(.width(32)) subtractor_23 (.a(adder_45_out), .b(B), .out(subtractor_23_out));  // open: bin, bout
  or or_23 (or_23_out, comparator_23_gt, comparator_23_eq);
  Multiplexer #(.select(1), .width(32), .disabled("Z"), .enable("false")) multiplexer_45 (
    .in0(shifter_44_out), .in1(adder_44_out), .out(multiplexer_45_out), .sel(or_23_out));
  Multiplexer #(.select(1), .width(32), .disabled("Z"), .enable("false")) multiplexer_46 (
    .in0(adder_45_out), .in1(subtractor_23_out), .out(multiplexer_46_out), .sel(or_23_out));
  Shifter #(.width(32), .shift("ll")) shifter_46 (.in(multiplexer_45_out), .\dist (5'b00001), .out(shifter_46_out));
  BitSelector #(.width(32), .group(1)) bitselector_24 (
    .in(multiplexer_45_out), .out(bitselector_24_out), .sel({5{1'b1}}));
  Shifter #(.width(32), .shift("ll")) shifter_47 (.in(multiplexer_46_out), .\dist (5'b00001), .out(shifter_47_out));
  Adder #(.width(32)) adder_46 (.a(shifter_46_out), .b(32'h1), .out(adder_46_out));  // open: cin, cout
  assign bit_extender_24_out = {{31{1'b0}}, bitselector_24_out};  // Bit_Extender bit_extender_24
  Adder #(.width(32)) adder_47 (.a(bit_extender_24_out), .b(shifter_47_out), .out(adder_47_out));  // open: cin, cout
  Subtractor #(.width(32)) subtractor_24 (.a(adder_47_out), .b(B), .out(subtractor_24_out));  // open: bin, bout
  Comparator #(.width(32), .mode("unsigned")) comparator_24 (
    .a(adder_47_out), .b(B), .gt(comparator_24_gt), .eq(comparator_24_eq));  // open: lt
  Multiplexer #(.select(1), .width(32), .disabled("Z"), .enable("false")) multiplexer_47 (
    .in0(adder_47_out), .in1(subtractor_24_out), .out(multiplexer_47_out), .sel(or_24_out));
  or or_24 (or_24_out, comparator_24_gt, comparator_24_eq);
  Multiplexer #(.select(1), .width(32), .disabled("Z"), .enable("false")) multiplexer_48 (
    .in0(shifter_46_out), .in1(adder_46_out), .out(multiplexer_48_out), .sel(or_24_out));
  Shifter #(.width(32), .shift("ll")) shifter_48 (.in(multiplexer_48_out), .\dist (5'b00001), .out(shifter_48_out));
  BitSelector #(.width(32), .group(1)) bitselector_25 (
    .in(multiplexer_48_out), .out(bitselector_25_out), .sel({5{1'b1}}));
  assign bit_extender_25_out = {{31{1'b0}}, bitselector_25_out};  // Bit_Extender bit_extender_25
  Shifter #(.width(32), .shift("ll")) shifter_49 (.in(multiplexer_47_out), .\dist (5'b00001), .out(shifter_49_out));
  Adder #(.width(32)) adder_48 (.a(shifter_48_out), .b(32'h1), .out(adder_48_out));  // open: cin, cout
  Adder #(.width(32)) adder_49 (.a(bit_extender_25_out), .b(shifter_49_out), .out(adder_49_out));  // open: cin, cout
  Subtractor #(.width(32)) subtractor_25 (.a(adder_49_out), .b(B), .out(subtractor_25_out));  // open: bin, bout
  Comparator #(.width(32), .mode("unsigned")) comparator_25 (
    .a(adder_49_out), .b(B), .gt(comparator_25_gt), .eq(comparator_25_eq));  // open: lt
  or or_25 (or_25_out, comparator_25_gt, comparator_25_eq);
  Multiplexer #(.select(1), .width(32), .disabled("Z"), .enable("false")) multiplexer_49 (
    .in0(adder_49_out), .in1(subtractor_25_out), .out(multiplexer_49_out), .sel(or_25_out));
  Multiplexer #(.select(1), .width(32), .disabled("Z"), .enable("false")) multiplexer_50 (
    .in0(shifter_48_out), .in1(adder_48_out), .out(multiplexer_50_out), .sel(or_25_out));
  Shifter #(.width(32), .shift("ll")) shifter_50 (.in(multiplexer_50_out), .\dist (5'b00001), .out(shifter_50_out));
  BitSelector #(.width(32), .group(1)) bitselector_26 (
    .in(multiplexer_50_out), .out(bitselector_26_out), .sel({5{1'b1}}));
  Shifter #(.width(32), .shift("ll")) shifter_51 (.in(multiplexer_49_out), .\dist (5'b00001), .out(shifter_51_out));
  Adder #(.width(32)) adder_50 (.a(shifter_50_out), .b(32'h1), .out(adder_50_out));  // open: cin, cout
  assign bit_extender_26_out = {{31{1'b0}}, bitselector_26_out};  // Bit_Extender bit_extender_26
  Adder #(.width(32)) adder_51 (.a(bit_extender_26_out), .b(shifter_51_out), .out(adder_51_out));  // open: cin, cout
  Comparator #(.width(32), .mode("unsigned")) comparator_26 (
    .a(adder_51_out), .b(B), .gt(comparator_26_gt), .eq(comparator_26_eq));  // open: lt
  Subtractor #(.width(32)) subtractor_26 (.a(adder_51_out), .b(B), .out(subtractor_26_out));  // open: bin, bout
  or or_26 (or_26_out, comparator_26_gt, comparator_26_eq);
  Multiplexer #(.select(1), .width(32), .disabled("Z"), .enable("false")) multiplexer_51 (
    .in0(shifter_50_out), .in1(adder_50_out), .out(multiplexer_51_out), .sel(or_26_out));
  Multiplexer #(.select(1), .width(32), .disabled("Z"), .enable("false")) multiplexer_52 (
    .in0(adder_51_out), .in1(subtractor_26_out), .out(multiplexer_52_out), .sel(or_26_out));
  BitSelector #(.width(32), .group(1)) bitselector_27 (
    .in(multiplexer_51_out), .out(bitselector_27_out), .sel({5{1'b1}}));
  Shifter #(.width(32), .shift("ll")) shifter_52 (.in(multiplexer_51_out), .\dist (5'b00001), .out(shifter_52_out));
  assign bit_extender_27_out = {{31{1'b0}}, bitselector_27_out};  // Bit_Extender bit_extender_27
  Shifter #(.width(32), .shift("ll")) shifter_53 (.in(multiplexer_52_out), .\dist (5'b00001), .out(shifter_53_out));
  Adder #(.width(32)) adder_52 (.a(shifter_52_out), .b(32'h1), .out(adder_52_out));  // open: cin, cout
  Adder #(.width(32)) adder_53 (.a(bit_extender_27_out), .b(shifter_53_out), .out(adder_53_out));  // open: cin, cout
  Subtractor #(.width(32)) subtractor_27 (.a(adder_53_out), .b(B), .out(subtractor_27_out));  // open: bin, bout
  Comparator #(.width(32), .mode("unsigned")) comparator_27 (
    .a(adder_53_out), .b(B), .gt(comparator_27_gt), .eq(comparator_27_eq));  // open: lt
  Multiplexer #(.select(1), .width(32), .disabled("Z"), .enable("false")) multiplexer_53 (
    .in0(adder_53_out), .in1(subtractor_27_out), .out(multiplexer_53_out), .sel(or_27_out));
  or or_27 (or_27_out, comparator_27_gt, comparator_27_eq);
  Multiplexer #(.select(1), .width(32), .disabled("Z"), .enable("false")) multiplexer_54 (
    .in0(shifter_52_out), .in1(adder_52_out), .out(multiplexer_54_out), .sel(or_27_out));
  Shifter #(.width(32), .shift("ll")) shifter_54 (.in(multiplexer_54_out), .\dist (5'b00001), .out(shifter_54_out));
  BitSelector #(.width(32), .group(1)) bitselector_28 (
    .in(multiplexer_54_out), .out(bitselector_28_out), .sel({5{1'b1}}));
  Shifter #(.width(32), .shift("ll")) shifter_55 (.in(multiplexer_53_out), .\dist (5'b00001), .out(shifter_55_out));
  assign bit_extender_28_out = {{31{1'b0}}, bitselector_28_out};  // Bit_Extender bit_extender_28
  Adder #(.width(32)) adder_54 (.a(shifter_54_out), .b(32'h1), .out(adder_54_out));  // open: cin, cout
  Adder #(.width(32)) adder_55 (.a(bit_extender_28_out), .b(shifter_55_out), .out(adder_55_out));  // open: cin, cout
  Comparator #(.width(32), .mode("unsigned")) comparator_28 (
    .a(adder_55_out), .b(B), .gt(comparator_28_gt), .eq(comparator_28_eq));  // open: lt
  Subtractor #(.width(32)) subtractor_28 (.a(adder_55_out), .b(B), .out(subtractor_28_out));  // open: bin, bout
  or or_28 (or_28_out, comparator_28_gt, comparator_28_eq);
  Multiplexer #(.select(1), .width(32), .disabled("Z"), .enable("false")) multiplexer_55 (
    .in0(adder_55_out), .in1(subtractor_28_out), .out(multiplexer_55_out), .sel(or_28_out));
  Multiplexer #(.select(1), .width(32), .disabled("Z"), .enable("false")) multiplexer_56 (
    .in0(shifter_54_out), .in1(adder_54_out), .out(multiplexer_56_out), .sel(or_28_out));
  Shifter #(.width(32), .shift("ll")) shifter_56 (.in(multiplexer_56_out), .\dist (5'b00001), .out(shifter_56_out));
  BitSelector #(.width(32), .group(1)) bitselector_29 (
    .in(multiplexer_56_out), .out(bitselector_29_out), .sel({5{1'b1}}));
  Shifter #(.width(32), .shift("ll")) shifter_57 (.in(multiplexer_55_out), .\dist (5'b00001), .out(shifter_57_out));
  Adder #(.width(32)) adder_56 (.a(shifter_56_out), .b(32'h1), .out(adder_56_out));  // open: cin, cout
  assign bit_extender_29_out = {{31{1'b0}}, bitselector_29_out};  // Bit_Extender bit_extender_29
  Adder #(.width(32)) adder_57 (.a(bit_extender_29_out), .b(shifter_57_out), .out(adder_57_out));  // open: cin, cout
  Comparator #(.width(32), .mode("unsigned")) comparator_29 (
    .a(adder_57_out), .b(B), .gt(comparator_29_gt), .eq(comparator_29_eq));  // open: lt
  Subtractor #(.width(32)) subtractor_29 (.a(adder_57_out), .b(B), .out(subtractor_29_out));  // open: bin, bout
  or or_29 (or_29_out, comparator_29_gt, comparator_29_eq);
  Multiplexer #(.select(1), .width(32), .disabled("Z"), .enable("false")) multiplexer_57 (
    .in0(shifter_56_out), .in1(adder_56_out), .out(multiplexer_57_out), .sel(or_29_out));
  Multiplexer #(.select(1), .width(32), .disabled("Z"), .enable("false")) multiplexer_58 (
    .in0(adder_57_out), .in1(subtractor_29_out), .out(multiplexer_58_out), .sel(or_29_out));
  BitSelector #(.width(32), .group(1)) bitselector_30 (
    .in(multiplexer_57_out), .out(bitselector_30_out), .sel({5{1'b1}}));
  Shifter #(.width(32), .shift("ll")) shifter_58 (.in(multiplexer_57_out), .\dist (5'b00001), .out(shifter_58_out));
  assign bit_extender_30_out = {{31{1'b0}}, bitselector_30_out};  // Bit_Extender bit_extender_30
  Shifter #(.width(32), .shift("ll")) shifter_59 (.in(multiplexer_58_out), .\dist (5'b00001), .out(shifter_59_out));
  Adder #(.width(32)) adder_58 (.a(shifter_58_out), .b(32'h1), .out(adder_58_out));  // open: cin, cout
  Adder #(.width(32)) adder_59 (.a(bit_extender_30_out), .b(shifter_59_out), .out(adder_59_out));  // open: cin, cout
  Subtractor #(.width(32)) subtractor_30 (.a(adder_59_out), .b(B), .out(subtractor_30_out));  // open: bin, bout
  or or_30 (or_30_out, comparator_30_gt, comparator_30_eq);
  Comparator #(.width(32), .mode("unsigned")) comparator_30 (
    .a(adder_59_out), .b(B), .gt(comparator_30_gt), .eq(comparator_30_eq));  // open: lt
  Multiplexer #(.select(1), .width(32), .disabled("Z"), .enable("false")) multiplexer_59 (
    .in0(adder_59_out), .in1(subtractor_30_out), .out(multiplexer_59_out), .sel(or_30_out));
  Multiplexer #(.select(1), .width(32), .disabled("Z"), .enable("false")) multiplexer_60 (
    .in0(shifter_58_out), .in1(adder_58_out), .out(multiplexer_60_out), .sel(or_30_out));
  Shifter #(.width(32), .shift("ll")) shifter_60 (.in(multiplexer_60_out), .\dist (5'b00001), .out(shifter_60_out));
  BitSelector #(.width(32), .group(1)) bitselector_31 (
    .in(multiplexer_60_out), .out(bitselector_31_out), .sel({5{1'b1}}));
  Shifter #(.width(32), .shift("ll")) shifter_61 (.in(multiplexer_59_out), .\dist (5'b00001), .out(shifter_61_out));
  assign bit_extender_31_out = {{31{1'b0}}, bitselector_31_out};  // Bit_Extender bit_extender_31
  Adder #(.width(32)) adder_60 (.a(shifter_60_out), .b(32'h1), .out(adder_60_out));  // open: cin, cout
  Adder #(.width(32)) adder_61 (.a(bit_extender_31_out), .b(shifter_61_out), .out(adder_61_out));  // open: cin, cout
  Comparator #(.width(32), .mode("unsigned")) comparator_31 (
    .a(adder_61_out), .b(B), .gt(comparator_31_gt), .eq(comparator_31_eq));  // open: lt
  Subtractor #(.width(32)) subtractor_31 (.a(adder_61_out), .b(B), .out(subtractor_31_out));  // open: bin, bout
  or or_31 (or_31_out, comparator_31_gt, comparator_31_eq);
  Multiplexer #(.select(1), .width(32), .disabled("Z"), .enable("false")) multiplexer_61 (
    .in0(shifter_60_out), .in1(adder_60_out), .out(multiplexer_61_out), .sel(or_31_out));
  Multiplexer #(.select(1), .width(32), .disabled("Z"), .enable("false")) multiplexer_62 (
    .in0(adder_61_out), .in1(subtractor_31_out), .out(multiplexer_62_out), .sel(or_31_out));
  Shifter #(.width(32), .shift("ll")) shifter_62 (.in(multiplexer_61_out), .\dist (5'b00001), .out(shifter_62_out));
  BitSelector #(.width(32), .group(1)) bitselector_32 (
    .in(multiplexer_61_out), .out(bitselector_32_out), .sel({5{1'b1}}));
  Shifter #(.width(32), .shift("ll")) shifter_63 (.in(multiplexer_62_out), .\dist (5'b00001), .out(shifter_63_out));
  Adder #(.width(32)) adder_62 (.a(shifter_62_out), .b(32'h1), .out(adder_62_out));  // open: cin, cout
  assign bit_extender_32_out = {{31{1'b0}}, bitselector_32_out};  // Bit_Extender bit_extender_32
  Adder #(.width(32)) adder_63 (.a(bit_extender_32_out), .b(shifter_63_out), .out(adder_63_out));  // open: cin, cout
  Subtractor #(.width(32)) subtractor_32 (.a(adder_63_out), .b(B), .out(subtractor_32_out));  // open: bin, bout
  Comparator #(.width(32), .mode("unsigned")) comparator_32 (
    .a(adder_63_out), .b(B), .gt(comparator_32_gt), .eq(comparator_32_eq));  // open: lt
  Multiplexer #(.select(1), .width(32), .disabled("Z"), .enable("false")) multiplexer_63 (
    .in0(adder_63_out), .in1(subtractor_32_out), .out(rem), .sel(or_32_out));
  or or_32 (or_32_out, comparator_32_gt, comparator_32_eq);
  Multiplexer #(.select(1), .width(32), .disabled("Z"), .enable("false")) multiplexer_64 (
    .in0(shifter_62_out), .in1(adder_62_out), .out(quot), .sel(or_32_out));
endmodule

module \_32位除法器测试电路  (
  input  [31:0] A,
  input  [31:0] B,
  output [31:0] quot,
  output [31:0] rem
);

  // Probe on A
  // Probe on B
  // Probe on quot
  \_32位除法器  \u_32位除法器_1  (.A(A), .B(B), .quot(quot), .rem(rem));
  // Probe on rem
endmodule
