// Logisim project 74163.circ as structural Verilog: 1 circuit, main circuit 74163
module _74163 (
  input  D0,
  input  D1,
  input  D2,
  input  D3,
  input  CET,
  input  CEP,
  input  nPE,
  input  nMR,
  input  CP,
  output Q0,
  output Q1,
  output Q2,
  output Q3,
  output TC
);

  wire and_1_out, and_2_out, and_3_out, and_4_out, and_5_out, and_6_out, and_7_out, and_8_out, and_9_out,
       buffer_1_out, buffer_2_out, buffer_3_out, d_ff_1_q, d_ff_1_qn, d_ff_2_q, d_ff_2_qn, d_ff_3_q,
       d_ff_3_qn, d_ff_4_q, d_ff_4_qn, nand_1_out, nand_2_out, nor_1_out, nor_2_out, nor_3_out, nor_4_out,
       nor_5_out, nor_6_out, not_1_out, not_2_out, not_3_out, or_1_out, or_2_out, or_3_out, or_4_out,
       or_5_out, xnor_1_out, xnor_2_out, xnor_3_out;

  buf buffer_1 (buffer_1_out, nPE);
  buf buffer_2 (buffer_2_out, CET);
  buf buffer_3 (buffer_3_out, CEP);
  nor nor_1 (nor_1_out, buffer_1_out, not_1_out);
  not not_1 (not_1_out, nMR);
  not not_2 (not_2_out, CP);
  nand nand_1 (nand_1_out, buffer_2_out, buffer_3_out);
  nor nor_2 (nor_2_out, nor_1_out, not_1_out);
  and and_1 (and_1_out, D0, nor_1_out);
  not not_3 (not_3_out, nand_1_out);
  xnor xnor_1 (xnor_1_out, not_3_out, d_ff_1_qn);
  and and_2 (and_2_out, xnor_1_out, nor_2_out);
  or or_1 (or_1_out, and_1_out, and_2_out);
  D_Flip_Flop #(.trigger("falling")) d_ff_1 (
    .clk(not_2_out), .D(or_1_out), .Q(d_ff_1_q), .Qn(d_ff_1_qn));  // open: preset, en, reset
  nor nor_3 (nor_3_out, nand_1_out, d_ff_1_qn);
  xnor xnor_2 (xnor_2_out, nor_3_out, d_ff_2_qn);
  and and_3 (and_3_out, xnor_2_out, nor_2_out);
  and and_4 (and_4_out, D1, nor_1_out);
  or or_2 (or_2_out, and_4_out, and_3_out);
  not not_4 (Q0, d_ff_1_qn);
  D_Flip_Flop #(.trigger("falling")) d_ff_2 (
    .clk(not_2_out), .D(or_2_out), .Q(d_ff_2_q), .Qn(d_ff_2_qn));  // open: preset, en, reset
  not not_5 (Q1, d_ff_2_qn);
  nor nor_4 (nor_4_out, nand_1_out, d_ff_2_qn, d_ff_1_qn);
  xnor xnor_3 (xnor_3_out, nor_4_out, d_ff_3_qn);
  and and_5 (and_5_out, xnor_3_out, nor_2_out);
  and and_6 (and_6_out, D2, nor_1_out);
  or or_3 (or_3_out, and_6_out, and_5_out);
  nor nor_5 (nor_5_out, nand_1_out, d_ff_3_qn, d_ff_2_qn, d_ff_1_qn);
  and and_7 (and_7_out, D3, nor_1_out);
  or or_4 (or_4_out, and_7_out, and_9_out);
  D_Flip_Flop #(.trigger("falling")) d_ff_3 (
    .clk(not_2_out), .D(or_3_out), .Q(d_ff_3_q), .Qn(d_ff_3_qn));  // open: preset, en, reset
  not not_6 (Q2, d_ff_3_qn);
  nor nor_6 (nor_6_out, nor_5_out, d_ff_4_qn);
  and and_8 (and_8_out, nor_5_out, d_ff_4_qn);
  or or_5 (or_5_out, and_8_out, nor_6_out);
  and and_9 (and_9_out, nor_2_out, or_5_out);
  D_Flip_Flop #(.trigger("falling")) d_ff_4 (
    .clk(not_2_out), .D(or_4_out), .Q(d_ff_4_q), .Qn(d_ff_4_qn));  // open: preset, en, reset
  not not_7 (Q3, d_ff_4_qn);
  nand nand_2 (nand_2_out, d_ff_4_q, d_ff_3_q, d_ff_2_q, d_ff_1_q, buffer_2_out);
  not not_8 (TC, nand_2_out);
endmodule
