// Logisim project test 74181.circ as structural Verilog: 1 circuit, main circuit main
module main (
  input  [3:0] S,
  input  [3:0] A,
  input  [3:0] B,
  input  M,
  input  Cn,
  input  in_6,
  input  in_7,
  output G,
  output Cn_4,
  output P,
  output A_B,
  output [3:0] F
);

  wire clock_1_out, n74181_1_cn_4, not_1_out, undriven_2;
  wire [2:0] bitadder_1_out;
  wire [3:0] counter_1_q, ram_1_data, undriven;

  BitAdder #(.width(4)) bitadder_1 (.in0(undriven), .out(bitadder_1_out));
  Clock clock_1 (.out(clock_1_out));
  not not_1 (not_1_out, Cn);
  Counter #(.width(4), .max('hf)) counter_1 (
    .load(in_6), .count(in_7), .Q(counter_1_q), .clk(clock_1_out), .clr(undriven_2));  // open: D, carry
  LED led_1 (.in(clock_1_out));
  _74181 u_74181_1 (
    .S3(S[3]), .S2(S[2]), .S1(S[1]), .S0(S[0]), .B3(B[3]), .A3(A[3]), .B2(B[2]), .A2(A[2]), .B1(B[1]),
    .A1(A[1]), .B0(B[0]), .A0(A[0]), .M(M), .Cn(not_1_out), .G(G), .Cn_4(n74181_1_cn_4), .P(P), .F3(F[3]),
    .F2(F[2]), .A_B(A_B), .F1(F[1]), .F0(F[0]));
  not not_2 (Cn_4, n74181_1_cn_4);
  Hex_Digit_Display hex_digit_display_1 (.value(counter_1_q));  // open: dp
  Hex_Digit_Display hex_digit_display_2 (.value(F));  // open: dp
  Register register_1 ();  // open: D, en, Q, clk, clr
  Multiplexer #(.enable("false")) multiplexer_1 ();  // open: in0, in1, out, sel
  RAM #(.addrWidth(4), .dataWidth(4)) ram_1 (.addr(counter_1_q), .data(ram_1_data), .sel(1'b1));  // open: clk, ld, clr
  Hex_Digit_Display hex_digit_display_3 (.value(ram_1_data));  // open: dp
endmodule
