// Logisim project 74182.circ as structural Verilog: 1 circuit, main circuit 74182
module _74182 (
  input  G0,
  input  P0,
  input  Cn,
  input  G1,
  input  P1,
  input  G2,
  input  P2,
  input  G3,
  input  P3,
  output Cn_x,
  output Cn_y,
  output Cn_z,
  output G,
  output P
);

  wire and_1_out, and_2_out, and_3_out, and_4_out, and_5_out, and_6_out, and_7_out, and_8_out, and_9_out,
       and_10_out, and_11_out, and_12_out, and_13_out, not_1_out;

  nor nor_1 (Cn_x, and_2_out, and_1_out);
  and and_1 (and_1_out, G0, not_1_out);
  and and_2 (and_2_out, G0, P0);
  not not_1 (not_1_out, Cn);
  nor nor_2 (Cn_y, and_3_out, and_4_out, and_5_out);
  and and_3 (and_3_out, G1, P1);
  and and_4 (and_4_out, G0, P0, G1);
  and and_5 (and_5_out, not_1_out, G0, G1);
  nor nor_3 (Cn_z, and_6_out, and_6_out, and_7_out, and_8_out, and_9_out);
  and and_6 (and_6_out, G2, P2);
  and and_7 (and_7_out, G1, P1, G2);
  and and_8 (and_8_out, G0, G0, P0, G1, G2);
  and and_9 (and_9_out, not_1_out, not_1_out, G0, G1, G2);
  and and_10 (and_10_out, G3, P3);
  and and_11 (and_11_out, G2, P2, G3);
  or or_1 (G, and_10_out, and_10_out, and_11_out, and_12_out, and_13_out);
  and and_12 (and_12_out, G1, G1, P1, G2, G3);
  and and_13 (and_13_out, G0, G0, G1, G2, G3);
  or or_2 (P, P0, P0, P1, P2, P3);
endmodule
