// Logisim project 基本.circ as structural Verilog: 1 circuit, main circuit main
module main (
  input  a,
  input  b,
  input  jk1_j,
  input  jk_k,
  input  D1,
  input  D2,
  input  D3,
  input  D4,
  input  D5,
  input  D6,
  input  D7,
  input  D8,
  output f
);

  wire an1_out, d_ff_1_q, d_ff_1_qn, j_k_ff_1_q;

  Button an1 (.out(an1_out));
  and and_1 (f, an1_out, a, b);
  LED led_1 (.in(f));
  LED led_2 (.in(d_ff_1_q));
  D_Flip_Flop d_ff_1 (.clk(an1_out), .D(d_ff_1_qn), .Q(d_ff_1_q), .Qn(d_ff_1_qn));  // open: preset, en, reset
  J_K_Flip_Flop j_k_ff_1 (.J(jk1_j), .clk(an1_out), .K(jk_k), .Q(j_k_ff_1_q));  // open: Qn, preset, en, reset
  _7_Segment_Display u_7_segment_display_1 (.g(D4), .f(D3), .a(D2), .b(D1), .e(D5), .d(D6), .c(D7), .dp(D8));
  LED led_3 (.in(j_k_ff_1_q));
endmodule
