// Logisim project 实验3-CS2008-15533-徐瑞达.circ as structural Verilog: 6 circuits, main circuit 四位乘法器测试电路
// 四位乘法器测试电路
module \四位乘法器  (
  input  [3:0] a_3_0,
  input  [3:0] b_3_0,
  output [7:0] P_7_0
);

  wire bitselector_1_out, bitselector_2_out, bitselector_3_out, bitselector_4_out;
  wire [7:0] adder_1_out, adder_2_out, adder_3_out, adder_4_out, bit_extender_1_out, multiplexer_1_out,
       multiplexer_2_out, multiplexer_3_out, shifter_1_out, shifter_2_out, shifter_3_out;

  assign bit_extender_1_out = {{4{1'b0}}, b_3_0};  // Bit_Extender bit_extender_1
  BitSelector #(.width(4), .group(1)) bitselector_1 (.in(a_3_0), .out(bitselector_1_out), .sel(2'b00));
  Adder #(.width(8)) adder_1 (.a({8{1'b0}}), .b(bit_extender_1_out), .out(adder_1_out), .cin(1'b0));  // open: cout
  Multiplexer #(.select(1), .width(8), .disabled("Z"), .enable("false")) multiplexer_1 (
    .in0({8{1'b0}}), .in1(adder_1_out), .out(multiplexer_1_out), .sel(bitselector_1_out));
  Shifter #(.width(8), .shift("ll")) shifter_1 (.in(bit_extender_1_out), .\dist (3'b001), .out(shifter_1_out));
  BitSelector #(.width(4), .group(1)) bitselector_2 (.in(a_3_0), .out(bitselector_2_out), .sel(2'b01));
  Adder #(.width(8)) adder_2 (.a(multiplexer_1_out), .b(shifter_1_out), .out(adder_2_out), .cin(1'b0));  // open: cout
  Multiplexer #(.select(1), .width(8), .disabled("Z"), .enable("false")) multiplexer_2 (
    .in0(multiplexer_1_out), .in1(adder_2_out), .out(multiplexer_2_out), .sel(bitselector_2_out));
  Shifter #(.width(8), .shift("ll")) shifter_2 (.in(shifter_1_out), .\dist (3'b001), .out(shifter_2_out));
  BitSelector #(.width(4), .group(1)) bitselector_3 (.in(a_3_0), .out(bitselector_3_out), .sel(2'b10));
  Multiplexer #(.select(1), .width(8), .disabled("Z"), .enable("false")) multiplexer_3 (
    .in0(multiplexer_2_out), .in1(adder_3_out), .out(multiplexer_3_out), .sel(bitselector_3_out));
  Adder #(.width(8)) adder_3 (.a(multiplexer_2_out), .b(shifter_2_out), .out(adder_3_out), .cin(1'b0));  // open: cout
  Shifter #(.width(8), .shift("ll")) shifter_3 (.in(shifter_2_out), .\dist (3'b001), .out(shifter_3_out));
  Adder #(.width(8)) adder_4 (.a(multiplexer_3_out), .b(shifter_3_out), .out(adder_4_out), .cin(1'b0));  // open: cout
  BitSelector #(.width(4), .group(1)) bitselector_4 (.in(a_3_0), .out(bitselector_4_out), .sel(2'b11));
  Multiplexer #(.select(1), .width(8), .disabled("Z"), .enable("false")) multiplexer_4 (
    .in0(multiplexer_3_out), .in1(adder_4_out), .out(P_7_0), .sel(bitselector_4_out));
endmodule

module \四位乘法器测试电路  (
  input  [3:0] a_3_0,
  input  [3:0] b_3_0,
  output [7:0] P_7_0
);

  \四位乘法器  \u_四位乘法器_1  (.b_3_0(a_3_0), .P_7_0(P_7_0), .a_3_0(b_3_0));
endmodule

// 32X4乘法器测试电路
module \_32X4乘法器  (
  input  [3:0] a_3_0,
  input  [31:0] b_31_0,
  output [31:0] P_31_0
);

  wire bitselector_1_out, bitselector_2_out, bitselector_3_out, bitselector_4_out;
  wire [31:0] adder_1_out, adder_2_out, adder_3_out, adder_4_out, multiplexer_1_out, multiplexer_2_out,
       multiplexer_3_out, shifter_1_out, shifter_2_out, shifter_3_out;

  BitSelector #(.width(4), .group(1)) bitselector_1 (.in(a_3_0), .out(bitselector_1_out), .sel(2'b00));
  Adder #(.width(32)) adder_1 (.a({32{1'b0}}), .b(b_31_0), .out(adder_1_out), .cin(1'b0));  // open: cout
  Multiplexer #(.select(1), .width(32), .disabled("Z"), .enable("false")) multiplexer_1 (
    .in0({32{1'b0}}), .in1(adder_1_out), .out(multiplexer_1_out), .sel(bitselector_1_out));
  Shifter #(.width(32), .shift("ll")) shifter_1 (.in(b_31_0), .\dist (5'b00001), .out(shifter_1_out));
  BitSelector #(.width(4), .group(1)) bitselector_2 (.in(a_3_0), .out(bitselector_2_out), .sel(2'b01));
  Adder #(.width(32)) adder_2 (.a(multiplexer_1_out), .b(shifter_1_out), .out(adder_2_out), .cin(1'b0));  // open: cout
  Multiplexer #(.select(1), .width(32), .disabled("Z"), .enable("false")) multiplexer_2 (
    .in0(multiplexer_1_out), .in1(adder_2_out), .out(multiplexer_2_out), .sel(bitselector_2_out));
  Shifter #(.width(32), .shift("ll")) shifter_2 (.in(shifter_1_out), .\dist (5'b00001), .out(shifter_2_out));
  BitSelector #(.width(4), .group(1)) bitselector_3 (.in(a_3_0), .out(bitselector_3_out), .sel(2'b10));
  Multiplexer #(.select(1), .width(32), .disabled("Z"), .enable("false")) multiplexer_3 (
    .in0(multiplexer_2_out), .in1(adder_3_out), .out(multiplexer_3_out), .sel(bitselector_3_out));
  Adder #(.width(32)) adder_3 (.a(multiplexer_2_out), .b(shifter_2_out), .out(adder_3_out), .cin(1'b0));  // open: cout
  Shifter #(.width(32), .shift("ll")) shifter_3 (.in(shifter_2_out), .\dist (5'b00001), .out(shifter_3_out));
  Adder #(.width(32)) adder_4 (.a(multiplexer_3_out), .b(shifter_3_out), .out(adder_4_out), .cin(1'b0));  // open: cout
  BitSelector #(.width(4), .group(1)) bitselector_4 (.in(a_3_0), .out(bitselector_4_out), .sel(2'b11));
  Multiplexer #(.select(1), .width(32), .disabled("Z"), .enable("false")) multiplexer_4 (
    .in0(multiplexer_3_out), .in1(adder_4_out), .out(P_31_0), .sel(bitselector_4_out));
endmodule

module \_32X4乘法器测试电路  (
  input  [3:0] a_3_0,
  input  [31:0] b_31_0,
  output [31:0] P_31_0
);

  \_32X4乘法器  \u_32x4乘法器_1  (.b_31_0(b_31_0), .P_31_0(P_31_0), .a_3_0(a_3_0));
endmodule

// 32X32乘法器测试电路
module \_32X32乘法器  (
  input  [31:0] a_31_0,
  input  [31:0] b_31_0,
  output [31:0] P_31_0
);

  wire [3:0] bitselector_1_out, bitselector_2_out, bitselector_3_out, bitselector_4_out, bitselector_5_out,
       bitselector_6_out, bitselector_7_out, bitselector_8_out;
  wire [31:0] adder_1_out, adder_2_out, adder_3_out, adder_4_out, adder_5_out, adder_6_out,
       \n32x4乘法器_1_p_31_0 , \n32x4乘法器_2_p_31_0 , \n32x4乘法器_3_p_31_0 , \n32x4乘法器_4_p_31_0 ,
       \n32x4乘法器_5_p_31_0 , \n32x4乘法器_6_p_31_0 , \n32x4乘法器_7_p_31_0 , \n32x4乘法器_8_p_31_0 , shifter_1_out,
       shifter_2_out, shifter_3_out, shifter_4_out, shifter_5_out, shifter_6_out, shifter_7_out,
       shifter_8_out;

  BitSelector #(.width(32), .group(4)) bitselector_1 (.in(a_31_0), .out(bitselector_1_out), .sel(3'b000));
  \_32X4乘法器  \u_32x4乘法器_1  (.b_31_0(b_31_0), .P_31_0(\n32x4乘法器_1_p_31_0 ), .a_3_0(bitselector_1_out));
  Shifter #(.width(32), .shift("ll")) shifter_1 (.in(\n32x4乘法器_1_p_31_0 ), .\dist ({5{1'b0}}), .out(shifter_1_out));
  BitSelector #(.width(32), .group(4)) bitselector_2 (.in(a_31_0), .out(bitselector_2_out), .sel(3'b001));
  \_32X4乘法器  \u_32x4乘法器_2  (.b_31_0(b_31_0), .P_31_0(\n32x4乘法器_2_p_31_0 ), .a_3_0(bitselector_2_out));
  Shifter #(.width(32), .shift("ll")) shifter_2 (.in(\n32x4乘法器_2_p_31_0 ), .\dist (5'b00100), .out(shifter_2_out));
  BitSelector #(.width(32), .group(4)) bitselector_3 (.in(a_31_0), .out(bitselector_3_out), .sel(3'b010));
  Adder #(.width(32)) adder_1 (.a(shifter_1_out), .b(shifter_2_out), .out(adder_1_out), .cin(1'b0));  // open: cout
  \_32X4乘法器  \u_32x4乘法器_3  (.b_31_0(b_31_0), .P_31_0(\n32x4乘法器_3_p_31_0 ), .a_3_0(bitselector_3_out));
  BitSelector #(.width(32), .group(4)) bitselector_4 (.in(a_31_0), .out(bitselector_4_out), .sel(3'b011));
  Shifter #(.width(32), .shift("ll")) shifter_3 (.in(\n32x4乘法器_3_p_31_0 ), .\dist (5'b01000), .out(shifter_3_out));
  Adder #(.width(32)) adder_2 (.a(adder_1_out), .b(shifter_3_out), .out(adder_2_out), .cin(1'b0));  // open: cout
  \_32X4乘法器  \u_32x4乘法器_4  (.b_31_0(b_31_0), .P_31_0(\n32x4乘法器_4_p_31_0 ), .a_3_0(bitselector_4_out));
  BitSelector #(.width(32), .group(4)) bitselector_5 (.in(a_31_0), .out(bitselector_5_out), .sel(3'b100));
  Shifter #(.width(32), .shift("ll")) shifter_4 (.in(\n32x4乘法器_4_p_31_0 ), .\dist (5'b01100), .out(shifter_4_out));
  Adder #(.width(32)) adder_3 (.a(adder_2_out), .b(shifter_4_out), .out(adder_3_out), .cin(1'b0));  // open: cout
  \_32X4乘法器  \u_32x4乘法器_5  (.b_31_0(b_31_0), .P_31_0(\n32x4乘法器_5_p_31_0 ), .a_3_0(bitselector_5_out));
  Shifter #(.width(32), .shift("ll")) shifter_5 (.in(\n32x4乘法器_5_p_31_0 ), .\dist (5'b10000), .out(shifter_5_out));
  BitSelector #(.width(32), .group(4)) bitselector_6 (.in(a_31_0), .out(bitselector_6_out), .sel(3'b101));
  Adder #(.width(32)) adder_4 (.a(adder_3_out), .b(shifter_5_out), .out(adder_4_out), .cin(1'b0));  // open: cout
  \_32X4乘法器  \u_32x4乘法器_6  (.b_31_0(b_31_0), .P_31_0(\n32x4乘法器_6_p_31_0 ), .a_3_0(bitselector_6_out));
  Shifter #(.width(32), .shift("ll")) shifter_6 (.in(\n32x4乘法器_6_p_31_0 ), .\dist (5'b10100), .out(shifter_6_out));
  BitSelector #(.width(32), .group(4)) bitselector_7 (.in(a_31_0), .out(bitselector_7_out), .sel(3'b110));
  Adder #(.width(32)) adder_5 (.a(adder_4_out), .b(shifter_6_out), .out(adder_5_out), .cin(1'b0));  // open: cout
  \_32X4乘法器  \u_32x4乘法器_7  (.b_31_0(b_31_0), .P_31_0(\n32x4乘法器_7_p_31_0 ), .a_3_0(bitselector_7_out));
  BitSelector #(.width(32), .group(4)) bitselector_8 (.in(a_31_0), .out(bitselector_8_out), .sel(3'b111));
  Shifter #(.width(32), .shift("ll")) shifter_7 (.in(\n32x4乘法器_7_p_31_0 ), .\dist (5'b11000), .out(shifter_7_out));
  Adder #(.width(32)) adder_6 (.a(adder_5_out), .b(shifter_7_out), .out(adder_6_out), .cin(1'b0));  // open: cout
  \_32X4乘法器  \u_32x4乘法器_8  (.b_31_0(b_31_0), .P_31_0(\n32x4乘法器_8_p_31_0 ), .a_3_0(bitselector_8_out));
  Shifter #(.width(32), .shift("ll")) shifter_8 (.in(\n32x4乘法器_8_p_31_0 ), .\dist (5'b11100), .out(shifter_8_out));
  Adder #(.width(32)) adder_7 (.a(adder_6_out), .b(shifter_8_out), .out(P_31_0), .cin(1'b0));  // open: cout
endmodule

module \_32X32乘法器测试电路  (
  input  [31:0] a_31_0,
  input  [31:0] b_31_0,
  output [31:0] P_31_0
);

  \_32X32乘法器  \u_32x32乘法器_1  (.b_31_0(a_31_0), .P_31_0(P_31_0), .a_31_0(b_31_0));
endmodule
