// Logisim project 实验5-CS2008-15533-徐瑞达.circ as structural Verilog: 13 circuits, main circuit 多功能数字钟
module \四位二进制可逆计数器  (
  input  CPD,
  input  CLR,
  input  CPU,
  output QA,
  output QB,
  output QC,
  output QD,
  output QJ
);

  wire and_1_out, and_2_out, and_3_out, and_4_out, and_5_out, and_6_out, and_7_out, and_8_out, and_9_out,
       d_ff_5_qn, not_1_out, not_2_out, not_3_out, not_4_out, not_5_out, not_6_out, not_7_out, not_8_out,
       or_1_out, or_2_out, or_3_out, or_4_out, or_5_out;

  not not_1 (not_1_out, QA);
  not not_2 (not_2_out, QB);
  not not_3 (not_3_out, QC);
  not not_4 (not_4_out, QD);
  or or_1 (or_1_out, CPD, CPU);
  and and_1 (and_1_out, QA, CPU);
  or or_2 (or_2_out, and_1_out, and_2_out);
  and and_2 (and_2_out, not_1_out, CPD);
  and and_3 (and_3_out, QB, QA, CPU);
  or or_3 (or_3_out, and_3_out, and_4_out);
  and and_4 (and_4_out, not_2_out, not_1_out, CPD);
  and and_5 (and_5_out, QA, QC, CPU, QB);
  or or_4 (or_4_out, and_5_out, and_6_out);
  and and_6 (and_6_out, not_1_out, not_3_out, CPD, not_2_out);
  and and_7 (and_7_out, QB, QD, QA, CPU, QC);
  and and_8 (and_8_out, not_1_out, not_4_out, not_2_out, 1'b0, not_3_out);
  and and_9 (and_9_out, not_3_out, not_2_out, not_4_out, not_1_out, QJ);
  or or_5 (or_5_out, and_7_out, and_9_out, and_8_out);
  not not_5 (not_5_out, QA);
  not not_6 (not_6_out, QB);
  not not_7 (not_7_out, QC);
  not not_8 (not_8_out, QD);
  D_Flip_Flop #(.trigger("falling"), .Pre_Clr_Positions("ABOVE_BELOW"), .NegatePresetClear("false"), .enable("false"), .NewFFLayout("true")) d_ff_1 (
    .clk(or_1_out), .D(not_5_out), .Q(QA), .reset(CLR));  // open: Qn, preset
  D_Flip_Flop #(.trigger("falling"), .Pre_Clr_Positions("ABOVE_BELOW"), .NegatePresetClear("false"), .enable("false"), .NewFFLayout("true")) d_ff_2 (
    .clk(or_2_out), .D(not_6_out), .Q(QB), .reset(CLR));  // open: Qn, preset
  D_Flip_Flop #(.trigger("falling"), .Pre_Clr_Positions("ABOVE_BELOW"), .NegatePresetClear("false"), .enable("false"), .NewFFLayout("true")) d_ff_3 (
    .clk(or_3_out), .D(not_7_out), .Q(QC), .reset(CLR));  // open: Qn, preset
  D_Flip_Flop #(.trigger("falling"), .Pre_Clr_Positions("ABOVE_BELOW"), .NegatePresetClear("false"), .enable("false"), .NewFFLayout("true")) d_ff_4 (
    .clk(or_4_out), .D(not_8_out), .Q(QD), .reset(CLR));  // open: Qn, preset
  D_Flip_Flop #(.trigger("rising"), .Pre_Clr_Positions("ABOVE_BELOW"), .NegatePresetClear("false"), .enable("false"), .NewFFLayout("true")) d_ff_5 (
    .clk(or_5_out), .D(d_ff_5_qn), .Q(QJ), .Qn(d_ff_5_qn), .reset(CLR));  // open: preset
endmodule

module \八位二进制转8421码  (
  input  A0,
  input  A1,
  input  A2,
  input  A3,
  input  A4,
  input  A5,
  output Q1D,
  output Q1C,
  output Q1B,
  output Q1A,
  output Q0D,
  output Q0C,
  output Q0B,
  output Q0A
);

  wire and_1_out, and_2_out, and_3_out, and_4_out, and_5_out, and_6_out, and_7_out, and_8_out, and_9_out,
       and_10_out, and_11_out, and_12_out, and_13_out, and_14_out, and_15_out, and_16_out, and_17_out,
       and_18_out, and_19_out, and_20_out, and_21_out, and_22_out, and_23_out, and_24_out, and_25_out,
       and_26_out, and_27_out, and_28_out, and_29_out, and_30_out, and_31_out, and_32_out, and_33_out,
       and_34_out, and_35_out, and_36_out, and_37_out, and_38_out, not_1_out, not_2_out, not_3_out,
       not_4_out, not_5_out, not_6_out, not_7_out, not_8_out, not_9_out, not_10_out, not_11_out, not_12_out,
       not_13_out, not_14_out, not_15_out, not_16_out, not_17_out, not_18_out, not_19_out, not_20_out,
       not_21_out, not_22_out, not_23_out, not_24_out, not_25_out, not_26_out, not_27_out, not_28_out,
       not_29_out, not_30_out, not_31_out, not_32_out, not_33_out, not_34_out, not_35_out, not_36_out,
       not_37_out, not_38_out, not_39_out, not_40_out, not_41_out, not_42_out, not_43_out, not_44_out,
       not_45_out, not_46_out, not_47_out, not_48_out, not_49_out, not_50_out, not_51_out, not_52_out,
       not_53_out, not_54_out, not_55_out, not_56_out, not_57_out, not_58_out, not_59_out, not_60_out,
       not_61_out, not_62_out, not_63_out, not_64_out, not_65_out, not_66_out, not_67_out, not_68_out,
       not_69_out, not_70_out, not_71_out;

  and and_1 (and_1_out, A0, A2);
  and and_2 (and_2_out, A0, A1);
  not not_1 (not_1_out, A0);
  not not_2 (not_2_out, A0);
  not not_3 (not_3_out, A1);
  not not_4 (not_4_out, A2);
  not not_5 (not_5_out, A0);
  not not_6 (not_6_out, A1);
  not not_7 (not_7_out, A0);
  not not_8 (not_8_out, A1);
  not not_9 (not_9_out, A0);
  not not_10 (not_10_out, A0);
  not not_11 (not_11_out, A2);
  not not_12 (not_12_out, A3);
  not not_13 (not_13_out, A1);
  not not_14 (not_14_out, A2);
  not not_15 (not_15_out, A2);
  not not_16 (not_16_out, A2);
  not not_17 (not_17_out, A3);
  not not_18 (not_18_out, A0);
  not not_19 (not_19_out, A1);
  not not_20 (not_20_out, A3);
  not not_21 (not_21_out, A4);
  not not_22 (not_22_out, A0);
  not not_23 (not_23_out, A2);
  not not_24 (not_24_out, A3);
  not not_25 (not_25_out, A0);
  not not_26 (not_26_out, A4);
  not not_27 (not_27_out, A1);
  not not_28 (not_28_out, A2);
  not not_29 (not_29_out, A2);
  not not_30 (not_30_out, A3);
  not not_31 (not_31_out, A4);
  not not_32 (not_32_out, A3);
  not not_33 (not_33_out, A1);
  not not_34 (not_34_out, A2);
  not not_35 (not_35_out, A4);
  not not_36 (not_36_out, A0);
  not not_37 (not_37_out, A1);
  not not_38 (not_38_out, A0);
  not not_39 (not_39_out, A3);
  not not_40 (not_40_out, A4);
  not not_41 (not_41_out, A0);
  not not_42 (not_42_out, A3);
  not not_43 (not_43_out, A3);
  not not_44 (not_44_out, A4);
  not not_45 (not_45_out, A1);
  not not_46 (not_46_out, A2);
  not not_47 (not_47_out, A3);
  not not_48 (not_48_out, A1);
  not not_49 (not_49_out, A2);
  not not_50 (not_50_out, A0);
  not not_51 (not_51_out, A1);
  not not_52 (not_52_out, A2);
  not not_53 (not_53_out, A0);
  not not_54 (not_54_out, A2);
  not not_55 (not_55_out, A0);
  not not_56 (not_56_out, A1);
  not not_57 (not_57_out, A4);
  not not_58 (not_58_out, A0);
  not not_59 (not_59_out, A2);
  not not_60 (not_60_out, A3);
  not not_61 (not_61_out, A4);
  not not_62 (not_62_out, A0);
  not not_63 (not_63_out, A3);
  not not_64 (not_64_out, A1);
  not not_65 (not_65_out, A2);
  not not_66 (not_66_out, A4);
  not not_67 (not_67_out, A2);
  not not_68 (not_68_out, A4);
  not not_69 (not_69_out, A1);
  not not_70 (not_70_out, A3);
  not not_71 (not_71_out, A4);
  or or_1 (Q1C, and_1_out, and_2_out);
  and and_3 (and_3_out, not_1_out, A1, A3);
  and and_4 (and_4_out, not_2_out, A1, A2);
  and and_5 (and_5_out, A1, A2, A3);
  and and_6 (and_6_out, A0, not_3_out, not_4_out);
  and and_7 (and_7_out, not_5_out, not_6_out, A2, A4);
  and and_8 (and_8_out, not_7_out, not_8_out, A2, A3);
  and and_9 (and_9_out, not_9_out, A2, A3, A4);
  and and_10 (and_10_out, not_10_out, A1, not_11_out, not_12_out);
  and and_11 (and_11_out, A0, not_13_out, not_14_out);
  and and_12 (and_12_out, A0, not_15_out, A4);
  and and_13 (and_13_out, A0, not_16_out, A3);
  and and_14 (and_14_out, A0, A1, A2, not_17_out);
  and and_15 (and_15_out, not_18_out, not_19_out, A2, not_20_out, not_21_out);
  and and_16 (and_16_out, not_22_out, A1, not_23_out, not_24_out, A4);
  and and_17 (and_17_out, not_25_out, A1, A2, A3, not_26_out);
  and and_18 (and_18_out, A0, not_27_out, not_28_out, A3, A4);
  and and_19 (and_19_out, A0, A1, not_29_out, not_30_out, not_31_out);
  and and_20 (and_20_out, A0, A1, A2, not_32_out, A4);
  and and_21 (and_21_out, not_33_out, not_34_out, A3, not_35_out);
  and and_22 (and_22_out, not_36_out, not_37_out, A3, A4);
  and and_23 (and_23_out, not_38_out, A1, not_39_out, not_40_out);
  and and_24 (and_24_out, not_41_out, A1, A2, not_42_out);
  and and_25 (and_25_out, A1, A2, not_43_out, not_44_out);
  and and_26 (and_26_out, A0, not_45_out, not_46_out, not_47_out, A4);
  and and_27 (and_27_out, A0, not_48_out, A2, A3);
  and and_28 (and_28_out, A0, A1, not_49_out, A3, A4);
  and and_29 (and_29_out, not_50_out, not_51_out, not_52_out, A4);
  and and_30 (and_30_out, not_53_out, not_54_out, A3, A4);
  and and_31 (and_31_out, not_55_out, not_56_out, A2, A3, not_57_out);
  and and_32 (and_32_out, not_58_out, A1, not_59_out, not_60_out, not_61_out);
  and and_33 (and_33_out, not_62_out, A1, A2, not_63_out, A4);
  and and_34 (and_34_out, A0, not_64_out, not_65_out, not_66_out);
  and and_35 (and_35_out, A0, not_67_out, A3, not_68_out);
  and and_36 (and_36_out, A0, not_69_out, A2, A4);
  and and_37 (and_37_out, A0, A2, A3, A4);
  and and_38 (and_38_out, A0, A1, A2, not_70_out, not_71_out);
  or or_2 (Q1B, and_3_out, and_4_out, and_5_out, and_6_out);
  or or_3 (Q1A, and_7_out, and_8_out, and_9_out, and_10_out, and_11_out, and_12_out, and_13_out, and_14_out);
  or or_4 (Q0D, and_15_out, and_16_out, and_17_out, and_18_out, and_19_out, and_20_out);
  or or_5 (Q0C, and_21_out, and_22_out, and_23_out, and_24_out, and_25_out, and_26_out, and_27_out, and_28_out);
  or or_6 (Q0B, and_29_out, and_30_out, and_31_out, and_32_out, and_33_out, and_34_out, and_35_out, and_36_out, and_37_out, and_38_out);

  assign Q0A = A5;
  assign Q1D = 1'b0;
endmodule

module \六十进制计数器  (
  input  Adj,
  input  CPD,
  input  CLR,
  input  CPU,
  output out_5,
  output out_6,
  output out_7,
  output out_8,
  output out_9,
  output out_10,
  output out_11,
  output out_12,
  output QCC
);

  wire and_1_out, and_2_out, nor_1_out, not_1_out, not_2_out, or_1_out, or_2_out, or_3_out, or_4_out,
       or_5_out, \低位_qa , \低位_qb , \低位_qc , \低位_qd , \低位_qj , \高位_qa , \高位_qb , \高位_qc , \高位_qd ;

  or or_1 (or_1_out, \高位_qa , \高位_qb , \高位_qc , \高位_qd );
  and and_1 (and_1_out, or_1_out, nor_1_out, CPD);
  nor nor_1 (nor_1_out, \低位_qd , \低位_qc , \低位_qb , \低位_qa );
  or or_2 (or_2_out, \低位_qa , \低位_qb , \低位_qc , \低位_qd );
  or or_3 (or_3_out, or_1_out, or_2_out);
  and and_2 (and_2_out, or_3_out, Adj, CPD);
  or or_4 (or_4_out, CLR, QCC);
  or or_5 (or_5_out, CLR, QCC);
  \四位二进制可逆计数器  \u_高位  (
    .CPD(and_1_out), .CLR(or_4_out), .CPU(\低位_qj ), .QA(\高位_qa ), .QB(\高位_qb ), .QC(\高位_qc ), .QD(\高位_qd ));  // open: QJ
  \四位二进制可逆计数器  \u_低位  (
    .CPD(and_2_out), .CLR(or_5_out), .CPU(CPU), .QA(\低位_qa ), .QB(\低位_qb ), .QC(\低位_qc ), .QD(\低位_qd ),
    .QJ(\低位_qj ));
  \八位二进制转8421码  \u_八位二进制转8421码_1  (
    .A0(\高位_qb ), .A1(\高位_qa ), .A2(\低位_qd ), .A3(\低位_qc ), .A4(\低位_qb ), .A5(\低位_qa ), .Q1D(out_5),
    .Q1C(out_6), .Q1B(out_7), .Q1A(out_8), .Q0D(out_9), .Q0C(out_10), .Q0B(out_11), .Q0A(out_12));
  not not_1 (not_1_out, \低位_qa );
  not not_2 (not_2_out, \低位_qb );
  and and_3 (QCC, \高位_qa , \高位_qb , not_1_out, not_2_out, \低位_qd , \低位_qc );
endmodule

module \六十进制计数器测试电路  (
  input  Adj,
  input  CLR,
  output QCC
);

  wire clock_1_out, CPD_out, CPU_out, multiplexer_1_out;
  wire [3:0] \六十进制计数器_1_out_8 , \六十进制计数器_1_out_12 ;

  Button CPD (.out(CPD_out));
  Clock #(.highDuration(1), .lowDuration(1)) clock_1 (.out(clock_1_out));
  Multiplexer #(.select(1), .width(1), .disabled("Z"), .enable("false")) multiplexer_1 (
    .in0(clock_1_out), .in1(CPU_out), .out(multiplexer_1_out), .sel(Adj));
  Button CPU (.out(CPU_out));
  Hex_Digit_Display hex_digit_display_1 (.value(\六十进制计数器_1_out_8 ));  // open: dp
  Hex_Digit_Display hex_digit_display_2 (.value(\六十进制计数器_1_out_12 ));  // open: dp
  \六十进制计数器  \u_六十进制计数器_1  (
    .Adj(Adj), .CPD(CPD_out), .CLR(CLR), .CPU(multiplexer_1_out), .QCC(QCC), .out_5(\六十进制计数器_1_out_8 [3]),
    .out_6(\六十进制计数器_1_out_8 [2]), .out_7(\六十进制计数器_1_out_8 [1]), .out_8(\六十进制计数器_1_out_8 [0]),
    .out_9(\六十进制计数器_1_out_12 [3]), .out_10(\六十进制计数器_1_out_12 [2]), .out_11(\六十进制计数器_1_out_12 [1]),
    .out_12(\六十进制计数器_1_out_12 [0]));
endmodule

// 十二或二十四进制的计数器电路
module \十二进制计数器或二十四进制的计数器  (
  input  Adj,
  input  CPD,
  input  CPU,
  input  CLR,
  input  SET,
  output QCC,
  output out_7,
  output out_8,
  output out_9,
  output out_10,
  output out_11,
  output out_12,
  output out_13,
  output out_14
);

  wire and_2_out, or_1_out, or_2_out;
  wire [7:0] _12_out_12, _24_out_12;

  \六十进制计数器  _12 (
    .Adj(Adj), .CPD(CPD), .CLR(or_1_out), .CPU(CPU), .out_5(_12_out_12[7]), .out_6(_12_out_12[6]),
    .out_7(_12_out_12[5]), .out_8(_12_out_12[4]), .out_9(_12_out_12[3]), .out_10(_12_out_12[2]),
    .out_11(_12_out_12[1]), .out_12(_12_out_12[0]));  // open: QCC
  or or_1 (or_1_out, QCC, CLR);
  \六十进制计数器  _24 (
    .Adj(Adj), .CPD(CPD), .CLR(or_2_out), .CPU(CPU), .out_5(_24_out_12[7]), .out_6(_24_out_12[6]),
    .out_7(_24_out_12[5]), .out_8(_24_out_12[4]), .out_9(_24_out_12[3]), .out_10(_24_out_12[2]),
    .out_11(_24_out_12[1]), .out_12(_24_out_12[0]));  // open: QCC
  or or_2 (or_2_out, and_2_out, CLR);
  and and_1 (QCC, _12_out_12[4], _12_out_12[1]);
  and and_2 (and_2_out, _24_out_12[5], _24_out_12[2]);
  Multiplexer #(.select(1), .width(8), .disabled("Z"), .enable("false")) multiplexer_1 (
    .in0(_12_out_12), .in1(_24_out_12), .out({out_14, out_13, out_12, out_11, out_10, out_8, out_9, out_7}),
    .sel(SET));
endmodule

module \十二进制计数器或二十四进制的计数器测试电路  (
  input  Adj,
  input  SET,
  input  CLR,
  output QCC
);

  wire CPD_out, CPU_out;
  wire [3:0] \十二进制计数器或二十四进制的计数器_1_out_7 , \十二进制计数器或二十四进制的计数器_1_out_11 ;

  Button CPD (.out(CPD_out));
  Button CPU (.out(CPU_out));
  Hex_Digit_Display hex_digit_display_1 (.value(\十二进制计数器或二十四进制的计数器_1_out_11 ));  // open: dp
  Hex_Digit_Display hex_digit_display_2 (.value(\十二进制计数器或二十四进制的计数器_1_out_7 ));  // open: dp
  \十二进制计数器或二十四进制的计数器  \u_十二进制计数器或二十四进制的计数器_1  (
    .Adj(Adj), .CPD(CPD_out), .CPU(CPU_out), .QCC(QCC), .out_7(\十二进制计数器或二十四进制的计数器_1_out_7 [0]),
    .out_9(\十二进制计数器或二十四进制的计数器_1_out_7 [1]), .out_8(\十二进制计数器或二十四进制的计数器_1_out_7 [2]),
    .out_10(\十二进制计数器或二十四进制的计数器_1_out_7 [3]), .out_11(\十二进制计数器或二十四进制的计数器_1_out_11 [0]),
    .out_12(\十二进制计数器或二十四进制的计数器_1_out_11 [1]), .out_13(\十二进制计数器或二十四进制的计数器_1_out_11 [2]),
    .out_14(\十二进制计数器或二十四进制的计数器_1_out_11 [3]), .CLR(CLR), .SET(SET));
endmodule

// 上下午
module \上下午文字显示的电路  (
  input  TT,
  input  AM_FM,
  output [4:0] D,
  output [4:0] C,
  output [4:0] B,
  output [4:0] A
);

  wire not_1_out;
  wire [4:0] multiplexer_1_out, multiplexer_4_out, multiplexer_6_out, multiplexer_8_out;

  not not_1 (not_1_out, TT);
  Multiplexer #(.select(1), .width(5), .disabled("Z"), .enable("false")) multiplexer_1 (
    .in0(5'b00001), .in1(5'b10000), .out(multiplexer_1_out), .sel(AM_FM));
  Multiplexer #(.select(1), .width(5), .disabled("Z"), .enable("false")) multiplexer_2 (
    .in0(multiplexer_1_out), .in1({5{1'b0}}), .out(D), .sel(not_1_out));
  Multiplexer #(.select(1), .width(5), .disabled("Z"), .enable("false")) multiplexer_3 (
    .in0(multiplexer_4_out), .in1({5{1'b0}}), .out(C), .sel(not_1_out));
  Multiplexer #(.select(1), .width(5), .disabled("Z"), .enable("false")) multiplexer_4 (
    .in0({5{1'b1}}), .in1({5{1'b1}}), .out(multiplexer_4_out), .sel(AM_FM));
  Multiplexer #(.select(1), .width(5), .disabled("Z"), .enable("false")) multiplexer_5 (
    .in0(multiplexer_6_out), .in1({5{1'b0}}), .out(B), .sel(not_1_out));
  Multiplexer #(.select(1), .width(5), .disabled("Z"), .enable("false")) multiplexer_6 (
    .in0(5'b00101), .in1(5'b10100), .out(multiplexer_6_out), .sel(AM_FM));
  Multiplexer #(.select(1), .width(5), .disabled("Z"), .enable("false")) multiplexer_7 (
    .in0(multiplexer_8_out), .in1({5{1'b0}}), .out(A), .sel(not_1_out));
  Multiplexer #(.select(1), .width(5), .disabled("Z"), .enable("false")) multiplexer_8 (
    .in0(5'b00001), .in1(5'b10000), .out(multiplexer_8_out), .sel(AM_FM));
endmodule

module \上下午文字显示测试电路  (
  input  AM_FM,
  input  TT
);

  wire [4:0] \上下午文字显示的电路_1_a , \上下午文字显示的电路_1_b , \上下午文字显示的电路_1_c , \上下午文字显示的电路_1_d ;

  DotMatrix #(.inputtype("column"), .matrixcols(4), .matrixrows(5), .persist(0), .dotshape("square")) dotmatrix_1 (
    .col0(\上下午文字显示的电路_1_d ), .col1(\上下午文字显示的电路_1_c ), .col2(\上下午文字显示的电路_1_b ), .col3(\上下午文字显示的电路_1_a ));
  \上下午文字显示的电路  \u_上下午文字显示的电路_1  (
    .TT(TT), .AM_FM(AM_FM), .D(\上下午文字显示的电路_1_d ), .C(\上下午文字显示的电路_1_c ), .B(\上下午文字显示的电路_1_b ),
    .A(\上下午文字显示的电路_1_a ));
endmodule

module \电子钟整点报时电路  (
  input  Adj1,
  input  CPDM,
  input  CPDS,
  input  CPUS,
  input  CPUM,
  input  CLR,
  output [3:0] \分钟高位 ,
  output [3:0] \分钟低位 ,
  output [3:0] \秒钟高位 ,
  output [3:0] \秒钟低位 ,
  output LED,
  output \进位 
);

  wire and_1_out, comparator_1_eq, comparator_2_eq, comparator_3_eq, comparator_4_eq, comparator_5_lt,
       d_ff_1_q, multiplexer_1_out, not_1_out, \六十进制计数器_2_qcc ;
  wire [3:0] counter_1_q;

  not not_1 (not_1_out, Adj1);
  Multiplexer #(.select(1), .width(1), .disabled("Z"), .enable("false")) multiplexer_1 (
    .in0(CPUM), .in1(\六十进制计数器_2_qcc ), .out(multiplexer_1_out), .sel(not_1_out));
  \六十进制计数器  \u_六十进制计数器_1  (
    .Adj(Adj1), .CPD(CPDM), .CLR(CLR), .CPU(multiplexer_1_out), .QCC(\进位 ), .out_5(\分钟高位 [3]),
    .out_6(\分钟高位 [2]), .out_7(\分钟高位 [1]), .out_8(\分钟高位 [0]), .out_9(\分钟低位 [3]), .out_10(\分钟低位 [2]),
    .out_11(\分钟低位 [1]), .out_12(\分钟低位 [0]));
  Comparator #(.width(4), .mode("twosComplement")) comparator_1 (
    .a(\分钟高位 ), .b(4'b0101), .eq(comparator_1_eq));  // open: gt, lt
  Comparator #(.width(4), .mode("twosComplement")) comparator_2 (
    .a(\分钟低位 ), .b(4'b1001), .eq(comparator_2_eq));  // open: gt, lt
  \六十进制计数器  \u_六十进制计数器_2  (
    .Adj(1'b0), .CPD(CPDS), .CLR(CLR), .CPU(CPUS), .QCC(\六十进制计数器_2_qcc ), .out_5(\秒钟高位 [3]),
    .out_6(\秒钟高位 [2]), .out_7(\秒钟高位 [1]), .out_8(\秒钟高位 [0]), .out_9(\秒钟低位 [3]), .out_10(\秒钟低位 [2]),
    .out_11(\秒钟低位 [1]), .out_12(\秒钟低位 [0]));
  Comparator #(.width(4), .mode("twosComplement")) comparator_3 (
    .a(\秒钟高位 ), .b(4'b0101), .eq(comparator_3_eq));  // open: gt, lt
  Comparator #(.width(4), .mode("twosComplement")) comparator_4 (
    .a(\秒钟低位 ), .b(4'b0000), .eq(comparator_4_eq));  // open: gt, lt
  and and_1 (and_1_out, comparator_1_eq, comparator_2_eq, comparator_3_eq, comparator_4_eq);
  D_Flip_Flop #(.trigger("rising"), .Pre_Clr_Positions("ABOVE_BELOW"), .NegatePresetClear("false"), .enable("false"), .NewFFLayout("true")) d_ff_1 (
    .clk(and_1_out), .D(and_1_out), .Q(d_ff_1_q), .reset(\六十进制计数器_2_qcc ));  // open: Qn, preset
  Comparator #(.width(4), .mode("unsigned")) comparator_5 (
    .a(counter_1_q), .b(4'b1010), .lt(comparator_5_lt));  // open: gt, eq
  Counter #(.width(4), .max('ha), .ongoal("stay"), .trigger("rising"), .behavior("new")) counter_1 (
    .count(d_ff_1_q), .Q(counter_1_q), .clk(CPUS), .clr(\六十进制计数器_2_qcc ));  // open: load, D, carry, preset, down
  and and_2 (LED, comparator_5_lt, d_ff_1_q);
endmodule

module \电子钟整点报时电路测试电路  (
  input  Adj1,
  input  CLR,
  output \分钟进位 
);

  wire CPDM_out, CPDS_out, CPUM_out, CPUS_out, \电子钟整点报时电路_1_led ;
  wire [3:0] \电子钟整点报时电路_1_分钟低位 , \电子钟整点报时电路_1_分钟高位 , \电子钟整点报时电路_1_秒钟低位 , \电子钟整点报时电路_1_秒钟高位 ;

  Hex_Digit_Display hex_digit_display_1 (.value(\电子钟整点报时电路_1_分钟高位 ));  // open: dp
  Hex_Digit_Display hex_digit_display_2 (.value(\电子钟整点报时电路_1_分钟低位 ));  // open: dp
  Button CPDM (.out(CPDM_out));
  Hex_Digit_Display hex_digit_display_3 (.value(\电子钟整点报时电路_1_秒钟高位 ));  // open: dp
  Button CPDS (.out(CPDS_out));
  Button CPUM (.out(CPUM_out));
  Button CPUS (.out(CPUS_out));
  Hex_Digit_Display hex_digit_display_4 (.value(\电子钟整点报时电路_1_秒钟低位 ));  // open: dp
  LED #(.active("true")) \u_整点报时  (.in(\电子钟整点报时电路_1_led ));
  \电子钟整点报时电路  \u_电子钟整点报时电路_1  (
    .Adj1(Adj1), .CPDM(CPDM_out), .LED(\电子钟整点报时电路_1_led ), .CPUM(CPUM_out), .CPUS(CPUS_out), .CLR(CLR),
    .\进位 (\分钟进位 ), .CPDS(CPDS_out), .\分钟高位 (\电子钟整点报时电路_1_分钟高位 ), .\分钟低位 (\电子钟整点报时电路_1_分钟低位 ),
    .\秒钟高位 (\电子钟整点报时电路_1_秒钟高位 ), .\秒钟低位 (\电子钟整点报时电路_1_秒钟低位 ));
endmodule

module \秒脉冲产生电路  (
  input  in_1,
  output \进位 
);

  \四位二进制可逆计数器  \u_四位二进制可逆计数器_1  (.CPD(1'b0), .CLR(\进位 ), .CPU(in_1), .QD(\进位 ));  // open: QA, QB, QC, QJ
endmodule

module \多功能数字钟  (
  input  Adj0,
  input  Adj1,
  input  CPD,
  input  CPU,
  input  CLR,
  input  CP,
  input  SET,
  output [4:0] D,
  output [4:0] C,
  output [4:0] B,
  output [4:0] A,
  output [3:0] \分钟高位 ,
  output [3:0] \分钟低位 ,
  output [3:0] \时钟高位 ,
  output [3:0] \时钟低位 ,
  output [3:0] \秒钟高位 ,
  output [3:0] \秒钟低位 ,
  output LED
);

  wire and_1_out, comparator_1_eq, comparator_2_eq, comparator_3_eq, comparator_4_eq, comparator_5_lt,
       counter_1_q, d_ff_1_q, demultiplexer_1_out1, demultiplexer_2_out1, demultiplexer_3_out0,
       demultiplexer_3_out1, demultiplexer_4_out0, demultiplexer_4_out1, multiplexer_1_out,
       multiplexer_2_out, not_1_out, not_2_out, \六十进制计数器_1_qcc , \六十进制计数器_2_qcc , \十二进制计数器或二十四进制的计数器_1_qcc ,
       \秒脉冲产生电路_1_进位 ;
  wire [3:0] counter_2_q;

  Demultiplexer #(.select(1), .width(1), .tristate("false"), .disabled("Z"), .enable("false")) demultiplexer_1 (
    .out1(demultiplexer_1_out1), .in(CPD), .sel(Adj0));  // open: out0
  Demultiplexer #(.select(1), .width(1), .tristate("false"), .disabled("Z"), .enable("false")) demultiplexer_2 (
    .out1(demultiplexer_2_out1), .in(CPU), .sel(Adj0));  // open: out0
  Demultiplexer #(.select(1), .width(1), .tristate("false"), .disabled("Z"), .enable("false")) demultiplexer_3 (
    .out0(demultiplexer_3_out0), .out1(demultiplexer_3_out1), .in(demultiplexer_1_out1), .sel(Adj1));
  Demultiplexer #(.select(1), .width(1), .tristate("false"), .disabled("Z"), .enable("false")) demultiplexer_4 (
    .out0(demultiplexer_4_out0), .out1(demultiplexer_4_out1), .in(demultiplexer_2_out1), .sel(Adj1));
  not not_1 (not_1_out, Adj0);
  Multiplexer #(.select(1), .width(1), .disabled("Z"), .enable("false")) multiplexer_1 (
    .in0(demultiplexer_4_out0), .in1(\六十进制计数器_1_qcc ), .out(multiplexer_1_out), .sel(not_1_out));
  \秒脉冲产生电路  \u_秒脉冲产生电路_1  (.in_1(CP), .\进位 (\秒脉冲产生电路_1_进位 ));
  Counter #(.width(1), .max('h1), .ongoal("wrap"), .trigger("rising"), .behavior("new")) counter_1 (
    .Q(counter_1_q), .clk(\十二进制计数器或二十四进制的计数器_1_qcc ));  // open: load, D, count, carry, clr, preset, down
  \十二进制计数器或二十四进制的计数器  \u_十二进制计数器或二十四进制的计数器_1  (
    .Adj(1'b1), .CPD(demultiplexer_3_out0), .CPU(multiplexer_1_out), .QCC(\十二进制计数器或二十四进制的计数器_1_qcc ),
    .out_7(\时钟低位 [0]), .out_9(\时钟低位 [1]), .out_8(\时钟低位 [2]), .out_10(\时钟低位 [3]), .out_11(\时钟高位 [0]),
    .out_12(\时钟高位 [1]), .out_13(\时钟高位 [2]), .out_14(\时钟高位 [3]), .CLR(CLR), .SET(SET));
  not not_2 (not_2_out, SET);
  \上下午文字显示的电路  \u_上下午文字显示的电路_1  (.TT(not_2_out), .AM_FM(counter_1_q), .D(D), .C(C), .B(B), .A(A));
  Multiplexer #(.select(1), .width(1), .disabled("Z"), .enable("false")) multiplexer_2 (
    .in0(demultiplexer_4_out1), .in1(\六十进制计数器_2_qcc ), .out(multiplexer_2_out), .sel(not_1_out));
  Comparator #(.width(4), .mode("unsigned")) comparator_1 (
    .a(\分钟高位 ), .b(4'b0101), .eq(comparator_1_eq));  // open: gt, lt
  Comparator #(.width(4), .mode("unsigned")) comparator_2 (
    .a(\分钟低位 ), .b(4'b1001), .eq(comparator_2_eq));  // open: gt, lt
  \六十进制计数器  \u_六十进制计数器_1  (
    .Adj(1'b1), .CPD(demultiplexer_3_out1), .CLR(CLR), .CPU(multiplexer_2_out), .QCC(\六十进制计数器_1_qcc ),
    .out_5(\分钟高位 [3]), .out_6(\分钟高位 [2]), .out_7(\分钟高位 [1]), .out_8(\分钟高位 [0]), .out_9(\分钟低位 [3]),
    .out_10(\分钟低位 [2]), .out_11(\分钟低位 [1]), .out_12(\分钟低位 [0]));
  \六十进制计数器  \u_六十进制计数器_2  (
    .Adj(1'b1), .CPD(1'b0), .CLR(CLR), .CPU(\秒脉冲产生电路_1_进位 ), .QCC(\六十进制计数器_2_qcc ), .out_5(\秒钟高位 [3]),
    .out_6(\秒钟高位 [2]), .out_7(\秒钟高位 [1]), .out_8(\秒钟高位 [0]), .out_9(\秒钟低位 [3]), .out_10(\秒钟低位 [2]),
    .out_11(\秒钟低位 [1]), .out_12(\秒钟低位 [0]));
  Comparator #(.width(4), .mode("unsigned")) comparator_3 (
    .a(\秒钟高位 ), .b(4'b0101), .eq(comparator_3_eq));  // open: gt, lt
  Comparator #(.width(4), .mode("unsigned")) comparator_4 (
    .a(\秒钟低位 ), .b(4'b0000), .eq(comparator_4_eq));  // open: gt, lt
  and and_1 (and_1_out, comparator_1_eq, comparator_2_eq, comparator_3_eq, comparator_4_eq);
  D_Flip_Flop #(.trigger("rising"), .Pre_Clr_Positions("ABOVE_BELOW"), .NegatePresetClear("false"), .enable("false"), .NewFFLayout("true")) d_ff_1 (
    .clk(and_1_out), .D(and_1_out), .Q(d_ff_1_q), .reset(\六十进制计数器_2_qcc ));  // open: Qn, preset
  Counter #(.width(4), .max('ha), .ongoal("stay"), .trigger("rising"), .behavior("new")) counter_2 (
    .count(d_ff_1_q), .Q(counter_2_q), .clk(\秒脉冲产生电路_1_进位 ), .clr(\六十进制计数器_2_qcc ));  // open: load, D, carry, preset, down
  Comparator #(.width(4), .mode("unsigned")) comparator_5 (
    .a(counter_2_q), .b(4'b1010), .lt(comparator_5_lt));  // open: gt, eq
  and and_2 (LED, comparator_5_lt, d_ff_1_q);
endmodule

module \多功能数字钟测试电路  (
  input  in_1,
  input  in_2,
  input  in_3,
  input  in_4
);

  wire button_1_out, button_2_out, clock_1_out, \多功能数字钟_1_led ;
  wire [3:0] \多功能数字钟_1_分钟低位 , \多功能数字钟_1_分钟高位 , \多功能数字钟_1_时钟低位 , \多功能数字钟_1_时钟高位 , \多功能数字钟_1_秒钟低位 ,
       \多功能数字钟_1_秒钟高位 ;
  wire [4:0] \多功能数字钟_1_a , \多功能数字钟_1_b , \多功能数字钟_1_c , \多功能数字钟_1_d ;

  DotMatrix #(.inputtype("column"), .matrixcols(4), .matrixrows(5), .persist(0), .dotshape("square")) dotmatrix_1 (
    .col0(\多功能数字钟_1_d ), .col1(\多功能数字钟_1_c ), .col2(\多功能数字钟_1_b ), .col3(\多功能数字钟_1_a ));
  Clock #(.highDuration(1), .lowDuration(1)) clock_1 (.out(clock_1_out));
  Hex_Digit_Display hex_digit_display_1 (.value(\多功能数字钟_1_时钟高位 ));  // open: dp
  Hex_Digit_Display hex_digit_display_2 (.value(\多功能数字钟_1_时钟低位 ));  // open: dp
  Button button_1 (.out(button_1_out));
  Hex_Digit_Display hex_digit_display_3 (.value(\多功能数字钟_1_分钟低位 ));  // open: dp
  Hex_Digit_Display hex_digit_display_4 (.value(\多功能数字钟_1_分钟高位 ));  // open: dp
  Button button_2 (.out(button_2_out));
  Hex_Digit_Display hex_digit_display_5 (.value(\多功能数字钟_1_秒钟高位 ));  // open: dp
  Hex_Digit_Display hex_digit_display_6 (.value(\多功能数字钟_1_秒钟低位 ));  // open: dp
  LED #(.active("true")) led_1 (.in(\多功能数字钟_1_led ));
  \多功能数字钟  \u_多功能数字钟_1  (
    .D(\多功能数字钟_1_d ), .C(\多功能数字钟_1_c ), .B(\多功能数字钟_1_b ), .A(\多功能数字钟_1_a ), .SET(in_3), .Adj1(in_2),
    .Adj0(in_1), .\时钟低位 (\多功能数字钟_1_时钟低位 ), .CPD(button_2_out), .CPU(button_1_out), .CLR(in_4),
    .CP(clock_1_out), .\分钟高位 (\多功能数字钟_1_分钟高位 ), .\分钟低位 (\多功能数字钟_1_分钟低位 ), .\秒钟高位 (\多功能数字钟_1_秒钟高位 ),
    .\秒钟低位 (\多功能数字钟_1_秒钟低位 ), .LED(\多功能数字钟_1_led ), .\时钟高位 (\多功能数字钟_1_时钟高位 ));
endmodule
