// Logisim project 实验6-CS2008-15533-徐瑞达.circ as structural Verilog: 6 circuits, main circuit sqrX
module sqrX (
  input  [31:0] a,
  input  [31:0] b,
  input  [31:0] c,
  input  [31:0] d,
  output [31:0] a1,
  output [31:0] c1,
  output [31:0] b1,
  output [31:0] d1
);

  wire [31:0] multiplier_1_out, multiplier_2_out, multiplier_3_out, multiplier_4_out, multiplier_5_out,
       multiplier_6_out, multiplier_7_out, multiplier_8_out;

  Multiplier #(.width(32)) multiplier_1 (.a(a), .b(a), .out(multiplier_1_out));  // open: cin, cout
  Multiplier #(.width(32)) multiplier_2 (.a(b), .b(c), .out(multiplier_2_out));  // open: cin, cout
  Multiplier #(.width(32)) multiplier_3 (.a(a), .b(b), .out(multiplier_3_out));  // open: cin, cout
  Multiplier #(.width(32)) multiplier_4 (.a(d), .b(b), .out(multiplier_4_out));  // open: cin, cout
  Multiplier #(.width(32)) multiplier_5 (.a(d), .b(d), .out(multiplier_5_out));  // open: cin, cout
  Multiplier #(.width(32)) multiplier_6 (.a(b), .b(c), .out(multiplier_6_out));  // open: cin, cout
  Adder #(.width(32)) adder_1 (.a(multiplier_1_out), .b(multiplier_2_out), .out(a1));  // open: cin, cout
  Multiplier #(.width(32)) multiplier_7 (.a(a), .b(c), .out(multiplier_7_out));  // open: cin, cout
  Multiplier #(.width(32)) multiplier_8 (.a(d), .b(c), .out(multiplier_8_out));  // open: cin, cout
  Adder #(.width(32)) adder_2 (.a(multiplier_3_out), .b(multiplier_4_out), .out(b1));  // open: cin, cout
  Adder #(.width(32)) adder_3 (.a(multiplier_5_out), .b(multiplier_6_out), .out(d1));  // open: cin, cout
  Adder #(.width(32)) adder_4 (.a(multiplier_7_out), .b(multiplier_8_out), .out(c1));  // open: cin, cout
endmodule

module sqrX_A (
  input  [31:0] a,
  input  [31:0] b,
  input  [31:0] c,
  input  [31:0] d,
  output [31:0] a1,
  output [31:0] b1,
  output [31:0] c1,
  output [31:0] d1
);

  wire [31:0] sqrx_1_a1, sqrx_1_c1;

  sqrX sqrx_1 (.a(a), .b(b), .c(c), .d(d), .a1(sqrx_1_a1), .c1(sqrx_1_c1), .b1(a1), .d1(c1));
  Adder #(.width(32)) adder_1 (.a(sqrx_1_a1), .b(a1), .out(b1));  // open: cin, cout
  Adder #(.width(32)) adder_2 (.a(sqrx_1_c1), .b(c1), .out(d1));  // open: cin, cout
endmodule

module Fibo (
  input  start,
  input  clr,
  input  clk,
  input  ni_1,
  output [31:0] Fi
);

  wire not_1_out;
  wire [31:0] multiplexer_1_out, multiplexer_2_out, multiplexer_3_out, multiplexer_4_out, multiplexer_6_out,
       multiplexer_7_out, multiplexer_8_out, multiplexer_9_out, register_1_q, register_2_q, register_3_q,
       register_4_q, sqrx_1_a1, sqrx_1_b1, sqrx_1_c1, sqrx_1_d1, sqrx_a_1_a1, sqrx_a_1_b1, sqrx_a_1_c1,
       sqrx_a_1_d1;

  Multiplexer #(.select(1), .width(32), .disabled("Z"), .enable("false")) multiplexer_1 (
    .in0(multiplexer_6_out), .in1({32{1'b0}}), .out(multiplexer_1_out), .sel(not_1_out));
  Multiplexer #(.select(1), .width(32), .disabled("Z"), .enable("false")) multiplexer_2 (
    .in0(multiplexer_7_out), .in1(32'h1), .out(multiplexer_2_out), .sel(not_1_out));
  Multiplexer #(.select(1), .width(32), .disabled("Z"), .enable("false")) multiplexer_3 (
    .in0(multiplexer_8_out), .in1(32'h1), .out(multiplexer_3_out), .sel(not_1_out));
  Multiplexer #(.select(1), .width(32), .disabled("Z"), .enable("false")) multiplexer_4 (
    .in0(multiplexer_9_out), .in1(32'h1), .out(multiplexer_4_out), .sel(not_1_out));
  not not_1 (not_1_out, start);
  Register #(.width(32), .trigger("rising"), .Select("low")) register_1 (
    .D(multiplexer_1_out), .Q(register_1_q), .clk(clk), .clr(clr));  // open: en
  Register #(.width(32), .trigger("rising"), .Select("low")) register_2 (
    .D(multiplexer_2_out), .Q(register_2_q), .clk(clk), .clr(clr));  // open: en
  Register #(.width(32), .trigger("rising"), .Select("low")) register_3 (
    .D(multiplexer_3_out), .Q(register_3_q), .clk(clk), .clr(clr));  // open: en
  Register #(.width(32), .trigger("rising"), .Select("low")) register_4 (
    .D(multiplexer_4_out), .Q(register_4_q), .clk(clk), .clr(clr));  // open: en
  sqrX sqrx_1 (
    .a(register_1_q), .b(register_2_q), .c(register_3_q), .d(register_4_q), .a1(sqrx_1_a1), .c1(sqrx_1_c1),
    .b1(sqrx_1_b1), .d1(sqrx_1_d1));
  sqrX_A sqrx_a_1 (
    .a(register_1_q), .b(register_2_q), .c(register_3_q), .d(register_4_q), .a1(sqrx_a_1_a1),
    .b1(sqrx_a_1_b1), .c1(sqrx_a_1_c1), .d1(sqrx_a_1_d1));
  Multiplexer #(.select(1), .width(32), .disabled("Z"), .enable("false")) multiplexer_5 (
    .in0(register_2_q), .in1({32{1'b0}}), .out(Fi), .sel(not_1_out));
  Multiplexer #(.select(1), .width(32), .disabled("Z"), .enable("false")) multiplexer_6 (
    .in0(sqrx_1_a1), .in1(sqrx_a_1_a1), .out(multiplexer_6_out), .sel(ni_1));
  Multiplexer #(.select(1), .width(32), .disabled("Z"), .enable("false")) multiplexer_7 (
    .in0(sqrx_1_b1), .in1(sqrx_a_1_b1), .out(multiplexer_7_out), .sel(ni_1));
  Multiplexer #(.select(1), .width(32), .disabled("Z"), .enable("false")) multiplexer_8 (
    .in0(sqrx_1_c1), .in1(sqrx_a_1_c1), .out(multiplexer_8_out), .sel(ni_1));
  Multiplexer #(.select(1), .width(32), .disabled("Z"), .enable("false")) multiplexer_9 (
    .in0(sqrx_1_d1), .in1(sqrx_a_1_d1), .out(multiplexer_9_out), .sel(ni_1));
endmodule

// Fibonacci数显示
module \Fibonacci数显示模块  (
  input  [31:0] in_1,
  output [3:0] out_2,
  output [3:0] out_3,
  output [3:0] out_4,
  output [3:0] out_5,
  output [3:0] out_6,
  output [3:0] out_7,
  output [3:0] out_8,
  output [3:0] out_9,
  output [3:0] out_10,
  output [3:0] out_11
);

  wire [31:0] divider_1_out, divider_1_rem, divider_2_out, divider_2_rem, divider_3_out, divider_3_rem,
       divider_4_out, divider_4_rem, divider_5_out, divider_5_rem, divider_6_out, divider_6_rem,
       divider_7_out, divider_7_rem, divider_8_out, divider_8_rem, divider_9_out, divider_9_rem;

  BitSelector #(.width(32), .group(4)) bitselector_1 (.in(divider_1_rem), .out(out_2), .sel(3'b000));
  Divider #(.width(32)) divider_1 (.a(in_1), .b(32'ha), .out(divider_1_out), .rem(divider_1_rem));  // open: upper
  Divider #(.width(32)) divider_2 (
    .a(divider_1_out), .b(32'ha), .out(divider_2_out), .rem(divider_2_rem));  // open: upper
  BitSelector #(.width(32), .group(4)) bitselector_2 (.in(divider_2_rem), .out(out_3), .sel(3'b000));
  Divider #(.width(32)) divider_3 (
    .a(divider_2_out), .b(32'ha), .out(divider_3_out), .rem(divider_3_rem));  // open: upper
  BitSelector #(.width(32), .group(4)) bitselector_3 (.in(divider_3_rem), .out(out_4), .sel(3'b000));
  Divider #(.width(32)) divider_4 (
    .a(divider_3_out), .b(32'ha), .out(divider_4_out), .rem(divider_4_rem));  // open: upper
  BitSelector #(.width(32), .group(4)) bitselector_4 (.in(divider_4_rem), .out(out_5), .sel(3'b000));
  BitSelector #(.width(32), .group(4)) bitselector_5 (.in(divider_5_rem), .out(out_6), .sel(3'b000));
  Divider #(.width(32)) divider_5 (
    .a(divider_4_out), .b(32'ha), .out(divider_5_out), .rem(divider_5_rem));  // open: upper
  Divider #(.width(32)) divider_6 (
    .a(divider_5_out), .b(32'ha), .out(divider_6_out), .rem(divider_6_rem));  // open: upper
  BitSelector #(.width(32), .group(4)) bitselector_6 (.in(divider_6_rem), .out(out_7), .sel(3'b000));
  Divider #(.width(32)) divider_7 (
    .a(divider_6_out), .b(32'ha), .out(divider_7_out), .rem(divider_7_rem));  // open: upper
  BitSelector #(.width(32), .group(4)) bitselector_7 (.in(divider_7_rem), .out(out_8), .sel(3'b000));
  Divider #(.width(32)) divider_8 (
    .a(divider_7_out), .b(32'ha), .out(divider_8_out), .rem(divider_8_rem));  // open: upper
  BitSelector #(.width(32), .group(4)) bitselector_8 (.in(divider_9_rem), .out(out_10), .sel(3'b000));
  BitSelector #(.width(32), .group(4)) bitselector_9 (.in(divider_8_rem), .out(out_9), .sel(3'b000));
  Divider #(.width(32)) divider_9 (
    .a(divider_8_out), .b(32'ha), .out(divider_9_out), .rem(divider_9_rem));  // open: upper
  BitSelector #(.width(32), .group(4)) bitselector_10 (.in(divider_9_out), .out(out_11), .sel(3'b000));
endmodule

// 斐波那契数列计算器
module \斐波那契_Fibonacci_数列计算器  (
  input  [5:0] n,
  input  clear,
  input  clock,
  output [3:0] out_4,
  output [3:0] out_5,
  output [3:0] out_6,
  output [3:0] out_7,
  output [3:0] out_8,
  output [3:0] out_9,
  output [3:0] out_10,
  output [3:0] out_11,
  output [3:0] out_12,
  output [3:0] out_13
);

  wire and_1_out, comparator_1_eq, d_ff_1_q, displaydecoder_1_p1, displaydecoder_1_p2, displaydecoder_1_p3,
       displaydecoder_1_p4, displaydecoder_1_p6, displaydecoder_1_p7, displaydecoder_1_p8,
       displaydecoder_2_p1, displaydecoder_2_p2, displaydecoder_2_p3, displaydecoder_2_p4,
       displaydecoder_2_p6, displaydecoder_2_p7, displaydecoder_2_p8, displaydecoder_3_p1,
       displaydecoder_3_p2, displaydecoder_3_p3, displaydecoder_3_p4, displaydecoder_3_p6,
       displaydecoder_3_p7, displaydecoder_3_p8, displaydecoder_4_p1, displaydecoder_4_p2,
       displaydecoder_4_p3, displaydecoder_4_p4, displaydecoder_4_p6, displaydecoder_4_p7,
       displaydecoder_4_p8, displaydecoder_5_p1, displaydecoder_5_p2, displaydecoder_5_p3,
       displaydecoder_5_p4, displaydecoder_5_p6, displaydecoder_5_p7, displaydecoder_5_p8,
       displaydecoder_6_p1, displaydecoder_6_p2, displaydecoder_6_p3, displaydecoder_6_p4,
       displaydecoder_6_p6, displaydecoder_6_p7, displaydecoder_6_p8, displaydecoder_7_p1,
       displaydecoder_7_p2, displaydecoder_7_p3, displaydecoder_7_p4, displaydecoder_7_p6,
       displaydecoder_7_p7, displaydecoder_7_p8, displaydecoder_8_p1, displaydecoder_8_p2,
       displaydecoder_8_p3, displaydecoder_8_p4, displaydecoder_8_p6, displaydecoder_8_p7,
       displaydecoder_8_p8, displaydecoder_9_p1, displaydecoder_9_p2, displaydecoder_9_p3,
       displaydecoder_9_p4, displaydecoder_9_p6, displaydecoder_9_p7, displaydecoder_9_p8,
       displaydecoder_10_p1, displaydecoder_10_p2, displaydecoder_10_p3, displaydecoder_10_p4,
       displaydecoder_10_p6, displaydecoder_10_p7, displaydecoder_10_p8, not_1_out, or_1_out, or_2_out,
       shift_register_1_out;
  wire [7:0] counter_1_q;
  wire [31:0] fibo_1_fi;

  Shift_Register #(.width(1), .length(6), .parallel("true"), .trigger("rising")) shift_register_1 (
    .shift(1'b1), .in(1'b0), .clk(or_1_out), .out(shift_register_1_out), .load(clear), .d0(n[0]), .d1(n[1]),
    .d2(n[2]), .d3(n[3]), .d4(n[4]), .d5(n[5]));  // open: clr, q0, q1, q2, q3, q4, q5
  Counter #(.width(8), .max('h6), .ongoal("stay"), .trigger("rising"), .behavior("new")) counter_1 (
    .D({8{1'b0}}), .Q(counter_1_q), .clk(clock), .clr(clear));  // open: load, count, carry, preset, down
  Comparator #(.width(8), .mode("twosComplement")) comparator_1 (
    .a(counter_1_q), .b(8'h6), .eq(comparator_1_eq));  // open: gt, lt
  not not_1 (not_1_out, comparator_1_eq);
  or or_1 (or_1_out, clear, and_1_out);
  and and_1 (and_1_out, not_1_out, clock);
  or or_2 (or_2_out, d_ff_1_q, shift_register_1_out);
  D_Flip_Flop #(.trigger("rising"), .Pre_Clr_Positions("LEGACY"), .NegatePresetClear("false"), .enable("true"), .NewFFLayout("false")) d_ff_1 (
    .clk(and_1_out), .D(or_2_out), .Q(d_ff_1_q), .reset(clear));  // open: Qn, preset, en
  Fibo fibo_1 (.start(d_ff_1_q), .clr(clear), .clk(and_1_out), .ni_1(shift_register_1_out), .Fi(fibo_1_fi));
  _7_Segment_Display #(.active("true")) u_7_segment_display_1 (
    .g(displaydecoder_1_p8), .f(displaydecoder_1_p7), .a(displaydecoder_1_p1), .b(displaydecoder_1_p2),
    .e(displaydecoder_1_p6), .d(displaydecoder_1_p4), .c(displaydecoder_1_p3));  // open: dp
  // DisplayDecoder #(.multibit("true")) displaydecoder_1: pin names not known; wires that end beside it: displaydecoder_1_p1, displaydecoder_1_p2, displaydecoder_1_p3, displaydecoder_1_p4, out_13, displaydecoder_1_p6, displaydecoder_1_p7, displaydecoder_1_p8
  \Fibonacci数显示模块  \fibonacci数显示模块_1  (
    .in_1(fibo_1_fi), .out_2(out_4), .out_3(out_5), .out_4(out_6), .out_5(out_7), .out_6(out_8),
    .out_7(out_9), .out_8(out_10), .out_9(out_11), .out_10(out_12), .out_11(out_13));
  _7_Segment_Display #(.active("true")) u_7_segment_display_2 (
    .g(displaydecoder_2_p8), .f(displaydecoder_2_p7), .a(displaydecoder_2_p1), .b(displaydecoder_2_p2),
    .e(displaydecoder_2_p6), .d(displaydecoder_2_p4), .c(displaydecoder_2_p3));  // open: dp
  // DisplayDecoder #(.multibit("true")) displaydecoder_2: pin names not known; wires that end beside it: displaydecoder_2_p1, displaydecoder_2_p2, displaydecoder_2_p3, displaydecoder_2_p4, out_12, displaydecoder_2_p6, displaydecoder_2_p7, displaydecoder_2_p8
  _7_Segment_Display #(.active("true")) u_7_segment_display_3 (
    .g(displaydecoder_3_p8), .f(displaydecoder_3_p7), .a(displaydecoder_3_p1), .b(displaydecoder_3_p2),
    .e(displaydecoder_3_p6), .d(displaydecoder_3_p4), .c(displaydecoder_3_p3));  // open: dp
  // DisplayDecoder #(.multibit("true")) displaydecoder_3: pin names not known; wires that end beside it: displaydecoder_3_p1, displaydecoder_3_p2, displaydecoder_3_p3, displaydecoder_3_p4, out_11, displaydecoder_3_p6, displaydecoder_3_p7, displaydecoder_3_p8
  _7_Segment_Display #(.active("true")) u_7_segment_display_4 (
    .g(displaydecoder_4_p8), .f(displaydecoder_4_p7), .a(displaydecoder_4_p1), .b(displaydecoder_4_p2),
    .e(displaydecoder_4_p6), .d(displaydecoder_4_p4), .c(displaydecoder_4_p3));  // open: dp
  // DisplayDecoder #(.multibit("true")) displaydecoder_4: pin names not known; wires that end beside it: displaydecoder_4_p1, displaydecoder_4_p2, displaydecoder_4_p3, displaydecoder_4_p4, out_10, displaydecoder_4_p6, displaydecoder_4_p7, displaydecoder_4_p8
  _7_Segment_Display #(.active("true")) u_7_segment_display_5 (
    .g(displaydecoder_5_p8), .f(displaydecoder_5_p7), .a(displaydecoder_5_p1), .b(displaydecoder_5_p2),
    .e(displaydecoder_5_p6), .d(displaydecoder_5_p4), .c(displaydecoder_5_p3));  // open: dp
  // DisplayDecoder #(.multibit("true")) displaydecoder_5: pin names not known; wires that end beside it: displaydecoder_5_p1, displaydecoder_5_p2, displaydecoder_5_p3, displaydecoder_5_p4, out_9, displaydecoder_5_p6, displaydecoder_5_p7, displaydecoder_5_p8
  _7_Segment_Display #(.active("true")) u_7_segment_display_6 (
    .g(displaydecoder_6_p8), .f(displaydecoder_6_p7), .a(displaydecoder_6_p1), .b(displaydecoder_6_p2),
    .e(displaydecoder_6_p6), .d(displaydecoder_6_p4), .c(displaydecoder_6_p3));  // open: dp
  // DisplayDecoder #(.multibit("true")) displaydecoder_6: pin names not known; wires that end beside it: displaydecoder_6_p1, displaydecoder_6_p2, displaydecoder_6_p3, displaydecoder_6_p4, out_8, displaydecoder_6_p6, displaydecoder_6_p7, displaydecoder_6_p8
  _7_Segment_Display #(.active("true")) u_7_segment_display_7 (
    .g(displaydecoder_7_p8), .f(displaydecoder_7_p7), .a(displaydecoder_7_p1), .b(displaydecoder_7_p2),
    .e(displaydecoder_7_p6), .d(displaydecoder_7_p4), .c(displaydecoder_7_p3));  // open: dp
  // DisplayDecoder #(.multibit("true")) displaydecoder_7: pin names not known; wires that end beside it: displaydecoder_7_p1, displaydecoder_7_p2, displaydecoder_7_p3, displaydecoder_7_p4, out_7, displaydecoder_7_p6, displaydecoder_7_p7, displaydecoder_7_p8
  _7_Segment_Display #(.active("true")) u_7_segment_display_8 (
    .g(displaydecoder_8_p8), .f(displaydecoder_8_p7), .a(displaydecoder_8_p1), .b(displaydecoder_8_p2),
    .e(displaydecoder_8_p6), .d(displaydecoder_8_p4), .c(displaydecoder_8_p3));  // open: dp
  // DisplayDecoder #(.multibit("true")) displaydecoder_8: pin names not known; wires that end beside it: displaydecoder_8_p1, displaydecoder_8_p2, displaydecoder_8_p3, displaydecoder_8_p4, out_6, displaydecoder_8_p6, displaydecoder_8_p7, displaydecoder_8_p8
  _7_Segment_Display #(.active("true")) u_7_segment_display_9 (
    .g(displaydecoder_9_p8), .f(displaydecoder_9_p7), .a(displaydecoder_9_p1), .b(displaydecoder_9_p2),
    .e(displaydecoder_9_p6), .d(displaydecoder_9_p4), .c(displaydecoder_9_p3));  // open: dp
  // DisplayDecoder #(.multibit("true")) displaydecoder_9: pin names not known; wires that end beside it: displaydecoder_9_p1, displaydecoder_9_p2, displaydecoder_9_p3, displaydecoder_9_p4, out_5, displaydecoder_9_p6, displaydecoder_9_p7, displaydecoder_9_p8
  _7_Segment_Display #(.active("true")) u_7_segment_display_10 (
    .g(displaydecoder_10_p8), .f(displaydecoder_10_p7), .a(displaydecoder_10_p1), .b(displaydecoder_10_p2),
    .e(displaydecoder_10_p6), .d(displaydecoder_10_p4), .c(displaydecoder_10_p3));  // open: dp
  // DisplayDecoder #(.multibit("true")) displaydecoder_10: pin names not known; wires that end beside it: displaydecoder_10_p1, displaydecoder_10_p2, displaydecoder_10_p3, displaydecoder_10_p4, out_4, displaydecoder_10_p6, displaydecoder_10_p7, displaydecoder_10_p8
endmodule

module \斐波那契_Fibonacci_数列计算器验证电路  (
  input  [5:0] in_1,
  input  clear
);

  wire clock_1_out, displaydecoder_1_p1, displaydecoder_1_p2, displaydecoder_1_p3, displaydecoder_1_p4,
       displaydecoder_1_p6, displaydecoder_1_p7, displaydecoder_1_p8, displaydecoder_2_p1,
       displaydecoder_2_p2, displaydecoder_2_p3, displaydecoder_2_p4, displaydecoder_2_p6,
       displaydecoder_2_p7, displaydecoder_2_p8, displaydecoder_3_p1, displaydecoder_3_p2,
       displaydecoder_3_p3, displaydecoder_3_p4, displaydecoder_3_p6, displaydecoder_3_p7,
       displaydecoder_3_p8, displaydecoder_4_p1, displaydecoder_4_p2, displaydecoder_4_p3,
       displaydecoder_4_p4, displaydecoder_4_p6, displaydecoder_4_p7, displaydecoder_4_p8,
       displaydecoder_5_p1, displaydecoder_5_p2, displaydecoder_5_p3, displaydecoder_5_p4,
       displaydecoder_5_p6, displaydecoder_5_p7, displaydecoder_5_p8, displaydecoder_6_p1,
       displaydecoder_6_p2, displaydecoder_6_p3, displaydecoder_6_p4, displaydecoder_6_p6,
       displaydecoder_6_p7, displaydecoder_6_p8, displaydecoder_7_p1, displaydecoder_7_p2,
       displaydecoder_7_p3, displaydecoder_7_p4, displaydecoder_7_p6, displaydecoder_7_p7,
       displaydecoder_7_p8, displaydecoder_8_p1, displaydecoder_8_p2, displaydecoder_8_p3,
       displaydecoder_8_p4, displaydecoder_8_p6, displaydecoder_8_p7, displaydecoder_8_p8,
       displaydecoder_9_p1, displaydecoder_9_p2, displaydecoder_9_p3, displaydecoder_9_p4,
       displaydecoder_9_p6, displaydecoder_9_p7, displaydecoder_9_p8, displaydecoder_10_p1,
       displaydecoder_10_p2, displaydecoder_10_p3, displaydecoder_10_p4, displaydecoder_10_p6,
       displaydecoder_10_p7, displaydecoder_10_p8;
  wire [3:0] \斐波那契_fibonacci_数列计算器_1_out_4 , \斐波那契_fibonacci_数列计算器_1_out_5 , \斐波那契_fibonacci_数列计算器_1_out_6 ,
       \斐波那契_fibonacci_数列计算器_1_out_7 , \斐波那契_fibonacci_数列计算器_1_out_8 , \斐波那契_fibonacci_数列计算器_1_out_9 ,
       \斐波那契_fibonacci_数列计算器_1_out_10 , \斐波那契_fibonacci_数列计算器_1_out_11 , \斐波那契_fibonacci_数列计算器_1_out_12 ,
       \斐波那契_fibonacci_数列计算器_1_out_13 ;

  Clock #(.highDuration(1), .lowDuration(1)) clock_1 (.out(clock_1_out));
  \斐波那契_Fibonacci_数列计算器  \u_斐波那契_fibonacci_数列计算器_1  (
    .clear(clear), .clock(clock_1_out), .n(in_1), .out_4(\斐波那契_fibonacci_数列计算器_1_out_4 ),
    .out_5(\斐波那契_fibonacci_数列计算器_1_out_5 ), .out_6(\斐波那契_fibonacci_数列计算器_1_out_6 ),
    .out_7(\斐波那契_fibonacci_数列计算器_1_out_7 ), .out_8(\斐波那契_fibonacci_数列计算器_1_out_8 ),
    .out_9(\斐波那契_fibonacci_数列计算器_1_out_9 ), .out_10(\斐波那契_fibonacci_数列计算器_1_out_10 ),
    .out_11(\斐波那契_fibonacci_数列计算器_1_out_11 ), .out_12(\斐波那契_fibonacci_数列计算器_1_out_12 ),
    .out_13(\斐波那契_fibonacci_数列计算器_1_out_13 ));
  _7_Segment_Display #(.active("true")) u_7_segment_display_1 (
    .g(displaydecoder_1_p8), .f(displaydecoder_1_p7), .a(displaydecoder_1_p1), .b(displaydecoder_1_p2),
    .e(displaydecoder_1_p6), .d(displaydecoder_1_p4), .c(displaydecoder_1_p3));  // open: dp
  // DisplayDecoder #(.multibit("true")) displaydecoder_1: pin names not known; wires that end beside it: displaydecoder_1_p1, displaydecoder_1_p2, displaydecoder_1_p3, displaydecoder_1_p4, \斐波那契_fibonacci_数列计算器_1_out_13 , displaydecoder_1_p6, displaydecoder_1_p7, displaydecoder_1_p8
  _7_Segment_Display #(.active("true")) u_7_segment_display_2 (
    .g(displaydecoder_2_p8), .f(displaydecoder_2_p7), .a(displaydecoder_2_p1), .b(displaydecoder_2_p2),
    .e(displaydecoder_2_p6), .d(displaydecoder_2_p4), .c(displaydecoder_2_p3));  // open: dp
  // DisplayDecoder #(.multibit("true")) displaydecoder_2: pin names not known; wires that end beside it: displaydecoder_2_p1, displaydecoder_2_p2, displaydecoder_2_p3, displaydecoder_2_p4, \斐波那契_fibonacci_数列计算器_1_out_12 , displaydecoder_2_p6, displaydecoder_2_p7, displaydecoder_2_p8
  _7_Segment_Display #(.active("true")) u_7_segment_display_3 (
    .g(displaydecoder_3_p8), .f(displaydecoder_3_p7), .a(displaydecoder_3_p1), .b(displaydecoder_3_p2),
    .e(displaydecoder_3_p6), .d(displaydecoder_3_p4), .c(displaydecoder_3_p3));  // open: dp
  // DisplayDecoder #(.multibit("true")) displaydecoder_3: pin names not known; wires that end beside it: displaydecoder_3_p1, displaydecoder_3_p2, displaydecoder_3_p3, displaydecoder_3_p4, \斐波那契_fibonacci_数列计算器_1_out_11 , displaydecoder_3_p6, displaydecoder_3_p7, displaydecoder_3_p8
  _7_Segment_Display #(.active("true")) u_7_segment_display_4 (
    .g(displaydecoder_4_p8), .f(displaydecoder_4_p7), .a(displaydecoder_4_p1), .b(displaydecoder_4_p2),
    .e(displaydecoder_4_p6), .d(displaydecoder_4_p4), .c(displaydecoder_4_p3));  // open: dp
  // DisplayDecoder #(.multibit("true")) displaydecoder_4: pin names not known; wires that end beside it: displaydecoder_4_p1, displaydecoder_4_p2, displaydecoder_4_p3, displaydecoder_4_p4, \斐波那契_fibonacci_数列计算器_1_out_10 , displaydecoder_4_p6, displaydecoder_4_p7, displaydecoder_4_p8
  _7_Segment_Display #(.active("true")) u_7_segment_display_5 (
    .g(displaydecoder_5_p8), .f(displaydecoder_5_p7), .a(displaydecoder_5_p1), .b(displaydecoder_5_p2),
    .e(displaydecoder_5_p6), .d(displaydecoder_5_p4), .c(displaydecoder_5_p3));  // open: dp
  // DisplayDecoder #(.multibit("true")) displaydecoder_5: pin names not known; wires that end beside it: displaydecoder_5_p1, displaydecoder_5_p2, displaydecoder_5_p3, displaydecoder_5_p4, \斐波那契_fibonacci_数列计算器_1_out_9 , displaydecoder_5_p6, displaydecoder_5_p7, displaydecoder_5_p8
  _7_Segment_Display #(.active("true")) u_7_segment_display_6 (
    .g(displaydecoder_6_p8), .f(displaydecoder_6_p7), .a(displaydecoder_6_p1), .b(displaydecoder_6_p2),
    .e(displaydecoder_6_p6), .d(displaydecoder_6_p4), .c(displaydecoder_6_p3));  // open: dp
  // DisplayDecoder #(.multibit("true")) displaydecoder_6: pin names not known; wires that end beside it: displaydecoder_6_p1, displaydecoder_6_p2, displaydecoder_6_p3, displaydecoder_6_p4, \斐波那契_fibonacci_数列计算器_1_out_8 , displaydecoder_6_p6, displaydecoder_6_p7, displaydecoder_6_p8
  _7_Segment_Display #(.active("true")) u_7_segment_display_7 (
    .g(displaydecoder_7_p8), .f(displaydecoder_7_p7), .a(displaydecoder_7_p1), .b(displaydecoder_7_p2),
    .e(displaydecoder_7_p6), .d(displaydecoder_7_p4), .c(displaydecoder_7_p3));  // open: dp
  // DisplayDecoder #(.multibit("true")) displaydecoder_7: pin names not known; wires that end beside it: displaydecoder_7_p1, displaydecoder_7_p2, displaydecoder_7_p3, displaydecoder_7_p4, \斐波那契_fibonacci_数列计算器_1_out_7 , displaydecoder_7_p6, displaydecoder_7_p7, displaydecoder_7_p8
  _7_Segment_Display #(.active("true")) u_7_segment_display_8 (
    .g(displaydecoder_8_p8), .f(displaydecoder_8_p7), .a(displaydecoder_8_p1), .b(displaydecoder_8_p2),
    .e(displaydecoder_8_p6), .d(displaydecoder_8_p4), .c(displaydecoder_8_p3));  // open: dp
  // DisplayDecoder #(.multibit("true")) displaydecoder_8: pin names not known; wires that end beside it: displaydecoder_8_p1, displaydecoder_8_p2, displaydecoder_8_p3, displaydecoder_8_p4, \斐波那契_fibonacci_数列计算器_1_out_6 , displaydecoder_8_p6, displaydecoder_8_p7, displaydecoder_8_p8
  _7_Segment_Display #(.active("true")) u_7_segment_display_9 (
    .g(displaydecoder_9_p8), .f(displaydecoder_9_p7), .a(displaydecoder_9_p1), .b(displaydecoder_9_p2),
    .e(displaydecoder_9_p6), .d(displaydecoder_9_p4), .c(displaydecoder_9_p3));  // open: dp
  // DisplayDecoder #(.multibit("true")) displaydecoder_9: pin names not known; wires that end beside it: displaydecoder_9_p1, displaydecoder_9_p2, displaydecoder_9_p3, displaydecoder_9_p4, \斐波那契_fibonacci_数列计算器_1_out_5 , displaydecoder_9_p6, displaydecoder_9_p7, displaydecoder_9_p8
  _7_Segment_Display #(.active("true")) u_7_segment_display_10 (
    .g(displaydecoder_10_p8), .f(displaydecoder_10_p7), .a(displaydecoder_10_p1), .b(displaydecoder_10_p2),
    .e(displaydecoder_10_p6), .d(displaydecoder_10_p4), .c(displaydecoder_10_p3));  // open: dp
  // DisplayDecoder #(.multibit("true")) displaydecoder_10: pin names not known; wires that end beside it: displaydecoder_10_p1, displaydecoder_10_p2, displaydecoder_10_p3, displaydecoder_10_p4, \斐波那契_fibonacci_数列计算器_1_out_4 , displaydecoder_10_p6, displaydecoder_10_p7, displaydecoder_10_p8
endmodule
