// Logisim project 单总线CPU设计(变长指令周期3级时序).circ as structural Verilog: 15 circuits, main circuit ◇硬布线控制器
// 硬布线
module \硬布线控制器  (
  input  CLK,
  input  [31:0] IR,
  input  EQUAL,
  output [6:0] \状态节拍信号 ,
  output [21:0] ControlBus
);

  wire ADDI, BEQ, LW, Other;
  wire [3:0] register_1_q, \时序发生器状态机_变长指令周期_1_n0 ;
  wire [12:9] OCInput;

  \时序发生器状态机_变长指令周期  \u_时序发生器状态机_变长指令周期_1  (
    .LW(LW), .SW(OCInput[9]), .BEQ(BEQ), .SLT(OCInput[12]), .ADDI(ADDI), .S3(register_1_q[3]),
    .S2(register_1_q[2]), .S1(register_1_q[1]), .S0(register_1_q[0]), .N3(\时序发生器状态机_变长指令周期_1_n0 [3]),
    .N2(\时序发生器状态机_变长指令周期_1_n0 [2]), .N1(\时序发生器状态机_变长指令周期_1_n0 [1]), .N0(\时序发生器状态机_变长指令周期_1_n0 [0]));
  Register #(.width(4), .trigger("falling"), .Select("low")) register_1 (
    .D(\时序发生器状态机_变长指令周期_1_n0 ), .Q(register_1_q), .clk(CLK));  // open: en, clr
  \时序发生器输出函数_变长指令周期  \u_时序发生器输出函数_变长指令周期_1  (
    .S3(register_1_q[3]), .S2(register_1_q[2]), .S1(register_1_q[1]), .S0(register_1_q[0]),
    .Mif(\状态节拍信号 [0]), .Mcal(\状态节拍信号 [1]), .Mex(\状态节拍信号 [2]), .T1(\状态节拍信号 [3]), .T2(\状态节拍信号 [4]),
    .T3(\状态节拍信号 [5]), .T4(\状态节拍信号 [6]));
  \指令译码器  \u_指令译码器_1  (
    .IR(IR), .LW(LW), .SW(OCInput[9]), .BEQ(BEQ), .ADDI(ADDI), .SLT(OCInput[12]), .OtherInstr(Other));
  \硬布线控制器组合逻辑单元  \u_硬布线控制器组合逻辑单元_1  (
    .SLT(OCInput[12]), .ADDI(ADDI), .LW(LW), .SW(OCInput[9]), .BEQ(BEQ), .Mif(\状态节拍信号 [0]),
    .Mcal(\状态节拍信号 [1]), .Mex(\状态节拍信号 [2]), .T1(\状态节拍信号 [3]), .T2(\状态节拍信号 [4]), .T3(\状态节拍信号 [5]),
    .T4(\状态节拍信号 [6]), .EQUAL(EQUAL), .Pcout(ControlBus[21]), .DRout(ControlBus[20]), .Zout(ControlBus[19]),
    .Rout(ControlBus[18]), .IRiout(ControlBus[17]), .IRaout(ControlBus[16]), .DREout(ControlBus[15]),
    .Pcin(ControlBus[14]), .ARin(ControlBus[13]), .DREin(ControlBus[12]), .DRin(ControlBus[11]),
    .Xin(ControlBus[10]), .Rin(ControlBus[9]), .IRin(ControlBus[8]), .PSWin(ControlBus[7]),
    .RegTgt(ControlBus[6]), .RegDst(ControlBus[5]), .Add(ControlBus[4]), .Add4(ControlBus[3]),
    .Slt_2(ControlBus[2]), .READ(ControlBus[1]), .WRITE(ControlBus[0]));

  // Other names for the same wires on the sheet: Write = ControlBus[0]; READ = ControlBus[1]; Slt_t = ControlBus[2];
  //   Add4 = ControlBus[3]; Add = ControlBus[4]; RegDst = ControlBus[5]; RegTgt = ControlBus[6];
  //   PSWin = ControlBus[7]; IRin = ControlBus[8]; Rin = ControlBus[9]; Xin = ControlBus[10]; DRin = ControlBus[11];
  //   DREin = ControlBus[12]; ARin = ControlBus[13]; PCin = ControlBus[14]; DREout = ControlBus[15];
  //   IR_A_out = ControlBus[16]; IR_I_out = ControlBus[17]; Rout = ControlBus[18]; Zout = ControlBus[19];
  //   DRout = ControlBus[20]; PCout = ControlBus[21];
  //   OCInput (some bits) = {ADDI, LW, BEQ, \状态节拍信号 [0], \状态节拍信号 [1], \状态节拍信号 [2], \状态节拍信号 [3], \状态节拍信号 [4], \状态节拍信号 [5], \状态节拍信号 [6], EQUAL};
  //   T4 = \状态节拍信号 [6]; T3 = \状态节拍信号 [5]; T2 = \状态节拍信号 [4]; T1 = \状态节拍信号 [3]; Mex = \状态节拍信号 [2]; Mcal = \状态节拍信号 [1];
  //   Mif = \状态节拍信号 [0]; SW = OCInput[9]; SLT = OCInput[12]; 指令字[31:0] = IR

  // Notes on the sheet:
  //   指令译码信号
  //   状态机
  //   现态
  //   不要改变此引脚区域内容，也不要改变封装形式
  //   次态
  //   状态寄存器
  //   如发现控制信号有错可以直接查看具体哪位信号出错
  //   输出函数
  //   输入输出引脚
  //   时序发生器TG
  //   指令译码器
  //   指令译码信号
  //   指令译码逻辑ID
  //   硬布线控制器组合逻辑单元
endmodule

module \单总线CPU_3级时序  (
  output [21:0] \控制总线 
);

  wire and_1_out, CLK, comparator_1_eq, equal, Mcal, Mex, Mif, Mint, mips_alu_1_equal, not_1_out, RST, T1,
       T2, T3, T4;
  wire [4:0] registerfile_1_p4, registerfile_1_p5;
  wire [11:0] Clks, \指令数 ;
  wire [31:0] AR_q, bit_extender_1_out, controlled_buffer_1_out, controlled_buffer_2_out, DR_q, IR,
       mips_alu_1_result, PC_q, ram_1_data, registerfile_1_p6, shifter_1_out, X_q, Z_q, \内部总线 ;

  LED #(.active("true")) led_1 (.in(Mcal));
  LED #(.active("true")) led_2 (.in(Mif));
  // Probe on Clks
  Register #(.width(32), .trigger("rising"), .Select("low")) AR (
    .D(\内部总线 ), .en(\控制总线 [13]), .Q(AR_q), .clk(CLK));  // open: clr
  // Digital_Oscilloscope #(.nState(35), .frontlines("rising"), .showclock("true")) digital_oscilloscope_1: pin names not known; wires that end beside it: CLK, Mif, Mcal, Mex, T1, T2, T3, T4, \控制总线 [2]
  LED #(.active("true")) led_3 (.in(Mint));
  LED #(.active("true")) led_4 (.in(Mex));
  LED #(.active("true")) led_5 (.in(T1));
  // Mips_Probe mips_probe_1: pin names not known; wires that end beside it: IR
  // Probe on controlled_buffer_1_out
  Register #(.width(32), .trigger("rising"), .Select("low")) X (
    .D(\内部总线 ), .en(\控制总线 [10]), .Q(X_q), .clk(CLK));  // open: clr
  LED #(.active("true")) led_6 (.in(T3));
  LED #(.active("true")) led_7 (.in(T2));
  // Probe on \指令数 
  LED #(.active("true")) led_8 (.in(T4));
  RAM #(.addrWidth(10), .dataWidth(32), .bus("separate"), .Select("high")) ram_1 (
    .addr(AR_q[11:2]), .din(controlled_buffer_1_out), .data(ram_1_data), .str(\控制总线 [0]), .clk(CLK),
    .ld(\控制总线 [1]));  // open: sel, clr
  assign controlled_buffer_1_out = \控制总线 [15] ? DR_q : 32'bz;  // Controlled_Buffer controlled_buffer_1
  MIPS_ALU mips_alu_1 (
    .X(X_q), .Y(\内部总线 ), .Equal(mips_alu_1_equal), .Result(mips_alu_1_result), .ADD(\控制总线 [4]),
    .ADD4(\控制总线 [3]), .SLT(\控制总线 [2]));  // open: SUB
  assign controlled_buffer_2_out = \控制总线 [11] ? \内部总线  : 32'bz;  // Controlled_Buffer controlled_buffer_2
  assign controlled_buffer_2_out = \控制总线 [12] ? ram_1_data : 32'bz;  // Controlled_Buffer controlled_buffer_3
  // Probe on \内部总线 
  Register #(.width(32), .trigger("rising"), .Select("low")) PC (
    .D(\内部总线 ), .en(\控制总线 [14]), .Q(PC_q), .clk(CLK), .clr(RST));
  assign \内部总线  = \控制总线 [21] ? PC_q : 32'bz;  // Controlled_Buffer controlled_buffer_4
  Register #(.width(32), .trigger("rising"), .Select("low")) DR (
    .D(controlled_buffer_2_out), .Q(DR_q), .clk(CLK));  // open: en, clr
  assign \内部总线  = \控制总线 [20] ? DR_q : 32'bz;  // Controlled_Buffer controlled_buffer_5
  Register #(.width(1), .trigger("rising"), .Select("low")) PSW (
    .D(mips_alu_1_equal), .en(\控制总线 [7]), .Q(equal), .clk(CLK));  // open: clr
  Register #(.width(32), .trigger("rising"), .Select("low")) Z (
    .D(mips_alu_1_result), .Q(Z_q), .clk(CLK));  // open: en, clr
  assign \内部总线  = \控制总线 [19] ? Z_q : 32'bz;  // Controlled_Buffer controlled_buffer_6
  Register #(.width(32), .trigger("rising"), .Select("low")) u_IR (
    .D(\内部总线 ), .en(\控制总线 [8]), .Q(IR), .clk(CLK));  // open: clr
  assign \内部总线  = \控制总线 [17] ? bit_extender_1_out : 32'bz;  // Controlled_Buffer controlled_buffer_7
  assign \内部总线  = \控制总线 [16] ? shifter_1_out : 32'bz;  // Controlled_Buffer controlled_buffer_8
  \硬布线控制器  \u_硬布线控制器_1  (
    .\状态节拍信号 ({T4, T3, T2, T1, Mex, Mcal, Mif}), .CLK(CLK), .IR(IR), .ControlBus(\控制总线 ), .EQUAL(equal));
  // RegisterFile registerfile_1: pin names not known; wires that end beside it: \内部总线 , CLK, \控制总线 [9], registerfile_1_p4, registerfile_1_p5, registerfile_1_p6
  assign bit_extender_1_out = {{16{IR[15]}}, IR[15:0]};  // Bit_Extender bit_extender_1
  assign \内部总线  = \控制总线 [18] ? registerfile_1_p6 : 32'bz;  // Controlled_Buffer controlled_buffer_9
  Multiplexer #(.select(1), .width(5), .disabled("Z"), .enable("false")) multiplexer_1 (
    .in0(IR[25:21]), .in1(IR[20:16]), .out(registerfile_1_p5), .sel(\控制总线 [6]));
  Multiplexer #(.select(1), .width(5), .disabled("Z"), .enable("false")) multiplexer_2 (
    .in0(IR[20:16]), .in1(IR[15:11]), .out(registerfile_1_p4), .sel(\控制总线 [5]));
  not not_1 (not_1_out, comparator_1_eq);
  Comparator #(.width(32), .mode("twosComplement")) comparator_1 (
    .a(IR), .b(32'h1000ffff), .eq(comparator_1_eq));  // open: gt, lt
  Clock #(.highDuration(1), .lowDuration(1)) clock_1 (.out(CLK));
  Shifter #(.width(32), .shift("ll")) shifter_1 (.in(bit_extender_1_out), .\dist (5'b00010), .out(shifter_1_out));
  Counter #(.width(12), .max('hfff), .ongoal("wrap"), .trigger("falling"), .behavior("new")) counter_1 (
    .count(not_1_out), .Q(Clks), .clk(CLK));  // open: load, D, carry, clr, preset, down
  and and_1 (and_1_out, not_1_out, Mif, T1);
  Counter #(.width(12), .max('hfff), .ongoal("wrap"), .trigger("falling"), .behavior("old")) counter_2 (
    .count(and_1_out), .Q(\指令数 ), .clk(CLK));  // open: load, D, carry, clr, preset

  // Other names for the same wires on the sheet: rd[4:0] = IR[15:11]; rt[4:0] = IR[20:16]; rs[4:0] = IR[25:21];
  //   Write = \控制总线 [0]; READ = \控制总线 [1]; Slt = \控制总线 [2]; Add4 = \控制总线 [3]; Add = \控制总线 [4]; RegDst = \控制总线 [5];
  //   RegTgt = \控制总线 [6]; PSWin = \控制总线 [7]; IRin = \控制总线 [8]; Rin = \控制总线 [9]; Xin = \控制总线 [10]; DRin = \控制总线 [11];
  //   DREin = \控制总线 [12]; ARin = \控制总线 [13]; PCin = \控制总线 [14]; DREout = \控制总线 [15]; IR_A_out = \控制总线 [16];
  //   IR_I_out = \控制总线 [17]; Rout = \控制总线 [18]; Zout = \控制总线 [19]; DRout = \控制总线 [20]; PCout = \控制总线 [21];
  //   状态节拍信号[6:0] = {T4, T3, T2, T1, Mex, Mcal, Mif}

  // Notes on the sheet:
  //   单总线结构 MIPS CPU
  //   MEM
  //   外部总线
  //   内部总线
  //   三级时序
  //   Immediate32
  //   AddressOffset32
endmodule

// Decoder
module \指令译码器  (
  input  [31:0] IR,
  output LW,
  output SW,
  output BEQ,
  output ADDI,
  output SLT,
  output OtherInstr
);

  wire comparator_5_eq, comparator_6_eq;

  Comparator #(.width(6), .mode("twosComplement")) comparator_1 (
    .a(IR[31:26]), .b(6'b100011), .eq(LW));  // open: gt, lt
  Comparator #(.width(6), .mode("twosComplement")) comparator_2 (
    .a(IR[31:26]), .b(6'b101011), .eq(SW));  // open: gt, lt
  Comparator #(.width(6), .mode("twosComplement")) comparator_3 (
    .a(IR[31:26]), .b(6'b000100), .eq(BEQ));  // open: gt, lt
  Comparator #(.width(6), .mode("twosComplement")) comparator_4 (
    .a(IR[31:26]), .b(6'b001000), .eq(ADDI));  // open: gt, lt
  Comparator #(.width(6), .mode("twosComplement")) comparator_5 (
    .a(IR[31:26]), .b({6{1'b0}}), .eq(comparator_5_eq));  // open: gt, lt
  Comparator #(.width(6), .mode("twosComplement")) comparator_6 (
    .a(IR[5:0]), .b(6'b101010), .eq(comparator_6_eq));  // open: gt, lt
  and and_1 (SLT, comparator_6_eq, comparator_5_eq);
  nor nor_1 (OtherInstr, BEQ, SW, LW, ADDI, SLT);

  // Other names for the same wires on the sheet: FUNCT[5:0] = IR[5:0]; OP[5:0] = IR[31:26]

  // Notes on the sheet:
  //   注释：此电路负责根据OP和FUNCT字段生成指令操作类型信号
  //   常用常量
  //   请勿增删改引脚，否则可能引起子电路外观变化，无法自动测试
  //   将指令字IR转换成指令译码信息，每一个输出代表一条不同的指令
endmodule

// 状态机
module \时序发生器状态机_定长指令周期  (
  input  S3,
  input  S2,
  input  S1,
  input  S0,
  output N3,
  output N2,
  output N1,
  output N0
);

  wire and_1_out, and_2_out, and_3_out, and_4_out, and_5_out, and_6_out, and_7_out, and_8_out, and_9_out,
       and_10_out, and_11_out, and_12_out, not_1_out, not_2_out, not_3_out, not_4_out, not_5_out, not_6_out,
       not_7_out, not_8_out, not_9_out, not_10_out, not_11_out, not_12_out, not_13_out, not_14_out,
       not_15_out, not_16_out, not_17_out, not_18_out, not_19_out, not_20_out, not_21_out, not_22_out,
       not_23_out;

  not not_1 (not_1_out, S3);
  not not_2 (not_2_out, S2);
  not not_3 (not_3_out, S1);
  not not_4 (not_4_out, S2);
  not not_5 (not_5_out, S0);
  not not_6 (not_6_out, S3);
  not not_7 (not_7_out, S2);
  not not_8 (not_8_out, S3);
  not not_9 (not_9_out, S1);
  not not_10 (not_10_out, S3);
  not not_11 (not_11_out, S0);
  not not_12 (not_12_out, S3);
  not not_13 (not_13_out, S1);
  and and_1 (and_1_out, not_12_out, not_13_out, S0);
  not not_14 (not_14_out, S2);
  and and_2 (and_2_out, not_14_out, not_15_out, S0);
  not not_15 (not_15_out, S1);
  not not_16 (not_16_out, S3);
  and and_3 (and_3_out, not_16_out, S1, not_17_out);
  not not_17 (not_17_out, S0);
  not not_18 (not_18_out, S2);
  and and_4 (and_4_out, not_18_out, S1, not_19_out);
  not not_19 (not_19_out, S0);
  not not_20 (not_20_out, S3);
  and and_5 (and_5_out, not_20_out, not_21_out);
  not not_21 (not_21_out, S0);
  not not_22 (not_22_out, S2);
  and and_6 (and_6_out, not_22_out, not_23_out);
  not not_23 (not_23_out, S0);
  and and_7 (and_7_out, not_1_out, S2, S1, S0);
  or or_1 (N3, and_7_out, and_8_out, and_9_out);
  and and_8 (and_8_out, S3, not_2_out, not_3_out);
  and and_9 (and_9_out, S3, not_4_out, not_5_out);
  and and_10 (and_10_out, not_6_out, not_7_out, S1, S0);
  and and_11 (and_11_out, not_8_out, S2, not_9_out);
  or or_2 (N2, and_10_out, and_11_out, and_12_out);
  and and_12 (and_12_out, not_10_out, S2, not_11_out);
  or or_3 (N1, and_1_out, and_2_out, and_3_out, and_4_out);
  or or_4 (N0, and_5_out, and_6_out);
endmodule

// 输出函数
module \时序发生器输出函数_定长指令周期  (
  input  S3,
  input  S2,
  input  S1,
  input  S0,
  output Mif,
  output Mcal,
  output Mex,
  output T1,
  output T2,
  output T3,
  output T4
);

  wire and_4_out, and_5_out, and_6_out, and_7_out, and_8_out, and_9_out, and_10_out, and_11_out, and_12_out,
       and_13_out, and_14_out, and_15_out, and_16_out, and_17_out, and_18_out, and_19_out, not_1_out,
       not_2_out, not_3_out, not_4_out, not_5_out, not_6_out, not_7_out, not_8_out, not_9_out, not_10_out,
       not_11_out, not_12_out, not_13_out, not_14_out, not_15_out, not_16_out, not_17_out, not_18_out,
       not_19_out, not_20_out;

  not not_1 (not_1_out, S3);
  and and_1 (Mif, not_1_out, not_2_out);
  not not_2 (not_2_out, S2);
  not not_3 (not_3_out, S3);
  and and_2 (Mcal, not_3_out, S2);
  and and_3 (Mex, S3, not_4_out);
  not not_4 (not_4_out, S2);
  not not_5 (not_5_out, S3);
  and and_4 (and_4_out, not_5_out, not_6_out);
  not not_6 (not_6_out, S1);
  not not_7 (not_7_out, S0);
  not not_8 (not_8_out, S2);
  and and_5 (and_5_out, not_8_out, not_9_out);
  not not_9 (not_9_out, S1);
  not not_10 (not_10_out, S0);
  not not_11 (not_11_out, S3);
  and and_6 (and_6_out, not_11_out, not_12_out);
  not not_12 (not_12_out, S1);
  not not_13 (not_13_out, S2);
  and and_7 (and_7_out, not_13_out, not_14_out);
  not not_14 (not_14_out, S1);
  not not_15 (not_15_out, S3);
  and and_8 (and_8_out, not_15_out, S1);
  not not_16 (not_16_out, S0);
  not not_17 (not_17_out, S2);
  and and_9 (and_9_out, not_17_out, S1);
  not not_18 (not_18_out, S0);
  not not_19 (not_19_out, S3);
  and and_10 (and_10_out, not_19_out, S1);
  not not_20 (not_20_out, S2);
  and and_11 (and_11_out, not_20_out, S1);
  and and_12 (and_12_out, and_4_out, not_7_out);
  and and_13 (and_13_out, and_5_out, not_10_out);
  and and_14 (and_14_out, and_6_out, S0);
  and and_15 (and_15_out, and_7_out, S0);
  and and_16 (and_16_out, and_8_out, not_16_out);
  and and_17 (and_17_out, and_9_out, not_18_out);
  and and_18 (and_18_out, and_10_out, S0);
  and and_19 (and_19_out, and_11_out, S0);
  or or_1 (T1, and_12_out, and_13_out);
  or or_2 (T2, and_14_out, and_15_out);
  or or_3 (T3, and_16_out, and_17_out);
  or or_4 (T4, and_18_out, and_19_out);
endmodule

// 状态机
module \时序发生器状态机_变长指令周期  (
  input  LW,
  input  SW,
  input  BEQ,
  input  SLT,
  input  ADDI,
  input  S3,
  input  S2,
  input  S1,
  input  S0,
  output N3,
  output N2,
  output N1,
  output N0
);

  wire and_2_out, and_3_out, and_4_out, and_5_out, and_6_out, and_7_out, and_8_out, and_9_out, and_10_out,
       and_11_out, and_12_out, not_1_out, not_2_out, not_3_out, not_4_out, not_5_out, not_6_out, not_7_out,
       not_8_out, not_9_out, not_10_out, not_11_out, not_12_out, not_13_out, not_14_out, not_15_out,
       not_16_out, not_17_out, not_18_out, not_19_out, not_20_out, not_21_out, not_22_out, not_23_out,
       not_24_out, not_25_out, not_26_out, not_27_out, not_28_out;

  not not_1 (not_1_out, S3);
  not not_2 (not_2_out, S3);
  not not_3 (not_3_out, S2);
  not not_4 (not_4_out, S3);
  not not_5 (not_5_out, S1);
  not not_6 (not_6_out, S3);
  not not_7 (not_7_out, S0);
  not not_8 (not_8_out, LW);
  not not_9 (not_9_out, SW);
  not not_10 (not_10_out, BEQ);
  not not_11 (not_11_out, S3);
  not not_12 (not_12_out, S2);
  not not_13 (not_13_out, S3);
  not not_14 (not_14_out, S1);
  not not_15 (not_15_out, S3);
  not not_16 (not_16_out, S0);
  not not_17 (not_17_out, S3);
  not not_18 (not_18_out, S2);
  not not_19 (not_19_out, S3);
  not not_20 (not_20_out, S2);
  not not_21 (not_21_out, S3);
  not not_22 (not_22_out, S2);
  not not_23 (not_23_out, S3);
  not not_24 (not_24_out, S2);
  not not_25 (not_25_out, S3);
  not not_26 (not_26_out, S2);
  not not_27 (not_27_out, S3);
  not not_28 (not_28_out, S0);
  and and_1 (N3, not_1_out, S2, S1, S0);
  and and_2 (and_2_out, not_2_out, not_3_out, S1, S0);
  and and_3 (and_3_out, not_4_out, S2, not_5_out);
  and and_4 (and_4_out, not_6_out, S2, not_7_out);
  and and_5 (and_5_out, not_8_out, not_9_out, not_10_out, not_11_out, not_12_out, S0);
  and and_6 (and_6_out, not_13_out, not_14_out, S0);
  and and_7 (and_7_out, not_15_out, S1, not_16_out);
  and and_8 (and_8_out, ADDI, not_17_out, not_18_out, S1);
  and and_9 (and_9_out, SLT, not_19_out, not_20_out, S1);
  and and_10 (and_10_out, SW, BEQ, not_21_out, not_22_out, S1);
  and and_11 (and_11_out, LW, BEQ, not_23_out, not_24_out, S1);
  and and_12 (and_12_out, LW, SW, not_25_out, not_26_out, S1);
  and and_13 (N0, not_27_out, not_28_out);
  or or_1 (N2, and_2_out, and_3_out, and_4_out);
  or or_2 (N1, and_5_out, and_6_out, and_7_out, and_8_out, and_9_out, and_10_out, and_11_out, and_12_out);
endmodule

module \时序发生器输出函数_变长指令周期  (
  input  S3,
  input  S2,
  input  S1,
  input  S0,
  output Mif,
  output Mcal,
  output Mex,
  output T1,
  output T2,
  output T3,
  output T4
);

  wire and_3_out, and_4_out, and_5_out, and_6_out, and_7_out, and_8_out, not_1_out, not_2_out, not_3_out,
       not_4_out, not_5_out, not_6_out, not_7_out, not_8_out, not_9_out, not_10_out, not_11_out;

  not not_1 (not_1_out, S3);
  and and_1 (Mif, not_1_out, not_2_out);
  not not_2 (not_2_out, S2);
  and and_2 (Mcal, S2, not_3_out);
  not not_3 (not_3_out, S1);
  and and_3 (and_3_out, S2, S1);
  not not_4 (not_4_out, S3);
  not not_5 (not_5_out, S1);
  and and_4 (and_4_out, not_4_out, not_5_out, not_6_out);
  not not_6 (not_6_out, S0);
  and and_5 (and_5_out, S2, not_7_out);
  not not_7 (not_7_out, S0);
  not not_8 (not_8_out, S1);
  and and_6 (and_6_out, not_8_out, S0);
  and and_7 (and_7_out, S2, S0);
  not not_9 (not_9_out, S2);
  and and_8 (and_8_out, not_9_out, S1, not_10_out);
  not not_10 (not_10_out, S0);
  not not_11 (not_11_out, S2);
  and and_9 (T4, not_11_out, S1, S0);
  or or_1 (Mex, and_3_out, S3);
  or or_2 (T1, and_4_out, and_5_out);
  or or_3 (T2, and_6_out, and_7_out);
  or or_4 (T3, and_8_out, S3);
endmodule

// 硬布线控制器组合逻辑单元
module \硬布线控制器组合逻辑单元  (
  input  SLT,
  input  ADDI,
  input  LW,
  input  SW,
  input  BEQ,
  input  Mif,
  input  Mcal,
  input  Mex,
  input  T1,
  input  T2,
  input  T3,
  input  T4,
  input  EQUAL,
  output Pcout,
  output DRout,
  output Zout,
  output Rout,
  output IRiout,
  output IRaout,
  output DREout,
  output Pcin,
  output ARin,
  output DREin,
  output DRin,
  output Xin,
  output Rin,
  output IRin,
  output PSWin,
  output RegTgt,
  output RegDst,
  output Add,
  output Add4,
  output Slt_2,
  output READ,
  output WRITE
);

  wire and_1_out, and_2_out, and_3_out, and_4_out, and_5_out, and_6_out, and_7_out, and_8_out, and_9_out,
       and_10_out, and_11_out, and_12_out, and_13_out, and_14_out, and_15_out, and_16_out, and_17_out,
       and_18_out, and_19_out, and_20_out, and_21_out, and_22_out, and_23_out, and_24_out, and_25_out,
       and_26_out, and_27_out, and_28_out, and_29_out, and_30_out, and_32_out, and_33_out, and_34_out,
       and_35_out, and_36_out, and_37_out, and_38_out, and_39_out, and_41_out, and_42_out, and_43_out,
       and_44_out, and_45_out, and_46_out, and_47_out, and_48_out, and_49_out, and_50_out, and_51_out,
       and_52_out, and_53_out, and_54_out, and_55_out, and_56_out, and_57_out, and_58_out, and_59_out,
       and_60_out, and_61_out, and_62_out, and_63_out, and_64_out, and_67_out, and_68_out, and_69_out,
       and_70_out, and_71_out, and_72_out, and_73_out, and_75_out, and_76_out, and_77_out, and_78_out,
       and_79_out, and_80_out, and_81_out, and_82_out, and_83_out, and_84_out, and_86_out, and_87_out,
       and_88_out, and_90_out, and_91_out, and_92_out, and_93_out, and_95_out, and_96_out, and_98_out,
       and_99_out, and_100_out, and_101_out, and_102_out, and_103_out, and_104_out, or_3_out, or_4_out,
       or_5_out, or_6_out, or_7_out, or_8_out, or_9_out, or_11_out, or_13_out, or_14_out, or_15_out,
       or_16_out, or_17_out, or_18_out, or_19_out, or_21_out, or_23_out, or_24_out, or_26_out, or_29_out,
       or_31_out;

  and and_1 (and_1_out, BEQ, Mex);
  and and_2 (and_2_out, LW, Mex);
  and and_3 (and_3_out, BEQ, Mex);
  and and_4 (and_4_out, T3, EQUAL);
  and and_5 (and_5_out, LW, Mex);
  and and_6 (and_6_out, ADDI, Mex);
  and and_7 (and_7_out, BEQ, Mcal);
  and and_8 (and_8_out, BEQ, Mcal);
  and and_9 (and_9_out, SW, Mex);
  and and_10 (and_10_out, SW, Mcal);
  and and_11 (and_11_out, LW, Mcal);
  and and_12 (and_12_out, ADDI, Mex);
  and and_13 (and_13_out, SLT, Mex);
  and and_14 (and_14_out, SLT, Mex);
  and and_15 (and_15_out, SW, Mcal);
  and and_16 (and_16_out, LW, Mcal);
  and and_17 (and_17_out, BEQ, Mex);
  and and_18 (and_18_out, SW, Mex);
  and and_19 (and_19_out, BEQ, Mex);
  and and_20 (and_20_out, T3, EQUAL);
  and and_21 (and_21_out, SW, Mex);
  and and_22 (and_22_out, LW, Mex);
  and and_23 (and_23_out, SW, Mex);
  and and_24 (and_24_out, BEQ, Mex);
  and and_25 (and_25_out, BEQ, Mcal);
  and and_26 (and_26_out, SW, Mcal);
  and and_27 (and_27_out, LW, Mcal);
  and and_28 (and_28_out, ADDI, Mex);
  and and_29 (and_29_out, LW, Mex);
  and and_30 (and_30_out, ADDI, Mex);
  and and_31 (IRin, Mif, T4);
  and and_32 (and_32_out, BEQ, Mcal);
  and and_33 (and_33_out, BEQ, Mcal);
  and and_34 (and_34_out, SW, Mex);
  and and_35 (and_35_out, SLT, Mex);
  and and_36 (and_36_out, BEQ, Mex);
  and and_37 (and_37_out, SW, Mcal);
  and and_38 (and_38_out, LW, Mcal);
  and and_39 (and_39_out, ADDI, Mex);
  and and_40 (Add4, Mif, T2);
  and and_41 (and_41_out, SLT, Mex);
  and and_42 (and_42_out, LW, Mex);
  and and_43 (and_43_out, SW, Mex);
  and and_44 (and_44_out, Mif, T1);
  and and_45 (and_45_out, and_1_out, T1);
  and and_46 (and_46_out, Mif, T4);
  and and_47 (and_47_out, and_2_out, T3);
  and and_48 (and_48_out, Mif, T3);
  and and_49 (and_49_out, and_3_out, and_4_out);
  and and_50 (and_50_out, SW, Mex);
  and and_51 (and_51_out, and_5_out, T1);
  and and_52 (and_52_out, and_6_out, T3);
  and and_53 (and_53_out, SLT, Mex);
  and and_54 (and_54_out, and_7_out, T2);
  and and_55 (and_55_out, and_8_out, T1);
  and and_56 (and_56_out, and_9_out, T2);
  and and_57 (and_57_out, and_10_out, T1);
  and and_58 (and_58_out, and_11_out, T1);
  and and_59 (and_59_out, and_12_out, T1);
  and and_60 (and_60_out, and_13_out, T2);
  and and_61 (and_61_out, and_14_out, T1);
  and and_62 (and_62_out, and_15_out, T2);
  and and_63 (and_63_out, and_16_out, T2);
  and and_64 (and_64_out, ADDI, Mex);
  and and_65 (IRaout, and_17_out, T2);
  and and_66 (DREout, and_18_out, T3);
  and and_67 (and_67_out, Mif, T3);
  and and_68 (and_68_out, and_19_out, and_20_out);
  and and_69 (and_69_out, Mif, T1);
  and and_70 (and_70_out, and_21_out, T1);
  and and_71 (and_71_out, LW, Mex);
  and and_72 (and_72_out, Mif, T3);
  and and_73 (and_73_out, and_22_out, T2);
  and and_74 (DRin, and_23_out, T2);
  and and_75 (and_75_out, Mif, T1);
  and and_76 (and_76_out, and_24_out, T1);
  and and_77 (and_77_out, and_25_out, T1);
  and and_78 (and_78_out, and_26_out, T1);
  and and_79 (and_79_out, and_27_out, T1);
  and and_80 (and_80_out, and_28_out, T1);
  and and_81 (and_81_out, SLT, Mex);
  and and_82 (and_82_out, and_29_out, T3);
  and and_83 (and_83_out, and_30_out, T3);
  and and_84 (and_84_out, SLT, Mex);
  and and_85 (PSWin, and_32_out, T2);
  and and_86 (and_86_out, and_33_out, T2);
  and and_87 (and_87_out, and_34_out, T2);
  and and_88 (and_88_out, SLT, Mex);
  and and_89 (RegDst, and_35_out, T3);
  and and_90 (and_90_out, and_36_out, T2);
  and and_91 (and_91_out, and_37_out, T2);
  and and_92 (and_92_out, and_38_out, T2);
  and and_93 (and_93_out, and_39_out, T2);
  and and_94 (Slt_2, and_41_out, T2);
  and and_95 (and_95_out, Mif, T3);
  and and_96 (and_96_out, and_42_out, T2);
  and and_97 (WRITE, and_43_out, T3);
  or or_1 (Pcout, and_44_out, and_45_out);
  or or_2 (DRout, and_46_out, and_47_out);
  or or_3 (or_3_out, and_48_out, and_49_out);
  and and_98 (and_98_out, and_50_out, T1);
  or or_4 (or_4_out, and_51_out, and_52_out);
  and and_99 (and_99_out, and_53_out, T3);
  or or_5 (or_5_out, and_54_out, and_55_out);
  or or_6 (or_6_out, and_56_out, and_57_out);
  or or_7 (or_7_out, and_58_out, and_59_out);
  or or_8 (or_8_out, and_60_out, and_61_out);
  or or_9 (or_9_out, and_62_out, and_63_out);
  and and_100 (and_100_out, and_64_out, T2);
  or or_10 (Pcin, and_67_out, and_68_out);
  or or_11 (or_11_out, and_69_out, and_70_out);
  and and_101 (and_101_out, and_71_out, T1);
  or or_12 (DREin, and_72_out, and_73_out);
  or or_13 (or_13_out, and_75_out, and_76_out);
  or or_14 (or_14_out, and_77_out, and_78_out);
  or or_15 (or_15_out, and_79_out, and_80_out);
  and and_102 (and_102_out, and_81_out, T1);
  or or_16 (or_16_out, and_82_out, and_83_out);
  and and_103 (and_103_out, and_84_out, T3);
  or or_17 (or_17_out, and_86_out, and_87_out);
  and and_104 (and_104_out, and_88_out, T2);
  or or_18 (or_18_out, and_90_out, and_91_out);
  or or_19 (or_19_out, and_92_out, and_93_out);
  or or_20 (READ, and_95_out, and_96_out);
  or or_21 (or_21_out, or_3_out, and_98_out);
  or or_22 (Zout, or_21_out, or_23_out);
  or or_23 (or_23_out, or_4_out, and_99_out);
  or or_24 (or_24_out, or_5_out, or_6_out);
  or or_25 (Rout, or_24_out, or_26_out);
  or or_26 (or_26_out, or_7_out, or_8_out);
  or or_27 (IRiout, or_9_out, and_100_out);
  or or_28 (ARin, or_11_out, and_101_out);
  or or_29 (or_29_out, or_13_out, or_14_out);
  or or_30 (Xin, or_29_out, or_31_out);
  or or_31 (or_31_out, or_15_out, and_102_out);
  or or_32 (Rin, or_16_out, and_103_out);
  or or_33 (RegTgt, or_17_out, and_104_out);
  or or_34 (Add, or_18_out, or_19_out);
endmodule

module \单总线CPU_中断_3级时序  (
  input  [1:0] EduInt,
  output [21:0] \EDU控制总线 ,
  output [4:0] \EDU中断信号 
);

  wire _1_out, _2_out, and_1_out, CLK, comparator_1_eq, equal, Mcal, Mex, Mif, Mint, mips_alu_1_equal,
       not_1_out, T1, T2, T3, T4, \中断控制器_1_ir1w , \中断控制器_1_ir2w , \中断请求 ;
  wire [4:0] registerfile_1_p5, registerfile_1_p6;
  wire [11:0] Clks, \指令数 ;
  wire [31:0] AR_q, bit_extender_1_out, controlled_buffer_1_out, controlled_buffer_3_out, DR_q, IR,
       mips_alu_1_result, PC_q, ram_1_data, registerfile_1_p7, shifter_1_out, X_q, Z_q, \内部总线 ;

  LED #(.active("true")) led_1 (.in(Mif));
  LED #(.active("true")) led_2 (.in(Mex));
  LED #(.active("true")) led_3 (.in(Mcal));
  LED #(.active("true")) led_4 (.in(Mint));
  // Probe on Clks
  Register #(.width(32), .trigger("rising"), .Select("low")) AR (
    .D(\内部总线 ), .en(\EDU控制总线 [13]), .Q(AR_q), .clk(CLK));  // open: clr
  // Probe on controlled_buffer_3_out
  // Digital_Oscilloscope #(.nState(35), .frontlines("rising"), .showclock("true")) digital_oscilloscope_1: pin names not known; wires that end beside it: CLK, Mif, Mcal, Mex, Mint, T1, T2, T3, T4
  LED #(.active("true")) led_5 (.in(T1));
  LED #(.active("true")) led_6 (.in(T2));
  // Mips_Probe mips_probe_1: pin names not known; wires that end beside it: IR
  Register #(.width(32), .trigger("rising"), .Select("low")) X (
    .D(\内部总线 ), .en(\EDU控制总线 [10]), .Q(X_q), .clk(CLK));  // open: clr
  LED #(.active("true")) led_7 (.in(T4));
  LED #(.active("true")) led_8 (.in(T3));
  // Probe on \指令数 
  RAM #(.addrWidth(10), .dataWidth(32), .bus("separate"), .Select("high")) ram_1 (
    .addr(AR_q[11:2]), .din(controlled_buffer_3_out), .data(ram_1_data), .str(\EDU控制总线 [0]), .clk(CLK),
    .ld(\EDU控制总线 [1]));  // open: sel, clr
  MIPS_ALU mips_alu_1 (
    .X(X_q), .Y(\内部总线 ), .Equal(mips_alu_1_equal), .Result(mips_alu_1_result), .ADD(\EDU控制总线 [4]),
    .ADD4(\EDU控制总线 [3]), .SLT(\EDU控制总线 [2]));  // open: SUB
  assign controlled_buffer_1_out = \EDU控制总线 [11] ? \内部总线  : 32'bz;  // Controlled_Buffer controlled_buffer_1
  assign controlled_buffer_1_out = \EDU控制总线 [12] ? ram_1_data : 32'bz;  // Controlled_Buffer controlled_buffer_2
  assign controlled_buffer_3_out = \EDU控制总线 [15] ? DR_q : 32'bz;  // Controlled_Buffer controlled_buffer_3
  // Probe on \内部总线 
  Register #(.width(32), .trigger("rising"), .Select("low")) PC (
    .D(\内部总线 ), .en(\EDU控制总线 [14]), .Q(PC_q), .clk(CLK));  // open: clr
  Register #(.width(32), .trigger("rising"), .Select("low")) DR (
    .D(controlled_buffer_1_out), .Q(DR_q), .clk(CLK));  // open: en, clr
  Register #(.width(1), .trigger("rising"), .Select("low")) PSW (
    .D(mips_alu_1_equal), .en(\EDU控制总线 [7]), .Q(equal), .clk(CLK));  // open: clr
  Register #(.width(32), .trigger("rising"), .Select("low")) Z (
    .D(mips_alu_1_result), .Q(Z_q), .clk(CLK));  // open: en, clr
  assign \内部总线  = \EDU控制总线 [21] ? PC_q : 32'bz;  // Controlled_Buffer controlled_buffer_4
  // Probe on \内部总线 
  assign \内部总线  = \EDU控制总线 [20] ? DR_q : 32'bz;  // Controlled_Buffer controlled_buffer_5
  assign \内部总线  = \EDU控制总线 [19] ? Z_q : 32'bz;  // Controlled_Buffer controlled_buffer_6
  assign \内部总线  = \EDU控制总线 [17] ? bit_extender_1_out : 32'bz;  // Controlled_Buffer controlled_buffer_7
  assign \内部总线  = \EDU控制总线 [16] ? shifter_1_out : 32'bz;  // Controlled_Buffer controlled_buffer_8
  Register #(.width(32), .trigger("rising"), .Select("low")) u_IR (
    .D(\内部总线 ), .en(\EDU控制总线 [8]), .Q(IR), .clk(CLK));  // open: clr
  \硬布线控制器_中断  \u_硬布线控制器_中断_1  (
    .CLK(CLK), .IR(IR), .EQUAL(equal), .M_T({Mif, Mcal, Mex, Mint, T1, T2, T3, T4}), .ControlBus(\EDU控制总线 ),
    .IntSignals(\EDU中断信号 ), .IntR(\中断请求 ));
  // RegisterFile registerfile_1: pin names not known; wires that end beside it: \内部总线 , CLK, \EDU控制总线 [15], \EDU控制总线 [9], registerfile_1_p5, registerfile_1_p6, registerfile_1_p7
  assign bit_extender_1_out = {{16{IR[15]}}, IR[15:0]};  // Bit_Extender bit_extender_1
  assign \内部总线  = \EDU控制总线 [18] ? registerfile_1_p7 : 32'bz;  // Controlled_Buffer controlled_buffer_9
  Multiplexer #(.select(1), .width(5), .disabled("Z"), .enable("false")) multiplexer_1 (
    .in0(IR[25:21]), .in1(IR[20:16]), .out(registerfile_1_p6), .sel(\EDU控制总线 [6]));
  Multiplexer #(.select(1), .width(5), .disabled("Z"), .enable("false")) multiplexer_2 (
    .in0(IR[20:16]), .in1(IR[15:11]), .out(registerfile_1_p5), .sel(\EDU控制总线 [5]));
  Shifter #(.width(32), .shift("ll")) shifter_1 (.in(bit_extender_1_out), .\dist (5'b00010), .out(shifter_1_out));
  D_Flip_Flop #(.trigger("rising"), .Pre_Clr_Positions("LEGACY"), .NegatePresetClear("false"), .enable("true"), .NewFFLayout("false")) d_ff_1 (
    .preset(\EDU中断信号 [0]), .reset(\EDU中断信号 [1]));  // open: clk, D, Q, Qn, en
  Button _1 (.out(_1_out));
  Button _2 (.out(_2_out));
  Comparator #(.width(32), .mode("twosComplement")) comparator_1 (
    .a(IR), .b(32'h1000ffff), .eq(comparator_1_eq));  // open: gt, lt
  Register #(.width(32), .trigger("rising"), .Select("low")) EPC (.clk(CLK));  // open: D, en, Q, clr
  LED #(.active("true")) _1_2 (.in(\中断控制器_1_ir1w ));
  LED #(.active("true")) _2_2 (.in(\中断控制器_1_ir2w ));
  \中断控制器  \u_中断控制器_1  (
    .CLK(CLK), .Key1(_1_out), .Key2(_2_out), .Clr(\EDU中断信号 [1]), .IR1W(\中断控制器_1_ir1w ),
    .IR2W(\中断控制器_1_ir2w ), .EDU_TEST(EduInt));  // open: IR3W, IntNo, IntR, Key3
  Counter #(.width(12), .max('hfff), .ongoal("wrap"), .trigger("falling"), .behavior("new")) counter_1 (
    .count(not_1_out), .Q(Clks), .clk(CLK));  // open: load, D, carry, clr, preset, down
  not not_1 (not_1_out, comparator_1_eq);
  Clock #(.highDuration(1), .lowDuration(1)) clock_1 (.out(CLK));
  Counter #(.width(12), .max('hfff), .ongoal("wrap"), .trigger("falling"), .behavior("old")) counter_2 (
    .count(and_1_out), .Q(\指令数 ), .clk(CLK));  // open: load, D, carry, clr, preset
  and and_1 (and_1_out, not_1_out, Mif, T1);

  // Other names for the same wires on the sheet: rd[4:0] = IR[15:11]; rt[4:0] = IR[20:16]; rs[4:0] = IR[25:21];
  //   中断控制信号[4:0] = \EDU中断信号 ; 关中断 = \EDU中断信号 [0]; 开中断 = \EDU中断信号 [1]; Addrout = \EDU中断信号 [2]; EPCin = \EDU中断信号 [3];
  //   EPCout = \EDU中断信号 [4]; Write = \EDU控制总线 [0]; 控制总线[21:0] = \EDU控制总线 ; READ = \EDU控制总线 [1]; Slt = \EDU控制总线 [2];
  //   Add4 = \EDU控制总线 [3]; Add = \EDU控制总线 [4]; RegDst = \EDU控制总线 [5]; RegTgt = \EDU控制总线 [6]; PSWin = \EDU控制总线 [7];
  //   IRin = \EDU控制总线 [8]; Rin = \EDU控制总线 [9]; Xin = \EDU控制总线 [10]; DRin = \EDU控制总线 [11]; DREin = \EDU控制总线 [12];
  //   ARin = \EDU控制总线 [13]; PCin = \EDU控制总线 [14]; DREout = \EDU控制总线 [15]; IR_A_out = \EDU控制总线 [16];
  //   IR_I_out = \EDU控制总线 [17]; Rout = \EDU控制总线 [18]; Zout = \EDU控制总线 [19]; DRout = \EDU控制总线 [20];
  //   PCout = \EDU控制总线 [21]; 状态节拍信号[7:0] = {Mif, Mcal, Mex, Mint, T1, T2, T3, T4}

  // Notes on the sheet:
  //   单总线结构 MIPS CPU+中断
  //   MEM
  //   外部总线
  //   内部总线
  //   三级时序+中断
  //   Immediate32
  //   AddressOffset32
  //   中断使能寄存器
  //   EPC用于保存断点
  //   执行ERET时开中断，同时清除中断源
  //   中断逻辑
endmodule

// 控制器
module \硬布线控制器_中断  (
  input  CLK,
  input  [31:0] IR,
  input  EQUAL,
  input  IntR,
  output [7:0] M_T,
  output [21:0] ControlBus,
  output [4:0] IntSignals
);

  wire ADDI, BEQ, ERET, IntSignalsController_pcin, IntSignalsController_pcout, LW, PCin1, PCout1;
  wire [3:0] undriven;
  wire [12:9] OCInput;

  // 时序发生器状态机_中断 时序发生器状态机_中断_1: pin names not known; wires that end beside it: ADDI, OCInput[12]
  Register #(.width(4), .trigger("rising"), .Select("low")) register_1 ();  // open: D, en, Q, clk, clr
  \时序发生器输出函数_中断  \u_时序发生器输出函数_中断_1  (
    .S3(undriven[3]), .S2(undriven[2]), .S1(undriven[1]), .S0(undriven[0]), .Mif(M_T[7]), .Mcal(M_T[6]),
    .Mex(M_T[5]), .Mint(M_T[4]), .T1(M_T[3]), .T2(M_T[2]), .T3(M_T[1]), .T4(M_T[0]));
  \中断信号控制器  IntSignalsController (
    .ERET(ERET), .Mex(M_T[5]), .Mint(M_T[4]), .T1(M_T[3]), .T2(M_T[2]), .Pcout(IntSignalsController_pcout),
    .PCin(IntSignalsController_pcin), .EPCout(IntSignals[4]), .EPCin(IntSignals[3]), .Addrout(IntSignals[2]),
    .STI(IntSignals[1]), .CLI(IntSignals[0]));
  \指令译码器  \u_指令译码器_1  (.IR(IR), .LW(LW), .SW(OCInput[9]), .BEQ(BEQ), .ADDI(ADDI), .SLT(OCInput[12]), .OtherInstr(ERET));
  or or_1 (ControlBus[21], PCout1, IntSignalsController_pcout);
  or or_2 (ControlBus[14], IntSignalsController_pcin, PCin1);
  \硬布线控制器组合逻辑单元  \u_硬布线控制器组合逻辑单元_1  (
    .SLT(OCInput[12]), .ADDI(ADDI), .LW(LW), .SW(OCInput[9]), .BEQ(BEQ), .Mif(M_T[7]), .Mcal(M_T[6]),
    .Mex(M_T[5]), .T1(M_T[3]), .T2(M_T[2]), .T3(M_T[1]), .T4(M_T[0]), .EQUAL(EQUAL), .Pcout(PCout1),
    .DRout(ControlBus[20]), .Zout(ControlBus[19]), .Rout(ControlBus[18]), .IRiout(ControlBus[17]),
    .IRaout(ControlBus[16]), .DREout(ControlBus[15]), .Pcin(PCin1), .ARin(ControlBus[13]),
    .DREin(ControlBus[12]), .DRin(ControlBus[11]), .Xin(ControlBus[10]), .Rin(ControlBus[9]),
    .IRin(ControlBus[8]), .PSWin(ControlBus[7]), .RegTgt(ControlBus[6]), .RegDst(ControlBus[5]),
    .Add(ControlBus[4]), .Add4(ControlBus[3]), .Slt_2(ControlBus[2]), .READ(ControlBus[1]),
    .WRITE(ControlBus[0]));

  // Other names for the same wires on the sheet: PCin = ControlBus[14]; PCout = ControlBus[21]; Mint = M_T[4];
  //   OCInput (some bits) = {ADDI, LW, BEQ, M_T[7:5], M_T[3:0], EQUAL}; T4 = M_T[0]; T3 = M_T[1]; T2 = M_T[2];
  //   T1 = M_T[3]; Mex = M_T[5]; Mcal = M_T[6]; Mif = M_T[7]; SW = OCInput[9]; SLT = OCInput[12]; 指令字[31:0] = IR

  // Notes on the sheet:
  //   现态
  //   次态
  //   状态机
  //   中断控制相关信号生成逻辑
  //   不要改变此引脚区域内容，也不要改变封装形式
  //   指令译码信号
  //   状态寄存器
  //   状态寄存器应该下跳沿？
  //   状态寄存器应该下跳沿？
  //   FSM状态机
  //   输入输出引脚
  //   时序产生器TG
  //   指令译码器
  //   注意：IntSignals中的信号和上面的硬布线控制器组合逻辑单元无关，相关信号要合并处理
  //   指令译码信号
  //   指令译码逻辑ID
  //   操作控制器OC
endmodule

// 状态机
module \时序发生器状态机_中断  (
  input  ERET,
  input  LW,
  input  SW,
  input  BEQ,
  input  SLT,
  input  ADDI,
  input  IntR,
  input  S3,
  input  S2,
  input  S1,
  input  S0,
  output N3,
  output N2,
  output N1,
  output N0
);
endmodule

module \时序发生器输出函数_中断  (
  input  S3,
  input  S2,
  input  S1,
  input  S0,
  output Mif,
  output Mcal,
  output Mex,
  output Mint,
  output T1,
  output T2,
  output T3,
  output T4
);
endmodule

module \中断信号控制器  (
  input  ERET,
  input  Mex,
  input  Mint,
  input  T1,
  input  T2,
  output Pcout,
  output PCin,
  output EPCout,
  output EPCin,
  output Addrout,
  output STI,
  output CLI
);


  // Notes on the sheet:
  //   直接使用逻辑表达式生成，手写逻辑表达式
endmodule

// ALU
module MIPS_ALU (
  input  ADD,
  input  ADD4,
  input  [31:0] X,
  input  [31:0] Y,
  input  SUB,
  input  SLT,
  output Equal,
  output [31:0] Result
);

  wire [0:0] comparator_1_lt;
  wire [1:0] priority_encoder_1_out;
  wire [31:0] adder_1_out, adder_2_out, subtractor_1_out;

  Pull_Resistor #(.pull(0)) pull_resistor_1 (.node(Y));
  Adder #(.width(32)) adder_1 (.a(X), .b(Y), .out(adder_1_out));  // open: cin, cout
  Adder #(.width(32)) adder_2 (.a(X), .b(32'h4), .out(adder_2_out));  // open: cin, cout
  Subtractor #(.width(32)) subtractor_1 (.a(X), .b(Y), .out(subtractor_1_out));  // open: bin, bout
  Comparator #(.width(32), .mode("twosComplement")) comparator_1 (
    .a(X), .b(Y), .eq(Equal), .lt(comparator_1_lt[0]));  // open: gt
  Priority_Encoder #(.select(2), .disabled("Z")) priority_encoder_1 (
    .in0(ADD), .in1(ADD4), .in2(SUB), .in3(SLT), .out(priority_encoder_1_out));  // open: gs, en_out, en_in
  Pull_Resistor #(.pull(0)) pull_resistor_2 (.node(priority_encoder_1_out));
  Multiplexer #(.select(2), .width(32), .disabled("Z"), .enable("false")) multiplexer_1 (
    .in0(adder_1_out), .in1(adder_2_out), .in2(subtractor_1_out), .in3({{31{1'b0}}, comparator_1_lt[0]}),
    .out(Result), .sel(priority_encoder_1_out));

  // Notes on the sheet:
  //   不要改变此引脚区域内容，也不要改变ALU封装形式
  //   输入引脚
  //   输出引脚
endmodule

// 中断控制器
module \中断控制器  (
  input  CLK,
  input  Key1,
  input  Key2,
  input  Key3,
  input  Clr,
  input  [1:0] EDU_TEST,
  output IR1W,
  output IR2W,
  output IR3W,
  output [1:0] IntNo,
  output IntR
);

  wire and_1_out, and_2_out, and_3_out, Clr0, Clr1, Clr2, Clr3, d_ff_1_q, d_ff_2_q, d_ff_3_q, IR1_q, IR2_q,
       IR3_q, or_1_out, or_3_out, or_6_out, or_7_out, or_8_out;

  or or_1 (or_1_out, Key1, EDU_TEST[0]);
  or or_2 (IR1W, IR1_q, d_ff_2_q);
  or or_3 (or_3_out, Key2, EDU_TEST[1]);
  or or_4 (IR2W, IR2_q, d_ff_3_q);
  D_Flip_Flop #(.trigger("rising"), .Pre_Clr_Positions("LEGACY"), .NegatePresetClear("false"), .enable("true"), .NewFFLayout("false")) d_ff_1 (
    .clk(Key3), .D(1'b1), .Q(d_ff_1_q), .reset(IR3_q));  // open: Qn, preset, en
  or or_5 (IR3W, IR3_q, d_ff_1_q);
  D_Flip_Flop #(.trigger("rising"), .Pre_Clr_Positions("LEGACY"), .NegatePresetClear("false"), .enable("true"), .NewFFLayout("false")) d_ff_2 (
    .clk(or_1_out), .D(1'b1), .Q(d_ff_2_q), .reset(IR1_q));  // open: Qn, preset, en
  D_Flip_Flop #(.trigger("rising"), .Pre_Clr_Positions("LEGACY"), .NegatePresetClear("false"), .enable("true"), .NewFFLayout("false")) d_ff_3 (
    .clk(or_3_out), .D(1'b1), .Q(d_ff_3_q), .reset(IR2_q));  // open: Qn, preset, en
  or or_6 (or_6_out, d_ff_2_q, IR1_q);
  and and_1 (and_1_out, or_6_out, ~Clr1);  // AND_Gate
  or or_7 (or_7_out, d_ff_3_q, IR2_q);
  and and_2 (and_2_out, or_7_out, ~Clr2);  // AND_Gate
  or or_8 (or_8_out, d_ff_1_q, IR3_q);
  and and_3 (and_3_out, or_8_out, ~Clr3);  // AND_Gate
  Pull_Resistor #(.pull(0)) pull_resistor_1 (.node(EDU_TEST));
  D_Flip_Flop #(.trigger("rising"), .Pre_Clr_Positions("LEGACY"), .NegatePresetClear("false"), .enable("true"), .NewFFLayout("false")) IR1 (
    .clk(CLK), .D(and_1_out), .Q(IR1_q));  // open: Qn, preset, en, reset
  D_Flip_Flop #(.trigger("rising"), .Pre_Clr_Positions("LEGACY"), .NegatePresetClear("false"), .enable("true"), .NewFFLayout("false")) IR2 (
    .clk(CLK), .D(and_2_out), .Q(IR2_q));  // open: Qn, preset, en, reset
  D_Flip_Flop #(.trigger("rising"), .Pre_Clr_Positions("LEGACY"), .NegatePresetClear("false"), .enable("true"), .NewFFLayout("false")) IR3 (
    .clk(CLK), .D(and_3_out), .Q(IR3_q));  // open: Qn, preset, en, reset
  Priority_Encoder #(.select(2), .disabled("Z")) priority_encoder_1 (
    .in1(IR1_q), .in2(IR2_q), .in3(IR3_q), .out(IntNo), .gs(IntR));  // open: in0, en_out, en_in
  Decoder #(.select(2), .tristate("false"), .disabled(0), .enable("true")) decoder_1 (
    .out0(Clr0), .out1(Clr1), .out2(Clr2), .out3(Clr3), .sel(IntNo), .en(Clr));

  // Other names for the same wires on the sheet: EDU_INT1 = EDU_TEST[0]; EDU_INT2 = EDU_TEST[1]

  // Notes on the sheet:
  //   中断等待
  //   中断等待
  //   中断等待
  //   中断信号采样参考电路
  //   Reset 
  //   Reset 
  //   Reset 
  //   中断优先编码器
endmodule
