// Logisim project 数独.circ as structural Verilog: 15 circuits, main circuit 游戏界面
module \游戏界面  (
);

  wire CLK, or_1_out, RST, \成功 , \新游戏 , \游戏就绪 ;
  wire [3:0] \X坐标 , \Y坐标 ;
  wire [6:0] ASCII, X1, X2, X3, X4, X5, X6, X7, X8, X9, Y1, Y2, Y3, Y4, Y5, Y6, Y7, Y8, Y9;
  wire [15:0] C1, C2, C3, C4, C5, C6, C7, C8, C9;

  // LCD_Video lcd_video_1: pin names not known; wires that end beside it: RST, CLK, 1'b1, X1, Y1, C1, RST, CLK, 1'b1, X2
  // LCD_Video lcd_video_2: pin names not known; wires that end beside it: RST, CLK, 1'b1, X4, Y4, C4, RST, CLK, 1'b1, X5
  // LCD_Video lcd_video_3: pin names not known; wires that end beside it: RST, CLK, 1'b1, X7, Y7, C7, RST, CLK, 1'b1, X8
  // LCD_Video lcd_video_4: pin names not known; wires that end beside it: Y2, C2, RST, CLK, 1'b1, X3
  // LCD_Video lcd_video_5: pin names not known; wires that end beside it: Y5, C5, RST, CLK, 1'b1, X6
  // LCD_Video lcd_video_6: pin names not known; wires that end beside it: Y8, C8, RST, CLK, 1'b1, X9
  // LCD_Video lcd_video_7: pin names not known; wires that end beside it: Y3, C3
  // LCD_Video lcd_video_8: pin names not known; wires that end beside it: Y6, C6
  // LCD_Video lcd_video_9: pin names not known; wires that end beside it: Y9, C9
  Clock #(.highDuration(1), .lowDuration(1)) clock_1 (.out(CLK));
  Hex_Digit_Display hex_digit_display_1 (.value(\X坐标 ));  // open: dp
  Button button_1 (.out(\新游戏 ));
  Hex_Digit_Display hex_digit_display_2 (.value(\Y坐标 ));  // open: dp
  Button button_2 (.out(RST));
  LED #(.active("true")) led_1 (.in(\游戏就绪 ));
  Keyboard #(.Char_bit_width(7), .buflen(12), .trigger("rising")) keyboard_1 (
    .clk(CLK), .re(\游戏就绪 ), .clr(or_1_out), .data(ASCII));  // open: avail
  or or_1 (or_1_out, RST, ~\游戏就绪 );  // OR_Gate
  \主要逻辑  \u_主要逻辑_1  (
    .\新游戏 (\新游戏 ), .CLK(CLK), .RST(RST), .\键盘输入 (ASCII), .X1(X1), .Y1(Y1), .X2(X2), .Y2(Y2), .X3(X3),
    .Y3(Y3), .X4(X4), .Y4(Y4), .X5(X5), .Y5(Y5), .X6(X6), .Y6(Y6), .X7(X7), .Y7(Y7), .X8(X8), .Y8(Y8),
    .X9(X9), .Y9(Y9), .C1(C1), .C2(C2), .C3(C3), .C4(C4), .C5(C5), .C6(C6), .C7(C7), .C8(C8), .C9(C9),
    .\输出完成 (\游戏就绪 ), .\当前X坐标 (\X坐标 ), .\当前Y坐标 (\Y坐标 ), .\完成数独 (\成功 ));
  LED #(.active("true")) led_2 (.in(\成功 ));

  // Notes on the sheet:
  //   1
  //   2
  //   3
  //   4
  //   5
  //   6
  //   7
  //   8
  //   9
  //   1
  //   2
  //   3
  //   4
  //   数独游戏
  //   5
  //   6
  //   7
  //   8
  //   9
  //   当前X坐标
  //   当前Y坐标
  //   玩法说明
  //   1.开始游戏前请打开时钟，建议设置时钟频率为最高频率
  //   2.点击新游戏可以切换数独初盘，等待游戏就绪后方可进行游戏
  //   3.请不要进行电路复位，否则会导致无法切换数独初盘
  //   4.如果不慎复位，请在上方"主要逻辑"电路中的"CPU"电路中向RAM中加载数据
  //   5.横轴为X坐标，纵轴为Y坐标，使用手型工具点击键盘以从键盘输入
  //   6.数独初盘数字为白色，玩家填入数字为绿色
  //   7.使用WASD键调整当前坐标，使用0-9输入数字，输入数字0以清除所填内容
  //   8.获取焦点后使用0-9输入数字，输入数字0以清除所填内容
  //   9.填满数独并且正确后会提示成功，蜂鸣器将响起一段时间
  //   请使用手型工具点击以输入
endmodule

// 主要逻辑
module \主要逻辑  (
  input  \新游戏 ,
  input  CLK,
  input  RST,
  input  [6:0] \键盘输入 ,
  output \完成数独 ,
  output [6:0] X1,
  output [6:0] Y1,
  output [15:0] C1,
  output [6:0] X2,
  output [6:0] Y2,
  output [15:0] C2,
  output [6:0] X3,
  output [6:0] Y3,
  output [15:0] C3,
  output [6:0] X4,
  output [6:0] Y4,
  output [15:0] C4,
  output [6:0] X5,
  output [6:0] Y5,
  output [15:0] C5,
  output [6:0] X6,
  output [6:0] Y6,
  output [15:0] C6,
  output [3:0] \当前X坐标 ,
  output [6:0] X7,
  output \输出完成 ,
  output [6:0] Y7,
  output [3:0] \当前Y坐标 ,
  output [15:0] C7,
  output [6:0] X8,
  output [6:0] Y8,
  output [15:0] C8,
  output [6:0] X9,
  output [6:0] Y9,
  output [15:0] C9
);

  wire and_1_out, and_3_out, and_4_out, and_5_out, and_6_out, and_7_out, and_8_out, counter_1_carry, Down,
       Left, multiplexer_1_out, not_1_out, not_2_out, not_3_out, not_4_out, Num0, Num1, Num2, Num3, Num4,
       Num5, Num6, Num7, Num8, Num9, or_1_out, or_3_out, or_4_out, or_5_out, or_6_out, or_7_out, Right, Up,
       Y_1, Y_1_t, \初始化完毕 , \初盘已满 , \固有格局 , \当前寄存器_1_更改1 , \当前寄存器_1_更改2 , \当前寄存器_1_更改3 , \当前寄存器_1_更改4 ,
       \当前寄存器_1_更改5 , \当前寄存器_1_更改6 , \当前寄存器_1_更改7 , \当前寄存器_1_更改8 , \当前寄存器_1_更改9 , \当前寄存器_1_选中1 ,
       \当前寄存器_1_选中2 , \当前寄存器_1_选中3 , \当前寄存器_1_选中4 , \当前寄存器_1_选中5 , \当前寄存器_1_选中6 , \当前寄存器_1_选中7 ,
       \当前寄存器_1_选中8 , \当前寄存器_1_选中9 , \按下按键 , \按下数字 , \数据产生 , \终盘已满 , \输出完成1 , \输出完成2 , \输出完成3 , \输出完成4 ,
       \输出完成5 , \输出完成6 , \输出完成7 , \输出完成8 , \输出完成9 ;
  wire [3:0] A1, A2, A3, A4, A5, A6, A7, A8, A9, adder_1_out, B1, B2, B3, B4, B5, B6, B7, B8, B9, C1_t, C2_t,
       C3_t, C4_t, C5_t, C6_t, C7_t, C8_t, C9_t, D1, D2, D3, D4, D5, D6, D7, D8, D9, E1, E2, E3, E4, E5, E6,
       E7, E8, E9, F1, F2, F3, F4, F5, F6, F7, F8, F9, G1, G2, G3, G4, G5, G6, G7, G8, G9, H1, H2, H3, H4,
       H5, H6, H7, H8, H9, I1, I2, I3, I4, I5, I6, I7, I8, I9, multiplexer_2_out, multiplexer_3_out,
       multiplexer_4_out, multiplexer_5_out, multiplexer_6_out, multiplexer_7_out, NextDown, NextLeft,
       NextRight, NextUp, subtractor_2_out, \初始数据 , \宫格内序号 , \数字序号 , \首空X坐标 , \首空Y坐标 ;
  wire [31:0] \单周期cpu_1_leddata ;
  wire [31:4] subtractor_1_out;

  or or_1 (or_1_out, RST, \新游戏 );
  and and_1 (and_1_out, \完成数独 , \输出完成 );
  \单周期CPU  \u_单周期cpu_1  (.LedData(\单周期cpu_1_leddata ), .CLK(CLK), .\数据产生 (\数据产生 ), .RST(or_1_out), .\新游戏 (\新游戏 ));
  \键盘处理  \u_键盘处理_1  (
    .\键盘输入 (\键盘输入 ), .CLK(CLK), .RST(RST), .Up(Up), .Down(Down), .Left(Left), .Right(Right), .Num_1(Num1),
    .Num_2(Num2), .Num_3(Num3), .Num_4(Num4), .Num_5(Num5), .Num_6(Num6), .Num_7(Num7), .Num_8(Num8),
    .Num_9(Num9), .Num_0(Num0));  // open: Enter
  and and_2 (\输出完成 , \输出完成1 , \输出完成2 , \输出完成3 , \输出完成4 , \输出完成5 , \输出完成6 , \输出完成7 , \输出完成8 , \输出完成9 );
  or or_2 (\按下按键 , \按下数字 , Left, Right, Up, Down);
  Counter #(.width(20), .max('hff), .ongoal("stay"), .trigger("rising"), .behavior("new")) counter_1 (
    .count(and_1_out), .carry(counter_1_carry), .clk(CLK), .clr(RST));  // open: load, D, Q, preset, down
  Hex_Digit_Display hex_digit_display_1 (.value(\初始数据 ));  // open: dp
  Subtractor #(.width(32)) subtractor_1 (
    .a(\单周期cpu_1_leddata ), .b(32'h30), .out({subtractor_1_out, \初始数据 }));  // open: bin, bout
  Priority_Encoder #(.select(4), .disabled("Z")) priority_encoder_1 (
    .in0(Num0), .in1(Num1), .in2(Num2), .in3(Num3), .in4(Num4), .in5(Num5), .in6(Num6), .in7(Num7),
    .in8(Num8), .in9(Num9), .out(\数字序号 ), .gs(\按下数字 ));  // open: in10, in11, in12, in13, in14, in15, en_out, en_in
  and and_3 (and_3_out, \完成数独 , not_1_out);
  not not_1 (not_1_out, counter_1_carry);
  // Buzzer #(.freq_measure("Hz"), .vol_width(7)) buzzer_1: pin names not known; wires that end beside it: 14'hff, and_3_out, 7'b1000000
  Multiplexer #(.select(1), .width(1), .disabled("Z"), .enable("false")) multiplexer_1 (
    .in0(\数据产生 ), .in1(CLK), .out(multiplexer_1_out), .sel(\初盘已满 ));
  or or_3 (or_3_out, \新游戏 , RST);
  not not_2 (not_2_out, \初盘已满 );
  \当前寄存器  \u_当前寄存器_1  (
    .CLK(multiplexer_1_out), .RST(or_3_out), .\写入使能 (not_2_out), .\写入数据 (\初始数据 ), .A_2(A2), .A_3(A3),
    .A_4(A4), .A_5(A5), .A_6(A6), .A_7(A7), .A_8(A8), .A_9(A9), .B_1(B1), .B_2(B2), .B_3(B3), .B_4(B4),
    .B_5(B5), .B_6(B6), .B_7(B7), .B_8(B8), .B_9(B9), .C_1(C1_t), .C_2(C2_t), .C_3(C3_t), .C_4(C4_t),
    .C_5(C5_t), .C_6(C6_t), .C_7(C7_t), .C_8(C8_t), .C_9(C9_t), .D_1(D1), .D_2(D2), .D_3(D3), .D_4(D4),
    .D_5(D5), .D_6(D6), .D_7(D7), .D_8(D8), .D_9(D9), .E_1(E1), .E_2(E2), .E_3(E3), .E_4(E4), .E_5(E5),
    .E_6(E6), .E_7(E7), .E_8(E8), .E_9(E9), .F_1(F1), .F_2(F2), .F_3(F3), .F_4(F4), .F_5(F5), .F_6(F6),
    .F_7(F7), .F_8(F8), .F_9(F9), .G_1(G1), .G_2(G2), .G_3(G3), .G_4(G4), .G_5(G5), .G_6(G6), .G_7(G7),
    .G_8(G8), .G_9(G9), .H_1(H1), .H_2(H2), .H_3(H3), .H_4(H4), .H_5(H5), .H_6(H6), .H_7(H7), .H_8(H8),
    .H_9(H9), .I_1(I1), .I_2(I2), .I_3(I3), .I_4(I4), .I_5(I5), .I_6(I6), .I_7(I7), .I_8(I8), .I_9(I9),
    .A_1(A1), .\计数已满 (\初盘已满 ), .\X坐标 (\当前X坐标 ), .\Y坐标 (\当前Y坐标 ), .\更改使能 (\按下数字 ), .\更改数据 (\数字序号 ),
    .\选中1 (\当前寄存器_1_选中1 ), .\选中2 (\当前寄存器_1_选中2 ), .\选中3 (\当前寄存器_1_选中3 ), .\选中5 (\当前寄存器_1_选中5 ),
    .\选中7 (\当前寄存器_1_选中7 ), .\选中9 (\当前寄存器_1_选中9 ), .\选中6 (\当前寄存器_1_选中6 ), .\选中8 (\当前寄存器_1_选中8 ),
    .\选中4 (\当前寄存器_1_选中4 ), .\宫格内序号 (\宫格内序号 ), .\固有格局 (\固有格局 ), .\初始化完毕 (\初始化完毕 ), .\更改1 (\当前寄存器_1_更改1 ),
    .\更改4 (\当前寄存器_1_更改4 ), .\更改7 (\当前寄存器_1_更改7 ), .\更改2 (\当前寄存器_1_更改2 ), .\更改5 (\当前寄存器_1_更改5 ),
    .\更改8 (\当前寄存器_1_更改8 ), .\更改3 (\当前寄存器_1_更改3 ), .\更改6 (\当前寄存器_1_更改6 ), .\更改9 (\当前寄存器_1_更改9 ));
  \LCD数据源  \lcd数据源_1  (
    ._1(A1), ._4(B1), ._7(C1_t), .CLK(CLK), ._2(A2), ._5(B2), ._8(C2_t), ._3(A3), ._6(B3), ._9(C3_t),
    .\使能 (\初盘已满 ), .X(X1), .Y(Y1), .RST(RST), .\选中宫格序号 (\宫格内序号 ), .\选中 (\当前寄存器_1_选中1 ), .\输出完成 (\输出完成1 ),
    .\更改信号 (\当前寄存器_1_更改1 ), .\颜色 (C1), .\清除更改使能 (\按下按键 ));
  \LCD数据源  \lcd数据源_2  (
    ._1(A4), ._4(B4), ._7(C4_t), .CLK(CLK), ._2(A5), ._5(B5), ._8(C5_t), ._3(A6), ._6(B6), ._9(C6_t),
    .\使能 (\初盘已满 ), .X(X2), .Y(Y2), .RST(RST), .\选中宫格序号 (\宫格内序号 ), .\选中 (\当前寄存器_1_选中2 ), .\输出完成 (\输出完成2 ),
    .\更改信号 (\当前寄存器_1_更改2 ), .\颜色 (C2), .\清除更改使能 (\按下按键 ));
  \LCD数据源  \lcd数据源_3  (
    ._1(A7), ._4(B7), ._7(C7_t), .CLK(CLK), ._2(A8), ._5(B8), ._8(C8_t), ._3(A9), ._6(B9), ._9(C9_t),
    .\使能 (\初盘已满 ), .X(X3), .Y(Y3), .RST(RST), .\选中宫格序号 (\宫格内序号 ), .\选中 (\当前寄存器_1_选中3 ), .\输出完成 (\输出完成3 ),
    .\更改信号 (\当前寄存器_1_更改3 ), .\颜色 (C3), .\清除更改使能 (\按下按键 ));
  \LCD数据源  \lcd数据源_4  (
    ._1(D1), ._4(E1), ._7(F1), .CLK(CLK), ._2(D2), ._5(E2), ._8(F2), ._3(D3), ._6(E3), ._9(F3),
    .\使能 (\初盘已满 ), .X(X4), .Y(Y4), .RST(RST), .\选中宫格序号 (\宫格内序号 ), .\选中 (\当前寄存器_1_选中4 ), .\输出完成 (\输出完成4 ),
    .\更改信号 (\当前寄存器_1_更改4 ), .\颜色 (C4), .\清除更改使能 (\按下按键 ));
  \LCD数据源  \lcd数据源_5  (
    ._1(D4), ._4(E4), ._7(F4), .CLK(CLK), ._2(D5), ._5(E5), ._8(F5), ._3(D6), ._6(E6), ._9(F6),
    .\使能 (\初盘已满 ), .X(X5), .Y(Y5), .RST(RST), .\选中宫格序号 (\宫格内序号 ), .\选中 (\当前寄存器_1_选中5 ), .\输出完成 (\输出完成5 ),
    .\更改信号 (\当前寄存器_1_更改5 ), .\颜色 (C5), .\清除更改使能 (\按下按键 ));
  \LCD数据源  \lcd数据源_6  (
    ._1(D7), ._4(E7), ._7(F7), .CLK(CLK), ._2(D8), ._5(E8), ._8(F8), ._3(D9), ._6(E9), ._9(F9),
    .\使能 (\初盘已满 ), .X(X6), .Y(Y6), .RST(RST), .\选中宫格序号 (\宫格内序号 ), .\选中 (\当前寄存器_1_选中6 ), .\输出完成 (\输出完成6 ),
    .\更改信号 (\当前寄存器_1_更改6 ), .\颜色 (C6), .\清除更改使能 (\按下按键 ));
  \LCD数据源  \lcd数据源_7  (
    ._1(G1), ._4(H1), ._7(I1), .CLK(CLK), ._2(G2), ._5(H2), ._8(I2), ._3(G3), ._6(H3), ._9(I3),
    .\使能 (\初盘已满 ), .X(X7), .Y(Y7), .RST(RST), .\选中宫格序号 (\宫格内序号 ), .\选中 (\当前寄存器_1_选中7 ), .\输出完成 (\输出完成7 ),
    .\更改信号 (\当前寄存器_1_更改7 ), .\颜色 (C7), .\清除更改使能 (\按下按键 ));
  \LCD数据源  \lcd数据源_8  (
    ._1(G4), ._4(H4), ._7(I4), .CLK(CLK), ._2(G5), ._5(H5), ._8(I5), ._3(G6), ._6(H6), ._9(I6),
    .\使能 (\初盘已满 ), .X(X8), .Y(Y8), .RST(RST), .\选中宫格序号 (\宫格内序号 ), .\选中 (\当前寄存器_1_选中8 ), .\输出完成 (\输出完成8 ),
    .\更改信号 (\当前寄存器_1_更改8 ), .\颜色 (C8), .\清除更改使能 (\按下按键 ));
  \LCD数据源  \lcd数据源_9  (
    ._1(G7), ._4(H7), ._7(I7), .CLK(CLK), ._2(G8), ._5(H8), ._8(I8), ._3(G9), ._6(H9), ._9(I9),
    .\使能 (\初盘已满 ), .X(X9), .Y(Y9), .RST(RST), .\选中宫格序号 (\宫格内序号 ), .\选中 (\当前寄存器_1_选中9 ), .\输出完成 (\输出完成9 ),
    .\更改信号 (\当前寄存器_1_更改9 ), .\颜色 (C9), .\清除更改使能 (\按下按键 ));
  Multiplexer #(.select(1), .width(4), .disabled("Z"), .enable("false")) multiplexer_2 (
    .in0(NextUp), .in1(NextDown), .out(multiplexer_2_out), .sel(Down));
  or or_4 (or_4_out, \新游戏 , RST);
  not not_3 (not_3_out, \初盘已满 );
  Multiplexer #(.select(1), .width(4), .disabled("Z"), .enable("false")) multiplexer_3 (
    .in0(NextRight), .in1(NextLeft), .out(multiplexer_3_out), .sel(Left));
  and and_4 (and_4_out, Y_1_t, \初盘已满 , Left);
  and and_5 (and_5_out, Y_1, \初盘已满 , Right);
  \初盘寄存器  \u_初盘寄存器_1  (
    .CLK(\数据产生 ), .RST(or_4_out), .\写入使能 (not_3_out), .\X坐标 (\当前X坐标 ), .\Y坐标 (\当前Y坐标 ), .\固有坐标 (\固有格局 ),
    .\数据 (\初始数据 ), .NextRight(NextRight), .NextLeft(NextLeft), .NextUp(NextUp), .NextDown(NextDown),
    .\首个空格X坐标 (\首空X坐标 ), .\首个空格Y坐标 (\首空Y坐标 ), .\跳转到上一行 (Y_1_t), .\跳转到下一行 (Y_1));
  Multiplexer #(.select(1), .width(4), .disabled("Z"), .enable("false")) multiplexer_4 (
    .in0(multiplexer_3_out), .in1(\首空X坐标 ), .out(multiplexer_4_out), .sel(\初始化完毕 ));
  or or_5 (or_5_out, Left, \初始化完毕 , Right);
  and and_6 (and_6_out, Y_1, \初盘已满 );
  Multiplexer #(.select(1), .width(4), .disabled("Z"), .enable("false")) multiplexer_5 (
    .in0(multiplexer_2_out), .in1(\首空Y坐标 ), .out(multiplexer_5_out), .sel(\初始化完毕 ));
  Multiplexer #(.select(1), .width(4), .disabled("Z"), .enable("false")) multiplexer_6 (
    .in0(multiplexer_5_out), .in1(adder_1_out), .out(multiplexer_6_out), .sel(and_6_out));
  Adder #(.width(4)) adder_1 (.a(\当前Y坐标 ), .b(4'b0001), .out(adder_1_out));  // open: cin, cout
  Register #(.width(4), .trigger("falling"), .Select("low")) \Y坐标  (
    .D(multiplexer_7_out), .Q(\当前Y坐标 ), .clk(or_6_out), .clr(RST));  // open: en
  or or_6 (or_6_out, and_4_out, Up, \初始化完毕 , Down, and_5_out);
  Register #(.width(4), .trigger("falling"), .Select("low")) \X坐标  (
    .D(multiplexer_4_out), .Q(\当前X坐标 ), .clk(or_5_out), .clr(RST));  // open: en
  and and_7 (and_7_out, Y_1_t, \初盘已满 );
  Subtractor #(.width(4)) subtractor_2 (.a(\当前Y坐标 ), .b(4'b0001), .out(subtractor_2_out));  // open: bin, bout
  Multiplexer #(.select(1), .width(4), .disabled("Z"), .enable("false")) multiplexer_7 (
    .in0(multiplexer_6_out), .in1(subtractor_2_out), .out(multiplexer_7_out), .sel(and_7_out));
  not not_4 (not_4_out, \终盘已满 );
  or or_7 (or_7_out, \新游戏 , RST);
  and and_8 (and_8_out, \初盘已满 , not_4_out);
  \终盘寄存器  \u_终盘寄存器_1  (
    .CLK(\数据产生 ), .RST(or_7_out), .\使能 (and_8_out), .\数据 (\初始数据 ), .\计数已满 (\终盘已满 ), .A1(A1), .B1(B1),
    .C1(C1_t), .D1(D1), .E1(E1), .F1(F1), .G1(G1), .H1(H1), .I1(I1), .A2(A2), .B2(B2), .C2(C2_t), .D2(D2),
    .E2(E2), .F2(F2), .G2(G2), .H2(H2), .I2(I2), .A3(A3), .B3(B3), .C3(C3_t), .D3(D3), .E3(E3), .F3(F3),
    .G3(G3), .H3(H3), .I3(I3), .A4(A4), .B4(B4), .C4(C4_t), .D4(D4), .E4(E4), .F4(F4), .G4(G4), .H4(H4),
    .I4(I4), .A5(A5), .B5(B5), .C5(C5_t), .D5(D5), .E5(E5), .F5(F5), .G5(G5), .H5(H5), .I5(I5), .A6(A6),
    .B6(B6), .C6(C6_t), .D6(D6), .E6(E6), .F6(F6), .G6(G6), .H6(H6), .I6(I6), .A7(A7), .B7(B7), .C7(C7_t),
    .D7(D7), .E7(E7), .F7(F7), .G7(G7), .H7(H7), .I7(I7), .A8(A8), .B8(B8), .C8(C8_t), .D8(D8), .E8(E8),
    .F8(F8), .G8(G8), .H8(H8), .I8(I8), .A9(A9), .B9(B9), .C9(C9_t), .D9(D9), .E9(E9), .F9(F9), .G9(G9),
    .H9(H9), .I9(I9), .\完成数独 (\完成数独 ));

  // Other names for the same wires on the sheet: X坐标[3:0] = \当前X坐标 ; Y坐标[3:0] = \当前Y坐标 
endmodule

// 键盘处理
module \键盘处理  (
  input  [6:0] \键盘输入 ,
  input  CLK,
  input  RST,
  output Up,
  output Down,
  output Left,
  output Right,
  output Num_1,
  output Num_2,
  output Num_3,
  output Num_4,
  output Num_5,
  output Num_6,
  output Num_7,
  output Num_8,
  output Num_9,
  output Num_0,
  output Enter
);

  wire comparator_1_eq, comparator_2_eq, comparator_3_eq, comparator_4_eq, comparator_5_eq, comparator_6_eq,
       comparator_7_eq, comparator_8_eq, comparator_9_eq, comparator_10_eq, comparator_11_eq,
       comparator_12_eq, comparator_13_eq, comparator_14_eq, comparator_15_eq, comparator_16_eq,
       comparator_17_eq, comparator_18_eq, comparator_19_eq, comparator_20_eq, comparator_21_eq,
       comparator_22_eq, comparator_23_eq, or_1_out, or_2_out, or_3_out, or_4_out;

  Comparator #(.width(7), .mode("twosComplement")) comparator_1 (
    .a(\键盘输入 ), .b(7'b1110111), .eq(comparator_1_eq));  // open: gt, lt
  Comparator #(.width(7), .mode("twosComplement")) comparator_2 (
    .a(\键盘输入 ), .b(7'b1010111), .eq(comparator_2_eq));  // open: gt, lt
  Comparator #(.width(7), .mode("twosComplement")) comparator_3 (
    .a(\键盘输入 ), .b(7'b0100110), .eq(comparator_3_eq));  // open: gt, lt
  Comparator #(.width(7), .mode("twosComplement")) comparator_4 (
    .a(\键盘输入 ), .b(7'b1110011), .eq(comparator_4_eq));  // open: gt, lt
  Comparator #(.width(7), .mode("twosComplement")) comparator_5 (
    .a(\键盘输入 ), .b(7'b1010011), .eq(comparator_5_eq));  // open: gt, lt
  Comparator #(.width(7), .mode("twosComplement")) comparator_6 (
    .a(\键盘输入 ), .b(7'b0101000), .eq(comparator_6_eq));  // open: gt, lt
  Comparator #(.width(7), .mode("twosComplement")) comparator_7 (
    .a(\键盘输入 ), .b(7'b1100001), .eq(comparator_7_eq));  // open: gt, lt
  Comparator #(.width(7), .mode("twosComplement")) comparator_8 (
    .a(\键盘输入 ), .b(7'b1000001), .eq(comparator_8_eq));  // open: gt, lt
  Comparator #(.width(7), .mode("twosComplement")) comparator_9 (
    .a(\键盘输入 ), .b(7'b0100101), .eq(comparator_9_eq));  // open: gt, lt
  Comparator #(.width(7), .mode("twosComplement")) comparator_10 (
    .a(\键盘输入 ), .b(7'b1100100), .eq(comparator_10_eq));  // open: gt, lt
  Comparator #(.width(7), .mode("twosComplement")) comparator_11 (
    .a(\键盘输入 ), .b(7'b1000100), .eq(comparator_11_eq));  // open: gt, lt
  Comparator #(.width(7), .mode("twosComplement")) comparator_12 (
    .a(\键盘输入 ), .b(7'b0100111), .eq(comparator_12_eq));  // open: gt, lt
  Comparator #(.width(7), .mode("twosComplement")) comparator_13 (
    .a(\键盘输入 ), .b(7'b0110001), .eq(comparator_13_eq));  // open: gt, lt
  Comparator #(.width(7), .mode("twosComplement")) comparator_14 (
    .a(\键盘输入 ), .b(7'b0110010), .eq(comparator_14_eq));  // open: gt, lt
  Comparator #(.width(7), .mode("twosComplement")) comparator_15 (
    .a(\键盘输入 ), .b(7'b0110011), .eq(comparator_15_eq));  // open: gt, lt
  Comparator #(.width(7), .mode("twosComplement")) comparator_16 (
    .a(\键盘输入 ), .b(7'b0110100), .eq(comparator_16_eq));  // open: gt, lt
  Comparator #(.width(7), .mode("twosComplement")) comparator_17 (
    .a(\键盘输入 ), .b(7'b0110101), .eq(comparator_17_eq));  // open: gt, lt
  Comparator #(.width(7), .mode("twosComplement")) comparator_18 (
    .a(\键盘输入 ), .b(7'b0110110), .eq(comparator_18_eq));  // open: gt, lt
  Comparator #(.width(7), .mode("twosComplement")) comparator_19 (
    .a(\键盘输入 ), .b(7'b0110111), .eq(comparator_19_eq));  // open: gt, lt
  Comparator #(.width(7), .mode("twosComplement")) comparator_20 (
    .a(\键盘输入 ), .b(7'b0111000), .eq(comparator_20_eq));  // open: gt, lt
  Comparator #(.width(7), .mode("twosComplement")) comparator_21 (
    .a(\键盘输入 ), .b(7'b0111001), .eq(comparator_21_eq));  // open: gt, lt
  Comparator #(.width(7), .mode("twosComplement")) comparator_22 (
    .a(\键盘输入 ), .b(7'b0110000), .eq(comparator_22_eq));  // open: gt, lt
  Comparator #(.width(7), .mode("twosComplement")) comparator_23 (
    .a(\键盘输入 ), .b(7'b0001010), .eq(comparator_23_eq));  // open: gt, lt
  or or_1 (or_1_out, comparator_1_eq, comparator_2_eq, comparator_3_eq);
  or or_2 (or_2_out, comparator_4_eq, comparator_5_eq, comparator_6_eq);
  or or_3 (or_3_out, comparator_7_eq, comparator_8_eq, comparator_9_eq);
  or or_4 (or_4_out, comparator_10_eq, comparator_11_eq, comparator_12_eq);
  Register #(.width(1), .trigger("rising"), .Select("low")) register_1 (
    .D(or_1_out), .Q(Up), .clk(CLK), .clr(RST));  // open: en
  Register #(.width(1), .trigger("rising"), .Select("low")) register_2 (
    .D(or_2_out), .Q(Down), .clk(CLK), .clr(RST));  // open: en
  Register #(.width(1), .trigger("rising"), .Select("low")) register_3 (
    .D(or_3_out), .Q(Left), .clk(CLK), .clr(RST));  // open: en
  Register #(.width(1), .trigger("rising"), .Select("low")) register_4 (
    .D(or_4_out), .Q(Right), .clk(CLK), .clr(RST));  // open: en
  Register #(.width(1), .trigger("rising"), .Select("low")) register_5 (
    .D(comparator_13_eq), .Q(Num_1), .clk(CLK), .clr(RST));  // open: en
  Register #(.width(1), .trigger("rising"), .Select("low")) register_6 (
    .D(comparator_14_eq), .Q(Num_2), .clk(CLK), .clr(RST));  // open: en
  Register #(.width(1), .trigger("rising"), .Select("low")) register_7 (
    .D(comparator_15_eq), .Q(Num_3), .clk(CLK), .clr(RST));  // open: en
  Register #(.width(1), .trigger("rising"), .Select("low")) register_8 (
    .D(comparator_16_eq), .Q(Num_4), .clk(CLK), .clr(RST));  // open: en
  Register #(.width(1), .trigger("rising"), .Select("low")) register_9 (
    .D(comparator_17_eq), .Q(Num_5), .clk(CLK), .clr(RST));  // open: en
  Register #(.width(1), .trigger("rising"), .Select("low")) register_10 (
    .D(comparator_18_eq), .Q(Num_6), .clk(CLK), .clr(RST));  // open: en
  Register #(.width(1), .trigger("rising"), .Select("low")) register_11 (
    .D(comparator_19_eq), .Q(Num_7), .clk(CLK), .clr(RST));  // open: en
  Register #(.width(1), .trigger("rising"), .Select("low")) register_12 (
    .D(comparator_20_eq), .Q(Num_8), .clk(CLK), .clr(RST));  // open: en
  Register #(.width(1), .trigger("rising"), .Select("low")) register_13 (
    .D(comparator_21_eq), .Q(Num_9), .clk(CLK), .clr(RST));  // open: en
  Register #(.width(1), .trigger("rising"), .Select("low")) register_14 (
    .D(comparator_22_eq), .Q(Num_0), .clk(CLK), .clr(RST));  // open: en
  Register #(.width(1), .trigger("rising"), .Select("low")) register_15 (
    .D(comparator_23_eq), .Q(Enter), .clk(CLK), .clr(RST));  // open: en
endmodule

// LCD数据源
module \LCD数据源  (
  input  CLK,
  input  [3:0] _1,
  input  [3:0] _2,
  input  [3:0] _3,
  input  [3:0] \选中宫格序号 ,
  input  \使能 ,
  input  [3:0] _4,
  input  [3:0] _5,
  input  [3:0] _6,
  input  RST,
  input  [3:0] _7,
  input  [3:0] _8,
  input  [3:0] _9,
  input  \更改信号 ,
  input  \选中 ,
  input  \清除更改使能 ,
  output [15:0] \颜色 ,
  output \输出完成 ,
  output [6:0] X,
  output [6:0] Y
);

  wire \_1完成 , \_2完成 , \_3完成 , \_4完成 , \_5完成 , \_6完成 , \_7完成 , \_8完成 , \_9完成 , and_1_out, not_1_out,
       not_2_out, not_3_out, not_4_out, not_5_out, not_6_out, not_7_out, not_8_out, not_9_out, not_10_out,
       priority_encoder_1_en_out, \分隔线完成 , \更改使能 , \选中1 , \选中2 , \选中3 , \选中4 , \选中5 , \选中6 , \选中7 , \选中8 ,
       \选中9 ;
  wire [3:0] priority_encoder_1_out, subtractor_1_out, \选择 ;
  wire [15:0] adder_1_out, adder_2_out, adder_3_out, adder_4_out, adder_5_out, adder_6_out, adder_7_out,
       adder_8_out, adder_9_out, adder_10_out, \分隔线颜色 , \数字点阵库_1_点位坐标_x_y各占8位 , \数字点阵库_2_点位坐标_x_y各占8位 ,
       \数字点阵库_3_点位坐标_x_y各占8位 , \数字点阵库_4_点位坐标_x_y各占8位 , \数字点阵库_5_点位坐标_x_y各占8位 , \数字点阵库_6_点位坐标_x_y各占8位 ,
       \数字点阵库_7_点位坐标_x_y各占8位 , \数字点阵库_8_点位坐标_x_y各占8位 , \数字点阵库_9_点位坐标_x_y各占8位 , \数字点阵库_10_点位坐标_x_y各占8位 ,
       \颜色1 , \颜色2 , \颜色3 , \颜色4 , \颜色5 , \颜色6 , \颜色7 , \颜色8 , \颜色9 ;
  wire [15:7] multiplexer_1_out;

  \数字点阵库  \u_数字点阵库_1  (
    .CLK(CLK), .\使用分隔线 (1'b1), .\点位坐标_X_Y各占8位 (\数字点阵库_1_点位坐标_x_y各占8位 ), .\使能 (\使能 ), .\输出结束 (\分隔线完成 ),
    .RST(RST), .\选中 (1'b0), .\颜色 (\分隔线颜色 ));  // open: 数字
  \数字点阵库  \u_数字点阵库_2  (
    .CLK(CLK), .\使用分隔线 (1'b0), .\数字 (_1), .\点位坐标_X_Y各占8位 (\数字点阵库_2_点位坐标_x_y各占8位 ), .\使能 (\分隔线完成 ),
    .\输出结束 (\_1完成 ), .RST(RST), .\选中 (\选中1 ), .\颜色 (\颜色1 ));
  \数字点阵库  \u_数字点阵库_3  (
    .CLK(CLK), .\使用分隔线 (1'b0), .\数字 (_2), .\点位坐标_X_Y各占8位 (\数字点阵库_3_点位坐标_x_y各占8位 ), .\使能 (\_1完成 ),
    .\输出结束 (\_2完成 ), .RST(RST), .\选中 (\选中2 ), .\颜色 (\颜色2 ));
  \数字点阵库  \u_数字点阵库_4  (
    .CLK(CLK), .\使用分隔线 (1'b0), .\数字 (_3), .\点位坐标_X_Y各占8位 (\数字点阵库_4_点位坐标_x_y各占8位 ), .\使能 (\_2完成 ),
    .\输出结束 (\_3完成 ), .RST(RST), .\选中 (\选中3 ), .\颜色 (\颜色3 ));
  \数字点阵库  \u_数字点阵库_5  (
    .CLK(CLK), .\使用分隔线 (1'b0), .\数字 (_4), .\点位坐标_X_Y各占8位 (\数字点阵库_5_点位坐标_x_y各占8位 ), .\使能 (\_3完成 ),
    .\输出结束 (\_4完成 ), .RST(RST), .\选中 (\选中4 ), .\颜色 (\颜色4 ));
  \数字点阵库  \u_数字点阵库_6  (
    .CLK(CLK), .\使用分隔线 (1'b0), .\数字 (_5), .\点位坐标_X_Y各占8位 (\数字点阵库_6_点位坐标_x_y各占8位 ), .\使能 (\_4完成 ),
    .\输出结束 (\_5完成 ), .RST(RST), .\选中 (\选中5 ), .\颜色 (\颜色5 ));
  \数字点阵库  \u_数字点阵库_7  (
    .CLK(CLK), .\使用分隔线 (1'b0), .\数字 (_6), .\点位坐标_X_Y各占8位 (\数字点阵库_7_点位坐标_x_y各占8位 ), .\使能 (\_5完成 ),
    .\输出结束 (\_6完成 ), .RST(RST), .\选中 (\选中6 ), .\颜色 (\颜色6 ));
  \数字点阵库  \u_数字点阵库_8  (
    .CLK(CLK), .\使用分隔线 (1'b0), .\数字 (_7), .\点位坐标_X_Y各占8位 (\数字点阵库_8_点位坐标_x_y各占8位 ), .\使能 (\_6完成 ),
    .\输出结束 (\_7完成 ), .RST(RST), .\选中 (\选中7 ), .\颜色 (\颜色7 ));
  \数字点阵库  \u_数字点阵库_9  (
    .CLK(CLK), .\使用分隔线 (1'b0), .\数字 (_8), .\点位坐标_X_Y各占8位 (\数字点阵库_9_点位坐标_x_y各占8位 ), .\使能 (\_7完成 ),
    .\输出结束 (\_8完成 ), .RST(RST), .\选中 (\选中8 ), .\颜色 (\颜色8 ));
  \数字点阵库  \u_数字点阵库_10  (
    .CLK(CLK), .\使用分隔线 (1'b0), .\数字 (_9), .\点位坐标_X_Y各占8位 (\数字点阵库_10_点位坐标_x_y各占8位 ), .\使能 (\_8完成 ),
    .\输出结束 (\_9完成 ), .RST(RST), .\选中 (\选中9 ), .\颜色 (\颜色9 ));
  Adder #(.width(16)) adder_1 (.a(\数字点阵库_1_点位坐标_x_y各占8位 ), .b({16{1'b0}}), .out(adder_1_out));  // open: cin, cout
  Adder #(.width(16)) adder_2 (.a(\数字点阵库_2_点位坐标_x_y各占8位 ), .b({16{1'b0}}), .out(adder_2_out));  // open: cin, cout
  Adder #(.width(16)) adder_3 (.a(\数字点阵库_3_点位坐标_x_y各占8位 ), .b(16'h2d00), .out(adder_3_out));  // open: cin, cout
  Adder #(.width(16)) adder_4 (.a(\数字点阵库_4_点位坐标_x_y各占8位 ), .b(16'h5900), .out(adder_4_out));  // open: cin, cout
  Adder #(.width(16)) adder_5 (.a(\数字点阵库_5_点位坐标_x_y各占8位 ), .b(16'h2d), .out(adder_5_out));  // open: cin, cout
  Adder #(.width(16)) adder_6 (.a(\数字点阵库_6_点位坐标_x_y各占8位 ), .b(16'h2d2d), .out(adder_6_out));  // open: cin, cout
  Adder #(.width(16)) adder_7 (.a(\数字点阵库_7_点位坐标_x_y各占8位 ), .b(16'h592d), .out(adder_7_out));  // open: cin, cout
  Adder #(.width(16)) adder_8 (.a(\数字点阵库_8_点位坐标_x_y各占8位 ), .b(16'h59), .out(adder_8_out));  // open: cin, cout
  Adder #(.width(16)) adder_9 (.a(\数字点阵库_9_点位坐标_x_y各占8位 ), .b(16'h2d59), .out(adder_9_out));  // open: cin, cout
  Adder #(.width(16)) adder_10 (.a(\数字点阵库_10_点位坐标_x_y各占8位 ), .b(16'h5959), .out(adder_10_out));  // open: cin, cout
  Multiplexer #(.select(4), .width(16), .disabled("Z"), .enable("false")) multiplexer_1 (
    .in0(adder_1_out), .in1(adder_2_out), .in2(adder_3_out), .in3(adder_4_out), .in4(adder_5_out),
    .in5(adder_6_out), .in6(adder_7_out), .in7(adder_8_out), .in8(adder_9_out), .in9(adder_10_out),
    .in10({16{1'b0}}), .in11({16{1'b0}}), .in12({16{1'b0}}), .in13({16{1'b0}}), .in14({16{1'b0}}),
    .in15({16{1'b0}}), .out({multiplexer_1_out[15], X, multiplexer_1_out[7], Y}), .sel(\选择 ));
  D_Flip_Flop #(.trigger("high"), .Pre_Clr_Positions("ABOVE_BELOW"), .NegatePresetClear("false"), .enable("false"), .NewFFLayout("true")) d_ff_1 (
    .clk(\更改信号 ), .D(1'b1), .Q(\更改使能 ), .reset(\清除更改使能 ));  // open: Qn, preset
  Multiplexer #(.select(4), .width(16), .disabled("Z"), .enable("false")) multiplexer_2 (
    .in0(\分隔线颜色 ), .in1(\颜色1 ), .in2(\颜色2 ), .in3(\颜色3 ), .in4(\颜色4 ), .in5(\颜色5 ), .in6(\颜色6 ), .in7(\颜色7 ),
    .in8(\颜色8 ), .in9(\颜色9 ), .in10({16{1'b0}}), .in11({16{1'b0}}), .in12({16{1'b0}}), .in13({16{1'b0}}),
    .in14({16{1'b0}}), .in15({16{1'b0}}), .out(\颜色 ), .sel(\选择 ));
  not not_1 (not_1_out, \_8完成 );
  not not_2 (not_2_out, \_6完成 );
  not not_3 (not_3_out, \_4完成 );
  not not_4 (not_4_out, \_2完成 );
  not not_5 (not_5_out, \分隔线完成 );
  not not_6 (not_6_out, \_9完成 );
  not not_7 (not_7_out, \_7完成 );
  not not_8 (not_8_out, \_5完成 );
  not not_9 (not_9_out, \_3完成 );
  not not_10 (not_10_out, \_1完成 );
  and and_1 (and_1_out, \选中 , \更改使能 );
  Priority_Encoder #(.select(4), .disabled("Z")) priority_encoder_1 (
    .in0(not_6_out), .in1(not_1_out), .in2(not_7_out), .in3(not_2_out), .in4(not_8_out), .in5(not_3_out),
    .in6(not_9_out), .in7(not_4_out), .in8(not_10_out), .in9(not_5_out), .out(priority_encoder_1_out),
    .en_out(priority_encoder_1_en_out));  // open: in10, in11, in12, in13, in14, in15, gs, en_in
  Decoder #(.select(4), .tristate("false"), .disabled(0), .enable("true")) decoder_1 (
    .out1(\选中1 ), .out2(\选中2 ), .out3(\选中3 ), .out4(\选中4 ), .out5(\选中5 ), .out6(\选中6 ), .out7(\选中7 ),
    .out8(\选中8 ), .out9(\选中9 ), .sel(\选中宫格序号 ), .en(and_1_out));  // open: out0, out10, out11, out12, out13, out14, out15
  Subtractor #(.width(4)) subtractor_1 (
    .a(4'b1001), .b(priority_encoder_1_out), .out(subtractor_1_out));  // open: bin, bout
  and and_2 (\输出完成 , \_9完成 , \_7完成 , \_5完成 , \_3完成 , \_1完成 , \_8完成 , \_4完成 , \_6完成 , \_2完成 , \分隔线完成 );
  Multiplexer #(.select(1), .width(4), .disabled("Z"), .enable("false")) multiplexer_3 (
    .in0(subtractor_1_out), .in1(4'b1010), .out(\选择 ), .sel(priority_encoder_1_en_out));
endmodule

// 点阵库
module \数字点阵库  (
  input  CLK,
  input  RST,
  input  \使用分隔线 ,
  input  \使能 ,
  input  [3:0] \数字 ,
  input  \选中 ,
  output \输出结束 ,
  output [15:0] \点位坐标_X_Y各占8位 ,
  output [15:0] \颜色 
);

  wire and_2_out, and_3_out, multiplexer_5_out, multiplexer_7_out, not_1_out, or_2_out, RST_t, \清除中 , \清除计数 ,
       \计满0 , \计满1 , \计满2 , \计满3 , \计满4 , \计满5 , \计满6 , \计满7 , \计满8 , \计满9 , \计满分隔线 , \计满清除 ;
  wire [7:0] \地址0_q , \地址1_q , \地址2_q , \地址3_q , \地址4_q , \地址5_q , \地址6_q , \地址7_q , \地址8_q , \地址9_q ;
  wire [9:0] \清除_q ;
  wire [11:0] \分隔线地址_q ;
  wire [15:0] multiplexer_1_out, multiplexer_2_out, multiplexer_4_out, \分隔线 , \数字0 , \数字1 , \数字2 , \数字3 ,
       \数字4 , \数字5 , \数字6 , \数字7 , \数字8 , \数字9 , \清除坐标 ;

  Counter #(.width(8), .max('h10), .ongoal("stay"), .trigger("rising"), .behavior("new")) \u_地址0  (
    .count(\使能 ), .Q(\地址0_q ), .carry(\计满0 ), .clk(CLK), .clr(RST_t));  // open: load, D, preset, down
  Counter #(.width(8), .max('hb0), .ongoal("stay"), .trigger("rising"), .behavior("new")) \u_地址2  (
    .count(\使能 ), .Q(\地址2_q ), .carry(\计满2 ), .clk(CLK), .clr(RST_t));  // open: load, D, preset, down
  Counter #(.width(8), .max('hd0), .ongoal("stay"), .trigger("rising"), .behavior("new")) \u_地址4  (
    .count(\使能 ), .Q(\地址4_q ), .carry(\计满4 ), .clk(CLK), .clr(RST_t));  // open: load, D, preset, down
  Counter #(.width(8), .max('hd0), .ongoal("stay"), .trigger("rising"), .behavior("new")) \u_地址6  (
    .count(\使能 ), .Q(\地址6_q ), .carry(\计满6 ), .clk(CLK), .clr(RST_t));  // open: load, D, preset, down
  Counter #(.width(8), .max('hf0), .ongoal("stay"), .trigger("rising"), .behavior("new")) \u_地址8  (
    .count(\使能 ), .Q(\地址8_q ), .carry(\计满8 ), .clk(CLK), .clr(RST_t));  // open: load, D, preset, down
  ROM #(.addrWidth(8), .dataWidth(16), .Select("low")) rom_1 (.addr(\地址0_q ), .data(\数字0 ));
  ROM #(.addrWidth(8), .dataWidth(16), .Select("low")) rom_2 (.addr(\地址2_q ), .data(\数字2 ));
  ROM #(.addrWidth(8), .dataWidth(16), .Select("low")) rom_3 (.addr(\地址4_q ), .data(\数字4 ));
  ROM #(.addrWidth(8), .dataWidth(16), .Select("low")) rom_4 (.addr(\地址6_q ), .data(\数字6 ));
  ROM #(.addrWidth(8), .dataWidth(16), .Select("low")) rom_5 (.addr(\地址8_q ), .data(\数字8 ));
  Multiplexer #(.select(4), .width(16), .disabled("Z"), .enable("false")) multiplexer_1 (
    .in0(\数字0 ), .in1(\数字1 ), .in2(\数字2 ), .in3(\数字3 ), .in4(\数字4 ), .in5(\数字5 ), .in6(\数字6 ), .in7(\数字7 ),
    .in8(\数字8 ), .in9(\数字9 ), .out(multiplexer_1_out), .sel(\数字 ));  // open: in10, in11, in12, in13, in14, in15
  Counter #(.width(8), .max('h70), .ongoal("stay"), .trigger("rising"), .behavior("new")) \u_地址1  (
    .count(\使能 ), .Q(\地址1_q ), .carry(\计满1 ), .clk(CLK), .clr(RST_t));  // open: load, D, preset, down
  Counter #(.width(8), .max('hc0), .ongoal("stay"), .trigger("rising"), .behavior("new")) \u_地址3  (
    .count(\使能 ), .Q(\地址3_q ), .carry(\计满3 ), .clk(CLK), .clr(RST_t));  // open: load, D, preset, down
  Counter #(.width(8), .max('he0), .ongoal("stay"), .trigger("rising"), .behavior("new")) \u_地址5  (
    .count(\使能 ), .Q(\地址5_q ), .carry(\计满5 ), .clk(CLK), .clr(RST_t));  // open: load, D, preset, down
  Counter #(.width(8), .max('ha0), .ongoal("stay"), .trigger("rising"), .behavior("new")) \u_地址7  (
    .count(\使能 ), .Q(\地址7_q ), .carry(\计满7 ), .clk(CLK), .clr(RST_t));  // open: load, D, preset, down
  Counter #(.width(8), .max('hc0), .ongoal("stay"), .trigger("rising"), .behavior("new")) \u_地址9  (
    .count(\使能 ), .Q(\地址9_q ), .carry(\计满9 ), .clk(CLK), .clr(RST_t));  // open: load, D, preset, down
  Multiplexer #(.select(1), .width(16), .disabled("Z"), .enable("false")) multiplexer_2 (
    .in0(multiplexer_1_out), .in1(\分隔线 ), .out(multiplexer_2_out), .sel(\使用分隔线 ));
  ROM #(.addrWidth(8), .dataWidth(16), .Select("low")) rom_6 (.addr(\地址1_q ), .data(\数字1 ));
  ROM #(.addrWidth(8), .dataWidth(16), .Select("low")) rom_7 (.addr(\地址3_q ), .data(\数字3 ));
  ROM #(.addrWidth(8), .dataWidth(16), .Select("low")) rom_8 (.addr(\地址5_q ), .data(\数字5 ));
  ROM #(.addrWidth(8), .dataWidth(16), .Select("low")) rom_9 (.addr(\地址7_q ), .data(\数字7 ));
  ROM #(.addrWidth(8), .dataWidth(16), .Select("low")) rom_10 (.addr(\地址9_q ), .data(\数字9 ));
  Multiplexer #(.select(1), .width(16), .disabled("Z"), .enable("false")) multiplexer_3 (
    .in0(multiplexer_2_out), .in1(\清除坐标 ), .out(\点位坐标_X_Y各占8位 ), .sel(\清除中 ));
  Counter #(.width(12), .max('h810), .ongoal("stay"), .trigger("rising"), .behavior("new")) \u_分隔线地址  (
    .count(\使能 ), .Q(\分隔线地址_q ), .carry(\计满分隔线 ), .clk(CLK), .clr(RST_t));  // open: load, D, preset, down
  and and_1 (\清除中 , ~\计满清除 , \选中 );  // AND_Gate
  and and_2 (and_2_out, \选中 , \清除计数 );
  Multiplexer #(.select(1), .width(16), .disabled("Z"), .enable("false")) multiplexer_4 (
    .in0({16{1'b1}}), .in1(16'h1f1f), .out(multiplexer_4_out), .sel(\选中 ));
  Multiplexer #(.select(4), .width(1), .disabled("Z"), .enable("false")) multiplexer_5 (
    .in0(\计满0 ), .in1(\计满1 ), .in2(\计满2 ), .in3(\计满3 ), .in4(\计满4 ), .in5(\计满5 ), .in6(\计满6 ), .in7(\计满7 ),
    .in8(\计满8 ), .in9(\计满9 ), .out(multiplexer_5_out), .sel(\数字 ));  // open: in10, in11, in12, in13, in14, in15
  or or_1 (RST_t, and_2_out, RST);
  Multiplexer #(.select(1), .width(16), .disabled("Z"), .enable("false")) multiplexer_6 (
    .in0(multiplexer_4_out), .in1({16{1'b0}}), .out(\颜色 ), .sel(\清除中 ));
  ROM #(.addrWidth(12), .dataWidth(16), .Select("low")) rom_11 (.addr(\分隔线地址_q ), .data(\分隔线 ));
  Multiplexer #(.select(1), .width(1), .disabled("Z"), .enable("false")) multiplexer_7 (
    .in0(multiplexer_5_out), .in1(\计满分隔线 ), .out(multiplexer_7_out), .sel(\使用分隔线 ));
  Multiplexer #(.select(1), .width(1), .disabled("Z"), .enable("false")) multiplexer_8 (
    .in0(multiplexer_7_out), .in1(1'b0), .out(\输出结束 ), .sel(\清除中 ));
  and and_3 (and_3_out, \选中 , ~\计满清除 );  // AND_Gate
  Counter #(.width(10), .max('h290), .ongoal("wrap"), .trigger("rising"), .behavior("new")) \u_清除  (
    .count(and_3_out), .Q(\清除_q ), .carry(\清除计数 ), .clk(CLK), .clr(or_2_out));  // open: load, D, preset, down
  or or_2 (or_2_out, not_1_out, \计满清除 );
  not not_1 (not_1_out, \选中 );
  D_Flip_Flop #(.trigger("high"), .Pre_Clr_Positions("ABOVE_BELOW"), .NegatePresetClear("false"), .enable("false"), .NewFFLayout("true")) d_ff_1 (
    .clk(\清除计数 ), .D(1'b1), .Q(\计满清除 ), .reset(not_1_out));  // open: Qn, preset
  ROM #(.addrWidth(10), .dataWidth(16), .Select("low")) rom_12 (.addr(\清除_q ), .data(\清除坐标 ));

  // Other names for the same wires on the sheet: RST信号 = RST; 输出数据[15:0] = \点位坐标_X_Y各占8位 

  // Notes on the sheet:
  //   contents of rom_2 (hex, n*v repeats v):
  //   b0c c0a c0b c0c c1e c1f c20 d09 d0a d0b d0c d0d d1d d1e d1f d20 e08 e09 e0a e0b e0c e1c e1d e1e e1f
  //   e20 f07 f08 f09 f0a f1b f1c f1d f1e f1f f20 1006 1007 1008 1009 101a 101b 101c 101d 101e 101f 1020
  //   1106 1107 1108 1109 1118 1119 111a 111b 111c 111e 111f 1120 1206 1207 1208 1217 1218 1219 121a 121b
  //   121e 121f 1220 1306 1307 1308 1316 1317 1318 1319 131a 131e 131f 1320 1406 1407 1408 1415 1416 1417
  //   1418 1419 141e 141f 1420 1506 1507 1508 1513 1514 1515 1516 1517 151e 151f 1520 1606 1607 1608 1609
  //   1611 1612 1613 1614 1615 1616 161e 161f 1620 1707 1708 1709 170a 170f 1710 1711 1712 1713 1714 1715
  //   171e 171f 1720 1807 1808 1809 180a 180b 180c 180d 180e 180f 1810 1811 1812 1813 181e 181f 1820 1908
  //   1909 190a 190b 190c 190d 190e 190f 1910 1911 1912 191e 191f 1920 1a09 1a0a 1a0b 1a0c 1a0d 1a0e 1a0f
  //   1a10 1a1e 1a1f 1a20 1b1e 1b1f 1b20
  //   contents of rom_3 (hex, n*v repeats v):
  //   a18 a19 a1a b17 b18 b19 b1a c15 c16 c17 c18 c19 c1a d14 d15 d16 d17 d18 d19 d1a e12 e13 e14 e15 e16
  //   e17 e18 e19 e1a f11 f12 f13 f14 f15 f18 f19 f1a 1010 1011 1012 1013 1014 1018 1019 101a 110e 110f
  //   1110 1111 1112 1118 1119 111a 120d 120e 120f 1210 1211 1218 1219 121a 130b 130c 130d 130e 130f 1310
  //   1318 1319 131a 140a 140b 140c 140d 140e 1418 1419 141a 1508 1509 150a 150b 150c 150d 1518 1519 151a
  //   1607 1608 1609 160a 160b 160c 160d 160e 160f 1610 1611 1612 1613 1614 1615 1616 1617 1618 1619 161a
  //   161b 161c 161d 161e 161f 1620 1706 1707 1708 1709 170a 170b 170c 170d 170e 170f 1710 1711 1712 1713
  //   1714 1715 1716 1717 1718 1719 171a 171b 171c 171d 171e 171f 1720 1806 1807 1808 1809 180a 180b 180c
  //   180d 180e 180f 1810 1811 1812 1813 1814 1815 1816 1817 1818 1819 181a 181b 181c 181d 181e 181f 1820
  //   1906 1907 1908 1909 190a 190b 190c 190d 190e 190f 1910 1911 1912 1913 1914 1915 1916 1917 1918 1919
  //   191a 191b 191c 191d 191e 191f 1920 1a18 1a19 1a1a 1b18 1b19 1b1a 1c18 1c19 1c1a
  //   contents of rom_4 (hex, n*v repeats v):
  //   b17 b18 b19 c14 c15 c16 c17 c18 c19 c1a c1b c1c d12 d13 d14 d15 d16 d17 d18 d19 d1a d1b d1c d1d d1e
  //   e10 e11 e12 e13 e14 e15 e16 e17 e18 e19 e1a e1b e1c e1d e1e e1f f0e f0f f10 f11 f12 f13 f14 f15 f1b
  //   f1c f1d f1e f1f f20 100d 100e 100f 1010 1011 1012 1013 101d 101e 101f 1020 110b 110c 110d 110e 110f
  //   1110 1111 1112 111e 111f 1120 120a 120b 120c 120d 120e 120f 1210 1211 1212 121e 121f 1220 1221 1308
  //   1309 130a 130b 130c 130d 1310 1311 1312 131f 1320 1321 1407 1408 1409 140a 140b 140c 1410 1411 1412
  //   141f 1420 1421 1506 1507 1508 1509 150a 1510 1511 1512 151f 1520 1521 1606 1607 1608 1609 1610 1611
  //   1612 161e 161f 1620 1706 1707 1710 1711 1712 1713 171e 171f 1720 1811 1812 1813 1814 181c 181d 181e
  //   181f 1820 1911 1912 1913 1914 1915 1916 1919 191a 191b 191c 191d 191e 191f 1a12 1a13 1a14 1a15 1a16
  //   1a17 1a18 1a19 1a1a 1a1b 1a1c 1a1d 1a1e 1b13 1b14 1b15 1b16 1b17 1b18 1b19 1b1a 1b1b 1b1c 1b1d 1c15
  //   1c16 1c17 1c18 1c19 1c1a 1c1b
  //   contents of rom_5 (hex, n*v repeats v):
  //   b17 b18 b19 b1a b1b b1c c0a c0b c0c c0d c0e c0f c15 c16 c17 c18 c19 c1a c1b c1c c1d c1e d09 d0a d0b
  //   d0c d0d d0e d0f d10 d11 d14 d15 d16 d17 d18 d19 d1a d1b d1c d1d d1e d1f e08 e09 e0a e0b e0c e0d e0e
  //   e0f e10 e11 e12 e13 e14 e15 e16 e17 e18 e1b e1c e1d e1e e1f e20 f07 f08 f09 f0a f0f f10 f11 f12 f13
  //   f14 f15 f1d f1e f1f f20 1006 1007 1008 1009 1010 1011 1012 1013 1014 1015 101e 101f 1020 1106 1107
  //   1108 1111 1112 1113 1114 111e 111f 1120 1206 1207 1208 1211 1212 1213 1214 121e 121f 1220 1221 1306
  //   1307 1308 1311 1312 1313 1314 131e 131f 1320 1321 1406 1407 1408 1411 1412 1413 1414 141e 141f 1420
  //   1421 1506 1507 1508 1511 1512 1513 1514 151e 151f 1520 1606 1607 1608 1609 1610 1611 1612 1613 1614
  //   1615 161e 161f 1620 1707 1708 1709 170a 170f 1710 1711 1712 1713 1714 1715 171d 171e 171f 1720 1807
  //   1808 1809 180a 180b 180c 180d 180e 180f 1810 1811 1813 1814 1815 1816 1817 181b 181c 181d 181e 181f
  //   1820 1908 1909 190a 190b 190c 190d 190e 190f 1910 1914 1915 1916 1917 1918 1919 191a 191b 191c 191d
  //   191e 191f 1a0a 1a0b 1a0c 1a0d 1a0e 1a0f 1a15 1a16 1a17 1a18 1a19 1a1a 1a1b 1a1c 1a1d 1a1e 1b16 1b17
  //   1b18 1b19 1b1a 1b1b 1b1c
  //   contents of rom_6 (hex, n*v repeats v):
  //   e0c e0d e0e f0b f0c f0d 100a 100b 100c 100d 1109 110a 110b 110c 1208 1209 120a 120b 120c 1307 1308
  //   1309 130a 130b 130c 130d 130e 130f 1310 1311 1312 1313 1314 1315 1316 1317 1318 1319 131a 131b 131c
  //   131d 131e 131f 1320 1406 1407 1408 1409 140a 140b 140c 140d 140e 140f 1410 1411 1412 1413 1414 1415
  //   1416 1417 1418 1419 141a 141b 141c 141d 141e 141f 1420 1506 1507 1508 1509 150a 150b 150c 150d 150e
  //   150f 1510 1511 1512 1513 1514 1515 1516 1517 1518 1519 151a 151b 151c 151d 151e 151f 1520
  //   contents of rom_7 (hex, n*v repeats v):
  //   c0b c0c c1a c1b c1c d09 d0a d0b d0c d1a d1b d1c d1d d1e e08 e09 e0a e0b e0c e1a e1b e1c e1d e1e e1f
  //   f07 f08 f09 f0a f0b f1c f1d f1e f1f 1007 1008 1009 101d 101e 101f 1020 1106 1107 1108 1109 111e 111f
  //   1120 1206 1207 1208 1212 1213 121e 121f 1220 1306 1307 1308 1312 1313 131e 131f 1320 1406 1407 1408
  //   1411 1412 1413 1414 141e 141f 1420 1506 1507 1508 1511 1512 1513 1514 151e 151f 1520 1606 1607 1608
  //   1609 1610 1611 1612 1613 1614 1615 161d 161e 161f 1620 1707 1708 1709 170a 170f 1710 1711 1712 1713
  //   1714 1715 1716 171c 171d 171e 171f 1720 1807 1808 1809 180a 180b 180c 180d 180e 180f 1810 1811 1813
  //   1814 1815 1816 1817 1818 1819 181a 181b 181c 181d 181e 181f 1908 1909 190a 190b 190c 190d 190e 190f
  //   1910 1914 1915 1916 1917 1918 1919 191a 191b 191c 191d 191e 1a09 1a0a 1a0b 1a0c 1a0d 1a0e 1a0f 1a15
  //   1a16 1a17 1a18 1a19 1a1a 1a1b 1a1c 1a1d 1b17 1b18 1b19 1b1a 1b1b
  //   contents of rom_8 (hex, n*v repeats v):
  //   b13 b1a b1b b1c b1d c0f c10 c11 c12 c13 c1a c1b c1c c1d c1e d0a d0b d0c d0d d0e d0f d10 d11 d12 d13
  //   d1a d1b d1c d1d d1e d1f e07 e08 e09 e0a e0b e0c e0d e0e e0f e10 e11 e12 e13 e1c e1d e1e e1f e20 f06
  //   f07 f08 f09 f0a f0b f0c f0d f0e f0f f10 f11 f12 f1d f1e f1f f20 1006 1007 1008 1009 100a 1010 1011
  //   1012 101e 101f 1020 1106 1107 1108 1109 110f 1110 1111 111e 111f 1120 1121 1206 1207 1208 1209 120f
  //   1210 1211 121e 121f 1220 1221 1306 1307 1308 1309 130f 1310 1311 131e 131f 1320 1321 1406 1407 1408
  //   1409 140f 1410 1411 141e 141f 1420 1421 1506 1507 1508 1509 150f 1510 1511 1512 151e 151f 1520 1606
  //   1607 1608 1609 1610 1611 1612 161d 161e 161f 1620 1706 1707 1708 1709 1710 1711 1712 1713 1714 171c
  //   171d 171e 171f 1806 1807 1808 1809 1811 1812 1813 1814 1815 1816 1817 1818 1819 181a 181b 181c 181d
  //   181e 181f 1906 1907 1908 1909 1911 1912 1913 1914 1915 1916 1917 1918 1919 191a 191b 191c 191d 191e
  //   1a07 1a08 1a13 1a14 1a15 1a16 1a17 1a18 1a19 1a1a 1a1b 1a1c 1a1d 1b15 1b16 1b17 1b18 1b19 1b1a
  //   contents of rom_9 (hex, n*v repeats v):
  //   c06 c07 c08 c09 d06 d07 d08 d09 e06 e07 e08 e09 f06 f07 f08 f09 f20 1006 1007 1008 1009 101c 101d
  //   101e 101f 1020 1106 1107 1108 1109 1119 111a 111b 111c 111d 111e 111f 1120 1206 1207 1208 1209 1216
  //   1217 1218 1219 121a 121b 121c 121d 121e 121f 1220 1306 1307 1308 1309 1314 1315 1316 1317 1318 1319
  //   131a 131b 131c 131d 1406 1407 1408 1409 1412 1413 1414 1415 1416 1417 1418 1419 141a 1506 1507 1508
  //   1509 1510 1511 1512 1513 1514 1515 1516 1517 1606 1607 1608 1609 160e 160f 1610 1611 1612 1613 1614
  //   1706 1707 1708 1709 170c 170d 170e 170f 1710 1711 1712 1806 1807 1808 1809 180a 180b 180c 180d 180e
  //   180f 1810 1906 1907 1908 1909 190a 190b 190c 190d 190e 1a06 1a07 1a08 1a09 1a0a 1a0b 1a0c 1b06 1b07
  //   1b08 1b09 1b0a 1c06 1c07 1c08
  //   contents of rom_10 (hex, n*v repeats v):
  //   b0b b0c b0d b0e b0f b10 b11 b12 c09 c0a c0b c0c c0d c0e c0f c10 c11 c12 c13 c14 d08 d09 d0a d0b d0c
  //   d0d d0e d0f d10 d11 d12 d13 d14 d15 e07 e08 e09 e0a e0b e0c e11 e12 e13 e14 e15 f07 f08 f09 f0a f13
  //   f14 f15 f16 f20 f21 1006 1007 1008 1009 1014 1015 1016 101f 1020 1021 1106 1107 1108 1109 1114 1115
  //   1116 111d 111e 111f 1120 1121 1206 1207 1208 1214 1215 1216 121b 121c 121d 121e 121f 1220 1306 1307
  //   1308 1314 1315 1316 1319 131a 131b 131c 131d 131e 131f 1406 1407 1408 1414 1415 1416 1417 1418 1419
  //   141a 141b 141c 141d 1506 1507 1508 1509 1514 1515 1516 1517 1518 1519 151a 151b 151c 1606 1607 1608
  //   1609 160a 1615 1616 1617 1618 1619 161a 1707 1708 1709 170a 170b 1713 1714 1715 1716 1717 1718 1808
  //   1809 180a 180b 180c 180d 180e 180f 1810 1811 1812 1813 1814 1815 1816 1908 1909 190a 190b 190c 190d
  //   190e 190f 1910 1911 1912 1913 1914 1a0a 1a0b 1a0c 1a0d 1a0e 1a0f 1a10 1a11 1a12 1b0c 1b0d 1b0e 1b0f
  //   1b10
  //   contents of rom_11 (hex, n*v repeats v):
  //   29 2a 2b 2c 59 56 57 58 129 12a 12b 12c 159 156 157 158 229 22a 22b 22c 259 256 257 258 329 32a 32b
  //   32c 359 356 357 358 429 42a 42b 42c 459 456 457 458 529 52a 52b 52c 559 556 557 558 629 62a 62b 62c
  //   659 656 657 658 729 72a 72b 72c 759 756 757 758 829 82a 82b 82c 859 856 857 858 929 92a 92b 92c 959
  //   956 957 958 a29 a2a a2b a2c a59 a56 a57 a58 b29 b2a b2b b2c b59 b56 b57 b58 c29 c2a c2b c2c c59 c56
  //   c57 c58 d29 d2a d2b d2c d59 d56 d57 d58 e29 e2a e2b e2c e59 e56 e57 e58 f29 f2a f2b f2c f59 f56 f57
  //   f58 1029 102a 102b 102c 1059 1056 1057 1058 1129 112a 112b 112c 1159 1156 1157 1158 1229 122a 122b
  //   122c 1259 1256 1257 1258 1329 132a 132b 132c 1359 1356 1357 1358 1429 142a 142b 142c 1459 1456 1457
  //   1458 1529 152a 152b 152c 1559 1556 1557 1558 1629 162a 162b 162c 1659 1656 1657 1658 1729 172a 172b
  //   172c 1759 1756 1757 1758 1829 182a 182b 182c 1859 1856 1857 1858 1929 192a 192b 192c 1959 1956 1957
  //   1958 1a29 1a2a 1a2b 1a2c 1a59 1a56 1a57 1a58 1b29 1b2a 1b2b 1b2c 1b59 1b56 1b57 1b58 1c29 1c2a 1c2b
  //   1c2c 1c59 1c56 1c57 1c58 1d29 1d2a 1d2b 1d2c 1d59 1d56 1d57 1d58 1e29 1e2a 1e2b 1e2c 1e59 1e56 1e57
  //   1e58 1f29 1f2a 1f2b 1f2c 1f59 1f56 1f57 1f58 2029 202a 202b 202c 2059 2056 2057 2058 2129 212a 212b
  //   212c 2159 2156 2157 2158 2229 222a 222b 222c 2259 2256 2257 2258 2329 232a 232b 232c 2359 2356 2357
  //   2358 2429 242a 242b 242c 2459 2456 2457 2458 2529 252a 252b 252c 2559 2556 2557 2558 2629 262a 262b
  //   262c 2659 2656 2657 2658 2729 272a 272b 272c 2759 2756 2757 2758 2829 282a 282b 282c 2859 2856 2857
  //   2858 2929 292a 292b 292c 2959 2956 2957 2958 2a29 2a2a 2a2b 2a2c 2a59 2a56 2a57 2a58 2b29 2b2a 2b2b
  //   2b2c 2b59 2b56 2b57 2b58 2c29 2c2a 2c2b 2c2c 2c59 2c56 2c57 2c58 2d29 2d2a 2d2b 2d2c 2d59 2d56 2d57
  //   2d58 2e29 2e2a 2e2b 2e2c 2e59 2e56 2e57 2e58 2f29 2f2a 2f2b 2f2c 2f59 2f56 2f57 2f58 3029 302a 302b
  //   302c 3059 3056 3057 3058 3129 312a 312b 312c 3159 3156 3157 3158 3229 322a 322b 322c 3259 3256 3257
  //   3258 3329 332a 332b 332c 3359 3356 3357 3358 3429 342a 342b 342c 3459 3456 3457 3458 3529 352a 352b
  //   352c 3559 3556 3557 3558 3629 362a 362b 362c 3659 3656 3657 3658 3729 372a 372b 372c 3759 3756 3757
  //   3758 3829 382a 382b 382c 3859 3856 3857 3858 3929 392a 392b 392c 3959 3956 3957 3958 3a29 3a2a 3a2b
  //   3a2c 3a59 3a56 3a57 3a58 3b29 3b2a 3b2b 3b2c 3b59 3b56 3b57 3b58 3c29 3c2a 3c2b 3c2c 3c59 3c56 3c57
  //   3c58 3d29 3d2a 3d2b 3d2c 3d59 3d56 3d57 3d58 3e29 3e2a 3e2b 3e2c 3e59 3e56 3e57 3e58 3f29 3f2a 3f2b
  //   3f2c 3f59 3f56 3f57 3f58 4029 402a 402b 402c 4059 4056 4057 4058 4129 412a 412b 412c 4159 4156 4157
  //   4158 4229 422a 422b 422c 4259 4256 4257 4258 4329 432a 432b 432c 4359 4356 4357 4358 4429 442a 442b
  //   442c 4459 4456 4457 4458 4529 452a 452b 452c 4559 4556 4557 4558 4629 462a 462b 462c 4659 4656 4657
  //   4658 4729 472a 472b 472c 4759 4756 4757 4758 4829 482a 482b 482c 4859 4856 4857 4858 4929 492a 492b
  //   492c 4959 4956 4957 4958 4a29 4a2a 4a2b 4a2c 4a59 4a56 4a57 4a58 4b29 4b2a 4b2b 4b2c 4b59 4b56 4b57
  //   4b58 4c29 4c2a 4c2b 4c2c 4c59 4c56 4c57 4c58 4d29 4d2a 4d2b 4d2c 4d59 4d56 4d57 4d58 4e29 4e2a 4e2b
  //   4e2c 4e59 4e56 4e57 4e58 4f29 4f2a 4f2b 4f2c 4f59 4f56 4f57 4f58 5029 502a 502b 502c 5059 5056 5057
  //   5058 5129 512a 512b 512c 5159 5156 5157 5158 5229 522a 522b 522c 5259 5256 5257 5258 5329 532a 532b
  //   532c 5359 5356 5357 5358 5429 542a 542b 542c 5459 5456 5457 5458 5529 552a 552b 552c 5559 5556 5557
  //   5558 5629 562a 562b 562c 5659 5656 5657 5658 5729 572a 572b 572c 5759 5756 5757 5758 5829 582a 582b
  //   582c 5859 5856 5857 5858 5929 592a 592b 592c 5959 5956 5957 5958 5a29 5a2a 5a2b 5a2c 5a59 5a56 5a57
  //   5a58 5b29 5b2a 5b2b 5b2c 5b59 5b56 5b57 5b58 5c29 5c2a 5c2b 5c2c 5c59 5c56 5c57 5c58 5d29 5d2a 5d2b
  //   5d2c 5d59 5d56 5d57 5d58 5e29 5e2a 5e2b 5e2c 5e59 5e56 5e57 5e58 5f29 5f2a 5f2b 5f2c 5f59 5f56 5f57
  //   5f58 6029 602a 602b 602c 6059 6056 6057 6058 6129 612a 612b 612c 6159 6156 6157 6158 6229 622a 622b
  //   622c 6259 6256 6257 6258 6329 632a 632b 632c 6359 6356 6357 6358 6429 642a 642b 642c 6459 6456 6457
  //   6458 6529 652a 652b 652c 6559 6556 6557 6558 6629 662a 662b 662c 6659 6656 6657 6658 6729 672a 672b
  //   6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
  //   contents of rom_12 (hex, n*v repeats v):
  //   a05 a06 a07 a08 a09 a0a a0b a0c a0d a0e a0f a10 a11 a12 a13 a14 a15 a16 a17 a18 a19 a1a a1b a1c a1d
  //   a1e a1f a20 a21 a22 a23 b05 b06 b07 b08 b09 b0a b0b b0c b0d b0e b0f b10 b11 b12 b13 b14 b15 b16 b17
  //   b18 b19 b1a b1b b1c b1d b1e b1f b20 b21 b22 b23 c05 c06 c07 c08 c09 c0a c0b c0c c0d c0e c0f c10 c11
  //   c12 c13 c14 c15 c16 c17 c18 c19 c1a c1b c1c c1d c1e c1f c20 c21 c22 c23 d05 d06 d07 d08 d09 d0a d0b
  //   d0c d0d d0e d0f d10 d11 d12 d13 d14 d15 d16 d17 d18 d19 d1a d1b d1c d1d d1e d1f d20 d21 d22 d23 e05
  //   e06 e07 e08 e09 e0a e0b e0c e0d e0e e0f e10 e11 e12 e13 e14 e15 e16 e17 e18 e19 e1a e1b e1c e1d e1e
  //   e1f e20 e21 e22 e23 f05 f06 f07 f08 f09 f0a f0b f0c f0d f0e f0f f10 f11 f12 f13 f14 f15 f16 f17 f18
  //   f19 f1a f1b f1c f1d f1e f1f f20 f21 f22 f23 1005 1006 1007 1008 1009 100a 100b 100c 100d 100e 100f
  //   1010 1011 1012 1013 1014 1015 1016 1017 1018 1019 101a 101b 101c 101d 101e 101f 1020 1021 1022 1023
  //   1105 1106 1107 1108 1109 110a 110b 110c 110d 110e 110f 1110 1111 1112 1113 1114 1115 1116 1117 1118
  //   1119 111a 111b 111c 111d 111e 111f 1120 1121 1122 1123 1205 1206 1207 1208 1209 120a 120b 120c 120d
  //   120e 120f 1210 1211 1212 1213 1214 1215 1216 1217 1218 1219 121a 121b 121c 121d 121e 121f 1220 1221
  //   1222 1223 1305 1306 1307 1308 1309 130a 130b 130c 130d 130e 130f 1310 1311 1312 1313 1314 1315 1316
  //   1317 1318 1319 131a 131b 131c 131d 131e 131f 1320 1321 1322 1323 1405 1406 1407 1408 1409 140a 140b
  //   140c 140d 140e 140f 1410 1411 1412 1413 1414 1415 1416 1417 1418 1419 141a 141b 141c 141d 141e 141f
  //   1420 1421 1422 1423 1505 1506 1507 1508 1509 150a 150b 150c 150d 150e 150f 1510 1511 1512 1513 1514
  //   1515 1516 1517 1518 1519 151a 151b 151c 151d 151e 151f 1520 1521 1522 1523 1605 1606 1607 1608 1609
  //   160a 160b 160c 160d 160e 160f 1610 1611 1612 1613 1614 1615 1616 1617 1618 1619 161a 161b 161c 161d
  //   161e 161f 1620 1621 1622 1623 1705 1706 1707 1708 1709 170a 170b 170c 170d 170e 170f 1710 1711 1712
  //   1713 1714 1715 1716 1717 1718 1719 171a 171b 171c 171d 171e 171f 1720 1721 1722 1723 1805 1806 1807
  //   1808 1809 180a 180b 180c 180d 180e 180f 1810 1811 1812 1813 1814 1815 1816 1817 1818 1819 181a 181b
  //   181c 181d 181e 181f 1820 1821 1822 1823 1905 1906 1907 1908 1909 190a 190b 190c 190d 190e 190f 1910
  //   1911 1912 1913 1914 1915 1916 1917 1918 1919 191a 191b 191c 191d 191e 191f 1920 1921 1922 1923 1a05
  //   1a06 1a07 1a08 1a09 1a0a 1a0b 1a0c 1a0d 1a0e 1a0f 1a10 1a11 1a12 1a13 1a14 1a15 1a16 1a17 1a18 1a19
  //   1a1a 1a1b 1a1c 1a1d 1a1e 1a1f 1a20 1a21 1a22 1a23 1b05 1b06 1b07 1b08 1b09 1b0a 1b0b 1b0c 1b0d 1b0e
  //   1b0f 1b10 1b11 1b12 1b13 1b14 1b15 1b16 1b17 1b18 1b19 1b1a 1b1b 1b1c 1b1d 1b1e 1b1f 1b20 1b21 1b22
  //   1b23 1c05 1c06 1c07 1c08 1c09 1c0a 1c0b 1c0c 1c0d 1c0e 1c0f 1c10 1c11 1c12 1c13 1c14 1c15 1c16 1c17
  //   1c18 1c19 1c1a 1c1b 1c1c 1c1d 1c1e 1c1f 1c20 1c21 1c22 1c23 1d05 1d06 1d07 1d08 1d09 1d0a 1d0b 1d0c
  //   1d0d 1d0e 1d0f 1d10 1d11 1d12 1d13 1d14 1d15 1d16 1d17 1d18 1d19 1d1a 1d1b 1d1c 1d1d 1d1e 1d1f 1d20
  //   1d21 1d22 1d23 1e05 1e06 1e07 1e08 1e09 1e0a 1e0b 1e0c 1e0d 1e0e 1e0f 1e10 1e11 1e12 1e13 1e14 1e15
  //   1e16 1e17 1e18 1e19 1e1a 1e1b 1e1c 1e1d 1e1e 1e1f 1e20 1e21 1e22 1e23
endmodule

// 当前寄存器
module \当前寄存器  (
  input  CLK,
  input  RST,
  input  \写入使能 ,
  input  [3:0] \写入数据 ,
  input  [3:0] \X坐标 ,
  input  [3:0] \Y坐标 ,
  input  \更改使能 ,
  input  [3:0] \更改数据 ,
  input  \固有格局 ,
  output \更改1 ,
  output \更改2 ,
  output \更改3 ,
  output \计数已满 ,
  output \更改4 ,
  output \更改5 ,
  output \更改6 ,
  output \选中1 ,
  output \选中9 ,
  output \选中2 ,
  output \选中8 ,
  output \更改7 ,
  output \更改8 ,
  output \更改9 ,
  output [3:0] \宫格内序号 ,
  output \选中3 ,
  output \选中7 ,
  output \选中4 ,
  output \选中6 ,
  output \初始化完毕 ,
  output \选中5 ,
  output [3:0] A_1,
  output [3:0] A_2,
  output [3:0] A_3,
  output [3:0] A_4,
  output [3:0] A_5,
  output [3:0] A_6,
  output [3:0] A_7,
  output [3:0] A_8,
  output [3:0] A_9,
  output [3:0] B_1,
  output [3:0] B_2,
  output [3:0] B_3,
  output [3:0] B_4,
  output [3:0] B_5,
  output [3:0] B_6,
  output [3:0] B_7,
  output [3:0] B_8,
  output [3:0] B_9,
  output [3:0] C_1,
  output [3:0] C_2,
  output [3:0] C_3,
  output [3:0] C_4,
  output [3:0] C_5,
  output [3:0] C_6,
  output [3:0] C_7,
  output [3:0] C_8,
  output [3:0] C_9,
  output [3:0] D_1,
  output [3:0] D_2,
  output [3:0] D_3,
  output [3:0] D_4,
  output [3:0] D_5,
  output [3:0] D_6,
  output [3:0] D_7,
  output [3:0] D_8,
  output [3:0] D_9,
  output [3:0] E_1,
  output [3:0] E_2,
  output [3:0] E_3,
  output [3:0] E_4,
  output [3:0] E_5,
  output [3:0] E_6,
  output [3:0] E_7,
  output [3:0] E_8,
  output [3:0] E_9,
  output [3:0] F_1,
  output [3:0] F_2,
  output [3:0] F_3,
  output [3:0] F_4,
  output [3:0] F_5,
  output [3:0] F_6,
  output [3:0] F_7,
  output [3:0] F_8,
  output [3:0] F_9,
  output [3:0] G_1,
  output [3:0] G_2,
  output [3:0] G_3,
  output [3:0] G_4,
  output [3:0] G_5,
  output [3:0] G_6,
  output [3:0] G_7,
  output [3:0] G_8,
  output [3:0] G_9,
  output [3:0] H_1,
  output [3:0] H_2,
  output [3:0] H_3,
  output [3:0] H_4,
  output [3:0] H_5,
  output [3:0] H_6,
  output [3:0] H_7,
  output [3:0] H_8,
  output [3:0] H_9,
  output [3:0] I_1,
  output [3:0] I_2,
  output [3:0] I_3,
  output [3:0] I_4,
  output [3:0] I_5,
  output [3:0] I_6,
  output [3:0] I_7,
  output [3:0] I_8,
  output [3:0] I_9
);

  wire and_1_out, and_2_out, and_3_out, and_4_out, and_5_out, and_6_out, and_7_out, and_8_out, and_9_out,
       and_10_out, and_11_out, and_12_out, and_13_out, and_14_out, and_15_out, and_16_out, and_17_out,
       and_18_out, and_19_out, and_20_out, and_21_out, and_22_out, and_23_out, and_24_out, and_25_out,
       and_26_out, and_27_out, and_28_out, and_29_out, and_30_out, and_31_out, and_32_out, and_33_out,
       and_34_out, and_35_out, and_36_out, and_37_out, and_38_out, and_39_out, and_40_out, and_41_out,
       and_42_out, and_43_out, and_44_out, and_45_out, and_46_out, and_47_out, and_48_out, and_49_out,
       and_50_out, and_51_out, and_52_out, and_53_out, and_54_out, and_55_out, and_56_out, and_57_out,
       and_58_out, and_59_out, and_60_out, and_61_out, and_62_out, and_63_out, and_64_out, and_65_out,
       and_66_out, and_67_out, and_68_out, and_69_out, and_70_out, and_71_out, and_72_out, and_73_out,
       and_74_out, and_75_out, and_76_out, and_77_out, and_78_out, and_79_out, and_80_out, and_81_out,
       comparator_1_eq, comparator_2_eq, comparator_3_eq, comparator_4_eq, comparator_5_eq, comparator_6_eq,
       comparator_7_eq, comparator_8_eq, comparator_9_eq, comparator_10_eq, comparator_11_eq,
       comparator_12_eq, comparator_13_eq, comparator_14_eq, comparator_15_eq, comparator_16_eq,
       comparator_17_eq, comparator_18_eq, comparator_20_eq, comparator_21_eq, comparator_22_eq,
       comparator_23_eq, comparator_24_eq, comparator_25_eq, comparator_26_eq, comparator_27_eq,
       comparator_28_eq, comparator_29_eq, comparator_30_eq, comparator_31_eq, comparator_32_eq,
       comparator_33_eq, comparator_34_eq, comparator_35_eq, comparator_36_eq, comparator_37_eq,
       comparator_38_eq, comparator_39_eq, comparator_40_eq, comparator_41_eq, comparator_42_eq,
       comparator_43_eq, comparator_44_eq, comparator_45_eq, comparator_46_eq, comparator_47_eq,
       comparator_48_eq, comparator_49_eq, comparator_50_eq, comparator_51_eq, comparator_52_eq,
       comparator_53_eq, comparator_54_eq, comparator_55_eq, comparator_56_eq, comparator_57_eq,
       comparator_58_eq, comparator_59_eq, comparator_60_eq, comparator_61_eq, comparator_62_eq,
       comparator_63_eq, comparator_64_eq, comparator_65_eq, comparator_66_eq, comparator_67_eq,
       comparator_68_eq, comparator_69_eq, comparator_70_eq, comparator_71_eq, comparator_72_eq,
       comparator_73_eq, comparator_74_eq, comparator_75_eq, comparator_76_eq, comparator_77_eq,
       comparator_78_eq, comparator_79_eq, comparator_80_eq, comparator_81_eq, comparator_82_eq, not_1_out,
       \使能 , \未选中宫格 ;
  wire [3:0] subtractor_2_out, subtractor_3_out, \宫格序号 , \数据 ;
  wire [6:0] bit_extender_1_out, bit_extender_2_out, counter_2_q, multiplier_1_out, \寄存器计数 , \计数 , \选中位置 ;

  Comparator #(.width(7), .mode("unsigned")) comparator_1 (
    .a(\计数 ), .b({7{1'b0}}), .eq(comparator_1_eq));  // open: gt, lt
  and and_1 (and_1_out, comparator_1_eq, \使能 );
  Comparator #(.width(7), .mode("unsigned")) comparator_2 (
    .a(\计数 ), .b(7'b0001001), .eq(comparator_2_eq));  // open: gt, lt
  and and_2 (and_2_out, comparator_2_eq, \使能 );
  Comparator #(.width(7), .mode("unsigned")) comparator_3 (
    .a(\计数 ), .b(7'b0010010), .eq(comparator_3_eq));  // open: gt, lt
  and and_3 (and_3_out, comparator_3_eq, \使能 );
  Comparator #(.width(7), .mode("unsigned")) comparator_4 (
    .a(\计数 ), .b(7'b0011011), .eq(comparator_4_eq));  // open: gt, lt
  and and_4 (and_4_out, comparator_4_eq, \使能 );
  Comparator #(.width(7), .mode("unsigned")) comparator_5 (
    .a(\计数 ), .b(7'b0100100), .eq(comparator_5_eq));  // open: gt, lt
  and and_5 (and_5_out, comparator_5_eq, \使能 );
  Comparator #(.width(7), .mode("unsigned")) comparator_6 (
    .a(\计数 ), .b(7'b0101101), .eq(comparator_6_eq));  // open: gt, lt
  and and_6 (and_6_out, comparator_6_eq, \使能 );
  Comparator #(.width(7), .mode("unsigned")) comparator_7 (
    .a(\计数 ), .b(7'b0110110), .eq(comparator_7_eq));  // open: gt, lt
  and and_7 (and_7_out, comparator_7_eq, \使能 );
  Comparator #(.width(7), .mode("unsigned")) comparator_8 (
    .a(\计数 ), .b(7'b0111111), .eq(comparator_8_eq));  // open: gt, lt
  and and_8 (and_8_out, comparator_8_eq, \使能 );
  Comparator #(.width(7), .mode("unsigned")) comparator_9 (
    .a(\计数 ), .b(7'b1001000), .eq(comparator_9_eq));  // open: gt, lt
  and and_9 (and_9_out, comparator_9_eq, \使能 );
  Multiplexer #(.select(1), .width(1), .disabled("Z"), .enable("false")) multiplexer_1 (
    .in0(\写入使能 ), .in1(\更改使能 ), .out(\使能 ), .sel(\更改使能 ));
  Register #(.width(4), .trigger("falling"), .Select("low")) register_1 (
    .D(\数据 ), .en(and_1_out), .Q(A_1), .clk(CLK), .clr(RST));
  Register #(.width(4), .trigger("falling"), .Select("low")) register_2 (
    .D(\数据 ), .en(and_2_out), .Q(B_1), .clk(CLK), .clr(RST));
  Register #(.width(4), .trigger("falling"), .Select("low")) register_3 (
    .D(\数据 ), .en(and_3_out), .Q(C_1), .clk(CLK), .clr(RST));
  Register #(.width(4), .trigger("falling"), .Select("low")) register_4 (
    .D(\数据 ), .en(and_4_out), .Q(D_1), .clk(CLK), .clr(RST));
  Register #(.width(4), .trigger("falling"), .Select("low")) register_5 (
    .D(\数据 ), .en(and_5_out), .Q(E_1), .clk(CLK), .clr(RST));
  Register #(.width(4), .trigger("falling"), .Select("low")) register_6 (
    .D(\数据 ), .en(and_6_out), .Q(F_1), .clk(CLK), .clr(RST));
  Register #(.width(4), .trigger("falling"), .Select("low")) register_7 (
    .D(\数据 ), .en(and_7_out), .Q(G_1), .clk(CLK), .clr(RST));
  Register #(.width(4), .trigger("falling"), .Select("low")) register_8 (
    .D(\数据 ), .en(and_8_out), .Q(H_1), .clk(CLK), .clr(RST));
  Register #(.width(4), .trigger("falling"), .Select("low")) register_9 (
    .D(\数据 ), .en(and_9_out), .Q(I_1), .clk(CLK), .clr(RST));
  Multiplexer #(.select(1), .width(4), .disabled("Z"), .enable("false")) multiplexer_2 (
    .in0(\写入数据 ), .in1(\更改数据 ), .out(\数据 ), .sel(\更改使能 ));
  Comparator #(.width(7), .mode("unsigned")) comparator_10 (
    .a(\计数 ), .b(7'b0000001), .eq(comparator_10_eq));  // open: gt, lt
  Comparator #(.width(7), .mode("unsigned")) comparator_11 (
    .a(\计数 ), .b(7'b0001010), .eq(comparator_11_eq));  // open: gt, lt
  Comparator #(.width(7), .mode("unsigned")) comparator_12 (
    .a(\计数 ), .b(7'b0010011), .eq(comparator_12_eq));  // open: gt, lt
  Comparator #(.width(7), .mode("unsigned")) comparator_13 (
    .a(\计数 ), .b(7'b0011100), .eq(comparator_13_eq));  // open: gt, lt
  Comparator #(.width(7), .mode("unsigned")) comparator_14 (
    .a(\计数 ), .b(7'b0100101), .eq(comparator_14_eq));  // open: gt, lt
  Comparator #(.width(7), .mode("unsigned")) comparator_15 (
    .a(\计数 ), .b(7'b0101110), .eq(comparator_15_eq));  // open: gt, lt
  Comparator #(.width(7), .mode("unsigned")) comparator_16 (
    .a(\计数 ), .b(7'b0110111), .eq(comparator_16_eq));  // open: gt, lt
  Comparator #(.width(7), .mode("unsigned")) comparator_17 (
    .a(\计数 ), .b(7'b1000000), .eq(comparator_17_eq));  // open: gt, lt
  Comparator #(.width(7), .mode("unsigned")) comparator_18 (
    .a(\计数 ), .b(7'b1001001), .eq(comparator_18_eq));  // open: gt, lt
  not not_1 (not_1_out, \计数已满 );
  Counter #(.width(7), .max('h52), .ongoal("continue"), .trigger("rising"), .behavior("new")) counter_1 (
    .count(not_1_out), .carry(\初始化完毕 ), .clk(CLK), .clr(RST));  // open: load, D, Q, preset, down
  and and_10 (and_10_out, comparator_10_eq, \使能 );
  and and_11 (and_11_out, comparator_11_eq, \使能 );
  and and_12 (and_12_out, comparator_12_eq, \使能 );
  and and_13 (and_13_out, comparator_13_eq, \使能 );
  and and_14 (and_14_out, comparator_14_eq, \使能 );
  and and_15 (and_15_out, comparator_15_eq, \使能 );
  and and_16 (and_16_out, comparator_16_eq, \使能 );
  and and_17 (and_17_out, comparator_17_eq, \使能 );
  and and_18 (and_18_out, comparator_18_eq, \使能 );
  Comparator #(.width(7), .mode("unsigned")) comparator_19 (.a(\寄存器计数 ), .b(7'b1010001), .eq(\计数已满 ));  // open: gt, lt
  Register #(.width(4), .trigger("falling"), .Select("low")) register_10 (
    .D(\数据 ), .en(and_10_out), .Q(A_2), .clk(CLK), .clr(RST));
  Register #(.width(4), .trigger("falling"), .Select("low")) register_11 (
    .D(\数据 ), .en(and_11_out), .Q(B_2), .clk(CLK), .clr(RST));
  Register #(.width(4), .trigger("falling"), .Select("low")) register_12 (
    .D(\数据 ), .en(and_12_out), .Q(C_2), .clk(CLK), .clr(RST));
  Register #(.width(4), .trigger("falling"), .Select("low")) register_13 (
    .D(\数据 ), .en(and_13_out), .Q(D_2), .clk(CLK), .clr(RST));
  Register #(.width(4), .trigger("falling"), .Select("low")) register_14 (
    .D(\数据 ), .en(and_14_out), .Q(E_2), .clk(CLK), .clr(RST));
  Register #(.width(4), .trigger("falling"), .Select("low")) register_15 (
    .D(\数据 ), .en(and_15_out), .Q(F_2), .clk(CLK), .clr(RST));
  Register #(.width(4), .trigger("falling"), .Select("low")) register_16 (
    .D(\数据 ), .en(and_16_out), .Q(G_2), .clk(CLK), .clr(RST));
  Register #(.width(4), .trigger("falling"), .Select("low")) register_17 (
    .D(\数据 ), .en(and_17_out), .Q(H_2), .clk(CLK), .clr(RST));
  Register #(.width(4), .trigger("falling"), .Select("low")) register_18 (
    .D(\数据 ), .en(and_18_out), .Q(I_2), .clk(CLK), .clr(RST));
  Counter #(.width(7), .max('h54), .ongoal("stay"), .trigger("rising"), .behavior("new")) counter_2 (
    .count(\使能 ), .Q(counter_2_q), .clk(CLK), .clr(RST));  // open: load, D, carry, preset, down
  Subtractor #(.width(7)) subtractor_1 (.a(counter_2_q), .b(7'b0000011), .out(\寄存器计数 ));  // open: bin, bout
  Comparator #(.width(7), .mode("unsigned")) comparator_20 (
    .a(\计数 ), .b(7'b0000010), .eq(comparator_20_eq));  // open: gt, lt
  Comparator #(.width(7), .mode("unsigned")) comparator_21 (
    .a(\计数 ), .b(7'b0001011), .eq(comparator_21_eq));  // open: gt, lt
  Comparator #(.width(7), .mode("unsigned")) comparator_22 (
    .a(\计数 ), .b(7'b0010100), .eq(comparator_22_eq));  // open: gt, lt
  Comparator #(.width(7), .mode("unsigned")) comparator_23 (
    .a(\计数 ), .b(7'b0011101), .eq(comparator_23_eq));  // open: gt, lt
  Comparator #(.width(7), .mode("unsigned")) comparator_24 (
    .a(\计数 ), .b(7'b0100110), .eq(comparator_24_eq));  // open: gt, lt
  Comparator #(.width(7), .mode("unsigned")) comparator_25 (
    .a(\计数 ), .b(7'b0101111), .eq(comparator_25_eq));  // open: gt, lt
  Comparator #(.width(7), .mode("unsigned")) comparator_26 (
    .a(\计数 ), .b(7'b0111000), .eq(comparator_26_eq));  // open: gt, lt
  Comparator #(.width(7), .mode("unsigned")) comparator_27 (
    .a(\计数 ), .b(7'b1000001), .eq(comparator_27_eq));  // open: gt, lt
  Comparator #(.width(7), .mode("unsigned")) comparator_28 (
    .a(\计数 ), .b(7'b1001010), .eq(comparator_28_eq));  // open: gt, lt
  and and_19 (and_19_out, comparator_20_eq, \使能 );
  and and_20 (and_20_out, comparator_21_eq, \使能 );
  and and_21 (and_21_out, comparator_22_eq, \使能 );
  and and_22 (and_22_out, comparator_23_eq, \使能 );
  and and_23 (and_23_out, comparator_24_eq, \使能 );
  and and_24 (and_24_out, comparator_25_eq, \使能 );
  and and_25 (and_25_out, comparator_26_eq, \使能 );
  and and_26 (and_26_out, comparator_27_eq, \使能 );
  and and_27 (and_27_out, comparator_28_eq, \使能 );
  assign bit_extender_1_out = {{3{1'b0}}, subtractor_2_out};  // Bit_Extender bit_extender_1
  Subtractor #(.width(4)) subtractor_2 (.a(\X坐标 ), .b(4'b0001), .out(subtractor_2_out));  // open: bin, bout
  assign bit_extender_2_out = {{3{1'b0}}, subtractor_3_out};  // Bit_Extender bit_extender_2
  Subtractor #(.width(4)) subtractor_3 (.a(\Y坐标 ), .b(4'b0001), .out(subtractor_3_out));  // open: bin, bout
  Multiplexer #(.select(1), .width(7), .disabled("Z"), .enable("false")) multiplexer_3 (
    .in0(\寄存器计数 ), .in1(\选中位置 ), .out(\计数 ), .sel(\更改使能 ));
  Register #(.width(4), .trigger("falling"), .Select("low")) register_19 (
    .D(\数据 ), .en(and_19_out), .Q(A_3), .clk(CLK), .clr(RST));
  Register #(.width(4), .trigger("falling"), .Select("low")) register_20 (
    .D(\数据 ), .en(and_20_out), .Q(B_3), .clk(CLK), .clr(RST));
  Register #(.width(4), .trigger("falling"), .Select("low")) register_21 (
    .D(\数据 ), .en(and_21_out), .Q(C_3), .clk(CLK), .clr(RST));
  Register #(.width(4), .trigger("falling"), .Select("low")) register_22 (
    .D(\数据 ), .en(and_22_out), .Q(D_3), .clk(CLK), .clr(RST));
  Register #(.width(4), .trigger("falling"), .Select("low")) register_23 (
    .D(\数据 ), .en(and_23_out), .Q(E_3), .clk(CLK), .clr(RST));
  Register #(.width(4), .trigger("falling"), .Select("low")) register_24 (
    .D(\数据 ), .en(and_24_out), .Q(F_3), .clk(CLK), .clr(RST));
  Register #(.width(4), .trigger("falling"), .Select("low")) register_25 (
    .D(\数据 ), .en(and_25_out), .Q(G_3), .clk(CLK), .clr(RST));
  Register #(.width(4), .trigger("falling"), .Select("low")) register_26 (
    .D(\数据 ), .en(and_26_out), .Q(H_3), .clk(CLK), .clr(RST));
  Register #(.width(4), .trigger("falling"), .Select("low")) register_27 (
    .D(\数据 ), .en(and_27_out), .Q(I_3), .clk(CLK), .clr(RST));
  Multiplier #(.width(7)) multiplier_1 (
    .a(bit_extender_2_out), .b(7'b0001001), .out(multiplier_1_out));  // open: cin, cout
  // Probe on \选中位置 
  Adder #(.width(7)) adder_1 (.a(bit_extender_1_out), .b(multiplier_1_out), .out(\选中位置 ));  // open: cin, cout
  Comparator #(.width(7), .mode("unsigned")) comparator_29 (
    .a(\计数 ), .b(7'b0000011), .eq(comparator_29_eq));  // open: gt, lt
  and and_28 (and_28_out, comparator_29_eq, \使能 );
  Comparator #(.width(7), .mode("unsigned")) comparator_30 (
    .a(\计数 ), .b(7'b0001100), .eq(comparator_30_eq));  // open: gt, lt
  and and_29 (and_29_out, comparator_30_eq, \使能 );
  Comparator #(.width(7), .mode("unsigned")) comparator_31 (
    .a(\计数 ), .b(7'b0010101), .eq(comparator_31_eq));  // open: gt, lt
  and and_30 (and_30_out, comparator_31_eq, \使能 );
  Comparator #(.width(7), .mode("unsigned")) comparator_32 (
    .a(\计数 ), .b(7'b0011110), .eq(comparator_32_eq));  // open: gt, lt
  and and_31 (and_31_out, comparator_32_eq, \使能 );
  Comparator #(.width(7), .mode("unsigned")) comparator_33 (
    .a(\计数 ), .b(7'b0100111), .eq(comparator_33_eq));  // open: gt, lt
  and and_32 (and_32_out, comparator_33_eq, \使能 );
  Comparator #(.width(7), .mode("unsigned")) comparator_34 (
    .a(\计数 ), .b(7'b0110000), .eq(comparator_34_eq));  // open: gt, lt
  and and_33 (and_33_out, comparator_34_eq, \使能 );
  Comparator #(.width(7), .mode("unsigned")) comparator_35 (
    .a(\计数 ), .b(7'b0111001), .eq(comparator_35_eq));  // open: gt, lt
  and and_34 (and_34_out, comparator_35_eq, \使能 );
  Comparator #(.width(7), .mode("unsigned")) comparator_36 (
    .a(\计数 ), .b(7'b1000010), .eq(comparator_36_eq));  // open: gt, lt
  and and_35 (and_35_out, comparator_36_eq, \使能 );
  Comparator #(.width(7), .mode("unsigned")) comparator_37 (
    .a(\计数 ), .b(7'b1001011), .eq(comparator_37_eq));  // open: gt, lt
  and and_36 (and_36_out, comparator_37_eq, \使能 );
  \判断坐标宫格  \u_判断坐标宫格_1  (
    .\X坐标 (\X坐标 ), .\Y坐标 (\Y坐标 ), .\未选中宫格 (\未选中宫格 ), .\宫格内位置 (\宫格内序号 ), .\所属宫格位置_从左至右_从上至下_依次为0_8 (\宫格序号 ));
  Register #(.width(4), .trigger("falling"), .Select("low")) register_28 (
    .D(\数据 ), .en(and_28_out), .Q(A_4), .clk(CLK), .clr(RST));
  Register #(.width(4), .trigger("falling"), .Select("low")) register_29 (
    .D(\数据 ), .en(and_29_out), .Q(B_4), .clk(CLK), .clr(RST));
  Register #(.width(4), .trigger("falling"), .Select("low")) register_30 (
    .D(\数据 ), .en(and_30_out), .Q(C_4), .clk(CLK), .clr(RST));
  Register #(.width(4), .trigger("falling"), .Select("low")) register_31 (
    .D(\数据 ), .en(and_31_out), .Q(D_4), .clk(CLK), .clr(RST));
  Register #(.width(4), .trigger("falling"), .Select("low")) register_32 (
    .D(\数据 ), .en(and_32_out), .Q(E_4), .clk(CLK), .clr(RST));
  Register #(.width(4), .trigger("falling"), .Select("low")) register_33 (
    .D(\数据 ), .en(and_33_out), .Q(F_4), .clk(CLK), .clr(RST));
  Register #(.width(4), .trigger("falling"), .Select("low")) register_34 (
    .D(\数据 ), .en(and_34_out), .Q(G_4), .clk(CLK), .clr(RST));
  Register #(.width(4), .trigger("falling"), .Select("low")) register_35 (
    .D(\数据 ), .en(and_35_out), .Q(H_4), .clk(CLK), .clr(RST));
  Register #(.width(4), .trigger("falling"), .Select("low")) register_36 (
    .D(\数据 ), .en(and_36_out), .Q(I_4), .clk(CLK), .clr(RST));
  Comparator #(.width(7), .mode("unsigned")) comparator_38 (
    .a(\计数 ), .b(7'b0000100), .eq(comparator_38_eq));  // open: gt, lt
  Comparator #(.width(7), .mode("unsigned")) comparator_39 (
    .a(\计数 ), .b(7'b0001101), .eq(comparator_39_eq));  // open: gt, lt
  Comparator #(.width(7), .mode("unsigned")) comparator_40 (
    .a(\计数 ), .b(7'b0010110), .eq(comparator_40_eq));  // open: gt, lt
  Comparator #(.width(7), .mode("unsigned")) comparator_41 (
    .a(\计数 ), .b(7'b0011111), .eq(comparator_41_eq));  // open: gt, lt
  Comparator #(.width(7), .mode("unsigned")) comparator_42 (
    .a(\计数 ), .b(7'b0101000), .eq(comparator_42_eq));  // open: gt, lt
  Comparator #(.width(7), .mode("unsigned")) comparator_43 (
    .a(\计数 ), .b(7'b0110001), .eq(comparator_43_eq));  // open: gt, lt
  Comparator #(.width(7), .mode("unsigned")) comparator_44 (
    .a(\计数 ), .b(7'b0111010), .eq(comparator_44_eq));  // open: gt, lt
  Comparator #(.width(7), .mode("unsigned")) comparator_45 (
    .a(\计数 ), .b(7'b1000011), .eq(comparator_45_eq));  // open: gt, lt
  Comparator #(.width(7), .mode("unsigned")) comparator_46 (
    .a(\计数 ), .b(7'b1001100), .eq(comparator_46_eq));  // open: gt, lt
  Demultiplexer #(.select(4), .width(1), .tristate("false"), .disabled("Z"), .enable("false")) demultiplexer_1 (
    .out0(\选中1 ), .out1(\选中2 ), .out2(\选中3 ), .out3(\选中4 ), .out4(\选中5 ), .out5(\选中6 ), .out6(\选中7 ),
    .out7(\选中8 ), .out8(\选中9 ), .in(1'b1), .sel(\宫格序号 ));  // open: out9, out10, out11, out12, out13, out14, out15
  and and_37 (and_37_out, comparator_38_eq, \使能 );
  and and_38 (and_38_out, comparator_39_eq, \使能 );
  and and_39 (and_39_out, comparator_40_eq, \使能 );
  and and_40 (and_40_out, comparator_41_eq, \使能 );
  and and_41 (and_41_out, comparator_42_eq, \使能 );
  and and_42 (and_42_out, comparator_43_eq, \使能 );
  and and_43 (and_43_out, comparator_44_eq, \使能 );
  and and_44 (and_44_out, comparator_45_eq, \使能 );
  and and_45 (and_45_out, comparator_46_eq, \使能 );
  Register #(.width(4), .trigger("falling"), .Select("low")) register_37 (
    .D(\数据 ), .en(and_37_out), .Q(A_5), .clk(CLK), .clr(RST));
  Register #(.width(4), .trigger("falling"), .Select("low")) register_38 (
    .D(\数据 ), .en(and_38_out), .Q(B_5), .clk(CLK), .clr(RST));
  Register #(.width(4), .trigger("falling"), .Select("low")) register_39 (
    .D(\数据 ), .en(and_39_out), .Q(C_5), .clk(CLK), .clr(RST));
  Register #(.width(4), .trigger("falling"), .Select("low")) register_40 (
    .D(\数据 ), .en(and_40_out), .Q(D_5), .clk(CLK), .clr(RST));
  Register #(.width(4), .trigger("falling"), .Select("low")) register_41 (
    .D(\数据 ), .en(and_41_out), .Q(E_5), .clk(CLK), .clr(RST));
  Register #(.width(4), .trigger("falling"), .Select("low")) register_42 (
    .D(\数据 ), .en(and_42_out), .Q(F_5), .clk(CLK), .clr(RST));
  Register #(.width(4), .trigger("falling"), .Select("low")) register_43 (
    .D(\数据 ), .en(and_43_out), .Q(G_5), .clk(CLK), .clr(RST));
  Register #(.width(4), .trigger("falling"), .Select("low")) register_44 (
    .D(\数据 ), .en(and_44_out), .Q(H_5), .clk(CLK), .clr(RST));
  Register #(.width(4), .trigger("falling"), .Select("low")) register_45 (
    .D(\数据 ), .en(and_45_out), .Q(I_5), .clk(CLK), .clr(RST));
  Comparator #(.width(7), .mode("unsigned")) comparator_47 (
    .a(\计数 ), .b(7'b0000101), .eq(comparator_47_eq));  // open: gt, lt
  Comparator #(.width(7), .mode("unsigned")) comparator_48 (
    .a(\计数 ), .b(7'b0001110), .eq(comparator_48_eq));  // open: gt, lt
  Comparator #(.width(7), .mode("unsigned")) comparator_49 (
    .a(\计数 ), .b(7'b0010111), .eq(comparator_49_eq));  // open: gt, lt
  Comparator #(.width(7), .mode("unsigned")) comparator_50 (
    .a(\计数 ), .b(7'b0100000), .eq(comparator_50_eq));  // open: gt, lt
  Comparator #(.width(7), .mode("unsigned")) comparator_51 (
    .a(\计数 ), .b(7'b0101001), .eq(comparator_51_eq));  // open: gt, lt
  Comparator #(.width(7), .mode("unsigned")) comparator_52 (
    .a(\计数 ), .b(7'b0110010), .eq(comparator_52_eq));  // open: gt, lt
  Comparator #(.width(7), .mode("unsigned")) comparator_53 (
    .a(\计数 ), .b(7'b0111011), .eq(comparator_53_eq));  // open: gt, lt
  Comparator #(.width(7), .mode("unsigned")) comparator_54 (
    .a(\计数 ), .b(7'b1000100), .eq(comparator_54_eq));  // open: gt, lt
  Comparator #(.width(7), .mode("unsigned")) comparator_55 (
    .a(\计数 ), .b(7'b1001101), .eq(comparator_55_eq));  // open: gt, lt
  and and_46 (and_46_out, comparator_47_eq, \使能 );
  and and_47 (and_47_out, comparator_48_eq, \使能 );
  and and_48 (and_48_out, comparator_49_eq, \使能 );
  and and_49 (and_49_out, comparator_50_eq, \使能 );
  and and_50 (and_50_out, comparator_51_eq, \使能 );
  and and_51 (and_51_out, comparator_52_eq, \使能 );
  and and_52 (and_52_out, comparator_53_eq, \使能 );
  and and_53 (and_53_out, comparator_54_eq, \使能 );
  and and_54 (and_54_out, comparator_55_eq, \使能 );
  Register #(.width(4), .trigger("falling"), .Select("low")) register_46 (
    .D(\数据 ), .en(and_46_out), .Q(A_6), .clk(CLK), .clr(RST));
  Register #(.width(4), .trigger("falling"), .Select("low")) register_47 (
    .D(\数据 ), .en(and_47_out), .Q(B_6), .clk(CLK), .clr(RST));
  Register #(.width(4), .trigger("falling"), .Select("low")) register_48 (
    .D(\数据 ), .en(and_48_out), .Q(C_6), .clk(CLK), .clr(RST));
  Register #(.width(4), .trigger("falling"), .Select("low")) register_49 (
    .D(\数据 ), .en(and_49_out), .Q(D_6), .clk(CLK), .clr(RST));
  Register #(.width(4), .trigger("falling"), .Select("low")) register_50 (
    .D(\数据 ), .en(and_50_out), .Q(E_6), .clk(CLK), .clr(RST));
  Register #(.width(4), .trigger("falling"), .Select("low")) register_51 (
    .D(\数据 ), .en(and_51_out), .Q(F_6), .clk(CLK), .clr(RST));
  Register #(.width(4), .trigger("falling"), .Select("low")) register_52 (
    .D(\数据 ), .en(and_52_out), .Q(G_6), .clk(CLK), .clr(RST));
  Register #(.width(4), .trigger("falling"), .Select("low")) register_53 (
    .D(\数据 ), .en(and_53_out), .Q(H_6), .clk(CLK), .clr(RST));
  Register #(.width(4), .trigger("falling"), .Select("low")) register_54 (
    .D(\数据 ), .en(and_54_out), .Q(I_6), .clk(CLK), .clr(RST));
  Comparator #(.width(7), .mode("unsigned")) comparator_56 (
    .a(\计数 ), .b(7'b0000110), .eq(comparator_56_eq));  // open: gt, lt
  and and_55 (and_55_out, comparator_56_eq, \使能 );
  Comparator #(.width(7), .mode("unsigned")) comparator_57 (
    .a(\计数 ), .b(7'b0001111), .eq(comparator_57_eq));  // open: gt, lt
  and and_56 (and_56_out, comparator_57_eq, \使能 );
  Comparator #(.width(7), .mode("unsigned")) comparator_58 (
    .a(\计数 ), .b(7'b0011000), .eq(comparator_58_eq));  // open: gt, lt
  and and_57 (and_57_out, comparator_58_eq, \使能 );
  Comparator #(.width(7), .mode("unsigned")) comparator_59 (
    .a(\计数 ), .b(7'b0100001), .eq(comparator_59_eq));  // open: gt, lt
  and and_58 (and_58_out, comparator_59_eq, \使能 );
  Comparator #(.width(7), .mode("unsigned")) comparator_60 (
    .a(\计数 ), .b(7'b0101010), .eq(comparator_60_eq));  // open: gt, lt
  and and_59 (and_59_out, comparator_60_eq, \使能 );
  Comparator #(.width(7), .mode("unsigned")) comparator_61 (
    .a(\计数 ), .b(7'b0110011), .eq(comparator_61_eq));  // open: gt, lt
  and and_60 (and_60_out, comparator_61_eq, \使能 );
  Comparator #(.width(7), .mode("unsigned")) comparator_62 (
    .a(\计数 ), .b(7'b0111100), .eq(comparator_62_eq));  // open: gt, lt
  and and_61 (and_61_out, comparator_62_eq, \使能 );
  Comparator #(.width(7), .mode("unsigned")) comparator_63 (
    .a(\计数 ), .b(7'b1000101), .eq(comparator_63_eq));  // open: gt, lt
  and and_62 (and_62_out, comparator_63_eq, \使能 );
  Comparator #(.width(7), .mode("unsigned")) comparator_64 (
    .a(\计数 ), .b(7'b1001110), .eq(comparator_64_eq));  // open: gt, lt
  and and_63 (and_63_out, comparator_64_eq, \使能 );
  Register #(.width(4), .trigger("falling"), .Select("low")) register_55 (
    .D(\数据 ), .en(and_55_out), .Q(A_7), .clk(CLK), .clr(RST));
  Register #(.width(4), .trigger("falling"), .Select("low")) register_56 (
    .D(\数据 ), .en(and_56_out), .Q(B_7), .clk(CLK), .clr(RST));
  Register #(.width(4), .trigger("falling"), .Select("low")) register_57 (
    .D(\数据 ), .en(and_57_out), .Q(C_7), .clk(CLK), .clr(RST));
  Register #(.width(4), .trigger("falling"), .Select("low")) register_58 (
    .D(\数据 ), .en(and_58_out), .Q(D_7), .clk(CLK), .clr(RST));
  Register #(.width(4), .trigger("falling"), .Select("low")) register_59 (
    .D(\数据 ), .en(and_59_out), .Q(E_7), .clk(CLK), .clr(RST));
  Register #(.width(4), .trigger("falling"), .Select("low")) register_60 (
    .D(\数据 ), .en(and_60_out), .Q(F_7), .clk(CLK), .clr(RST));
  Register #(.width(4), .trigger("falling"), .Select("low")) register_61 (
    .D(\数据 ), .en(and_61_out), .Q(G_7), .clk(CLK), .clr(RST));
  Register #(.width(4), .trigger("falling"), .Select("low")) register_62 (
    .D(\数据 ), .en(and_62_out), .Q(H_7), .clk(CLK), .clr(RST));
  Register #(.width(4), .trigger("falling"), .Select("low")) register_63 (
    .D(\数据 ), .en(and_63_out), .Q(I_7), .clk(CLK), .clr(RST));
  Comparator #(.width(7), .mode("unsigned")) comparator_65 (
    .a(\计数 ), .b(7'b0000111), .eq(comparator_65_eq));  // open: gt, lt
  Comparator #(.width(7), .mode("unsigned")) comparator_66 (
    .a(\计数 ), .b(7'b0010000), .eq(comparator_66_eq));  // open: gt, lt
  Comparator #(.width(7), .mode("unsigned")) comparator_67 (
    .a(\计数 ), .b(7'b0011001), .eq(comparator_67_eq));  // open: gt, lt
  Comparator #(.width(7), .mode("unsigned")) comparator_68 (
    .a(\计数 ), .b(7'b0100010), .eq(comparator_68_eq));  // open: gt, lt
  Comparator #(.width(7), .mode("unsigned")) comparator_69 (
    .a(\计数 ), .b(7'b0101011), .eq(comparator_69_eq));  // open: gt, lt
  Comparator #(.width(7), .mode("unsigned")) comparator_70 (
    .a(\计数 ), .b(7'b0110100), .eq(comparator_70_eq));  // open: gt, lt
  Comparator #(.width(7), .mode("unsigned")) comparator_71 (
    .a(\计数 ), .b(7'b0111101), .eq(comparator_71_eq));  // open: gt, lt
  Comparator #(.width(7), .mode("unsigned")) comparator_72 (
    .a(\计数 ), .b(7'b1000110), .eq(comparator_72_eq));  // open: gt, lt
  Comparator #(.width(7), .mode("unsigned")) comparator_73 (
    .a(\计数 ), .b(7'b1001111), .eq(comparator_73_eq));  // open: gt, lt
  and and_64 (and_64_out, comparator_65_eq, \使能 );
  and and_65 (and_65_out, comparator_66_eq, \使能 );
  and and_66 (and_66_out, comparator_67_eq, \使能 );
  and and_67 (and_67_out, comparator_68_eq, \使能 );
  and and_68 (and_68_out, comparator_69_eq, \使能 );
  and and_69 (and_69_out, comparator_70_eq, \使能 );
  and and_70 (and_70_out, comparator_71_eq, \使能 );
  and and_71 (and_71_out, comparator_72_eq, \使能 );
  and and_72 (and_72_out, comparator_73_eq, \使能 );
  Register #(.width(4), .trigger("falling"), .Select("low")) register_64 (
    .D(\数据 ), .en(and_64_out), .Q(A_8), .clk(CLK), .clr(RST));
  Register #(.width(4), .trigger("falling"), .Select("low")) register_65 (
    .D(\数据 ), .en(and_65_out), .Q(B_8), .clk(CLK), .clr(RST));
  Register #(.width(4), .trigger("falling"), .Select("low")) register_66 (
    .D(\数据 ), .en(and_66_out), .Q(C_8), .clk(CLK), .clr(RST));
  Register #(.width(4), .trigger("falling"), .Select("low")) register_67 (
    .D(\数据 ), .en(and_67_out), .Q(D_8), .clk(CLK), .clr(RST));
  Register #(.width(4), .trigger("falling"), .Select("low")) register_68 (
    .D(\数据 ), .en(and_68_out), .Q(E_8), .clk(CLK), .clr(RST));
  Register #(.width(4), .trigger("falling"), .Select("low")) register_69 (
    .D(\数据 ), .en(and_69_out), .Q(F_8), .clk(CLK), .clr(RST));
  Register #(.width(4), .trigger("falling"), .Select("low")) register_70 (
    .D(\数据 ), .en(and_70_out), .Q(G_8), .clk(CLK), .clr(RST));
  Register #(.width(4), .trigger("falling"), .Select("low")) register_71 (
    .D(\数据 ), .en(and_71_out), .Q(H_8), .clk(CLK), .clr(RST));
  Register #(.width(4), .trigger("falling"), .Select("low")) register_72 (
    .D(\数据 ), .en(and_72_out), .Q(I_8), .clk(CLK), .clr(RST));
  Comparator #(.width(7), .mode("unsigned")) comparator_74 (
    .a(\计数 ), .b(7'b0001000), .eq(comparator_74_eq));  // open: gt, lt
  Comparator #(.width(7), .mode("unsigned")) comparator_75 (
    .a(\计数 ), .b(7'b0010001), .eq(comparator_75_eq));  // open: gt, lt
  Comparator #(.width(7), .mode("unsigned")) comparator_76 (
    .a(\计数 ), .b(7'b0011010), .eq(comparator_76_eq));  // open: gt, lt
  Comparator #(.width(7), .mode("unsigned")) comparator_77 (
    .a(\计数 ), .b(7'b0100011), .eq(comparator_77_eq));  // open: gt, lt
  Comparator #(.width(7), .mode("unsigned")) comparator_78 (
    .a(\计数 ), .b(7'b0101100), .eq(comparator_78_eq));  // open: gt, lt
  Comparator #(.width(7), .mode("unsigned")) comparator_79 (
    .a(\计数 ), .b(7'b0110101), .eq(comparator_79_eq));  // open: gt, lt
  Comparator #(.width(7), .mode("unsigned")) comparator_80 (
    .a(\计数 ), .b(7'b0111110), .eq(comparator_80_eq));  // open: gt, lt
  Comparator #(.width(7), .mode("unsigned")) comparator_81 (
    .a(\计数 ), .b(7'b1000111), .eq(comparator_81_eq));  // open: gt, lt
  Comparator #(.width(7), .mode("unsigned")) comparator_82 (
    .a(\计数 ), .b(7'b1010000), .eq(comparator_82_eq));  // open: gt, lt
  and and_73 (and_73_out, comparator_74_eq, \使能 );
  and and_74 (and_74_out, comparator_75_eq, \使能 );
  and and_75 (and_75_out, comparator_76_eq, \使能 );
  and and_76 (and_76_out, comparator_77_eq, \使能 );
  and and_77 (and_77_out, comparator_78_eq, \使能 );
  and and_78 (and_78_out, comparator_79_eq, \使能 );
  and and_79 (and_79_out, comparator_80_eq, \使能 );
  and and_80 (and_80_out, comparator_81_eq, \使能 );
  and and_81 (and_81_out, comparator_82_eq, \使能 );
  Register #(.width(4), .trigger("falling"), .Select("low")) register_73 (
    .D(\数据 ), .en(and_73_out), .Q(A_9), .clk(CLK), .clr(RST));
  Register #(.width(4), .trigger("falling"), .Select("low")) register_74 (
    .D(\数据 ), .en(and_74_out), .Q(B_9), .clk(CLK), .clr(RST));
  Register #(.width(4), .trigger("falling"), .Select("low")) register_75 (
    .D(\数据 ), .en(and_75_out), .Q(C_9), .clk(CLK), .clr(RST));
  Register #(.width(4), .trigger("falling"), .Select("low")) register_76 (
    .D(\数据 ), .en(and_76_out), .Q(D_9), .clk(CLK), .clr(RST));
  Register #(.width(4), .trigger("falling"), .Select("low")) register_77 (
    .D(\数据 ), .en(and_77_out), .Q(E_9), .clk(CLK), .clr(RST));
  Register #(.width(4), .trigger("falling"), .Select("low")) register_78 (
    .D(\数据 ), .en(and_78_out), .Q(F_9), .clk(CLK), .clr(RST));
  Register #(.width(4), .trigger("falling"), .Select("low")) register_79 (
    .D(\数据 ), .en(and_79_out), .Q(G_9), .clk(CLK), .clr(RST));
  Register #(.width(4), .trigger("falling"), .Select("low")) register_80 (
    .D(\数据 ), .en(and_80_out), .Q(H_9), .clk(CLK), .clr(RST));
  Register #(.width(4), .trigger("falling"), .Select("low")) register_81 (
    .D(\数据 ), .en(and_81_out), .Q(I_9), .clk(CLK), .clr(RST));

  assign \更改1  = \更改使能 ;
  assign \更改2  = \更改使能 ;
  assign \更改3  = \更改使能 ;
  assign \更改4  = \更改使能 ;
  assign \更改5  = \更改使能 ;
  assign \更改6  = \更改使能 ;
  assign \更改7  = \更改使能 ;
  assign \更改8  = \更改使能 ;
  assign \更改9  = \更改使能 ;
endmodule
// 初盘寄存器
module \初盘寄存器  (
  input  CLK,
  input  [3:0] \X坐标 ,
  input  RST,
  input  [3:0] \Y坐标 ,
  input  [3:0] \数据 ,
  input  \写入使能 ,
  output [3:0] NextRight,
  output [3:0] NextUp,
  output \固有坐标 ,
  output [3:0] \首个空格X坐标 ,
  output [3:0] NextLeft,
  output [3:0] NextDown,
  output [3:0] \首个空格Y坐标 ,
  output \跳转到下一行 ,
  output \跳转到上一行 
);

  wire and_1_out, and_2_out, and_3_out, and_4_out, and_5_out, and_6_out, and_7_out, and_8_out, and_9_out,
       and_10_out, and_11_out, and_12_out, and_13_out, and_14_out, and_15_out, and_16_out, and_17_out,
       and_18_out, and_19_out, and_20_out, and_21_out, and_22_out, and_23_out, and_24_out, and_25_out,
       and_26_out, and_27_out, and_29_out, and_30_out, and_31_out, and_32_out, and_33_out, and_34_out,
       and_35_out, and_36_out, and_37_out, and_38_out, and_39_out, and_40_out, and_41_out, and_42_out,
       and_43_out, and_44_out, and_45_out, and_46_out, and_47_out, and_48_out, and_50_out, and_51_out,
       and_52_out, and_53_out, and_54_out, and_55_out, and_56_out, and_57_out, and_58_out, and_59_out,
       and_60_out, and_61_out, and_62_out, and_63_out, and_64_out, and_65_out, and_66_out, and_67_out,
       and_68_out, and_69_out, and_70_out, and_71_out, and_72_out, and_73_out, and_74_out, and_75_out,
       and_76_out, and_77_out, and_78_out, and_79_out, and_80_out, and_81_out, and_82_out, and_83_out,
       and_84_out, and_85_out, and_86_out, and_87_out, and_88_out, and_89_out, and_90_out, and_91_out,
       and_92_out, and_93_out, and_94_out, and_95_out, and_96_out, and_97_out, and_98_out, and_99_out,
       and_100_out, and_101_out, and_102_out, and_103_out, and_104_out, and_105_out, and_106_out,
       and_107_out, and_108_out, and_109_out, and_110_out, and_111_out, and_112_out, and_113_out,
       and_114_out, and_115_out, and_116_out, and_117_out, and_118_out, and_119_out, and_120_out,
       and_121_out, comparator_1_eq, comparator_2_eq, comparator_3_eq, comparator_4_eq, comparator_5_eq,
       comparator_6_eq, comparator_7_eq, comparator_8_eq, comparator_9_eq, comparator_10_eq,
       comparator_11_gt, comparator_12_eq, comparator_13_gt, comparator_14_eq, comparator_15_gt,
       comparator_16_eq, comparator_17_gt, comparator_18_eq, comparator_19_gt, comparator_20_eq,
       comparator_21_gt, comparator_22_eq, comparator_23_gt, comparator_24_eq, comparator_25_gt,
       comparator_26_eq, comparator_27_gt, comparator_28_eq, comparator_29_eq, comparator_30_eq,
       comparator_31_eq, comparator_32_eq, comparator_33_eq, comparator_34_eq, comparator_35_eq,
       comparator_36_eq, comparator_37_eq, comparator_38_eq, comparator_39_eq, comparator_40_eq,
       comparator_41_eq, comparator_42_eq, comparator_43_eq, comparator_44_eq, comparator_45_eq,
       comparator_46_eq, comparator_47_eq, comparator_48_lt, comparator_49_eq, comparator_50_lt,
       comparator_51_eq, comparator_52_lt, comparator_53_eq, comparator_54_lt, comparator_55_eq,
       comparator_56_lt, comparator_57_eq, comparator_58_lt, comparator_59_eq, comparator_60_lt,
       comparator_61_eq, comparator_62_lt, comparator_63_eq, comparator_64_lt, comparator_65_eq,
       comparator_66_eq, comparator_67_eq, comparator_68_eq, comparator_69_eq, comparator_70_eq,
       comparator_71_eq, comparator_72_eq, comparator_73_eq, comparator_74_eq, comparator_76_eq,
       comparator_77_eq, comparator_78_eq, comparator_79_eq, comparator_80_eq, comparator_81_eq,
       comparator_82_eq, comparator_83_eq, comparator_84_eq, comparator_85_eq, comparator_86_eq,
       comparator_87_eq, comparator_88_eq, comparator_89_eq, comparator_90_eq, comparator_91_eq,
       comparator_92_eq, comparator_93_eq, comparator_94_eq, comparator_95_eq, comparator_96_eq,
       comparator_97_eq, comparator_98_eq, comparator_99_eq, comparator_100_eq, comparator_101_eq,
       comparator_102_eq, comparator_103_eq, comparator_104_gt, comparator_105_eq, comparator_106_gt,
       comparator_107_eq, comparator_108_gt, comparator_109_eq, comparator_110_gt, comparator_111_eq,
       comparator_112_gt, comparator_113_eq, comparator_114_gt, comparator_115_eq, comparator_116_gt,
       comparator_117_eq, comparator_118_gt, comparator_119_eq, comparator_120_gt, comparator_121_eq,
       comparator_122_eq, comparator_123_eq, comparator_124_eq, comparator_125_eq, comparator_126_eq,
       comparator_127_eq, comparator_128_eq, comparator_129_eq, comparator_130_eq, comparator_131_eq,
       comparator_132_eq, comparator_133_eq, comparator_134_eq, comparator_135_eq, comparator_136_eq,
       comparator_137_eq, comparator_138_eq, comparator_139_eq, comparator_140_lt, comparator_141_eq,
       comparator_142_lt, comparator_143_eq, comparator_144_lt, comparator_145_eq, comparator_146_lt,
       comparator_147_eq, comparator_148_lt, comparator_149_eq, comparator_150_lt, comparator_151_eq,
       comparator_152_lt, comparator_153_eq, comparator_154_lt, comparator_155_eq, comparator_156_lt,
       comparator_157_eq, comparator_158_eq, comparator_159_eq, comparator_160_eq, comparator_161_eq,
       comparator_162_eq, comparator_163_eq, comparator_164_eq, comparator_165_eq, comparator_166_eq,
       comparator_167_eq, comparator_168_eq, comparator_169_eq, comparator_170_eq, comparator_171_eq,
       comparator_172_eq, comparator_173_eq, comparator_174_eq, comparator_175_eq, comparator_176_eq,
       comparator_177_eq, comparator_178_eq, comparator_179_eq, comparator_180_eq, comparator_181_eq,
       comparator_182_eq, comparator_183_eq, comparator_184_eq, comparator_185_eq, comparator_186_eq,
       comparator_187_eq, comparator_188_eq, comparator_189_eq, comparator_190_eq, comparator_191_eq,
       comparator_192_eq, comparator_193_eq, comparator_194_eq, comparator_195_eq, comparator_196_eq,
       comparator_197_eq, comparator_198_eq, comparator_199_eq, comparator_200_eq, comparator_201_eq,
       comparator_202_eq, comparator_203_eq, comparator_204_eq, comparator_205_eq, comparator_206_eq,
       comparator_207_eq, comparator_208_eq, comparator_209_eq, comparator_210_eq, comparator_211_eq,
       comparator_212_eq, comparator_213_eq, comparator_214_eq, comparator_215_eq, comparator_216_eq,
       comparator_217_eq, comparator_218_eq, comparator_219_eq, comparator_220_eq, comparator_221_eq,
       comparator_222_eq, comparator_223_eq, comparator_224_eq, comparator_225_eq, comparator_226_eq,
       comparator_227_eq, comparator_228_eq, comparator_229_eq, comparator_230_eq, comparator_231_eq,
       comparator_232_eq, comparator_233_eq, comparator_234_eq, comparator_235_eq, comparator_236_eq,
       comparator_237_eq, comparator_238_eq, comparator_239_eq, comparator_240_eq, comparator_241_eq,
       comparator_242_eq, comparator_243_eq, comparator_244_eq, comparator_245_eq, comparator_246_eq,
       comparator_247_eq, comparator_248_eq, comparator_249_eq, comparator_250_eq, comparator_251_eq,
       comparator_252_eq, comparator_253_eq, comparator_254_eq, comparator_255_eq, priority_encoder_1_en_out,
       priority_encoder_3_en_out, priority_encoder_5_en_out, priority_encoder_6_en_out, undriven, \行1包含空格 ,
       \行2包含空格 , \行3包含空格 , \行4包含空格 , \行5包含空格 , \行6包含空格 , \行7包含空格 , \行8包含空格 , \行9包含空格 ;
  wire [3:0] A1, A2, A3, A4, A5, A6, A7, A8, A9, B1, B2, B3, B4, B5, B6, B7, B8, B9, C1, C2, C3, C4, C5, C6,
       C7, C8, C9, D1, D2, D3, D4, D5, D6, D7, D8, D9, E1, E2, E3, E4, E5, E6, E7, E8, E9, F1, F2, F3, F4,
       F5, F6, F7, F8, F9, G1, G2, G3, G4, G5, G6, G7, G8, G9, H1, H2, H3, H4, H5, H6, H7, H8, H9, I1, I2,
       I3, I4, I5, I6, I7, I8, I9, multiplexer_1_out, multiplexer_10_out, priority_encoder_1_out,
       priority_encoder_2_out, priority_encoder_3_out, priority_encoder_5_out, priority_encoder_6_out,
       priority_encoder_7_out, priority_encoder_8_out, priority_encoder_9_out, priority_encoder_10_out,
       priority_encoder_11_out, priority_encoder_12_out, priority_encoder_13_out, priority_encoder_14_out,
       priority_encoder_15_out, priority_encoder_16_out, subtractor_2_out, subtractor_5_out, \上一行Y坐标 ,
       \上一行列1 , \上一行列2 , \上一行列3 , \上一行列4 , \上一行列5 , \上一行列6 , \上一行列7 , \上一行列8 , \上一行列9 , \上一行末空 , \下一行Y坐标 ,
       \下一行列1 , \下一行列2 , \下一行列3 , \下一行列4 , \下一行列5 , \下一行列6 , \下一行列7 , \下一行列8 , \下一行列9 , \下一行首空 , \列1 , \列2 ,
       \列3 , \列4 , \列5 , \列6 , \列7 , \列8 , \列9 , \行1 , \行1空格坐标 , \行2 , \行2空格坐标 , \行3 , \行3空格坐标 , \行4 ,
       \行4空格坐标 , \行5 , \行5空格坐标 , \行6 , \行6空格坐标 , \行7 , \行7空格坐标 , \行8 , \行8空格坐标 , \行9 , \行9空格坐标 , \选中数据 ;
  wire [6:0] counter_1_q, \计数 ;

  Comparator #(.width(7), .mode("unsigned")) comparator_1 (
    .a(\计数 ), .b({7{1'b0}}), .eq(comparator_1_eq));  // open: gt, lt
  Comparator #(.width(7), .mode("unsigned")) comparator_2 (
    .a(\计数 ), .b(7'b0001001), .eq(comparator_2_eq));  // open: gt, lt
  Comparator #(.width(7), .mode("unsigned")) comparator_3 (
    .a(\计数 ), .b(7'b0010010), .eq(comparator_3_eq));  // open: gt, lt
  Comparator #(.width(7), .mode("unsigned")) comparator_4 (
    .a(\计数 ), .b(7'b0011011), .eq(comparator_4_eq));  // open: gt, lt
  Comparator #(.width(7), .mode("unsigned")) comparator_5 (
    .a(\计数 ), .b(7'b0100100), .eq(comparator_5_eq));  // open: gt, lt
  Comparator #(.width(7), .mode("unsigned")) comparator_6 (
    .a(\计数 ), .b(7'b0101101), .eq(comparator_6_eq));  // open: gt, lt
  Comparator #(.width(7), .mode("unsigned")) comparator_7 (
    .a(\计数 ), .b(7'b0110110), .eq(comparator_7_eq));  // open: gt, lt
  Comparator #(.width(7), .mode("unsigned")) comparator_8 (
    .a(\计数 ), .b(7'b0111111), .eq(comparator_8_eq));  // open: gt, lt
  Comparator #(.width(7), .mode("unsigned")) comparator_9 (
    .a(\计数 ), .b(7'b1001000), .eq(comparator_9_eq));  // open: gt, lt
  and and_1 (and_1_out, comparator_1_eq, \写入使能 );
  and and_2 (and_2_out, comparator_2_eq, \写入使能 );
  and and_3 (and_3_out, comparator_3_eq, \写入使能 );
  and and_4 (and_4_out, comparator_4_eq, \写入使能 );
  and and_5 (and_5_out, comparator_5_eq, \写入使能 );
  and and_6 (and_6_out, comparator_6_eq, \写入使能 );
  and and_7 (and_7_out, comparator_7_eq, \写入使能 );
  and and_8 (and_8_out, comparator_8_eq, \写入使能 );
  and and_9 (and_9_out, comparator_9_eq, \写入使能 );
  Comparator #(.width(4), .mode("unsigned")) comparator_10 (
    .a(\列9 ), .b(4'b0000), .eq(comparator_10_eq));  // open: gt, lt
  and and_10 (and_10_out, comparator_10_eq, comparator_11_gt);
  Comparator #(.width(4), .mode("unsigned")) comparator_11 (
    .a(4'b1001), .b(\X坐标 ), .gt(comparator_11_gt));  // open: eq, lt
  Comparator #(.width(4), .mode("unsigned")) comparator_12 (
    .a(\列8 ), .b(4'b0000), .eq(comparator_12_eq));  // open: gt, lt
  and and_11 (and_11_out, comparator_12_eq, comparator_13_gt);
  Comparator #(.width(4), .mode("unsigned")) comparator_13 (
    .a(4'b1000), .b(\X坐标 ), .gt(comparator_13_gt));  // open: eq, lt
  Comparator #(.width(4), .mode("unsigned")) comparator_14 (
    .a(\列7 ), .b(4'b0000), .eq(comparator_14_eq));  // open: gt, lt
  and and_12 (and_12_out, comparator_14_eq, comparator_15_gt);
  Comparator #(.width(4), .mode("unsigned")) comparator_15 (
    .a(4'b0111), .b(\X坐标 ), .gt(comparator_15_gt));  // open: eq, lt
  Comparator #(.width(4), .mode("unsigned")) comparator_16 (
    .a(\列6 ), .b(4'b0000), .eq(comparator_16_eq));  // open: gt, lt
  and and_13 (and_13_out, comparator_16_eq, comparator_17_gt);
  Comparator #(.width(4), .mode("unsigned")) comparator_17 (
    .a(4'b0110), .b(\X坐标 ), .gt(comparator_17_gt));  // open: eq, lt
  Comparator #(.width(4), .mode("unsigned")) comparator_18 (
    .a(\列5 ), .b(4'b0000), .eq(comparator_18_eq));  // open: gt, lt
  and and_14 (and_14_out, comparator_18_eq, comparator_19_gt);
  Comparator #(.width(4), .mode("unsigned")) comparator_19 (
    .a(4'b0101), .b(\X坐标 ), .gt(comparator_19_gt));  // open: eq, lt
  Comparator #(.width(4), .mode("unsigned")) comparator_20 (
    .a(\列4 ), .b(4'b0000), .eq(comparator_20_eq));  // open: gt, lt
  and and_15 (and_15_out, comparator_20_eq, comparator_21_gt);
  Comparator #(.width(4), .mode("unsigned")) comparator_21 (
    .a(4'b0100), .b(\X坐标 ), .gt(comparator_21_gt));  // open: eq, lt
  Comparator #(.width(4), .mode("unsigned")) comparator_22 (
    .a(\列3 ), .b(4'b0000), .eq(comparator_22_eq));  // open: gt, lt
  and and_16 (and_16_out, comparator_22_eq, comparator_23_gt);
  Comparator #(.width(4), .mode("unsigned")) comparator_23 (
    .a(4'b0011), .b(\X坐标 ), .gt(comparator_23_gt));  // open: eq, lt
  Comparator #(.width(4), .mode("unsigned")) comparator_24 (
    .a(\列2 ), .b(4'b0000), .eq(comparator_24_eq));  // open: gt, lt
  and and_17 (and_17_out, comparator_24_eq, comparator_25_gt);
  Comparator #(.width(4), .mode("unsigned")) comparator_25 (
    .a(4'b0010), .b(\X坐标 ), .gt(comparator_25_gt));  // open: eq, lt
  Comparator #(.width(4), .mode("unsigned")) comparator_26 (
    .a(\列1 ), .b(4'b0000), .eq(comparator_26_eq));  // open: gt, lt
  and and_18 (and_18_out, comparator_26_eq, comparator_27_gt);
  Comparator #(.width(4), .mode("unsigned")) comparator_27 (
    .a(4'b0001), .b(\X坐标 ), .gt(comparator_27_gt));  // open: eq, lt
  Comparator #(.width(4), .mode("unsigned")) comparator_28 (
    .a(\下一行列9 ), .b(4'b0000), .eq(comparator_28_eq));  // open: gt, lt
  Comparator #(.width(4), .mode("unsigned")) comparator_29 (
    .a(\下一行列8 ), .b(4'b0000), .eq(comparator_29_eq));  // open: gt, lt
  Comparator #(.width(4), .mode("unsigned")) comparator_30 (
    .a(\下一行列7 ), .b(4'b0000), .eq(comparator_30_eq));  // open: gt, lt
  Comparator #(.width(4), .mode("unsigned")) comparator_31 (
    .a(\下一行列6 ), .b(4'b0000), .eq(comparator_31_eq));  // open: gt, lt
  Comparator #(.width(4), .mode("unsigned")) comparator_32 (
    .a(\下一行列5 ), .b(4'b0000), .eq(comparator_32_eq));  // open: gt, lt
  Comparator #(.width(4), .mode("unsigned")) comparator_33 (
    .a(\下一行列4 ), .b(4'b0000), .eq(comparator_33_eq));  // open: gt, lt
  Comparator #(.width(4), .mode("unsigned")) comparator_34 (
    .a(\下一行列3 ), .b(4'b0000), .eq(comparator_34_eq));  // open: gt, lt
  Comparator #(.width(4), .mode("unsigned")) comparator_35 (
    .a(\下一行列2 ), .b(4'b0000), .eq(comparator_35_eq));  // open: gt, lt
  Comparator #(.width(4), .mode("unsigned")) comparator_36 (
    .a(\下一行列1 ), .b(4'b0000), .eq(comparator_36_eq));  // open: gt, lt
  Register #(.width(4), .trigger("rising"), .Select("low")) register_1 (
    .D(\数据 ), .en(and_1_out), .Q(A1), .clk(CLK), .clr(RST));
  Register #(.width(4), .trigger("rising"), .Select("low")) register_2 (
    .D(\数据 ), .en(and_2_out), .Q(B1), .clk(CLK), .clr(RST));
  Register #(.width(4), .trigger("rising"), .Select("low")) register_3 (
    .D(\数据 ), .en(and_3_out), .Q(C1), .clk(CLK), .clr(RST));
  Register #(.width(4), .trigger("rising"), .Select("low")) register_4 (
    .D(\数据 ), .en(and_4_out), .Q(D1), .clk(CLK), .clr(RST));
  Register #(.width(4), .trigger("rising"), .Select("low")) register_5 (
    .D(\数据 ), .en(and_5_out), .Q(E1), .clk(CLK), .clr(RST));
  Register #(.width(4), .trigger("rising"), .Select("low")) register_6 (
    .D(\数据 ), .en(and_6_out), .Q(F1), .clk(CLK), .clr(RST));
  Register #(.width(4), .trigger("rising"), .Select("low")) register_7 (
    .D(\数据 ), .en(and_7_out), .Q(G1), .clk(CLK), .clr(RST));
  Register #(.width(4), .trigger("rising"), .Select("low")) register_8 (
    .D(\数据 ), .en(and_8_out), .Q(H1), .clk(CLK), .clr(RST));
  Register #(.width(4), .trigger("rising"), .Select("low")) register_9 (
    .D(\数据 ), .en(and_9_out), .Q(I1), .clk(CLK), .clr(RST));
  Counter #(.width(7), .max('h53), .ongoal("stay"), .trigger("rising"), .behavior("new")) counter_1 (
    .count(\写入使能 ), .Q(counter_1_q), .clk(CLK), .clr(RST));  // open: load, D, carry, preset, down
  Priority_Encoder #(.select(4), .disabled("Z")) priority_encoder_1 (
    .in1(and_10_out), .in2(and_11_out), .in3(and_12_out), .in4(and_13_out), .in5(and_14_out),
    .in6(and_15_out), .in7(and_16_out), .in8(and_17_out), .in9(and_18_out), .out(priority_encoder_1_out),
    .en_out(priority_encoder_1_en_out));  // open: in0, in10, in11, in12, in13, in14, in15, gs, en_in
  Priority_Encoder #(.select(4), .disabled("Z")) priority_encoder_2 (
    .in1(comparator_28_eq), .in2(comparator_29_eq), .in3(comparator_30_eq), .in4(comparator_31_eq),
    .in5(comparator_32_eq), .in6(comparator_33_eq), .in7(comparator_34_eq), .in8(comparator_35_eq),
    .in9(comparator_36_eq), .out(priority_encoder_2_out));  // open: in0, in10, in11, in12, in13, in14, in15, gs, en_out, en_in
  Subtractor #(.width(7)) subtractor_1 (.a(counter_1_q), .b(7'b0000010), .out(\计数 ));  // open: bin, bout
  Subtractor #(.width(4)) subtractor_2 (
    .a(4'b1010), .b(priority_encoder_1_out), .out(subtractor_2_out));  // open: bin, bout
  Subtractor #(.width(4)) subtractor_3 (.a(4'b1010), .b(priority_encoder_2_out), .out(\下一行首空 ));  // open: bin, bout
  Comparator #(.width(7), .mode("unsigned")) comparator_37 (
    .a(\计数 ), .b(7'b0000001), .eq(comparator_37_eq));  // open: gt, lt
  Comparator #(.width(7), .mode("unsigned")) comparator_38 (
    .a(\计数 ), .b(7'b0001010), .eq(comparator_38_eq));  // open: gt, lt
  Comparator #(.width(7), .mode("unsigned")) comparator_39 (
    .a(\计数 ), .b(7'b0010011), .eq(comparator_39_eq));  // open: gt, lt
  Comparator #(.width(7), .mode("unsigned")) comparator_40 (
    .a(\计数 ), .b(7'b0011100), .eq(comparator_40_eq));  // open: gt, lt
  Comparator #(.width(7), .mode("unsigned")) comparator_41 (
    .a(\计数 ), .b(7'b0100101), .eq(comparator_41_eq));  // open: gt, lt
  Comparator #(.width(7), .mode("unsigned")) comparator_42 (
    .a(\计数 ), .b(7'b0101110), .eq(comparator_42_eq));  // open: gt, lt
  Comparator #(.width(7), .mode("unsigned")) comparator_43 (
    .a(\计数 ), .b(7'b0110111), .eq(comparator_43_eq));  // open: gt, lt
  Comparator #(.width(7), .mode("unsigned")) comparator_44 (
    .a(\计数 ), .b(7'b1000000), .eq(comparator_44_eq));  // open: gt, lt
  Comparator #(.width(7), .mode("unsigned")) comparator_45 (
    .a(\计数 ), .b(7'b1001001), .eq(comparator_45_eq));  // open: gt, lt
  Comparator #(.width(4), .mode("unsigned")) comparator_46 (
    .a(\Y坐标 ), .b(4'b1001), .eq(comparator_46_eq));  // open: gt, lt
  // Probe on NextRight
  // Probe on NextLeft
  and and_19 (and_19_out, comparator_37_eq, \写入使能 );
  and and_20 (and_20_out, comparator_38_eq, \写入使能 );
  and and_21 (and_21_out, comparator_39_eq, \写入使能 );
  and and_22 (and_22_out, comparator_40_eq, \写入使能 );
  and and_23 (and_23_out, comparator_41_eq, \写入使能 );
  and and_24 (and_24_out, comparator_42_eq, \写入使能 );
  and and_25 (and_25_out, comparator_43_eq, \写入使能 );
  and and_26 (and_26_out, comparator_44_eq, \写入使能 );
  and and_27 (and_27_out, comparator_45_eq, \写入使能 );
  and and_28 (\跳转到下一行 , priority_encoder_1_en_out, ~comparator_46_eq);  // AND_Gate
  and and_29 (and_29_out, priority_encoder_1_en_out, comparator_46_eq);
  Multiplexer #(.select(1), .width(4), .disabled("Z"), .enable("false")) multiplexer_1 (
    .in0(subtractor_2_out), .in1(\下一行首空 ), .out(multiplexer_1_out), .sel(priority_encoder_1_en_out));
  Register #(.width(4), .trigger("rising"), .Select("low")) register_10 (
    .D(\数据 ), .en(and_19_out), .Q(A2), .clk(CLK), .clr(RST));
  Register #(.width(4), .trigger("rising"), .Select("low")) register_11 (
    .D(\数据 ), .en(and_20_out), .Q(B2), .clk(CLK), .clr(RST));
  Register #(.width(4), .trigger("rising"), .Select("low")) register_12 (
    .D(\数据 ), .en(and_21_out), .Q(C2), .clk(CLK), .clr(RST));
  Register #(.width(4), .trigger("rising"), .Select("low")) register_13 (
    .D(\数据 ), .en(and_22_out), .Q(D2), .clk(CLK), .clr(RST));
  Register #(.width(4), .trigger("rising"), .Select("low")) register_14 (
    .D(\数据 ), .en(and_23_out), .Q(E2), .clk(CLK), .clr(RST));
  Register #(.width(4), .trigger("rising"), .Select("low")) register_15 (
    .D(\数据 ), .en(and_24_out), .Q(F2), .clk(CLK), .clr(RST));
  Register #(.width(4), .trigger("rising"), .Select("low")) register_16 (
    .D(\数据 ), .en(and_25_out), .Q(G2), .clk(CLK), .clr(RST));
  Register #(.width(4), .trigger("rising"), .Select("low")) register_17 (
    .D(\数据 ), .en(and_26_out), .Q(H2), .clk(CLK), .clr(RST));
  Register #(.width(4), .trigger("rising"), .Select("low")) register_18 (
    .D(\数据 ), .en(and_27_out), .Q(I2), .clk(CLK), .clr(RST));
  Multiplexer #(.select(1), .width(4), .disabled("Z"), .enable("false")) multiplexer_2 (
    .in0(multiplexer_1_out), .in1(\X坐标 ), .out(NextRight), .sel(and_29_out));
  // Probe on NextUp
  // Probe on NextDown
  Comparator #(.width(4), .mode("unsigned")) comparator_47 (
    .a(\列1 ), .b(4'b0000), .eq(comparator_47_eq));  // open: gt, lt
  Comparator #(.width(4), .mode("unsigned")) comparator_48 (
    .a(4'b0001), .b(\X坐标 ), .lt(comparator_48_lt));  // open: gt, eq
  Comparator #(.width(4), .mode("unsigned")) comparator_49 (
    .a(\列2 ), .b(4'b0000), .eq(comparator_49_eq));  // open: gt, lt
  Comparator #(.width(4), .mode("unsigned")) comparator_50 (
    .a(4'b0010), .b(\X坐标 ), .lt(comparator_50_lt));  // open: gt, eq
  Comparator #(.width(4), .mode("unsigned")) comparator_51 (
    .a(\列3 ), .b(4'b0000), .eq(comparator_51_eq));  // open: gt, lt
  Comparator #(.width(4), .mode("unsigned")) comparator_52 (
    .a(4'b0011), .b(\X坐标 ), .lt(comparator_52_lt));  // open: gt, eq
  Comparator #(.width(4), .mode("unsigned")) comparator_53 (
    .a(\列4 ), .b(4'b0000), .eq(comparator_53_eq));  // open: gt, lt
  Comparator #(.width(4), .mode("unsigned")) comparator_54 (
    .a(4'b0100), .b(\X坐标 ), .lt(comparator_54_lt));  // open: gt, eq
  Comparator #(.width(4), .mode("unsigned")) comparator_55 (
    .a(\列5 ), .b(4'b0000), .eq(comparator_55_eq));  // open: gt, lt
  Comparator #(.width(4), .mode("unsigned")) comparator_56 (
    .a(4'b0101), .b(\X坐标 ), .lt(comparator_56_lt));  // open: gt, eq
  Comparator #(.width(4), .mode("unsigned")) comparator_57 (
    .a(\列6 ), .b(4'b0000), .eq(comparator_57_eq));  // open: gt, lt
  Comparator #(.width(4), .mode("unsigned")) comparator_58 (
    .a(4'b0110), .b(\X坐标 ), .lt(comparator_58_lt));  // open: gt, eq
  Comparator #(.width(4), .mode("unsigned")) comparator_59 (
    .a(\列7 ), .b(4'b0000), .eq(comparator_59_eq));  // open: gt, lt
  Comparator #(.width(4), .mode("unsigned")) comparator_60 (
    .a(4'b0111), .b(\X坐标 ), .lt(comparator_60_lt));  // open: gt, eq
  Comparator #(.width(4), .mode("unsigned")) comparator_61 (
    .a(\列8 ), .b(4'b0000), .eq(comparator_61_eq));  // open: gt, lt
  Comparator #(.width(4), .mode("unsigned")) comparator_62 (
    .a(4'b1000), .b(\X坐标 ), .lt(comparator_62_lt));  // open: gt, eq
  Comparator #(.width(4), .mode("unsigned")) comparator_63 (
    .a(\列9 ), .b(4'b0000), .eq(comparator_63_eq));  // open: gt, lt
  Comparator #(.width(4), .mode("unsigned")) comparator_64 (
    .a(4'b1001), .b(\X坐标 ), .lt(comparator_64_lt));  // open: gt, eq
  Adder #(.width(4)) adder_1 (.a(\Y坐标 ), .b(4'b0001), .out(\下一行Y坐标 ));  // open: cin, cout
  Multiplexer #(.select(4), .width(4), .disabled("Z"), .enable("false")) multiplexer_3 (
    .in1(A1), .in2(B1), .in3(C1), .in4(D1), .in5(E1), .in6(F1), .in7(G1), .in8(H1), .in9(I1), .out(\下一行列1 ),
    .sel(\下一行Y坐标 ));  // open: in0, in10, in11, in12, in13, in14, in15
  Multiplexer #(.select(4), .width(4), .disabled("Z"), .enable("false")) multiplexer_4 (
    .in1(A4), .in2(B4), .in3(C4), .in4(D4), .in5(E4), .in6(F4), .in7(G4), .in8(H4), .in9(I4), .out(\下一行列4 ),
    .sel(\下一行Y坐标 ));  // open: in0, in10, in11, in12, in13, in14, in15
  Multiplexer #(.select(4), .width(4), .disabled("Z"), .enable("false")) multiplexer_5 (
    .in1(A7), .in2(B7), .in3(C7), .in4(D7), .in5(E7), .in6(F7), .in7(G7), .in8(H7), .in9(I7), .out(\下一行列7 ),
    .sel(\下一行Y坐标 ));  // open: in0, in10, in11, in12, in13, in14, in15
  and and_30 (and_30_out, comparator_47_eq, comparator_48_lt);
  and and_31 (and_31_out, comparator_49_eq, comparator_50_lt);
  and and_32 (and_32_out, comparator_51_eq, comparator_52_lt);
  and and_33 (and_33_out, comparator_53_eq, comparator_54_lt);
  and and_34 (and_34_out, comparator_55_eq, comparator_56_lt);
  and and_35 (and_35_out, comparator_57_eq, comparator_58_lt);
  and and_36 (and_36_out, comparator_59_eq, comparator_60_lt);
  and and_37 (and_37_out, comparator_61_eq, comparator_62_lt);
  and and_38 (and_38_out, comparator_63_eq, comparator_64_lt);
  Multiplexer #(.select(4), .width(4), .disabled("Z"), .enable("false")) multiplexer_6 (
    .in1(\列1 ), .in2(\列2 ), .in3(\列3 ), .in4(\列4 ), .in5(\列5 ), .in6(\列6 ), .in7(\列7 ), .in8(\列8 ),
    .in9(\列9 ), .out(\选中数据 ), .sel(\X坐标 ));  // open: in0, in10, in11, in12, in13, in14, in15
  Comparator #(.width(7), .mode("unsigned")) comparator_65 (
    .a(\计数 ), .b(7'b0000010), .eq(comparator_65_eq));  // open: gt, lt
  and and_39 (and_39_out, comparator_65_eq, \写入使能 );
  Comparator #(.width(7), .mode("unsigned")) comparator_66 (
    .a(\计数 ), .b(7'b0001011), .eq(comparator_66_eq));  // open: gt, lt
  and and_40 (and_40_out, comparator_66_eq, \写入使能 );
  Comparator #(.width(7), .mode("unsigned")) comparator_67 (
    .a(\计数 ), .b(7'b0010100), .eq(comparator_67_eq));  // open: gt, lt
  and and_41 (and_41_out, comparator_67_eq, \写入使能 );
  Comparator #(.width(7), .mode("unsigned")) comparator_68 (
    .a(\计数 ), .b(7'b0011101), .eq(comparator_68_eq));  // open: gt, lt
  and and_42 (and_42_out, comparator_68_eq, \写入使能 );
  Comparator #(.width(7), .mode("unsigned")) comparator_69 (
    .a(\计数 ), .b(7'b0100110), .eq(comparator_69_eq));  // open: gt, lt
  and and_43 (and_43_out, comparator_69_eq, \写入使能 );
  Comparator #(.width(7), .mode("unsigned")) comparator_70 (
    .a(\计数 ), .b(7'b0101111), .eq(comparator_70_eq));  // open: gt, lt
  and and_44 (and_44_out, comparator_70_eq, \写入使能 );
  Comparator #(.width(7), .mode("unsigned")) comparator_71 (
    .a(\计数 ), .b(7'b0111000), .eq(comparator_71_eq));  // open: gt, lt
  and and_45 (and_45_out, comparator_71_eq, \写入使能 );
  Comparator #(.width(7), .mode("unsigned")) comparator_72 (
    .a(\计数 ), .b(7'b1000001), .eq(comparator_72_eq));  // open: gt, lt
  and and_46 (and_46_out, comparator_72_eq, \写入使能 );
  Comparator #(.width(7), .mode("unsigned")) comparator_73 (
    .a(\计数 ), .b(7'b1001010), .eq(comparator_73_eq));  // open: gt, lt
  and and_47 (and_47_out, comparator_73_eq, \写入使能 );
  Multiplexer #(.select(4), .width(4), .disabled("Z"), .enable("false")) multiplexer_7 (
    .in1(A5), .in2(B5), .in3(C5), .in4(D5), .in5(E5), .in6(F5), .in7(G5), .in8(H5), .in9(I5), .out(\下一行列5 ),
    .sel(\下一行Y坐标 ));  // open: in0, in10, in11, in12, in13, in14, in15
  Priority_Encoder #(.select(4), .disabled("Z")) priority_encoder_3 (
    .in1(and_30_out), .in2(and_31_out), .in3(and_32_out), .in4(and_33_out), .in5(and_34_out),
    .in6(and_35_out), .in7(and_36_out), .in8(and_37_out), .in9(and_38_out), .out(priority_encoder_3_out),
    .en_out(priority_encoder_3_en_out));  // open: in0, in10, in11, in12, in13, in14, in15, gs, en_in
  Multiplexer #(.select(4), .width(4), .disabled("Z"), .enable("false")) multiplexer_8 (
    .in1(A2), .in2(B2), .in3(C2), .in4(D2), .in5(E2), .in6(F2), .in7(G2), .in8(H2), .in9(I2), .out(\下一行列2 ),
    .sel(\下一行Y坐标 ));  // open: in0, in10, in11, in12, in13, in14, in15
  Multiplexer #(.select(4), .width(4), .disabled("Z"), .enable("false")) multiplexer_9 (
    .in1(A8), .in2(B8), .in3(C8), .in4(D8), .in5(E8), .in6(F8), .in7(G8), .in8(H8), .in9(I8), .out(\下一行列8 ),
    .sel(\下一行Y坐标 ));  // open: in0, in10, in11, in12, in13, in14, in15
  Register #(.width(4), .trigger("rising"), .Select("low")) register_19 (
    .D(\数据 ), .en(and_39_out), .Q(A3), .clk(CLK), .clr(RST));
  Register #(.width(4), .trigger("rising"), .Select("low")) register_20 (
    .D(\数据 ), .en(and_40_out), .Q(B3), .clk(CLK), .clr(RST));
  Register #(.width(4), .trigger("rising"), .Select("low")) register_21 (
    .D(\数据 ), .en(and_41_out), .Q(C3), .clk(CLK), .clr(RST));
  Register #(.width(4), .trigger("rising"), .Select("low")) register_22 (
    .D(\数据 ), .en(and_42_out), .Q(D3), .clk(CLK), .clr(RST));
  Register #(.width(4), .trigger("rising"), .Select("low")) register_23 (
    .D(\数据 ), .en(and_43_out), .Q(E3), .clk(CLK), .clr(RST));
  Register #(.width(4), .trigger("rising"), .Select("low")) register_24 (
    .D(\数据 ), .en(and_44_out), .Q(F3), .clk(CLK), .clr(RST));
  Register #(.width(4), .trigger("rising"), .Select("low")) register_25 (
    .D(\数据 ), .en(and_45_out), .Q(G3), .clk(CLK), .clr(RST));
  Register #(.width(4), .trigger("rising"), .Select("low")) register_26 (
    .D(\数据 ), .en(and_46_out), .Q(H3), .clk(CLK), .clr(RST));
  Register #(.width(4), .trigger("rising"), .Select("low")) register_27 (
    .D(\数据 ), .en(and_47_out), .Q(I3), .clk(CLK), .clr(RST));
  Comparator #(.width(4), .mode("unsigned")) comparator_74 (
    .a(\Y坐标 ), .b(4'b0001), .eq(comparator_74_eq));  // open: gt, lt
  Multiplexer #(.select(1), .width(4), .disabled("Z"), .enable("false")) multiplexer_10 (
    .in0(priority_encoder_3_out), .in1(\上一行末空 ), .out(multiplexer_10_out), .sel(priority_encoder_3_en_out));
  Comparator #(.width(4), .mode("unsigned")) comparator_75 (.a(\选中数据 ), .b(4'b0000), .eq(\固有坐标 ));  // open: gt, lt
  and and_48 (and_48_out, priority_encoder_3_en_out, comparator_74_eq);
  Multiplexer #(.select(1), .width(4), .disabled("Z"), .enable("false")) multiplexer_11 (
    .in0(multiplexer_10_out), .in1(\X坐标 ), .out(NextLeft), .sel(and_48_out));
  Multiplexer #(.select(4), .width(4), .disabled("Z"), .enable("false")) multiplexer_12 (
    .in1(A3), .in2(B3), .in3(C3), .in4(D3), .in5(E3), .in6(F3), .in7(G3), .in8(H3), .in9(I3), .out(\下一行列3 ),
    .sel(\下一行Y坐标 ));  // open: in0, in10, in11, in12, in13, in14, in15
  Multiplexer #(.select(4), .width(4), .disabled("Z"), .enable("false")) multiplexer_13 (
    .in1(A6), .in2(B6), .in3(C6), .in4(D6), .in5(E6), .in6(F6), .in7(G6), .in8(H6), .in9(I6), .out(\下一行列6 ),
    .sel(\下一行Y坐标 ));  // open: in0, in10, in11, in12, in13, in14, in15
  Multiplexer #(.select(4), .width(4), .disabled("Z"), .enable("false")) multiplexer_14 (
    .in1(A9), .in2(B9), .in3(C9), .in4(D9), .in5(E9), .in6(F9), .in7(G9), .in8(H9), .in9(I9), .out(\下一行列9 ),
    .sel(\下一行Y坐标 ));  // open: in0, in10, in11, in12, in13, in14, in15
  and and_49 (\跳转到上一行 , priority_encoder_3_en_out, ~comparator_74_eq);  // AND_Gate
  Comparator #(.width(7), .mode("unsigned")) comparator_76 (
    .a(\计数 ), .b(7'b0000011), .eq(comparator_76_eq));  // open: gt, lt
  Comparator #(.width(7), .mode("unsigned")) comparator_77 (
    .a(\计数 ), .b(7'b0001100), .eq(comparator_77_eq));  // open: gt, lt
  Comparator #(.width(7), .mode("unsigned")) comparator_78 (
    .a(\计数 ), .b(7'b0010101), .eq(comparator_78_eq));  // open: gt, lt
  Comparator #(.width(7), .mode("unsigned")) comparator_79 (
    .a(\计数 ), .b(7'b0011110), .eq(comparator_79_eq));  // open: gt, lt
  Comparator #(.width(7), .mode("unsigned")) comparator_80 (
    .a(\计数 ), .b(7'b0100111), .eq(comparator_80_eq));  // open: gt, lt
  Comparator #(.width(7), .mode("unsigned")) comparator_81 (
    .a(\计数 ), .b(7'b0110000), .eq(comparator_81_eq));  // open: gt, lt
  Comparator #(.width(7), .mode("unsigned")) comparator_82 (
    .a(\计数 ), .b(7'b0111001), .eq(comparator_82_eq));  // open: gt, lt
  Comparator #(.width(7), .mode("unsigned")) comparator_83 (
    .a(\计数 ), .b(7'b1000010), .eq(comparator_83_eq));  // open: gt, lt
  Comparator #(.width(7), .mode("unsigned")) comparator_84 (
    .a(\计数 ), .b(7'b1001011), .eq(comparator_84_eq));  // open: gt, lt
  and and_50 (and_50_out, comparator_76_eq, \写入使能 );
  and and_51 (and_51_out, comparator_77_eq, \写入使能 );
  and and_52 (and_52_out, comparator_78_eq, \写入使能 );
  and and_53 (and_53_out, comparator_79_eq, \写入使能 );
  and and_54 (and_54_out, comparator_80_eq, \写入使能 );
  and and_55 (and_55_out, comparator_81_eq, \写入使能 );
  and and_56 (and_56_out, comparator_82_eq, \写入使能 );
  and and_57 (and_57_out, comparator_83_eq, \写入使能 );
  and and_58 (and_58_out, comparator_84_eq, \写入使能 );
  Register #(.width(4), .trigger("rising"), .Select("low")) register_28 (
    .D(\数据 ), .en(and_50_out), .Q(A4), .clk(CLK), .clr(RST));
  Register #(.width(4), .trigger("rising"), .Select("low")) register_29 (
    .D(\数据 ), .en(and_51_out), .Q(B4), .clk(CLK), .clr(RST));
  Register #(.width(4), .trigger("rising"), .Select("low")) register_30 (
    .D(\数据 ), .en(and_52_out), .Q(C4), .clk(CLK), .clr(RST));
  Register #(.width(4), .trigger("rising"), .Select("low")) register_31 (
    .D(\数据 ), .en(and_53_out), .Q(D4), .clk(CLK), .clr(RST));
  Register #(.width(4), .trigger("rising"), .Select("low")) register_32 (
    .D(\数据 ), .en(and_54_out), .Q(E4), .clk(CLK), .clr(RST));
  Register #(.width(4), .trigger("rising"), .Select("low")) register_33 (
    .D(\数据 ), .en(and_55_out), .Q(F4), .clk(CLK), .clr(RST));
  Register #(.width(4), .trigger("rising"), .Select("low")) register_34 (
    .D(\数据 ), .en(and_56_out), .Q(G4), .clk(CLK), .clr(RST));
  Register #(.width(4), .trigger("rising"), .Select("low")) register_35 (
    .D(\数据 ), .en(and_57_out), .Q(H4), .clk(CLK), .clr(RST));
  Register #(.width(4), .trigger("rising"), .Select("low")) register_36 (
    .D(\数据 ), .en(and_58_out), .Q(I4), .clk(CLK), .clr(RST));
  Comparator #(.width(4), .mode("unsigned")) comparator_85 (
    .a(\上一行列1 ), .b(4'b0000), .eq(comparator_85_eq));  // open: gt, lt
  Comparator #(.width(4), .mode("unsigned")) comparator_86 (
    .a(\上一行列2 ), .b(4'b0000), .eq(comparator_86_eq));  // open: gt, lt
  Comparator #(.width(4), .mode("unsigned")) comparator_87 (
    .a(\上一行列3 ), .b(4'b0000), .eq(comparator_87_eq));  // open: gt, lt
  Comparator #(.width(4), .mode("unsigned")) comparator_88 (
    .a(\上一行列4 ), .b(4'b0000), .eq(comparator_88_eq));  // open: gt, lt
  Comparator #(.width(4), .mode("unsigned")) comparator_89 (
    .a(\上一行列5 ), .b(4'b0000), .eq(comparator_89_eq));  // open: gt, lt
  Comparator #(.width(4), .mode("unsigned")) comparator_90 (
    .a(\上一行列6 ), .b(4'b0000), .eq(comparator_90_eq));  // open: gt, lt
  Comparator #(.width(4), .mode("unsigned")) comparator_91 (
    .a(\上一行列7 ), .b(4'b0000), .eq(comparator_91_eq));  // open: gt, lt
  Comparator #(.width(4), .mode("unsigned")) comparator_92 (
    .a(\上一行列8 ), .b(4'b0000), .eq(comparator_92_eq));  // open: gt, lt
  Comparator #(.width(4), .mode("unsigned")) comparator_93 (
    .a(\上一行列9 ), .b(4'b0000), .eq(comparator_93_eq));  // open: gt, lt
  Multiplexer #(.select(4), .width(4), .disabled("Z"), .enable("false")) multiplexer_15 (
    .in1(A1), .in2(B1), .in3(C1), .in4(D1), .in5(E1), .in6(F1), .in7(G1), .in8(H1), .in9(I1), .out(\列1 ),
    .sel(\Y坐标 ));  // open: in0, in10, in11, in12, in13, in14, in15
  Multiplexer #(.select(4), .width(4), .disabled("Z"), .enable("false")) multiplexer_16 (
    .in1(A4), .in2(B4), .in3(C4), .in4(D4), .in5(E4), .in6(F4), .in7(G4), .in8(H4), .in9(I4), .out(\列4 ),
    .sel(\Y坐标 ));  // open: in0, in10, in11, in12, in13, in14, in15
  Multiplexer #(.select(4), .width(4), .disabled("Z"), .enable("false")) multiplexer_17 (
    .in1(A7), .in2(B7), .in3(C7), .in4(D7), .in5(E7), .in6(F7), .in7(G7), .in8(H7), .in9(I7), .out(\列7 ),
    .sel(\Y坐标 ));  // open: in0, in10, in11, in12, in13, in14, in15
  Priority_Encoder #(.select(4), .disabled("Z")) priority_encoder_4 (
    .in1(comparator_85_eq), .in2(comparator_86_eq), .in3(comparator_87_eq), .in4(comparator_88_eq),
    .in5(comparator_89_eq), .in6(comparator_90_eq), .in7(comparator_91_eq), .in8(comparator_92_eq),
    .in9(comparator_93_eq), .out(\上一行末空 ));  // open: in0, in10, in11, in12, in13, in14, in15, gs, en_out, en_in
  Multiplexer #(.select(4), .width(4), .disabled("Z"), .enable("false")) multiplexer_18 (
    .in1(A2), .in2(B2), .in3(C2), .in4(D2), .in5(E2), .in6(F2), .in7(G2), .in8(H2), .in9(I2), .out(\列2 ),
    .sel(\Y坐标 ));  // open: in0, in10, in11, in12, in13, in14, in15
  Multiplexer #(.select(4), .width(4), .disabled("Z"), .enable("false")) multiplexer_19 (
    .in1(A5), .in2(B5), .in3(C5), .in4(D5), .in5(E5), .in6(F5), .in7(G5), .in8(H5), .in9(I5), .out(\列5 ),
    .sel(\Y坐标 ));  // open: in0, in10, in11, in12, in13, in14, in15
  Multiplexer #(.select(4), .width(4), .disabled("Z"), .enable("false")) multiplexer_20 (
    .in1(A8), .in2(B8), .in3(C8), .in4(D8), .in5(E8), .in6(F8), .in7(G8), .in8(H8), .in9(I8), .out(\列8 ),
    .sel(\Y坐标 ));  // open: in0, in10, in11, in12, in13, in14, in15
  Comparator #(.width(7), .mode("unsigned")) comparator_94 (
    .a(\计数 ), .b(7'b0000100), .eq(comparator_94_eq));  // open: gt, lt
  Comparator #(.width(7), .mode("unsigned")) comparator_95 (
    .a(\计数 ), .b(7'b0001101), .eq(comparator_95_eq));  // open: gt, lt
  Comparator #(.width(7), .mode("unsigned")) comparator_96 (
    .a(\计数 ), .b(7'b0010110), .eq(comparator_96_eq));  // open: gt, lt
  Comparator #(.width(7), .mode("unsigned")) comparator_97 (
    .a(\计数 ), .b(7'b0011111), .eq(comparator_97_eq));  // open: gt, lt
  Comparator #(.width(7), .mode("unsigned")) comparator_98 (
    .a(\计数 ), .b(7'b0101000), .eq(comparator_98_eq));  // open: gt, lt
  Comparator #(.width(7), .mode("unsigned")) comparator_99 (
    .a(\计数 ), .b(7'b0110001), .eq(comparator_99_eq));  // open: gt, lt
  Comparator #(.width(7), .mode("unsigned")) comparator_100 (
    .a(\计数 ), .b(7'b0111010), .eq(comparator_100_eq));  // open: gt, lt
  Comparator #(.width(7), .mode("unsigned")) comparator_101 (
    .a(\计数 ), .b(7'b1000011), .eq(comparator_101_eq));  // open: gt, lt
  Comparator #(.width(7), .mode("unsigned")) comparator_102 (
    .a(\计数 ), .b(7'b1001100), .eq(comparator_102_eq));  // open: gt, lt
  and and_59 (and_59_out, comparator_94_eq, \写入使能 );
  and and_60 (and_60_out, comparator_95_eq, \写入使能 );
  and and_61 (and_61_out, comparator_96_eq, \写入使能 );
  and and_62 (and_62_out, comparator_97_eq, \写入使能 );
  and and_63 (and_63_out, comparator_98_eq, \写入使能 );
  and and_64 (and_64_out, comparator_99_eq, \写入使能 );
  and and_65 (and_65_out, comparator_100_eq, \写入使能 );
  and and_66 (and_66_out, comparator_101_eq, \写入使能 );
  and and_67 (and_67_out, comparator_102_eq, \写入使能 );
  Register #(.width(4), .trigger("rising"), .Select("low")) register_37 (
    .D(\数据 ), .en(and_59_out), .Q(A5), .clk(CLK), .clr(RST));
  Register #(.width(4), .trigger("rising"), .Select("low")) register_38 (
    .D(\数据 ), .en(and_60_out), .Q(B5), .clk(CLK), .clr(RST));
  Register #(.width(4), .trigger("rising"), .Select("low")) register_39 (
    .D(\数据 ), .en(and_61_out), .Q(C5), .clk(CLK), .clr(RST));
  Register #(.width(4), .trigger("rising"), .Select("low")) register_40 (
    .D(\数据 ), .en(and_62_out), .Q(D5), .clk(CLK), .clr(RST));
  Register #(.width(4), .trigger("rising"), .Select("low")) register_41 (
    .D(\数据 ), .en(and_63_out), .Q(E5), .clk(CLK), .clr(RST));
  Register #(.width(4), .trigger("rising"), .Select("low")) register_42 (
    .D(\数据 ), .en(and_64_out), .Q(F5), .clk(CLK), .clr(RST));
  Register #(.width(4), .trigger("rising"), .Select("low")) register_43 (
    .D(\数据 ), .en(and_65_out), .Q(G5), .clk(CLK), .clr(RST));
  Register #(.width(4), .trigger("rising"), .Select("low")) register_44 (
    .D(\数据 ), .en(and_66_out), .Q(H5), .clk(CLK), .clr(undriven));
  Register #(.width(4), .trigger("rising"), .Select("low")) register_45 (
    .D(\数据 ), .en(and_67_out), .Q(I5), .clk(CLK), .clr(RST));
  Multiplexer #(.select(4), .width(4), .disabled("Z"), .enable("false")) multiplexer_21 (
    .in1(A3), .in2(B3), .in3(C3), .in4(D3), .in5(E3), .in6(F3), .in7(G3), .in8(H3), .in9(I3), .out(\列3 ),
    .sel(\Y坐标 ));  // open: in0, in10, in11, in12, in13, in14, in15
  Multiplexer #(.select(4), .width(4), .disabled("Z"), .enable("false")) multiplexer_22 (
    .in1(A6), .in2(B6), .in3(C6), .in4(D6), .in5(E6), .in6(F6), .in7(G6), .in8(H6), .in9(I6), .out(\列6 ),
    .sel(\Y坐标 ));  // open: in0, in10, in11, in12, in13, in14, in15
  Multiplexer #(.select(4), .width(4), .disabled("Z"), .enable("false")) multiplexer_23 (
    .in1(A9), .in2(B9), .in3(C9), .in4(D9), .in5(E9), .in6(F9), .in7(G9), .in8(H9), .in9(I9), .out(\列9 ),
    .sel(\Y坐标 ));  // open: in0, in10, in11, in12, in13, in14, in15
  Subtractor #(.width(4)) subtractor_4 (.a(\Y坐标 ), .b(4'b0001), .out(\上一行Y坐标 ));  // open: bin, bout
  Multiplexer #(.select(4), .width(4), .disabled("Z"), .enable("false")) multiplexer_24 (
    .in1(A1), .in2(B1), .in3(C1), .in4(D1), .in5(E1), .in6(F1), .in7(G1), .in8(H1), .in9(I1), .out(\上一行列1 ),
    .sel(\上一行Y坐标 ));  // open: in0, in10, in11, in12, in13, in14, in15
  Multiplexer #(.select(4), .width(4), .disabled("Z"), .enable("false")) multiplexer_25 (
    .in1(A4), .in2(B4), .in3(C4), .in4(D4), .in5(E4), .in6(F4), .in7(G4), .in8(H4), .in9(I4), .out(\上一行列4 ),
    .sel(\上一行Y坐标 ));  // open: in0, in10, in11, in12, in13, in14, in15
  Multiplexer #(.select(4), .width(4), .disabled("Z"), .enable("false")) multiplexer_26 (
    .in1(A7), .in2(B7), .in3(C7), .in4(D7), .in5(E7), .in6(F7), .in7(G7), .in8(H7), .in9(I7), .out(\上一行列7 ),
    .sel(\上一行Y坐标 ));  // open: in0, in10, in11, in12, in13, in14, in15
  Comparator #(.width(4), .mode("unsigned")) comparator_103 (
    .a(\行9 ), .b(4'b0000), .eq(comparator_103_eq));  // open: gt, lt
  and and_68 (and_68_out, comparator_103_eq, comparator_104_gt);
  Comparator #(.width(4), .mode("unsigned")) comparator_104 (
    .a(4'b1001), .b(\Y坐标 ), .gt(comparator_104_gt));  // open: eq, lt
  Comparator #(.width(4), .mode("unsigned")) comparator_105 (
    .a(\行8 ), .b(4'b0000), .eq(comparator_105_eq));  // open: gt, lt
  and and_69 (and_69_out, comparator_105_eq, comparator_106_gt);
  Comparator #(.width(4), .mode("unsigned")) comparator_106 (
    .a(4'b1000), .b(\Y坐标 ), .gt(comparator_106_gt));  // open: eq, lt
  Comparator #(.width(4), .mode("unsigned")) comparator_107 (
    .a(\行7 ), .b(4'b0000), .eq(comparator_107_eq));  // open: gt, lt
  and and_70 (and_70_out, comparator_107_eq, comparator_108_gt);
  Comparator #(.width(4), .mode("unsigned")) comparator_108 (
    .a(4'b0111), .b(\Y坐标 ), .gt(comparator_108_gt));  // open: eq, lt
  Comparator #(.width(4), .mode("unsigned")) comparator_109 (
    .a(\行6 ), .b(4'b0000), .eq(comparator_109_eq));  // open: gt, lt
  and and_71 (and_71_out, comparator_109_eq, comparator_110_gt);
  Comparator #(.width(4), .mode("unsigned")) comparator_110 (
    .a(4'b0110), .b(\Y坐标 ), .gt(comparator_110_gt));  // open: eq, lt
  Comparator #(.width(4), .mode("unsigned")) comparator_111 (
    .a(\行5 ), .b(4'b0000), .eq(comparator_111_eq));  // open: gt, lt
  and and_72 (and_72_out, comparator_111_eq, comparator_112_gt);
  Comparator #(.width(4), .mode("unsigned")) comparator_112 (
    .a(4'b0101), .b(\Y坐标 ), .gt(comparator_112_gt));  // open: eq, lt
  Comparator #(.width(4), .mode("unsigned")) comparator_113 (
    .a(\行4 ), .b(4'b0000), .eq(comparator_113_eq));  // open: gt, lt
  and and_73 (and_73_out, comparator_113_eq, comparator_114_gt);
  Comparator #(.width(4), .mode("unsigned")) comparator_114 (
    .a(4'b0100), .b(\Y坐标 ), .gt(comparator_114_gt));  // open: eq, lt
  Comparator #(.width(4), .mode("unsigned")) comparator_115 (
    .a(\行3 ), .b(4'b0000), .eq(comparator_115_eq));  // open: gt, lt
  and and_74 (and_74_out, comparator_115_eq, comparator_116_gt);
  Comparator #(.width(4), .mode("unsigned")) comparator_116 (
    .a(4'b0011), .b(\Y坐标 ), .gt(comparator_116_gt));  // open: eq, lt
  Comparator #(.width(4), .mode("unsigned")) comparator_117 (
    .a(\行2 ), .b(4'b0000), .eq(comparator_117_eq));  // open: gt, lt
  and and_75 (and_75_out, comparator_117_eq, comparator_118_gt);
  Comparator #(.width(4), .mode("unsigned")) comparator_118 (
    .a(4'b0010), .b(\Y坐标 ), .gt(comparator_118_gt));  // open: eq, lt
  Comparator #(.width(4), .mode("unsigned")) comparator_119 (
    .a(\行1 ), .b(4'b0000), .eq(comparator_119_eq));  // open: gt, lt
  and and_76 (and_76_out, comparator_119_eq, comparator_120_gt);
  Comparator #(.width(4), .mode("unsigned")) comparator_120 (
    .a(4'b0001), .b(\Y坐标 ), .gt(comparator_120_gt));  // open: eq, lt
  Comparator #(.width(7), .mode("unsigned")) comparator_121 (
    .a(\计数 ), .b(7'b0000101), .eq(comparator_121_eq));  // open: gt, lt
  and and_77 (and_77_out, comparator_121_eq, \写入使能 );
  Comparator #(.width(7), .mode("unsigned")) comparator_122 (
    .a(\计数 ), .b(7'b0001110), .eq(comparator_122_eq));  // open: gt, lt
  and and_78 (and_78_out, comparator_122_eq, \写入使能 );
  Comparator #(.width(7), .mode("unsigned")) comparator_123 (
    .a(\计数 ), .b(7'b0010111), .eq(comparator_123_eq));  // open: gt, lt
  and and_79 (and_79_out, comparator_123_eq, \写入使能 );
  Comparator #(.width(7), .mode("unsigned")) comparator_124 (
    .a(\计数 ), .b(7'b0100000), .eq(comparator_124_eq));  // open: gt, lt
  and and_80 (and_80_out, comparator_124_eq, \写入使能 );
  Comparator #(.width(7), .mode("unsigned")) comparator_125 (
    .a(\计数 ), .b(7'b0101001), .eq(comparator_125_eq));  // open: gt, lt
  and and_81 (and_81_out, comparator_125_eq, \写入使能 );
  Comparator #(.width(7), .mode("unsigned")) comparator_126 (
    .a(\计数 ), .b(7'b0110010), .eq(comparator_126_eq));  // open: gt, lt
  and and_82 (and_82_out, comparator_126_eq, \写入使能 );
  Comparator #(.width(7), .mode("unsigned")) comparator_127 (
    .a(\计数 ), .b(7'b0111011), .eq(comparator_127_eq));  // open: gt, lt
  and and_83 (and_83_out, comparator_127_eq, \写入使能 );
  Comparator #(.width(7), .mode("unsigned")) comparator_128 (
    .a(\计数 ), .b(7'b1000100), .eq(comparator_128_eq));  // open: gt, lt
  and and_84 (and_84_out, comparator_128_eq, \写入使能 );
  Comparator #(.width(7), .mode("unsigned")) comparator_129 (
    .a(\计数 ), .b(7'b1001101), .eq(comparator_129_eq));  // open: gt, lt
  and and_85 (and_85_out, comparator_129_eq, \写入使能 );
  Multiplexer #(.select(4), .width(4), .disabled("Z"), .enable("false")) multiplexer_27 (
    .in1(A2), .in2(B2), .in3(C2), .in4(D2), .in5(E2), .in6(F2), .in7(G2), .in8(H2), .in9(I2), .out(\上一行列2 ),
    .sel(\上一行Y坐标 ));  // open: in0, in10, in11, in12, in13, in14, in15
  Multiplexer #(.select(4), .width(4), .disabled("Z"), .enable("false")) multiplexer_28 (
    .in1(A5), .in2(B5), .in3(C5), .in4(D5), .in5(E5), .in6(F5), .in7(G5), .in8(H5), .in9(I5), .out(\上一行列5 ),
    .sel(\上一行Y坐标 ));  // open: in0, in10, in11, in12, in13, in14, in15
  Multiplexer #(.select(4), .width(4), .disabled("Z"), .enable("false")) multiplexer_29 (
    .in1(A8), .in2(B8), .in3(C8), .in4(D8), .in5(E8), .in6(F8), .in7(G8), .in8(H8), .in9(I8), .out(\上一行列8 ),
    .sel(\上一行Y坐标 ));  // open: in0, in10, in11, in12, in13, in14, in15
  Priority_Encoder #(.select(4), .disabled("Z")) priority_encoder_5 (
    .in1(and_68_out), .in2(and_69_out), .in3(and_70_out), .in4(and_71_out), .in5(and_72_out),
    .in6(and_73_out), .in7(and_74_out), .in8(and_75_out), .in9(and_76_out), .out(priority_encoder_5_out),
    .en_out(priority_encoder_5_en_out));  // open: in0, in10, in11, in12, in13, in14, in15, gs, en_in
  Register #(.width(4), .trigger("rising"), .Select("low")) register_46 (
    .D(\数据 ), .en(and_77_out), .Q(A6), .clk(CLK), .clr(RST));
  Register #(.width(4), .trigger("rising"), .Select("low")) register_47 (
    .D(\数据 ), .en(and_78_out), .Q(B6), .clk(CLK), .clr(RST));
  Register #(.width(4), .trigger("rising"), .Select("low")) register_48 (
    .D(\数据 ), .en(and_79_out), .Q(C6), .clk(CLK), .clr(RST));
  Register #(.width(4), .trigger("rising"), .Select("low")) register_49 (
    .D(\数据 ), .en(and_80_out), .Q(D6), .clk(CLK), .clr(RST));
  Register #(.width(4), .trigger("rising"), .Select("low")) register_50 (
    .D(\数据 ), .en(and_81_out), .Q(E6), .clk(CLK), .clr(RST));
  Register #(.width(4), .trigger("rising"), .Select("low")) register_51 (
    .D(\数据 ), .en(and_82_out), .Q(F6), .clk(CLK), .clr(RST));
  Register #(.width(4), .trigger("rising"), .Select("low")) register_52 (
    .D(\数据 ), .en(and_83_out), .Q(G6), .clk(CLK), .clr(RST));
  Register #(.width(4), .trigger("rising"), .Select("low")) register_53 (
    .D(\数据 ), .en(and_84_out), .Q(H6), .clk(CLK), .clr(RST));
  Register #(.width(4), .trigger("rising"), .Select("low")) register_54 (
    .D(\数据 ), .en(and_85_out), .Q(I6), .clk(CLK), .clr(RST));
  Subtractor #(.width(4)) subtractor_5 (
    .a(4'b1010), .b(priority_encoder_5_out), .out(subtractor_5_out));  // open: bin, bout
  Multiplexer #(.select(4), .width(4), .disabled("Z"), .enable("false")) multiplexer_30 (
    .in1(A3), .in2(B3), .in3(C3), .in4(D3), .in5(E3), .in6(F3), .in7(G3), .in8(H3), .in9(I3), .out(\上一行列3 ),
    .sel(\上一行Y坐标 ));  // open: in0, in10, in11, in12, in13, in14, in15
  Multiplexer #(.select(4), .width(4), .disabled("Z"), .enable("false")) multiplexer_31 (
    .in1(A6), .in2(B6), .in3(C6), .in4(D6), .in5(E6), .in6(F6), .in7(G6), .in8(H6), .in9(I6), .out(\上一行列6 ),
    .sel(\上一行Y坐标 ));  // open: in0, in10, in11, in12, in13, in14, in15
  Multiplexer #(.select(4), .width(4), .disabled("Z"), .enable("false")) multiplexer_32 (
    .in1(A9), .in2(B9), .in3(C9), .in4(D9), .in5(E9), .in6(F9), .in7(G9), .in8(H9), .in9(I9), .out(\上一行列9 ),
    .sel(\上一行Y坐标 ));  // open: in0, in10, in11, in12, in13, in14, in15
  Multiplexer #(.select(1), .width(4), .disabled("Z"), .enable("false")) multiplexer_33 (
    .in0(subtractor_5_out), .in1(\Y坐标 ), .out(NextDown), .sel(priority_encoder_5_en_out));
  Comparator #(.width(7), .mode("unsigned")) comparator_130 (
    .a(\计数 ), .b(7'b0000110), .eq(comparator_130_eq));  // open: gt, lt
  Comparator #(.width(7), .mode("unsigned")) comparator_131 (
    .a(\计数 ), .b(7'b0001111), .eq(comparator_131_eq));  // open: gt, lt
  Comparator #(.width(7), .mode("unsigned")) comparator_132 (
    .a(\计数 ), .b(7'b0011000), .eq(comparator_132_eq));  // open: gt, lt
  Comparator #(.width(7), .mode("unsigned")) comparator_133 (
    .a(\计数 ), .b(7'b0100001), .eq(comparator_133_eq));  // open: gt, lt
  Comparator #(.width(7), .mode("unsigned")) comparator_134 (
    .a(\计数 ), .b(7'b0101010), .eq(comparator_134_eq));  // open: gt, lt
  Comparator #(.width(7), .mode("unsigned")) comparator_135 (
    .a(\计数 ), .b(7'b0110011), .eq(comparator_135_eq));  // open: gt, lt
  Comparator #(.width(7), .mode("unsigned")) comparator_136 (
    .a(\计数 ), .b(7'b0111100), .eq(comparator_136_eq));  // open: gt, lt
  Comparator #(.width(7), .mode("unsigned")) comparator_137 (
    .a(\计数 ), .b(7'b1000101), .eq(comparator_137_eq));  // open: gt, lt
  Comparator #(.width(7), .mode("unsigned")) comparator_138 (
    .a(\计数 ), .b(7'b1001110), .eq(comparator_138_eq));  // open: gt, lt
  and and_86 (and_86_out, comparator_130_eq, \写入使能 );
  and and_87 (and_87_out, comparator_131_eq, \写入使能 );
  and and_88 (and_88_out, comparator_132_eq, \写入使能 );
  and and_89 (and_89_out, comparator_133_eq, \写入使能 );
  and and_90 (and_90_out, comparator_134_eq, \写入使能 );
  and and_91 (and_91_out, comparator_135_eq, \写入使能 );
  and and_92 (and_92_out, comparator_136_eq, \写入使能 );
  and and_93 (and_93_out, comparator_137_eq, \写入使能 );
  and and_94 (and_94_out, comparator_138_eq, \写入使能 );
  Comparator #(.width(4), .mode("unsigned")) comparator_139 (
    .a(\行1 ), .b(4'b0000), .eq(comparator_139_eq));  // open: gt, lt
  Comparator #(.width(4), .mode("unsigned")) comparator_140 (
    .a(4'b0001), .b(\Y坐标 ), .lt(comparator_140_lt));  // open: gt, eq
  Comparator #(.width(4), .mode("unsigned")) comparator_141 (
    .a(\行2 ), .b(4'b0000), .eq(comparator_141_eq));  // open: gt, lt
  Comparator #(.width(4), .mode("unsigned")) comparator_142 (
    .a(4'b0010), .b(\Y坐标 ), .lt(comparator_142_lt));  // open: gt, eq
  Comparator #(.width(4), .mode("unsigned")) comparator_143 (
    .a(\行3 ), .b(4'b0000), .eq(comparator_143_eq));  // open: gt, lt
  Comparator #(.width(4), .mode("unsigned")) comparator_144 (
    .a(4'b0011), .b(\Y坐标 ), .lt(comparator_144_lt));  // open: gt, eq
  Comparator #(.width(4), .mode("unsigned")) comparator_145 (
    .a(\行4 ), .b(4'b0000), .eq(comparator_145_eq));  // open: gt, lt
  Comparator #(.width(4), .mode("unsigned")) comparator_146 (
    .a(4'b0100), .b(\Y坐标 ), .lt(comparator_146_lt));  // open: gt, eq
  Comparator #(.width(4), .mode("unsigned")) comparator_147 (
    .a(\行5 ), .b(4'b0000), .eq(comparator_147_eq));  // open: gt, lt
  Comparator #(.width(4), .mode("unsigned")) comparator_148 (
    .a(4'b0101), .b(\Y坐标 ), .lt(comparator_148_lt));  // open: gt, eq
  Comparator #(.width(4), .mode("unsigned")) comparator_149 (
    .a(\行6 ), .b(4'b0000), .eq(comparator_149_eq));  // open: gt, lt
  Comparator #(.width(4), .mode("unsigned")) comparator_150 (
    .a(4'b0110), .b(\Y坐标 ), .lt(comparator_150_lt));  // open: gt, eq
  Comparator #(.width(4), .mode("unsigned")) comparator_151 (
    .a(\行7 ), .b(4'b0000), .eq(comparator_151_eq));  // open: gt, lt
  Comparator #(.width(4), .mode("unsigned")) comparator_152 (
    .a(4'b0111), .b(\Y坐标 ), .lt(comparator_152_lt));  // open: gt, eq
  Comparator #(.width(4), .mode("unsigned")) comparator_153 (
    .a(\行8 ), .b(4'b0000), .eq(comparator_153_eq));  // open: gt, lt
  Comparator #(.width(4), .mode("unsigned")) comparator_154 (
    .a(4'b1000), .b(\Y坐标 ), .lt(comparator_154_lt));  // open: gt, eq
  Comparator #(.width(4), .mode("unsigned")) comparator_155 (
    .a(\行9 ), .b(4'b0000), .eq(comparator_155_eq));  // open: gt, lt
  Comparator #(.width(4), .mode("unsigned")) comparator_156 (
    .a(4'b1001), .b(\Y坐标 ), .lt(comparator_156_lt));  // open: gt, eq
  Register #(.width(4), .trigger("rising"), .Select("low")) register_55 (
    .D(\数据 ), .en(and_86_out), .Q(A7), .clk(CLK), .clr(RST));
  Register #(.width(4), .trigger("rising"), .Select("low")) register_56 (
    .D(\数据 ), .en(and_87_out), .Q(B7), .clk(CLK), .clr(RST));
  Register #(.width(4), .trigger("rising"), .Select("low")) register_57 (
    .D(\数据 ), .en(and_88_out), .Q(C7), .clk(CLK), .clr(RST));
  Register #(.width(4), .trigger("rising"), .Select("low")) register_58 (
    .D(\数据 ), .en(and_89_out), .Q(D7), .clk(CLK), .clr(RST));
  Register #(.width(4), .trigger("rising"), .Select("low")) register_59 (
    .D(\数据 ), .en(and_90_out), .Q(E7), .clk(CLK), .clr(RST));
  Register #(.width(4), .trigger("rising"), .Select("low")) register_60 (
    .D(\数据 ), .en(and_91_out), .Q(F7), .clk(CLK), .clr(RST));
  Register #(.width(4), .trigger("rising"), .Select("low")) register_61 (
    .D(\数据 ), .en(and_92_out), .Q(G7), .clk(CLK), .clr(RST));
  Register #(.width(4), .trigger("rising"), .Select("low")) register_62 (
    .D(\数据 ), .en(and_93_out), .Q(H7), .clk(CLK), .clr(RST));
  Register #(.width(4), .trigger("rising"), .Select("low")) register_63 (
    .D(\数据 ), .en(and_94_out), .Q(I7), .clk(CLK), .clr(RST));
  and and_95 (and_95_out, comparator_139_eq, comparator_140_lt);
  and and_96 (and_96_out, comparator_141_eq, comparator_142_lt);
  and and_97 (and_97_out, comparator_143_eq, comparator_144_lt);
  and and_98 (and_98_out, comparator_145_eq, comparator_146_lt);
  and and_99 (and_99_out, comparator_147_eq, comparator_148_lt);
  and and_100 (and_100_out, comparator_149_eq, comparator_150_lt);
  and and_101 (and_101_out, comparator_151_eq, comparator_152_lt);
  and and_102 (and_102_out, comparator_153_eq, comparator_154_lt);
  and and_103 (and_103_out, comparator_155_eq, comparator_156_lt);
  Priority_Encoder #(.select(4), .disabled("Z")) priority_encoder_6 (
    .in1(and_95_out), .in2(and_96_out), .in3(and_97_out), .in4(and_98_out), .in5(and_99_out),
    .in6(and_100_out), .in7(and_101_out), .in8(and_102_out), .in9(and_103_out), .out(priority_encoder_6_out),
    .en_out(priority_encoder_6_en_out));  // open: in0, in10, in11, in12, in13, in14, in15, gs, en_in
  Multiplexer #(.select(1), .width(4), .disabled("Z"), .enable("false")) multiplexer_34 (
    .in0(priority_encoder_6_out), .in1(\Y坐标 ), .out(NextUp), .sel(priority_encoder_6_en_out));
  Comparator #(.width(7), .mode("unsigned")) comparator_157 (
    .a(\计数 ), .b(7'b0000111), .eq(comparator_157_eq));  // open: gt, lt
  Comparator #(.width(7), .mode("unsigned")) comparator_158 (
    .a(\计数 ), .b(7'b0010000), .eq(comparator_158_eq));  // open: gt, lt
  Comparator #(.width(7), .mode("unsigned")) comparator_159 (
    .a(\计数 ), .b(7'b0011001), .eq(comparator_159_eq));  // open: gt, lt
  Comparator #(.width(7), .mode("unsigned")) comparator_160 (
    .a(\计数 ), .b(7'b0100010), .eq(comparator_160_eq));  // open: gt, lt
  Comparator #(.width(7), .mode("unsigned")) comparator_161 (
    .a(\计数 ), .b(7'b0101011), .eq(comparator_161_eq));  // open: gt, lt
  Comparator #(.width(7), .mode("unsigned")) comparator_162 (
    .a(\计数 ), .b(7'b0110100), .eq(comparator_162_eq));  // open: gt, lt
  Comparator #(.width(7), .mode("unsigned")) comparator_163 (
    .a(\计数 ), .b(7'b0111101), .eq(comparator_163_eq));  // open: gt, lt
  Comparator #(.width(7), .mode("unsigned")) comparator_164 (
    .a(\计数 ), .b(7'b1000110), .eq(comparator_164_eq));  // open: gt, lt
  Comparator #(.width(7), .mode("unsigned")) comparator_165 (
    .a(\计数 ), .b(7'b1001111), .eq(comparator_165_eq));  // open: gt, lt
  and and_104 (and_104_out, comparator_157_eq, \写入使能 );
  and and_105 (and_105_out, comparator_158_eq, \写入使能 );
  and and_106 (and_106_out, comparator_159_eq, \写入使能 );
  and and_107 (and_107_out, comparator_160_eq, \写入使能 );
  and and_108 (and_108_out, comparator_161_eq, \写入使能 );
  and and_109 (and_109_out, comparator_162_eq, \写入使能 );
  and and_110 (and_110_out, comparator_163_eq, \写入使能 );
  and and_111 (and_111_out, comparator_164_eq, \写入使能 );
  and and_112 (and_112_out, comparator_165_eq, \写入使能 );
  Register #(.width(4), .trigger("rising"), .Select("low")) register_64 (
    .D(\数据 ), .en(and_104_out), .Q(A8), .clk(CLK), .clr(RST));
  Register #(.width(4), .trigger("rising"), .Select("low")) register_65 (
    .D(\数据 ), .en(and_105_out), .Q(B8), .clk(CLK), .clr(RST));
  Register #(.width(4), .trigger("rising"), .Select("low")) register_66 (
    .D(\数据 ), .en(and_106_out), .Q(C8), .clk(CLK), .clr(RST));
  Register #(.width(4), .trigger("rising"), .Select("low")) register_67 (
    .D(\数据 ), .en(and_107_out), .Q(D8), .clk(CLK), .clr(RST));
  Register #(.width(4), .trigger("rising"), .Select("low")) register_68 (
    .D(\数据 ), .en(and_108_out), .Q(E8), .clk(CLK), .clr(RST));
  Register #(.width(4), .trigger("rising"), .Select("low")) register_69 (
    .D(\数据 ), .en(and_109_out), .Q(F8), .clk(CLK), .clr(RST));
  Register #(.width(4), .trigger("rising"), .Select("low")) register_70 (
    .D(\数据 ), .en(and_110_out), .Q(G8), .clk(CLK), .clr(RST));
  Register #(.width(4), .trigger("rising"), .Select("low")) register_71 (
    .D(\数据 ), .en(and_111_out), .Q(H8), .clk(CLK), .clr(RST));
  Register #(.width(4), .trigger("rising"), .Select("low")) register_72 (
    .D(\数据 ), .en(and_112_out), .Q(I8), .clk(CLK), .clr(RST));
  Multiplexer #(.select(4), .width(4), .disabled("Z"), .enable("false")) multiplexer_35 (
    .in1(A1), .in2(A2), .in3(A3), .in4(A4), .in5(A5), .in6(A6), .in7(A7), .in8(A8), .in9(A9), .out(\行1 ),
    .sel(\X坐标 ));  // open: in0, in10, in11, in12, in13, in14, in15
  Multiplexer #(.select(4), .width(4), .disabled("Z"), .enable("false")) multiplexer_36 (
    .in1(D1), .in2(D2), .in3(D3), .in4(D4), .in5(D5), .in6(D6), .in7(D7), .in8(D8), .in9(D9), .out(\行4 ),
    .sel(\X坐标 ));  // open: in0, in10, in11, in12, in13, in14, in15
  Multiplexer #(.select(4), .width(4), .disabled("Z"), .enable("false")) multiplexer_37 (
    .in1(G1), .in2(G2), .in3(G3), .in4(G4), .in5(G5), .in6(G6), .in7(G7), .in8(G8), .in9(G9), .out(\行7 ),
    .sel(\X坐标 ));  // open: in0, in10, in11, in12, in13, in14, in15
  Multiplexer #(.select(4), .width(4), .disabled("Z"), .enable("false")) multiplexer_38 (
    .in1(B1), .in2(B2), .in3(B3), .in4(B4), .in5(B5), .in6(B6), .in7(B7), .in8(B8), .in9(B9), .out(\行2 ),
    .sel(\X坐标 ));  // open: in0, in10, in11, in12, in13, in14, in15
  Multiplexer #(.select(4), .width(4), .disabled("Z"), .enable("false")) multiplexer_39 (
    .in1(E1), .in2(E2), .in3(E3), .in4(E4), .in5(E5), .in6(E6), .in7(E7), .in8(E8), .in9(E9), .out(\行5 ),
    .sel(\X坐标 ));  // open: in0, in10, in11, in12, in13, in14, in15
  Multiplexer #(.select(4), .width(4), .disabled("Z"), .enable("false")) multiplexer_40 (
    .in1(H1), .in2(H2), .in3(H3), .in4(H4), .in5(H5), .in6(H6), .in7(H7), .in8(H8), .in9(H9), .out(\行8 ),
    .sel(\X坐标 ));  // open: in0, in10, in11, in12, in13, in14, in15
  Comparator #(.width(7), .mode("unsigned")) comparator_166 (
    .a(\计数 ), .b(7'b0001000), .eq(comparator_166_eq));  // open: gt, lt
  and and_113 (and_113_out, comparator_166_eq, \写入使能 );
  Comparator #(.width(7), .mode("unsigned")) comparator_167 (
    .a(\计数 ), .b(7'b0010001), .eq(comparator_167_eq));  // open: gt, lt
  and and_114 (and_114_out, comparator_167_eq, \写入使能 );
  Comparator #(.width(7), .mode("unsigned")) comparator_168 (
    .a(\计数 ), .b(7'b0011010), .eq(comparator_168_eq));  // open: gt, lt
  and and_115 (and_115_out, comparator_168_eq, \写入使能 );
  Comparator #(.width(7), .mode("unsigned")) comparator_169 (
    .a(\计数 ), .b(7'b0100011), .eq(comparator_169_eq));  // open: gt, lt
  and and_116 (and_116_out, comparator_169_eq, \写入使能 );
  Comparator #(.width(7), .mode("unsigned")) comparator_170 (
    .a(\计数 ), .b(7'b0101100), .eq(comparator_170_eq));  // open: gt, lt
  and and_117 (and_117_out, comparator_170_eq, \写入使能 );
  Comparator #(.width(7), .mode("unsigned")) comparator_171 (
    .a(\计数 ), .b(7'b0110101), .eq(comparator_171_eq));  // open: gt, lt
  and and_118 (and_118_out, comparator_171_eq, \写入使能 );
  Comparator #(.width(7), .mode("unsigned")) comparator_172 (
    .a(\计数 ), .b(7'b0111110), .eq(comparator_172_eq));  // open: gt, lt
  and and_119 (and_119_out, comparator_172_eq, \写入使能 );
  Comparator #(.width(7), .mode("unsigned")) comparator_173 (
    .a(\计数 ), .b(7'b1000111), .eq(comparator_173_eq));  // open: gt, lt
  and and_120 (and_120_out, comparator_173_eq, \写入使能 );
  Comparator #(.width(7), .mode("unsigned")) comparator_174 (
    .a(\计数 ), .b(7'b1010000), .eq(comparator_174_eq));  // open: gt, lt
  and and_121 (and_121_out, comparator_174_eq, \写入使能 );
  Multiplexer #(.select(4), .width(4), .disabled("Z"), .enable("false")) multiplexer_41 (
    .in1(C1), .in2(C2), .in3(C3), .in4(C4), .in5(C5), .in6(C6), .in7(C7), .in8(C8), .in9(C9), .out(\行3 ),
    .sel(\X坐标 ));  // open: in0, in10, in11, in12, in13, in14, in15
  Multiplexer #(.select(4), .width(4), .disabled("Z"), .enable("false")) multiplexer_42 (
    .in1(F1), .in2(F2), .in3(F3), .in4(F4), .in5(F5), .in6(F6), .in7(F7), .in8(F8), .in9(F9), .out(\行6 ),
    .sel(\X坐标 ));  // open: in0, in10, in11, in12, in13, in14, in15
  Multiplexer #(.select(4), .width(4), .disabled("Z"), .enable("false")) multiplexer_43 (
    .in1(I1), .in2(I2), .in3(I3), .in4(I4), .in5(I5), .in6(I6), .in7(I7), .in8(I8), .in9(I9), .out(\行9 ),
    .sel(\X坐标 ));  // open: in0, in10, in11, in12, in13, in14, in15
  Register #(.width(4), .trigger("rising"), .Select("low")) register_73 (
    .D(\数据 ), .en(and_113_out), .Q(A9), .clk(CLK), .clr(RST));
  Register #(.width(4), .trigger("rising"), .Select("low")) register_74 (
    .D(\数据 ), .en(and_114_out), .Q(B9), .clk(CLK), .clr(RST));
  Register #(.width(4), .trigger("rising"), .Select("low")) register_75 (
    .D(\数据 ), .en(and_115_out), .Q(C9), .clk(CLK), .clr(RST));
  Register #(.width(4), .trigger("rising"), .Select("low")) register_76 (
    .D(\数据 ), .en(and_116_out), .Q(D9), .clk(CLK), .clr(RST));
  Register #(.width(4), .trigger("rising"), .Select("low")) register_77 (
    .D(\数据 ), .en(and_117_out), .Q(E9), .clk(CLK), .clr(RST));
  Register #(.width(4), .trigger("rising"), .Select("low")) register_78 (
    .D(\数据 ), .en(and_118_out), .Q(F9), .clk(CLK), .clr(RST));
  Register #(.width(4), .trigger("rising"), .Select("low")) register_79 (
    .D(\数据 ), .en(and_119_out), .Q(G9), .clk(CLK), .clr(RST));
  Register #(.width(4), .trigger("rising"), .Select("low")) register_80 (
    .D(\数据 ), .en(and_120_out), .Q(H9), .clk(CLK), .clr(RST));
  Register #(.width(4), .trigger("rising"), .Select("low")) register_81 (
    .D(\数据 ), .en(and_121_out), .Q(I9), .clk(CLK), .clr(RST));
  Comparator #(.width(4), .mode("unsigned")) comparator_175 (
    .a(A9), .b(4'b0000), .eq(comparator_175_eq));  // open: gt, lt
  Comparator #(.width(4), .mode("unsigned")) comparator_176 (
    .a(A8), .b(4'b0000), .eq(comparator_176_eq));  // open: gt, lt
  Comparator #(.width(4), .mode("unsigned")) comparator_177 (
    .a(A7), .b(4'b0000), .eq(comparator_177_eq));  // open: gt, lt
  Comparator #(.width(4), .mode("unsigned")) comparator_178 (
    .a(A6), .b(4'b0000), .eq(comparator_178_eq));  // open: gt, lt
  Comparator #(.width(4), .mode("unsigned")) comparator_179 (
    .a(A5), .b(4'b0000), .eq(comparator_179_eq));  // open: gt, lt
  Comparator #(.width(4), .mode("unsigned")) comparator_180 (
    .a(A4), .b(4'b0000), .eq(comparator_180_eq));  // open: gt, lt
  Comparator #(.width(4), .mode("unsigned")) comparator_181 (
    .a(A3), .b(4'b0000), .eq(comparator_181_eq));  // open: gt, lt
  Comparator #(.width(4), .mode("unsigned")) comparator_182 (
    .a(A2), .b(4'b0000), .eq(comparator_182_eq));  // open: gt, lt
  Comparator #(.width(4), .mode("unsigned")) comparator_183 (
    .a(A1), .b(4'b0000), .eq(comparator_183_eq));  // open: gt, lt
  Comparator #(.width(4), .mode("unsigned")) comparator_184 (
    .a(B9), .b(4'b0000), .eq(comparator_184_eq));  // open: gt, lt
  Comparator #(.width(4), .mode("unsigned")) comparator_185 (
    .a(B8), .b(4'b0000), .eq(comparator_185_eq));  // open: gt, lt
  Comparator #(.width(4), .mode("unsigned")) comparator_186 (
    .a(B7), .b(4'b0000), .eq(comparator_186_eq));  // open: gt, lt
  Comparator #(.width(4), .mode("unsigned")) comparator_187 (
    .a(B6), .b(4'b0000), .eq(comparator_187_eq));  // open: gt, lt
  Comparator #(.width(4), .mode("unsigned")) comparator_188 (
    .a(B5), .b(4'b0000), .eq(comparator_188_eq));  // open: gt, lt
  Comparator #(.width(4), .mode("unsigned")) comparator_189 (
    .a(B4), .b(4'b0000), .eq(comparator_189_eq));  // open: gt, lt
  Comparator #(.width(4), .mode("unsigned")) comparator_190 (
    .a(B3), .b(4'b0000), .eq(comparator_190_eq));  // open: gt, lt
  Comparator #(.width(4), .mode("unsigned")) comparator_191 (
    .a(B2), .b(4'b0000), .eq(comparator_191_eq));  // open: gt, lt
  Comparator #(.width(4), .mode("unsigned")) comparator_192 (
    .a(B1), .b(4'b0000), .eq(comparator_192_eq));  // open: gt, lt
  Priority_Encoder #(.select(4), .disabled("Z")) priority_encoder_7 (
    .in1(comparator_175_eq), .in2(comparator_176_eq), .in3(comparator_177_eq), .in4(comparator_178_eq),
    .in5(comparator_179_eq), .in6(comparator_180_eq), .in7(comparator_181_eq), .in8(comparator_182_eq),
    .in9(comparator_183_eq), .out(priority_encoder_7_out), .gs(\行1包含空格 ));  // open: in0, in10, in11, in12, in13, in14, in15, en_out, en_in
  Priority_Encoder #(.select(4), .disabled("Z")) priority_encoder_8 (
    .in1(comparator_184_eq), .in2(comparator_185_eq), .in3(comparator_186_eq), .in4(comparator_187_eq),
    .in5(comparator_188_eq), .in6(comparator_189_eq), .in7(comparator_190_eq), .in8(comparator_191_eq),
    .in9(comparator_192_eq), .out(priority_encoder_8_out), .gs(\行2包含空格 ));  // open: in0, in10, in11, in12, in13, in14, in15, en_out, en_in
  Subtractor #(.width(4)) subtractor_6 (.a(4'b1010), .b(priority_encoder_7_out), .out(\行1空格坐标 ));  // open: bin, bout
  Subtractor #(.width(4)) subtractor_7 (.a(4'b1010), .b(priority_encoder_8_out), .out(\行2空格坐标 ));  // open: bin, bout
  Comparator #(.width(4), .mode("unsigned")) comparator_193 (
    .a(C9), .b(4'b0000), .eq(comparator_193_eq));  // open: gt, lt
  Comparator #(.width(4), .mode("unsigned")) comparator_194 (
    .a(C8), .b(4'b0000), .eq(comparator_194_eq));  // open: gt, lt
  Comparator #(.width(4), .mode("unsigned")) comparator_195 (
    .a(C7), .b(4'b0000), .eq(comparator_195_eq));  // open: gt, lt
  Comparator #(.width(4), .mode("unsigned")) comparator_196 (
    .a(C6), .b(4'b0000), .eq(comparator_196_eq));  // open: gt, lt
  Comparator #(.width(4), .mode("unsigned")) comparator_197 (
    .a(C5), .b(4'b0000), .eq(comparator_197_eq));  // open: gt, lt
  Comparator #(.width(4), .mode("unsigned")) comparator_198 (
    .a(C4), .b(4'b0000), .eq(comparator_198_eq));  // open: gt, lt
  Comparator #(.width(4), .mode("unsigned")) comparator_199 (
    .a(C3), .b(4'b0000), .eq(comparator_199_eq));  // open: gt, lt
  Comparator #(.width(4), .mode("unsigned")) comparator_200 (
    .a(C2), .b(4'b0000), .eq(comparator_200_eq));  // open: gt, lt
  Comparator #(.width(4), .mode("unsigned")) comparator_201 (
    .a(C1), .b(4'b0000), .eq(comparator_201_eq));  // open: gt, lt
  Comparator #(.width(4), .mode("unsigned")) comparator_202 (
    .a(D9), .b(4'b0000), .eq(comparator_202_eq));  // open: gt, lt
  Comparator #(.width(4), .mode("unsigned")) comparator_203 (
    .a(D8), .b(4'b0000), .eq(comparator_203_eq));  // open: gt, lt
  Comparator #(.width(4), .mode("unsigned")) comparator_204 (
    .a(D7), .b(4'b0000), .eq(comparator_204_eq));  // open: gt, lt
  Comparator #(.width(4), .mode("unsigned")) comparator_205 (
    .a(D6), .b(4'b0000), .eq(comparator_205_eq));  // open: gt, lt
  Comparator #(.width(4), .mode("unsigned")) comparator_206 (
    .a(D5), .b(4'b0000), .eq(comparator_206_eq));  // open: gt, lt
  Comparator #(.width(4), .mode("unsigned")) comparator_207 (
    .a(D4), .b(4'b0000), .eq(comparator_207_eq));  // open: gt, lt
  Comparator #(.width(4), .mode("unsigned")) comparator_208 (
    .a(D3), .b(4'b0000), .eq(comparator_208_eq));  // open: gt, lt
  Comparator #(.width(4), .mode("unsigned")) comparator_209 (
    .a(D2), .b(4'b0000), .eq(comparator_209_eq));  // open: gt, lt
  Comparator #(.width(4), .mode("unsigned")) comparator_210 (
    .a(D1), .b(4'b0000), .eq(comparator_210_eq));  // open: gt, lt
  Priority_Encoder #(.select(4), .disabled("Z")) priority_encoder_9 (
    .in1(comparator_193_eq), .in2(comparator_194_eq), .in3(comparator_195_eq), .in4(comparator_196_eq),
    .in5(comparator_197_eq), .in6(comparator_198_eq), .in7(comparator_199_eq), .in8(comparator_200_eq),
    .in9(comparator_201_eq), .out(priority_encoder_9_out), .gs(\行3包含空格 ));  // open: in0, in10, in11, in12, in13, in14, in15, en_out, en_in
  Priority_Encoder #(.select(4), .disabled("Z")) priority_encoder_10 (
    .in1(comparator_202_eq), .in2(comparator_203_eq), .in3(comparator_204_eq), .in4(comparator_205_eq),
    .in5(comparator_206_eq), .in6(comparator_207_eq), .in7(comparator_208_eq), .in8(comparator_209_eq),
    .in9(comparator_210_eq), .out(priority_encoder_10_out), .gs(\行4包含空格 ));  // open: in0, in10, in11, in12, in13, in14, in15, en_out, en_in
  Subtractor #(.width(4)) subtractor_8 (.a(4'b1010), .b(priority_encoder_9_out), .out(\行3空格坐标 ));  // open: bin, bout
  Subtractor #(.width(4)) subtractor_9 (.a(4'b1010), .b(priority_encoder_10_out), .out(\行4空格坐标 ));  // open: bin, bout
  Comparator #(.width(4), .mode("unsigned")) comparator_211 (
    .a(E9), .b(4'b0000), .eq(comparator_211_eq));  // open: gt, lt
  Comparator #(.width(4), .mode("unsigned")) comparator_212 (
    .a(E8), .b(4'b0000), .eq(comparator_212_eq));  // open: gt, lt
  Comparator #(.width(4), .mode("unsigned")) comparator_213 (
    .a(E7), .b(4'b0000), .eq(comparator_213_eq));  // open: gt, lt
  Comparator #(.width(4), .mode("unsigned")) comparator_214 (
    .a(E6), .b(4'b0000), .eq(comparator_214_eq));  // open: gt, lt
  Comparator #(.width(4), .mode("unsigned")) comparator_215 (
    .a(E5), .b(4'b0000), .eq(comparator_215_eq));  // open: gt, lt
  Comparator #(.width(4), .mode("unsigned")) comparator_216 (
    .a(E4), .b(4'b0000), .eq(comparator_216_eq));  // open: gt, lt
  Comparator #(.width(4), .mode("unsigned")) comparator_217 (
    .a(E3), .b(4'b0000), .eq(comparator_217_eq));  // open: gt, lt
  Comparator #(.width(4), .mode("unsigned")) comparator_218 (
    .a(E2), .b(4'b0000), .eq(comparator_218_eq));  // open: gt, lt
  Comparator #(.width(4), .mode("unsigned")) comparator_219 (
    .a(E1), .b(4'b0000), .eq(comparator_219_eq));  // open: gt, lt
  Comparator #(.width(4), .mode("unsigned")) comparator_220 (
    .a(F9), .b(4'b0000), .eq(comparator_220_eq));  // open: gt, lt
  Comparator #(.width(4), .mode("unsigned")) comparator_221 (
    .a(F8), .b(4'b0000), .eq(comparator_221_eq));  // open: gt, lt
  Comparator #(.width(4), .mode("unsigned")) comparator_222 (
    .a(F7), .b(4'b0000), .eq(comparator_222_eq));  // open: gt, lt
  Comparator #(.width(4), .mode("unsigned")) comparator_223 (
    .a(F6), .b(4'b0000), .eq(comparator_223_eq));  // open: gt, lt
  Comparator #(.width(4), .mode("unsigned")) comparator_224 (
    .a(F5), .b(4'b0000), .eq(comparator_224_eq));  // open: gt, lt
  Comparator #(.width(4), .mode("unsigned")) comparator_225 (
    .a(F4), .b(4'b0000), .eq(comparator_225_eq));  // open: gt, lt
  Comparator #(.width(4), .mode("unsigned")) comparator_226 (
    .a(F3), .b(4'b0000), .eq(comparator_226_eq));  // open: gt, lt
  Comparator #(.width(4), .mode("unsigned")) comparator_227 (
    .a(F2), .b(4'b0000), .eq(comparator_227_eq));  // open: gt, lt
  Comparator #(.width(4), .mode("unsigned")) comparator_228 (
    .a(F1), .b(4'b0000), .eq(comparator_228_eq));  // open: gt, lt
  Priority_Encoder #(.select(4), .disabled("Z")) priority_encoder_11 (
    .in1(comparator_211_eq), .in2(comparator_212_eq), .in3(comparator_213_eq), .in4(comparator_214_eq),
    .in5(comparator_215_eq), .in6(comparator_216_eq), .in7(comparator_217_eq), .in8(comparator_218_eq),
    .in9(comparator_219_eq), .out(priority_encoder_11_out), .gs(\行5包含空格 ));  // open: in0, in10, in11, in12, in13, in14, in15, en_out, en_in
  Priority_Encoder #(.select(4), .disabled("Z")) priority_encoder_12 (
    .in1(comparator_220_eq), .in2(comparator_221_eq), .in3(comparator_222_eq), .in4(comparator_223_eq),
    .in5(comparator_224_eq), .in6(comparator_225_eq), .in7(comparator_226_eq), .in8(comparator_227_eq),
    .in9(comparator_228_eq), .out(priority_encoder_12_out), .gs(\行6包含空格 ));  // open: in0, in10, in11, in12, in13, in14, in15, en_out, en_in
  Subtractor #(.width(4)) subtractor_10 (.a(4'b1010), .b(priority_encoder_11_out), .out(\行5空格坐标 ));  // open: bin, bout
  Subtractor #(.width(4)) subtractor_11 (.a(4'b1010), .b(priority_encoder_12_out), .out(\行6空格坐标 ));  // open: bin, bout
  Comparator #(.width(4), .mode("unsigned")) comparator_229 (
    .a(G9), .b(4'b0000), .eq(comparator_229_eq));  // open: gt, lt
  Comparator #(.width(4), .mode("unsigned")) comparator_230 (
    .a(G8), .b(4'b0000), .eq(comparator_230_eq));  // open: gt, lt
  Comparator #(.width(4), .mode("unsigned")) comparator_231 (
    .a(G7), .b(4'b0000), .eq(comparator_231_eq));  // open: gt, lt
  Comparator #(.width(4), .mode("unsigned")) comparator_232 (
    .a(G6), .b(4'b0000), .eq(comparator_232_eq));  // open: gt, lt
  Comparator #(.width(4), .mode("unsigned")) comparator_233 (
    .a(G5), .b(4'b0000), .eq(comparator_233_eq));  // open: gt, lt
  Comparator #(.width(4), .mode("unsigned")) comparator_234 (
    .a(G4), .b(4'b0000), .eq(comparator_234_eq));  // open: gt, lt
  Comparator #(.width(4), .mode("unsigned")) comparator_235 (
    .a(G3), .b(4'b0000), .eq(comparator_235_eq));  // open: gt, lt
  Comparator #(.width(4), .mode("unsigned")) comparator_236 (
    .a(G2), .b(4'b0000), .eq(comparator_236_eq));  // open: gt, lt
  Comparator #(.width(4), .mode("unsigned")) comparator_237 (
    .a(G1), .b(4'b0000), .eq(comparator_237_eq));  // open: gt, lt
  Comparator #(.width(4), .mode("unsigned")) comparator_238 (
    .a(H9), .b(4'b0000), .eq(comparator_238_eq));  // open: gt, lt
  Comparator #(.width(4), .mode("unsigned")) comparator_239 (
    .a(H8), .b(4'b0000), .eq(comparator_239_eq));  // open: gt, lt
  Comparator #(.width(4), .mode("unsigned")) comparator_240 (
    .a(H7), .b(4'b0000), .eq(comparator_240_eq));  // open: gt, lt
  Comparator #(.width(4), .mode("unsigned")) comparator_241 (
    .a(H6), .b(4'b0000), .eq(comparator_241_eq));  // open: gt, lt
  Comparator #(.width(4), .mode("unsigned")) comparator_242 (
    .a(H5), .b(4'b0000), .eq(comparator_242_eq));  // open: gt, lt
  Comparator #(.width(4), .mode("unsigned")) comparator_243 (
    .a(H4), .b(4'b0000), .eq(comparator_243_eq));  // open: gt, lt
  Comparator #(.width(4), .mode("unsigned")) comparator_244 (
    .a(H3), .b(4'b0000), .eq(comparator_244_eq));  // open: gt, lt
  Comparator #(.width(4), .mode("unsigned")) comparator_245 (
    .a(H2), .b(4'b0000), .eq(comparator_245_eq));  // open: gt, lt
  Comparator #(.width(4), .mode("unsigned")) comparator_246 (
    .a(H1), .b(4'b0000), .eq(comparator_246_eq));  // open: gt, lt
  Priority_Encoder #(.select(4), .disabled("Z")) priority_encoder_13 (
    .in1(comparator_229_eq), .in2(comparator_230_eq), .in3(comparator_231_eq), .in4(comparator_232_eq),
    .in5(comparator_233_eq), .in6(comparator_234_eq), .in7(comparator_235_eq), .in8(comparator_236_eq),
    .in9(comparator_237_eq), .out(priority_encoder_13_out), .gs(\行7包含空格 ));  // open: in0, in10, in11, in12, in13, in14, in15, en_out, en_in
  Priority_Encoder #(.select(4), .disabled("Z")) priority_encoder_14 (
    .in1(comparator_238_eq), .in2(comparator_239_eq), .in3(comparator_240_eq), .in4(comparator_241_eq),
    .in5(comparator_242_eq), .in6(comparator_243_eq), .in7(comparator_244_eq), .in8(comparator_245_eq),
    .in9(comparator_246_eq), .out(priority_encoder_14_out), .gs(\行8包含空格 ));  // open: in0, in10, in11, in12, in13, in14, in15, en_out, en_in
  Subtractor #(.width(4)) subtractor_12 (.a(4'b1010), .b(priority_encoder_13_out), .out(\行7空格坐标 ));  // open: bin, bout
  Subtractor #(.width(4)) subtractor_13 (.a(4'b1010), .b(priority_encoder_14_out), .out(\行8空格坐标 ));  // open: bin, bout
  Comparator #(.width(4), .mode("unsigned")) comparator_247 (
    .a(I9), .b(4'b0000), .eq(comparator_247_eq));  // open: gt, lt
  Comparator #(.width(4), .mode("unsigned")) comparator_248 (
    .a(I8), .b(4'b0000), .eq(comparator_248_eq));  // open: gt, lt
  Comparator #(.width(4), .mode("unsigned")) comparator_249 (
    .a(I7), .b(4'b0000), .eq(comparator_249_eq));  // open: gt, lt
  Comparator #(.width(4), .mode("unsigned")) comparator_250 (
    .a(I6), .b(4'b0000), .eq(comparator_250_eq));  // open: gt, lt
  Comparator #(.width(4), .mode("unsigned")) comparator_251 (
    .a(I5), .b(4'b0000), .eq(comparator_251_eq));  // open: gt, lt
  Comparator #(.width(4), .mode("unsigned")) comparator_252 (
    .a(I4), .b(4'b0000), .eq(comparator_252_eq));  // open: gt, lt
  Comparator #(.width(4), .mode("unsigned")) comparator_253 (
    .a(I3), .b(4'b0000), .eq(comparator_253_eq));  // open: gt, lt
  Comparator #(.width(4), .mode("unsigned")) comparator_254 (
    .a(I2), .b(4'b0000), .eq(comparator_254_eq));  // open: gt, lt
  Comparator #(.width(4), .mode("unsigned")) comparator_255 (
    .a(I1), .b(4'b0000), .eq(comparator_255_eq));  // open: gt, lt
  Priority_Encoder #(.select(4), .disabled("Z")) priority_encoder_15 (
    .in1(comparator_247_eq), .in2(comparator_248_eq), .in3(comparator_249_eq), .in4(comparator_250_eq),
    .in5(comparator_251_eq), .in6(comparator_252_eq), .in7(comparator_253_eq), .in8(comparator_254_eq),
    .in9(comparator_255_eq), .out(priority_encoder_15_out), .gs(\行9包含空格 ));  // open: in0, in10, in11, in12, in13, in14, in15, en_out, en_in
  Priority_Encoder #(.select(4), .disabled("Z")) priority_encoder_16 (
    .in1(\行9包含空格 ), .in2(\行8包含空格 ), .in3(\行7包含空格 ), .in4(\行6包含空格 ), .in5(\行5包含空格 ), .in6(\行4包含空格 ),
    .in7(\行3包含空格 ), .in8(\行2包含空格 ), .in9(\行1包含空格 ), .out(priority_encoder_16_out));  // open: in0, in10, in11, in12, in13, in14, in15, gs, en_out, en_in
  Multiplexer #(.select(4), .width(4), .disabled("Z"), .enable("false")) multiplexer_44 (
    .in1(\行1空格坐标 ), .in2(\行2空格坐标 ), .in3(\行3空格坐标 ), .in4(\行4空格坐标 ), .in5(\行5空格坐标 ), .in6(\行6空格坐标 ),
    .in7(\行6空格坐标 ), .in8(\行8空格坐标 ), .in9(\行7空格坐标 ), .out(\首个空格X坐标 ), .sel(\首个空格Y坐标 ));  // open: in0, in10, in11, in12, in13, in14, in15
  Subtractor #(.width(4)) subtractor_14 (.a(4'b1010), .b(priority_encoder_15_out), .out(\行9空格坐标 ));  // open: bin, bout
  Subtractor #(.width(4)) subtractor_15 (.a(4'b1010), .b(priority_encoder_16_out), .out(\首个空格Y坐标 ));  // open: bin, bout

  // Other names for the same wires on the sheet: 使能 = \写入使能 ; 首空X[3:0] = \首个空格X坐标 ; 首空Y[3:0] = \首个空格Y坐标 
endmodule
// 终盘寄存器
module \终盘寄存器  (
  input  CLK,
  input  RST,
  input  \使能 ,
  input  [3:0] \数据 ,
  input  [3:0] A1,
  input  [3:0] A2,
  input  [3:0] A3,
  input  [3:0] A4,
  input  [3:0] A5,
  input  [3:0] A7,
  input  [3:0] A6,
  input  [3:0] A8,
  input  [3:0] A9,
  input  [3:0] B1,
  input  [3:0] B2,
  input  [3:0] B3,
  input  [3:0] B4,
  input  [3:0] B5,
  input  [3:0] B7,
  input  [3:0] B6,
  input  [3:0] B8,
  input  [3:0] B9,
  input  [3:0] C1,
  input  [3:0] C2,
  input  [3:0] C3,
  input  [3:0] C4,
  input  [3:0] C5,
  input  [3:0] C7,
  input  [3:0] C6,
  input  [3:0] C8,
  input  [3:0] C9,
  input  [3:0] D1,
  input  [3:0] D2,
  input  [3:0] D3,
  input  [3:0] D4,
  input  [3:0] D5,
  input  [3:0] D7,
  input  [3:0] D6,
  input  [3:0] D8,
  input  [3:0] D9,
  input  [3:0] E1,
  input  [3:0] E2,
  input  [3:0] E3,
  input  [3:0] E4,
  input  [3:0] E5,
  input  [3:0] E7,
  input  [3:0] E6,
  input  [3:0] E8,
  input  [3:0] E9,
  input  [3:0] F1,
  input  [3:0] F2,
  input  [3:0] F3,
  input  [3:0] F4,
  input  [3:0] F5,
  input  [3:0] F7,
  input  [3:0] F6,
  input  [3:0] F8,
  input  [3:0] F9,
  input  [3:0] G1,
  input  [3:0] G2,
  input  [3:0] G3,
  input  [3:0] G4,
  input  [3:0] G5,
  input  [3:0] G7,
  input  [3:0] G6,
  input  [3:0] G8,
  input  [3:0] G9,
  input  [3:0] H1,
  input  [3:0] H2,
  input  [3:0] H3,
  input  [3:0] H4,
  input  [3:0] H5,
  input  [3:0] H7,
  input  [3:0] H6,
  input  [3:0] H8,
  input  [3:0] H9,
  input  [3:0] I1,
  input  [3:0] I2,
  input  [3:0] I3,
  input  [3:0] I4,
  input  [3:0] I5,
  input  [3:0] I7,
  input  [3:0] I6,
  input  [3:0] I8,
  input  [3:0] I9,
  output \计数已满 ,
  output \完成数独 
);

  wire and_1_out, and_2_out, and_3_out, and_4_out, and_5_out, and_6_out, and_7_out, and_8_out, and_9_out,
       and_11_out, and_12_out, and_13_out, and_14_out, and_15_out, and_16_out, and_17_out, and_18_out,
       and_19_out, and_22_out, and_23_out, and_24_out, and_25_out, and_26_out, and_27_out, and_28_out,
       and_29_out, and_30_out, and_32_out, and_33_out, and_34_out, and_35_out, and_36_out, and_37_out,
       and_38_out, and_39_out, and_40_out, and_42_out, and_43_out, and_44_out, and_45_out, and_46_out,
       and_47_out, and_48_out, and_49_out, and_50_out, and_52_out, and_53_out, and_54_out, and_55_out,
       and_56_out, and_57_out, and_58_out, and_59_out, and_60_out, and_62_out, and_63_out, and_64_out,
       and_65_out, and_66_out, and_67_out, and_68_out, and_69_out, and_70_out, and_72_out, and_73_out,
       and_74_out, and_75_out, and_76_out, and_77_out, and_78_out, and_79_out, and_80_out, and_82_out,
       and_83_out, and_84_out, and_85_out, and_86_out, and_87_out, and_88_out, and_89_out, and_90_out,
       comparator_1_eq, comparator_2_eq, comparator_3_eq, comparator_4_eq, comparator_5_eq, comparator_6_eq,
       comparator_7_eq, comparator_8_eq, comparator_9_eq, comparator_10_eq, comparator_11_eq,
       comparator_12_eq, comparator_13_eq, comparator_14_eq, comparator_15_eq, comparator_16_eq,
       comparator_17_eq, comparator_18_eq, comparator_20_eq, comparator_21_eq, comparator_22_eq,
       comparator_23_eq, comparator_24_eq, comparator_25_eq, comparator_26_eq, comparator_27_eq,
       comparator_28_eq, comparator_29_eq, comparator_30_eq, comparator_31_eq, comparator_32_eq,
       comparator_33_eq, comparator_34_eq, comparator_35_eq, comparator_36_eq, comparator_37_eq,
       comparator_38_eq, comparator_39_eq, comparator_40_eq, comparator_41_eq, comparator_42_eq,
       comparator_43_eq, comparator_44_eq, comparator_45_eq, comparator_46_eq, comparator_47_eq,
       comparator_48_eq, comparator_49_eq, comparator_50_eq, comparator_51_eq, comparator_52_eq,
       comparator_53_eq, comparator_54_eq, comparator_55_eq, comparator_56_eq, comparator_57_eq,
       comparator_58_eq, comparator_59_eq, comparator_60_eq, comparator_61_eq, comparator_62_eq,
       comparator_63_eq, comparator_64_eq, comparator_65_eq, comparator_66_eq, comparator_67_eq,
       comparator_68_eq, comparator_69_eq, comparator_70_eq, comparator_71_eq, comparator_72_eq,
       comparator_73_eq, comparator_74_eq, comparator_75_eq, comparator_76_eq, comparator_77_eq,
       comparator_78_eq, comparator_79_eq, comparator_80_eq, comparator_81_eq, comparator_82_eq,
       comparator_83_eq, comparator_84_eq, comparator_85_eq, comparator_86_eq, comparator_87_eq,
       comparator_88_eq, comparator_89_eq, comparator_90_eq, comparator_91_eq, comparator_92_eq,
       comparator_93_eq, comparator_94_eq, comparator_95_eq, comparator_96_eq, comparator_97_eq,
       comparator_98_eq, comparator_99_eq, comparator_100_eq, comparator_101_eq, comparator_102_eq,
       comparator_103_eq, comparator_104_eq, comparator_105_eq, comparator_106_eq, comparator_107_eq,
       comparator_108_eq, comparator_109_eq, comparator_110_eq, comparator_111_eq, comparator_112_eq,
       comparator_113_eq, comparator_114_eq, comparator_115_eq, comparator_116_eq, comparator_117_eq,
       comparator_118_eq, comparator_119_eq, comparator_120_eq, comparator_121_eq, comparator_122_eq,
       comparator_123_eq, comparator_124_eq, comparator_125_eq, comparator_126_eq, comparator_127_eq,
       comparator_128_eq, comparator_129_eq, comparator_130_eq, comparator_131_eq, comparator_132_eq,
       comparator_133_eq, comparator_134_eq, comparator_135_eq, comparator_136_eq, comparator_137_eq,
       comparator_138_eq, comparator_139_eq, comparator_140_eq, comparator_141_eq, comparator_142_eq,
       comparator_143_eq, comparator_144_eq, comparator_145_eq, comparator_146_eq, comparator_147_eq,
       comparator_148_eq, comparator_149_eq, comparator_150_eq, comparator_151_eq, comparator_152_eq,
       comparator_153_eq, comparator_154_eq, comparator_155_eq, comparator_156_eq, comparator_157_eq,
       comparator_158_eq, comparator_159_eq, comparator_160_eq, comparator_161_eq, comparator_162_eq,
       comparator_163_eq, \列1相等 , \列2相等 , \列3相等 , \列4相等 , \列5相等 , \列6相等 , \列7相等 , \列8相等 , \列9相等 ;
  wire [3:0] register_1_q, register_2_q, register_3_q, register_4_q, register_5_q, register_6_q,
       register_7_q, register_8_q, register_9_q, register_10_q, register_11_q, register_12_q, register_13_q,
       register_14_q, register_15_q, register_16_q, register_17_q, register_18_q, register_19_q,
       register_20_q, register_21_q, register_22_q, register_23_q, register_24_q, register_25_q,
       register_26_q, register_27_q, register_28_q, register_29_q, register_30_q, register_31_q,
       register_32_q, register_33_q, register_34_q, register_35_q, register_36_q, register_37_q,
       register_38_q, register_39_q, register_40_q, register_41_q, register_42_q, register_43_q,
       register_44_q, register_45_q, register_46_q, register_47_q, register_48_q, register_49_q,
       register_50_q, register_51_q, register_52_q, register_53_q, register_54_q, register_55_q,
       register_56_q, register_57_q, register_58_q, register_59_q, register_60_q, register_61_q,
       register_62_q, register_63_q, register_64_q, register_65_q, register_66_q, register_67_q,
       register_68_q, register_69_q, register_70_q, register_71_q, register_72_q, register_73_q,
       register_74_q, register_75_q, register_76_q, register_77_q, register_78_q, register_79_q,
       register_80_q, register_81_q;
  wire [6:0] counter_1_q, \计数 ;

  Comparator #(.width(7), .mode("unsigned")) comparator_1 (
    .a(\计数 ), .b({7{1'b0}}), .eq(comparator_1_eq));  // open: gt, lt
  and and_1 (and_1_out, comparator_1_eq, \使能 );
  Comparator #(.width(7), .mode("unsigned")) comparator_2 (
    .a(\计数 ), .b(7'b0001001), .eq(comparator_2_eq));  // open: gt, lt
  and and_2 (and_2_out, comparator_2_eq, \使能 );
  Comparator #(.width(7), .mode("unsigned")) comparator_3 (
    .a(\计数 ), .b(7'b0010010), .eq(comparator_3_eq));  // open: gt, lt
  and and_3 (and_3_out, comparator_3_eq, \使能 );
  Comparator #(.width(7), .mode("unsigned")) comparator_4 (
    .a(\计数 ), .b(7'b0011011), .eq(comparator_4_eq));  // open: gt, lt
  and and_4 (and_4_out, comparator_4_eq, \使能 );
  Comparator #(.width(7), .mode("unsigned")) comparator_5 (
    .a(\计数 ), .b(7'b0100100), .eq(comparator_5_eq));  // open: gt, lt
  and and_5 (and_5_out, comparator_5_eq, \使能 );
  Comparator #(.width(7), .mode("unsigned")) comparator_6 (
    .a(\计数 ), .b(7'b0101101), .eq(comparator_6_eq));  // open: gt, lt
  and and_6 (and_6_out, comparator_6_eq, \使能 );
  Comparator #(.width(7), .mode("unsigned")) comparator_7 (
    .a(\计数 ), .b(7'b0110110), .eq(comparator_7_eq));  // open: gt, lt
  and and_7 (and_7_out, comparator_7_eq, \使能 );
  Comparator #(.width(7), .mode("unsigned")) comparator_8 (
    .a(\计数 ), .b(7'b0111111), .eq(comparator_8_eq));  // open: gt, lt
  and and_8 (and_8_out, comparator_8_eq, \使能 );
  Comparator #(.width(7), .mode("unsigned")) comparator_9 (
    .a(\计数 ), .b(7'b1001000), .eq(comparator_9_eq));  // open: gt, lt
  and and_9 (and_9_out, comparator_9_eq, \使能 );
  Register #(.width(4), .trigger("falling"), .Select("low")) register_1 (
    .D(\数据 ), .en(and_1_out), .Q(register_1_q), .clk(CLK), .clr(RST));
  Register #(.width(4), .trigger("falling"), .Select("low")) register_2 (
    .D(\数据 ), .en(and_2_out), .Q(register_2_q), .clk(CLK), .clr(RST));
  Register #(.width(4), .trigger("falling"), .Select("low")) register_3 (
    .D(\数据 ), .en(and_3_out), .Q(register_3_q), .clk(CLK), .clr(RST));
  Register #(.width(4), .trigger("falling"), .Select("low")) register_4 (
    .D(\数据 ), .en(and_4_out), .Q(register_4_q), .clk(CLK), .clr(RST));
  Register #(.width(4), .trigger("falling"), .Select("low")) register_5 (
    .D(\数据 ), .en(and_5_out), .Q(register_5_q), .clk(CLK), .clr(RST));
  Register #(.width(4), .trigger("falling"), .Select("low")) register_6 (
    .D(\数据 ), .en(and_6_out), .Q(register_6_q), .clk(CLK), .clr(RST));
  Register #(.width(4), .trigger("falling"), .Select("low")) register_7 (
    .D(\数据 ), .en(and_7_out), .Q(register_7_q), .clk(CLK), .clr(RST));
  Register #(.width(4), .trigger("falling"), .Select("low")) register_8 (
    .D(\数据 ), .en(and_8_out), .Q(register_8_q), .clk(CLK), .clr(RST));
  Register #(.width(4), .trigger("falling"), .Select("low")) register_9 (
    .D(\数据 ), .en(and_9_out), .Q(register_9_q), .clk(CLK), .clr(RST));
  Comparator #(.width(4), .mode("unsigned")) comparator_10 (
    .a(A1), .b(register_1_q), .eq(comparator_10_eq));  // open: gt, lt
  Comparator #(.width(4), .mode("unsigned")) comparator_11 (
    .a(B1), .b(register_2_q), .eq(comparator_11_eq));  // open: gt, lt
  Comparator #(.width(4), .mode("unsigned")) comparator_12 (
    .a(C1), .b(register_3_q), .eq(comparator_12_eq));  // open: gt, lt
  Comparator #(.width(4), .mode("unsigned")) comparator_13 (
    .a(D1), .b(register_4_q), .eq(comparator_13_eq));  // open: gt, lt
  Comparator #(.width(4), .mode("unsigned")) comparator_14 (
    .a(E1), .b(register_5_q), .eq(comparator_14_eq));  // open: gt, lt
  Comparator #(.width(4), .mode("unsigned")) comparator_15 (
    .a(F1), .b(register_6_q), .eq(comparator_15_eq));  // open: gt, lt
  Comparator #(.width(4), .mode("unsigned")) comparator_16 (
    .a(G1), .b(register_7_q), .eq(comparator_16_eq));  // open: gt, lt
  Comparator #(.width(4), .mode("unsigned")) comparator_17 (
    .a(H1), .b(register_8_q), .eq(comparator_17_eq));  // open: gt, lt
  Comparator #(.width(4), .mode("unsigned")) comparator_18 (
    .a(I1), .b(register_9_q), .eq(comparator_18_eq));  // open: gt, lt
  Comparator #(.width(7), .mode("unsigned")) comparator_19 (.a(\计数 ), .b(7'b1010010), .eq(\计数已满 ));  // open: gt, lt
  and and_10 (\列1相等 , comparator_10_eq, comparator_11_eq, comparator_12_eq, comparator_13_eq, comparator_14_eq, comparator_15_eq, comparator_16_eq, comparator_17_eq, comparator_18_eq);
  Comparator #(.width(7), .mode("unsigned")) comparator_20 (
    .a(\计数 ), .b(7'b0000001), .eq(comparator_20_eq));  // open: gt, lt
  Comparator #(.width(7), .mode("unsigned")) comparator_21 (
    .a(\计数 ), .b(7'b0001010), .eq(comparator_21_eq));  // open: gt, lt
  Comparator #(.width(7), .mode("unsigned")) comparator_22 (
    .a(\计数 ), .b(7'b0010011), .eq(comparator_22_eq));  // open: gt, lt
  Comparator #(.width(7), .mode("unsigned")) comparator_23 (
    .a(\计数 ), .b(7'b0011100), .eq(comparator_23_eq));  // open: gt, lt
  Comparator #(.width(7), .mode("unsigned")) comparator_24 (
    .a(\计数 ), .b(7'b0100101), .eq(comparator_24_eq));  // open: gt, lt
  Comparator #(.width(7), .mode("unsigned")) comparator_25 (
    .a(\计数 ), .b(7'b0101110), .eq(comparator_25_eq));  // open: gt, lt
  Comparator #(.width(7), .mode("unsigned")) comparator_26 (
    .a(\计数 ), .b(7'b0110111), .eq(comparator_26_eq));  // open: gt, lt
  Comparator #(.width(7), .mode("unsigned")) comparator_27 (
    .a(\计数 ), .b(7'b1000000), .eq(comparator_27_eq));  // open: gt, lt
  Comparator #(.width(7), .mode("unsigned")) comparator_28 (
    .a(\计数 ), .b(7'b1001001), .eq(comparator_28_eq));  // open: gt, lt
  Counter #(.width(7), .max('h53), .ongoal("stay"), .trigger("rising"), .behavior("new")) counter_1 (
    .count(\使能 ), .Q(counter_1_q), .clk(CLK), .clr(RST));  // open: load, D, carry, preset, down
  and and_11 (and_11_out, comparator_20_eq, \使能 );
  and and_12 (and_12_out, comparator_21_eq, \使能 );
  and and_13 (and_13_out, comparator_22_eq, \使能 );
  and and_14 (and_14_out, comparator_23_eq, \使能 );
  and and_15 (and_15_out, comparator_24_eq, \使能 );
  and and_16 (and_16_out, comparator_25_eq, \使能 );
  and and_17 (and_17_out, comparator_26_eq, \使能 );
  and and_18 (and_18_out, comparator_27_eq, \使能 );
  and and_19 (and_19_out, comparator_28_eq, \使能 );
  Subtractor #(.width(7)) subtractor_1 (.a(counter_1_q), .b(7'b0000001), .out(\计数 ));  // open: bin, bout
  Register #(.width(4), .trigger("falling"), .Select("low")) register_10 (
    .D(\数据 ), .en(and_11_out), .Q(register_10_q), .clk(CLK), .clr(RST));
  Register #(.width(4), .trigger("falling"), .Select("low")) register_11 (
    .D(\数据 ), .en(and_12_out), .Q(register_11_q), .clk(CLK), .clr(RST));
  Register #(.width(4), .trigger("falling"), .Select("low")) register_12 (
    .D(\数据 ), .en(and_13_out), .Q(register_12_q), .clk(CLK), .clr(RST));
  Register #(.width(4), .trigger("falling"), .Select("low")) register_13 (
    .D(\数据 ), .en(and_14_out), .Q(register_13_q), .clk(CLK), .clr(RST));
  Register #(.width(4), .trigger("falling"), .Select("low")) register_14 (
    .D(\数据 ), .en(and_15_out), .Q(register_14_q), .clk(CLK), .clr(RST));
  Register #(.width(4), .trigger("falling"), .Select("low")) register_15 (
    .D(\数据 ), .en(and_16_out), .Q(register_15_q), .clk(CLK), .clr(RST));
  Register #(.width(4), .trigger("falling"), .Select("low")) register_16 (
    .D(\数据 ), .en(and_17_out), .Q(register_16_q), .clk(CLK), .clr(RST));
  Register #(.width(4), .trigger("falling"), .Select("low")) register_17 (
    .D(\数据 ), .en(and_18_out), .Q(register_17_q), .clk(CLK), .clr(RST));
  Register #(.width(4), .trigger("falling"), .Select("low")) register_18 (
    .D(\数据 ), .en(and_19_out), .Q(register_18_q), .clk(CLK), .clr(RST));
  Comparator #(.width(4), .mode("unsigned")) comparator_29 (
    .a(A2), .b(register_10_q), .eq(comparator_29_eq));  // open: gt, lt
  Comparator #(.width(4), .mode("unsigned")) comparator_30 (
    .a(B2), .b(register_11_q), .eq(comparator_30_eq));  // open: gt, lt
  Comparator #(.width(4), .mode("unsigned")) comparator_31 (
    .a(C2), .b(register_12_q), .eq(comparator_31_eq));  // open: gt, lt
  Comparator #(.width(4), .mode("unsigned")) comparator_32 (
    .a(D2), .b(register_13_q), .eq(comparator_32_eq));  // open: gt, lt
  Comparator #(.width(4), .mode("unsigned")) comparator_33 (
    .a(E2), .b(register_14_q), .eq(comparator_33_eq));  // open: gt, lt
  Comparator #(.width(4), .mode("unsigned")) comparator_34 (
    .a(F2), .b(register_15_q), .eq(comparator_34_eq));  // open: gt, lt
  Comparator #(.width(4), .mode("unsigned")) comparator_35 (
    .a(G2), .b(register_16_q), .eq(comparator_35_eq));  // open: gt, lt
  Comparator #(.width(4), .mode("unsigned")) comparator_36 (
    .a(H2), .b(register_17_q), .eq(comparator_36_eq));  // open: gt, lt
  Comparator #(.width(4), .mode("unsigned")) comparator_37 (
    .a(I2), .b(register_18_q), .eq(comparator_37_eq));  // open: gt, lt
  and and_20 (\完成数独 , \列1相等 , \列2相等 , \列3相等 , \列4相等 , \列5相等 , \列6相等 , \列7相等 , \列8相等 , \列9相等 , \计数已满 );
  and and_21 (\列2相等 , comparator_29_eq, comparator_30_eq, comparator_31_eq, comparator_32_eq, comparator_33_eq, comparator_34_eq, comparator_35_eq, comparator_36_eq, comparator_37_eq);
  Comparator #(.width(7), .mode("unsigned")) comparator_38 (
    .a(\计数 ), .b(7'b0000010), .eq(comparator_38_eq));  // open: gt, lt
  Comparator #(.width(7), .mode("unsigned")) comparator_39 (
    .a(\计数 ), .b(7'b0001011), .eq(comparator_39_eq));  // open: gt, lt
  Comparator #(.width(7), .mode("unsigned")) comparator_40 (
    .a(\计数 ), .b(7'b0010100), .eq(comparator_40_eq));  // open: gt, lt
  Comparator #(.width(7), .mode("unsigned")) comparator_41 (
    .a(\计数 ), .b(7'b0011101), .eq(comparator_41_eq));  // open: gt, lt
  Comparator #(.width(7), .mode("unsigned")) comparator_42 (
    .a(\计数 ), .b(7'b0100110), .eq(comparator_42_eq));  // open: gt, lt
  Comparator #(.width(7), .mode("unsigned")) comparator_43 (
    .a(\计数 ), .b(7'b0101111), .eq(comparator_43_eq));  // open: gt, lt
  Comparator #(.width(7), .mode("unsigned")) comparator_44 (
    .a(\计数 ), .b(7'b0111000), .eq(comparator_44_eq));  // open: gt, lt
  Comparator #(.width(7), .mode("unsigned")) comparator_45 (
    .a(\计数 ), .b(7'b1000001), .eq(comparator_45_eq));  // open: gt, lt
  Comparator #(.width(7), .mode("unsigned")) comparator_46 (
    .a(\计数 ), .b(7'b1001010), .eq(comparator_46_eq));  // open: gt, lt
  and and_22 (and_22_out, comparator_38_eq, \使能 );
  and and_23 (and_23_out, comparator_39_eq, \使能 );
  and and_24 (and_24_out, comparator_40_eq, \使能 );
  and and_25 (and_25_out, comparator_41_eq, \使能 );
  and and_26 (and_26_out, comparator_42_eq, \使能 );
  and and_27 (and_27_out, comparator_43_eq, \使能 );
  and and_28 (and_28_out, comparator_44_eq, \使能 );
  and and_29 (and_29_out, comparator_45_eq, \使能 );
  and and_30 (and_30_out, comparator_46_eq, \使能 );
  Register #(.width(4), .trigger("falling"), .Select("low")) register_19 (
    .D(\数据 ), .en(and_22_out), .Q(register_19_q), .clk(CLK), .clr(RST));
  Register #(.width(4), .trigger("falling"), .Select("low")) register_20 (
    .D(\数据 ), .en(and_23_out), .Q(register_20_q), .clk(CLK), .clr(RST));
  Register #(.width(4), .trigger("falling"), .Select("low")) register_21 (
    .D(\数据 ), .en(and_24_out), .Q(register_21_q), .clk(CLK), .clr(RST));
  Register #(.width(4), .trigger("falling"), .Select("low")) register_22 (
    .D(\数据 ), .en(and_25_out), .Q(register_22_q), .clk(CLK), .clr(RST));
  Register #(.width(4), .trigger("falling"), .Select("low")) register_23 (
    .D(\数据 ), .en(and_26_out), .Q(register_23_q), .clk(CLK), .clr(RST));
  Register #(.width(4), .trigger("falling"), .Select("low")) register_24 (
    .D(\数据 ), .en(and_27_out), .Q(register_24_q), .clk(CLK), .clr(RST));
  Register #(.width(4), .trigger("falling"), .Select("low")) register_25 (
    .D(\数据 ), .en(and_28_out), .Q(register_25_q), .clk(CLK), .clr(RST));
  Register #(.width(4), .trigger("falling"), .Select("low")) register_26 (
    .D(\数据 ), .en(and_29_out), .Q(register_26_q), .clk(CLK), .clr(RST));
  Register #(.width(4), .trigger("falling"), .Select("low")) register_27 (
    .D(\数据 ), .en(and_30_out), .Q(register_27_q), .clk(CLK), .clr(RST));
  Comparator #(.width(4), .mode("unsigned")) comparator_47 (
    .a(A3), .b(register_19_q), .eq(comparator_47_eq));  // open: gt, lt
  Comparator #(.width(4), .mode("unsigned")) comparator_48 (
    .a(B3), .b(register_20_q), .eq(comparator_48_eq));  // open: gt, lt
  Comparator #(.width(4), .mode("unsigned")) comparator_49 (
    .a(C3), .b(register_21_q), .eq(comparator_49_eq));  // open: gt, lt
  Comparator #(.width(4), .mode("unsigned")) comparator_50 (
    .a(D3), .b(register_22_q), .eq(comparator_50_eq));  // open: gt, lt
  Comparator #(.width(4), .mode("unsigned")) comparator_51 (
    .a(E3), .b(register_23_q), .eq(comparator_51_eq));  // open: gt, lt
  Comparator #(.width(4), .mode("unsigned")) comparator_52 (
    .a(F3), .b(register_24_q), .eq(comparator_52_eq));  // open: gt, lt
  Comparator #(.width(4), .mode("unsigned")) comparator_53 (
    .a(G3), .b(register_25_q), .eq(comparator_53_eq));  // open: gt, lt
  Comparator #(.width(4), .mode("unsigned")) comparator_54 (
    .a(H3), .b(register_26_q), .eq(comparator_54_eq));  // open: gt, lt
  Comparator #(.width(4), .mode("unsigned")) comparator_55 (
    .a(I3), .b(register_27_q), .eq(comparator_55_eq));  // open: gt, lt
  and and_31 (\列3相等 , comparator_47_eq, comparator_48_eq, comparator_49_eq, comparator_50_eq, comparator_51_eq, comparator_52_eq, comparator_53_eq, comparator_54_eq, comparator_55_eq);
  Comparator #(.width(7), .mode("unsigned")) comparator_56 (
    .a(\计数 ), .b(7'b0000011), .eq(comparator_56_eq));  // open: gt, lt
  and and_32 (and_32_out, comparator_56_eq, \使能 );
  Comparator #(.width(7), .mode("unsigned")) comparator_57 (
    .a(\计数 ), .b(7'b0001100), .eq(comparator_57_eq));  // open: gt, lt
  and and_33 (and_33_out, comparator_57_eq, \使能 );
  Comparator #(.width(7), .mode("unsigned")) comparator_58 (
    .a(\计数 ), .b(7'b0010101), .eq(comparator_58_eq));  // open: gt, lt
  and and_34 (and_34_out, comparator_58_eq, \使能 );
  Comparator #(.width(7), .mode("unsigned")) comparator_59 (
    .a(\计数 ), .b(7'b0011110), .eq(comparator_59_eq));  // open: gt, lt
  and and_35 (and_35_out, comparator_59_eq, \使能 );
  Comparator #(.width(7), .mode("unsigned")) comparator_60 (
    .a(\计数 ), .b(7'b0100111), .eq(comparator_60_eq));  // open: gt, lt
  and and_36 (and_36_out, comparator_60_eq, \使能 );
  Comparator #(.width(7), .mode("unsigned")) comparator_61 (
    .a(\计数 ), .b(7'b0110000), .eq(comparator_61_eq));  // open: gt, lt
  and and_37 (and_37_out, comparator_61_eq, \使能 );
  Comparator #(.width(7), .mode("unsigned")) comparator_62 (
    .a(\计数 ), .b(7'b0111001), .eq(comparator_62_eq));  // open: gt, lt
  and and_38 (and_38_out, comparator_62_eq, \使能 );
  Comparator #(.width(7), .mode("unsigned")) comparator_63 (
    .a(\计数 ), .b(7'b1000010), .eq(comparator_63_eq));  // open: gt, lt
  and and_39 (and_39_out, comparator_63_eq, \使能 );
  Comparator #(.width(7), .mode("unsigned")) comparator_64 (
    .a(\计数 ), .b(7'b1001011), .eq(comparator_64_eq));  // open: gt, lt
  and and_40 (and_40_out, comparator_64_eq, \使能 );
  Register #(.width(4), .trigger("falling"), .Select("low")) register_28 (
    .D(\数据 ), .en(and_32_out), .Q(register_28_q), .clk(CLK), .clr(RST));
  Register #(.width(4), .trigger("falling"), .Select("low")) register_29 (
    .D(\数据 ), .en(and_33_out), .Q(register_29_q), .clk(CLK), .clr(RST));
  Register #(.width(4), .trigger("falling"), .Select("low")) register_30 (
    .D(\数据 ), .en(and_34_out), .Q(register_30_q), .clk(CLK), .clr(RST));
  Register #(.width(4), .trigger("falling"), .Select("low")) register_31 (
    .D(\数据 ), .en(and_35_out), .Q(register_31_q), .clk(CLK), .clr(RST));
  Register #(.width(4), .trigger("falling"), .Select("low")) register_32 (
    .D(\数据 ), .en(and_36_out), .Q(register_32_q), .clk(CLK), .clr(RST));
  Register #(.width(4), .trigger("falling"), .Select("low")) register_33 (
    .D(\数据 ), .en(and_37_out), .Q(register_33_q), .clk(CLK), .clr(RST));
  Register #(.width(4), .trigger("falling"), .Select("low")) register_34 (
    .D(\数据 ), .en(and_38_out), .Q(register_34_q), .clk(CLK), .clr(RST));
  Register #(.width(4), .trigger("falling"), .Select("low")) register_35 (
    .D(\数据 ), .en(and_39_out), .Q(register_35_q), .clk(CLK), .clr(RST));
  Register #(.width(4), .trigger("falling"), .Select("low")) register_36 (
    .D(\数据 ), .en(and_40_out), .Q(register_36_q), .clk(CLK), .clr(RST));
  Comparator #(.width(4), .mode("unsigned")) comparator_65 (
    .a(A4), .b(register_28_q), .eq(comparator_65_eq));  // open: gt, lt
  Comparator #(.width(4), .mode("unsigned")) comparator_66 (
    .a(B4), .b(register_29_q), .eq(comparator_66_eq));  // open: gt, lt
  Comparator #(.width(4), .mode("unsigned")) comparator_67 (
    .a(C4), .b(register_30_q), .eq(comparator_67_eq));  // open: gt, lt
  Comparator #(.width(4), .mode("unsigned")) comparator_68 (
    .a(D4), .b(register_31_q), .eq(comparator_68_eq));  // open: gt, lt
  Comparator #(.width(4), .mode("unsigned")) comparator_69 (
    .a(E4), .b(register_32_q), .eq(comparator_69_eq));  // open: gt, lt
  Comparator #(.width(4), .mode("unsigned")) comparator_70 (
    .a(F4), .b(register_33_q), .eq(comparator_70_eq));  // open: gt, lt
  Comparator #(.width(4), .mode("unsigned")) comparator_71 (
    .a(G4), .b(register_34_q), .eq(comparator_71_eq));  // open: gt, lt
  Comparator #(.width(4), .mode("unsigned")) comparator_72 (
    .a(H4), .b(register_35_q), .eq(comparator_72_eq));  // open: gt, lt
  Comparator #(.width(4), .mode("unsigned")) comparator_73 (
    .a(I4), .b(register_36_q), .eq(comparator_73_eq));  // open: gt, lt
  and and_41 (\列4相等 , comparator_65_eq, comparator_66_eq, comparator_67_eq, comparator_68_eq, comparator_69_eq, comparator_70_eq, comparator_71_eq, comparator_72_eq, comparator_73_eq);
  Comparator #(.width(7), .mode("unsigned")) comparator_74 (
    .a(\计数 ), .b(7'b0000100), .eq(comparator_74_eq));  // open: gt, lt
  and and_42 (and_42_out, comparator_74_eq, \使能 );
  Comparator #(.width(7), .mode("unsigned")) comparator_75 (
    .a(\计数 ), .b(7'b0001101), .eq(comparator_75_eq));  // open: gt, lt
  and and_43 (and_43_out, comparator_75_eq, \使能 );
  Comparator #(.width(7), .mode("unsigned")) comparator_76 (
    .a(\计数 ), .b(7'b0010110), .eq(comparator_76_eq));  // open: gt, lt
  and and_44 (and_44_out, comparator_76_eq, \使能 );
  Comparator #(.width(7), .mode("unsigned")) comparator_77 (
    .a(\计数 ), .b(7'b0011111), .eq(comparator_77_eq));  // open: gt, lt
  and and_45 (and_45_out, comparator_77_eq, \使能 );
  Comparator #(.width(7), .mode("unsigned")) comparator_78 (
    .a(\计数 ), .b(7'b0101000), .eq(comparator_78_eq));  // open: gt, lt
  and and_46 (and_46_out, comparator_78_eq, \使能 );
  Comparator #(.width(7), .mode("unsigned")) comparator_79 (
    .a(\计数 ), .b(7'b0110001), .eq(comparator_79_eq));  // open: gt, lt
  and and_47 (and_47_out, comparator_79_eq, \使能 );
  Comparator #(.width(7), .mode("unsigned")) comparator_80 (
    .a(\计数 ), .b(7'b0111010), .eq(comparator_80_eq));  // open: gt, lt
  and and_48 (and_48_out, comparator_80_eq, \使能 );
  Comparator #(.width(7), .mode("unsigned")) comparator_81 (
    .a(\计数 ), .b(7'b1000011), .eq(comparator_81_eq));  // open: gt, lt
  and and_49 (and_49_out, comparator_81_eq, \使能 );
  Comparator #(.width(7), .mode("unsigned")) comparator_82 (
    .a(\计数 ), .b(7'b1001100), .eq(comparator_82_eq));  // open: gt, lt
  and and_50 (and_50_out, comparator_82_eq, \使能 );
  Register #(.width(4), .trigger("falling"), .Select("low")) register_37 (
    .D(\数据 ), .en(and_42_out), .Q(register_37_q), .clk(CLK), .clr(RST));
  Register #(.width(4), .trigger("falling"), .Select("low")) register_38 (
    .D(\数据 ), .en(and_43_out), .Q(register_38_q), .clk(CLK), .clr(RST));
  Register #(.width(4), .trigger("falling"), .Select("low")) register_39 (
    .D(\数据 ), .en(and_44_out), .Q(register_39_q), .clk(CLK), .clr(RST));
  Register #(.width(4), .trigger("falling"), .Select("low")) register_40 (
    .D(\数据 ), .en(and_45_out), .Q(register_40_q), .clk(CLK), .clr(RST));
  Register #(.width(4), .trigger("falling"), .Select("low")) register_41 (
    .D(\数据 ), .en(and_46_out), .Q(register_41_q), .clk(CLK), .clr(RST));
  Register #(.width(4), .trigger("falling"), .Select("low")) register_42 (
    .D(\数据 ), .en(and_47_out), .Q(register_42_q), .clk(CLK), .clr(RST));
  Register #(.width(4), .trigger("falling"), .Select("low")) register_43 (
    .D(\数据 ), .en(and_48_out), .Q(register_43_q), .clk(CLK), .clr(RST));
  Register #(.width(4), .trigger("falling"), .Select("low")) register_44 (
    .D(\数据 ), .en(and_49_out), .Q(register_44_q), .clk(CLK), .clr(RST));
  Register #(.width(4), .trigger("falling"), .Select("low")) register_45 (
    .D(\数据 ), .en(and_50_out), .Q(register_45_q), .clk(CLK), .clr(RST));
  Comparator #(.width(4), .mode("unsigned")) comparator_83 (
    .a(A5), .b(register_37_q), .eq(comparator_83_eq));  // open: gt, lt
  Comparator #(.width(4), .mode("unsigned")) comparator_84 (
    .a(B5), .b(register_38_q), .eq(comparator_84_eq));  // open: gt, lt
  Comparator #(.width(4), .mode("unsigned")) comparator_85 (
    .a(C5), .b(register_39_q), .eq(comparator_85_eq));  // open: gt, lt
  Comparator #(.width(4), .mode("unsigned")) comparator_86 (
    .a(D5), .b(register_40_q), .eq(comparator_86_eq));  // open: gt, lt
  Comparator #(.width(4), .mode("unsigned")) comparator_87 (
    .a(E5), .b(register_41_q), .eq(comparator_87_eq));  // open: gt, lt
  Comparator #(.width(4), .mode("unsigned")) comparator_88 (
    .a(F5), .b(register_42_q), .eq(comparator_88_eq));  // open: gt, lt
  Comparator #(.width(4), .mode("unsigned")) comparator_89 (
    .a(G5), .b(register_43_q), .eq(comparator_89_eq));  // open: gt, lt
  Comparator #(.width(4), .mode("unsigned")) comparator_90 (
    .a(H5), .b(register_44_q), .eq(comparator_90_eq));  // open: gt, lt
  Comparator #(.width(4), .mode("unsigned")) comparator_91 (
    .a(I5), .b(register_45_q), .eq(comparator_91_eq));  // open: gt, lt
  and and_51 (\列5相等 , comparator_83_eq, comparator_84_eq, comparator_85_eq, comparator_86_eq, comparator_87_eq, comparator_88_eq, comparator_89_eq, comparator_90_eq, comparator_91_eq);
  Comparator #(.width(7), .mode("unsigned")) comparator_92 (
    .a(\计数 ), .b(7'b0000101), .eq(comparator_92_eq));  // open: gt, lt
  and and_52 (and_52_out, comparator_92_eq, \使能 );
  Comparator #(.width(7), .mode("unsigned")) comparator_93 (
    .a(\计数 ), .b(7'b0001110), .eq(comparator_93_eq));  // open: gt, lt
  and and_53 (and_53_out, comparator_93_eq, \使能 );
  Comparator #(.width(7), .mode("unsigned")) comparator_94 (
    .a(\计数 ), .b(7'b0010111), .eq(comparator_94_eq));  // open: gt, lt
  and and_54 (and_54_out, comparator_94_eq, \使能 );
  Comparator #(.width(7), .mode("unsigned")) comparator_95 (
    .a(\计数 ), .b(7'b0100000), .eq(comparator_95_eq));  // open: gt, lt
  and and_55 (and_55_out, comparator_95_eq, \使能 );
  Comparator #(.width(7), .mode("unsigned")) comparator_96 (
    .a(\计数 ), .b(7'b0101001), .eq(comparator_96_eq));  // open: gt, lt
  and and_56 (and_56_out, comparator_96_eq, \使能 );
  Comparator #(.width(7), .mode("unsigned")) comparator_97 (
    .a(\计数 ), .b(7'b0110010), .eq(comparator_97_eq));  // open: gt, lt
  and and_57 (and_57_out, comparator_97_eq, \使能 );
  Comparator #(.width(7), .mode("unsigned")) comparator_98 (
    .a(\计数 ), .b(7'b0111011), .eq(comparator_98_eq));  // open: gt, lt
  and and_58 (and_58_out, comparator_98_eq, \使能 );
  Comparator #(.width(7), .mode("unsigned")) comparator_99 (
    .a(\计数 ), .b(7'b1000100), .eq(comparator_99_eq));  // open: gt, lt
  and and_59 (and_59_out, comparator_99_eq, \使能 );
  Comparator #(.width(7), .mode("unsigned")) comparator_100 (
    .a(\计数 ), .b(7'b1001101), .eq(comparator_100_eq));  // open: gt, lt
  and and_60 (and_60_out, comparator_100_eq, \使能 );
  Register #(.width(4), .trigger("falling"), .Select("low")) register_46 (
    .D(\数据 ), .en(and_52_out), .Q(register_46_q), .clk(CLK), .clr(RST));
  Register #(.width(4), .trigger("falling"), .Select("low")) register_47 (
    .D(\数据 ), .en(and_53_out), .Q(register_47_q), .clk(CLK), .clr(RST));
  Register #(.width(4), .trigger("falling"), .Select("low")) register_48 (
    .D(\数据 ), .en(and_54_out), .Q(register_48_q), .clk(CLK), .clr(RST));
  Register #(.width(4), .trigger("falling"), .Select("low")) register_49 (
    .D(\数据 ), .en(and_55_out), .Q(register_49_q), .clk(CLK), .clr(RST));
  Register #(.width(4), .trigger("falling"), .Select("low")) register_50 (
    .D(\数据 ), .en(and_56_out), .Q(register_50_q), .clk(CLK), .clr(RST));
  Register #(.width(4), .trigger("falling"), .Select("low")) register_51 (
    .D(\数据 ), .en(and_57_out), .Q(register_51_q), .clk(CLK), .clr(RST));
  Register #(.width(4), .trigger("falling"), .Select("low")) register_52 (
    .D(\数据 ), .en(and_58_out), .Q(register_52_q), .clk(CLK), .clr(RST));
  Register #(.width(4), .trigger("falling"), .Select("low")) register_53 (
    .D(\数据 ), .en(and_59_out), .Q(register_53_q), .clk(CLK), .clr(RST));
  Register #(.width(4), .trigger("falling"), .Select("low")) register_54 (
    .D(\数据 ), .en(and_60_out), .Q(register_54_q), .clk(CLK), .clr(RST));
  Comparator #(.width(4), .mode("unsigned")) comparator_101 (
    .a(A6), .b(register_46_q), .eq(comparator_101_eq));  // open: gt, lt
  Comparator #(.width(4), .mode("unsigned")) comparator_102 (
    .a(B6), .b(register_47_q), .eq(comparator_102_eq));  // open: gt, lt
  Comparator #(.width(4), .mode("unsigned")) comparator_103 (
    .a(C6), .b(register_48_q), .eq(comparator_103_eq));  // open: gt, lt
  Comparator #(.width(4), .mode("unsigned")) comparator_104 (
    .a(D6), .b(register_49_q), .eq(comparator_104_eq));  // open: gt, lt
  Comparator #(.width(4), .mode("unsigned")) comparator_105 (
    .a(E6), .b(register_50_q), .eq(comparator_105_eq));  // open: gt, lt
  Comparator #(.width(4), .mode("unsigned")) comparator_106 (
    .a(F6), .b(register_51_q), .eq(comparator_106_eq));  // open: gt, lt
  Comparator #(.width(4), .mode("unsigned")) comparator_107 (
    .a(G6), .b(register_52_q), .eq(comparator_107_eq));  // open: gt, lt
  Comparator #(.width(4), .mode("unsigned")) comparator_108 (
    .a(H6), .b(register_53_q), .eq(comparator_108_eq));  // open: gt, lt
  Comparator #(.width(4), .mode("unsigned")) comparator_109 (
    .a(I6), .b(register_54_q), .eq(comparator_109_eq));  // open: gt, lt
  and and_61 (\列6相等 , comparator_101_eq, comparator_102_eq, comparator_103_eq, comparator_104_eq, comparator_105_eq, comparator_106_eq, comparator_107_eq, comparator_108_eq, comparator_109_eq);
  Comparator #(.width(7), .mode("unsigned")) comparator_110 (
    .a(\计数 ), .b(7'b0000110), .eq(comparator_110_eq));  // open: gt, lt
  Comparator #(.width(7), .mode("unsigned")) comparator_111 (
    .a(\计数 ), .b(7'b0001111), .eq(comparator_111_eq));  // open: gt, lt
  Comparator #(.width(7), .mode("unsigned")) comparator_112 (
    .a(\计数 ), .b(7'b0011000), .eq(comparator_112_eq));  // open: gt, lt
  Comparator #(.width(7), .mode("unsigned")) comparator_113 (
    .a(\计数 ), .b(7'b0100001), .eq(comparator_113_eq));  // open: gt, lt
  Comparator #(.width(7), .mode("unsigned")) comparator_114 (
    .a(\计数 ), .b(7'b0101010), .eq(comparator_114_eq));  // open: gt, lt
  Comparator #(.width(7), .mode("unsigned")) comparator_115 (
    .a(\计数 ), .b(7'b0110011), .eq(comparator_115_eq));  // open: gt, lt
  Comparator #(.width(7), .mode("unsigned")) comparator_116 (
    .a(\计数 ), .b(7'b0111100), .eq(comparator_116_eq));  // open: gt, lt
  Comparator #(.width(7), .mode("unsigned")) comparator_117 (
    .a(\计数 ), .b(7'b1000101), .eq(comparator_117_eq));  // open: gt, lt
  Comparator #(.width(7), .mode("unsigned")) comparator_118 (
    .a(\计数 ), .b(7'b1001110), .eq(comparator_118_eq));  // open: gt, lt
  and and_62 (and_62_out, comparator_110_eq, \使能 );
  and and_63 (and_63_out, comparator_111_eq, \使能 );
  and and_64 (and_64_out, comparator_112_eq, \使能 );
  and and_65 (and_65_out, comparator_113_eq, \使能 );
  and and_66 (and_66_out, comparator_114_eq, \使能 );
  and and_67 (and_67_out, comparator_115_eq, \使能 );
  and and_68 (and_68_out, comparator_116_eq, \使能 );
  and and_69 (and_69_out, comparator_117_eq, \使能 );
  and and_70 (and_70_out, comparator_118_eq, \使能 );
  Register #(.width(4), .trigger("falling"), .Select("low")) register_55 (
    .D(\数据 ), .en(and_62_out), .Q(register_55_q), .clk(CLK), .clr(RST));
  Register #(.width(4), .trigger("falling"), .Select("low")) register_56 (
    .D(\数据 ), .en(and_63_out), .Q(register_56_q), .clk(CLK), .clr(RST));
  Register #(.width(4), .trigger("falling"), .Select("low")) register_57 (
    .D(\数据 ), .en(and_64_out), .Q(register_57_q), .clk(CLK), .clr(RST));
  Register #(.width(4), .trigger("falling"), .Select("low")) register_58 (
    .D(\数据 ), .en(and_65_out), .Q(register_58_q), .clk(CLK), .clr(RST));
  Register #(.width(4), .trigger("falling"), .Select("low")) register_59 (
    .D(\数据 ), .en(and_66_out), .Q(register_59_q), .clk(CLK), .clr(RST));
  Register #(.width(4), .trigger("falling"), .Select("low")) register_60 (
    .D(\数据 ), .en(and_67_out), .Q(register_60_q), .clk(CLK), .clr(RST));
  Register #(.width(4), .trigger("falling"), .Select("low")) register_61 (
    .D(\数据 ), .en(and_68_out), .Q(register_61_q), .clk(CLK), .clr(RST));
  Register #(.width(4), .trigger("falling"), .Select("low")) register_62 (
    .D(\数据 ), .en(and_69_out), .Q(register_62_q), .clk(CLK), .clr(RST));
  Register #(.width(4), .trigger("falling"), .Select("low")) register_63 (
    .D(\数据 ), .en(and_70_out), .Q(register_63_q), .clk(CLK), .clr(RST));
  Comparator #(.width(4), .mode("unsigned")) comparator_119 (
    .a(A7), .b(register_55_q), .eq(comparator_119_eq));  // open: gt, lt
  Comparator #(.width(4), .mode("unsigned")) comparator_120 (
    .a(B7), .b(register_56_q), .eq(comparator_120_eq));  // open: gt, lt
  Comparator #(.width(4), .mode("unsigned")) comparator_121 (
    .a(C7), .b(register_57_q), .eq(comparator_121_eq));  // open: gt, lt
  Comparator #(.width(4), .mode("unsigned")) comparator_122 (
    .a(D7), .b(register_58_q), .eq(comparator_122_eq));  // open: gt, lt
  Comparator #(.width(4), .mode("unsigned")) comparator_123 (
    .a(E7), .b(register_59_q), .eq(comparator_123_eq));  // open: gt, lt
  Comparator #(.width(4), .mode("unsigned")) comparator_124 (
    .a(F7), .b(register_60_q), .eq(comparator_124_eq));  // open: gt, lt
  Comparator #(.width(4), .mode("unsigned")) comparator_125 (
    .a(G7), .b(register_61_q), .eq(comparator_125_eq));  // open: gt, lt
  Comparator #(.width(4), .mode("unsigned")) comparator_126 (
    .a(H7), .b(register_62_q), .eq(comparator_126_eq));  // open: gt, lt
  Comparator #(.width(4), .mode("unsigned")) comparator_127 (
    .a(I7), .b(register_63_q), .eq(comparator_127_eq));  // open: gt, lt
  and and_71 (\列7相等 , comparator_119_eq, comparator_120_eq, comparator_121_eq, comparator_122_eq, comparator_123_eq, comparator_124_eq, comparator_125_eq, comparator_126_eq, comparator_127_eq);
  Comparator #(.width(7), .mode("unsigned")) comparator_128 (
    .a(\计数 ), .b(7'b0000111), .eq(comparator_128_eq));  // open: gt, lt
  Comparator #(.width(7), .mode("unsigned")) comparator_129 (
    .a(\计数 ), .b(7'b0010000), .eq(comparator_129_eq));  // open: gt, lt
  Comparator #(.width(7), .mode("unsigned")) comparator_130 (
    .a(\计数 ), .b(7'b0011001), .eq(comparator_130_eq));  // open: gt, lt
  Comparator #(.width(7), .mode("unsigned")) comparator_131 (
    .a(\计数 ), .b(7'b0100010), .eq(comparator_131_eq));  // open: gt, lt
  Comparator #(.width(7), .mode("unsigned")) comparator_132 (
    .a(\计数 ), .b(7'b0101011), .eq(comparator_132_eq));  // open: gt, lt
  Comparator #(.width(7), .mode("unsigned")) comparator_133 (
    .a(\计数 ), .b(7'b0110100), .eq(comparator_133_eq));  // open: gt, lt
  Comparator #(.width(7), .mode("unsigned")) comparator_134 (
    .a(\计数 ), .b(7'b0111101), .eq(comparator_134_eq));  // open: gt, lt
  Comparator #(.width(7), .mode("unsigned")) comparator_135 (
    .a(\计数 ), .b(7'b1000110), .eq(comparator_135_eq));  // open: gt, lt
  Comparator #(.width(7), .mode("unsigned")) comparator_136 (
    .a(\计数 ), .b(7'b1001111), .eq(comparator_136_eq));  // open: gt, lt
  and and_72 (and_72_out, comparator_128_eq, \使能 );
  and and_73 (and_73_out, comparator_129_eq, \使能 );
  and and_74 (and_74_out, comparator_130_eq, \使能 );
  and and_75 (and_75_out, comparator_131_eq, \使能 );
  and and_76 (and_76_out, comparator_132_eq, \使能 );
  and and_77 (and_77_out, comparator_133_eq, \使能 );
  and and_78 (and_78_out, comparator_134_eq, \使能 );
  and and_79 (and_79_out, comparator_135_eq, \使能 );
  and and_80 (and_80_out, comparator_136_eq, \使能 );
  Register #(.width(4), .trigger("falling"), .Select("low")) register_64 (
    .D(\数据 ), .en(and_72_out), .Q(register_64_q), .clk(CLK), .clr(RST));
  Register #(.width(4), .trigger("falling"), .Select("low")) register_65 (
    .D(\数据 ), .en(and_73_out), .Q(register_65_q), .clk(CLK), .clr(RST));
  Register #(.width(4), .trigger("falling"), .Select("low")) register_66 (
    .D(\数据 ), .en(and_74_out), .Q(register_66_q), .clk(CLK), .clr(RST));
  Register #(.width(4), .trigger("falling"), .Select("low")) register_67 (
    .D(\数据 ), .en(and_75_out), .Q(register_67_q), .clk(CLK), .clr(RST));
  Register #(.width(4), .trigger("falling"), .Select("low")) register_68 (
    .D(\数据 ), .en(and_76_out), .Q(register_68_q), .clk(CLK), .clr(RST));
  Register #(.width(4), .trigger("falling"), .Select("low")) register_69 (
    .D(\数据 ), .en(and_77_out), .Q(register_69_q), .clk(CLK), .clr(RST));
  Register #(.width(4), .trigger("falling"), .Select("low")) register_70 (
    .D(\数据 ), .en(and_78_out), .Q(register_70_q), .clk(CLK), .clr(RST));
  Register #(.width(4), .trigger("falling"), .Select("low")) register_71 (
    .D(\数据 ), .en(and_79_out), .Q(register_71_q), .clk(CLK), .clr(RST));
  Register #(.width(4), .trigger("falling"), .Select("low")) register_72 (
    .D(\数据 ), .en(and_80_out), .Q(register_72_q), .clk(CLK), .clr(RST));
  Comparator #(.width(4), .mode("unsigned")) comparator_137 (
    .a(A8), .b(register_64_q), .eq(comparator_137_eq));  // open: gt, lt
  Comparator #(.width(4), .mode("unsigned")) comparator_138 (
    .a(B8), .b(register_65_q), .eq(comparator_138_eq));  // open: gt, lt
  Comparator #(.width(4), .mode("unsigned")) comparator_139 (
    .a(C8), .b(register_66_q), .eq(comparator_139_eq));  // open: gt, lt
  Comparator #(.width(4), .mode("unsigned")) comparator_140 (
    .a(D8), .b(register_67_q), .eq(comparator_140_eq));  // open: gt, lt
  Comparator #(.width(4), .mode("unsigned")) comparator_141 (
    .a(E8), .b(register_68_q), .eq(comparator_141_eq));  // open: gt, lt
  Comparator #(.width(4), .mode("unsigned")) comparator_142 (
    .a(F8), .b(register_69_q), .eq(comparator_142_eq));  // open: gt, lt
  Comparator #(.width(4), .mode("unsigned")) comparator_143 (
    .a(G8), .b(register_70_q), .eq(comparator_143_eq));  // open: gt, lt
  Comparator #(.width(4), .mode("unsigned")) comparator_144 (
    .a(H8), .b(register_71_q), .eq(comparator_144_eq));  // open: gt, lt
  Comparator #(.width(4), .mode("unsigned")) comparator_145 (
    .a(I8), .b(register_72_q), .eq(comparator_145_eq));  // open: gt, lt
  and and_81 (\列8相等 , comparator_137_eq, comparator_138_eq, comparator_139_eq, comparator_140_eq, comparator_141_eq, comparator_142_eq, comparator_143_eq, comparator_144_eq, comparator_145_eq);
  Comparator #(.width(7), .mode("unsigned")) comparator_146 (
    .a(\计数 ), .b(7'b0001000), .eq(comparator_146_eq));  // open: gt, lt
  and and_82 (and_82_out, comparator_146_eq, \使能 );
  Comparator #(.width(7), .mode("unsigned")) comparator_147 (
    .a(\计数 ), .b(7'b0010001), .eq(comparator_147_eq));  // open: gt, lt
  and and_83 (and_83_out, comparator_147_eq, \使能 );
  Comparator #(.width(7), .mode("unsigned")) comparator_148 (
    .a(\计数 ), .b(7'b0011010), .eq(comparator_148_eq));  // open: gt, lt
  and and_84 (and_84_out, comparator_148_eq, \使能 );
  Comparator #(.width(7), .mode("unsigned")) comparator_149 (
    .a(\计数 ), .b(7'b0100011), .eq(comparator_149_eq));  // open: gt, lt
  and and_85 (and_85_out, comparator_149_eq, \使能 );
  Comparator #(.width(7), .mode("unsigned")) comparator_150 (
    .a(\计数 ), .b(7'b0101100), .eq(comparator_150_eq));  // open: gt, lt
  and and_86 (and_86_out, comparator_150_eq, \使能 );
  Comparator #(.width(7), .mode("unsigned")) comparator_151 (
    .a(\计数 ), .b(7'b0110101), .eq(comparator_151_eq));  // open: gt, lt
  and and_87 (and_87_out, comparator_151_eq, \使能 );
  Comparator #(.width(7), .mode("unsigned")) comparator_152 (
    .a(\计数 ), .b(7'b0111110), .eq(comparator_152_eq));  // open: gt, lt
  and and_88 (and_88_out, comparator_152_eq, \使能 );
  Comparator #(.width(7), .mode("unsigned")) comparator_153 (
    .a(\计数 ), .b(7'b1000111), .eq(comparator_153_eq));  // open: gt, lt
  and and_89 (and_89_out, comparator_153_eq, \使能 );
  Comparator #(.width(7), .mode("unsigned")) comparator_154 (
    .a(\计数 ), .b(7'b1010000), .eq(comparator_154_eq));  // open: gt, lt
  and and_90 (and_90_out, comparator_154_eq, \使能 );
  Register #(.width(4), .trigger("falling"), .Select("low")) register_73 (
    .D(\数据 ), .en(and_82_out), .Q(register_73_q), .clk(CLK), .clr(RST));
  Register #(.width(4), .trigger("falling"), .Select("low")) register_74 (
    .D(\数据 ), .en(and_83_out), .Q(register_74_q), .clk(CLK), .clr(RST));
  Register #(.width(4), .trigger("falling"), .Select("low")) register_75 (
    .D(\数据 ), .en(and_84_out), .Q(register_75_q), .clk(CLK), .clr(RST));
  Register #(.width(4), .trigger("falling"), .Select("low")) register_76 (
    .D(\数据 ), .en(and_85_out), .Q(register_76_q), .clk(CLK), .clr(RST));
  Register #(.width(4), .trigger("falling"), .Select("low")) register_77 (
    .D(\数据 ), .en(and_86_out), .Q(register_77_q), .clk(CLK), .clr(RST));
  Register #(.width(4), .trigger("falling"), .Select("low")) register_78 (
    .D(\数据 ), .en(and_87_out), .Q(register_78_q), .clk(CLK), .clr(RST));
  Register #(.width(4), .trigger("falling"), .Select("low")) register_79 (
    .D(\数据 ), .en(and_88_out), .Q(register_79_q), .clk(CLK), .clr(RST));
  Register #(.width(4), .trigger("falling"), .Select("low")) register_80 (
    .D(\数据 ), .en(and_89_out), .Q(register_80_q), .clk(CLK), .clr(RST));
  Register #(.width(4), .trigger("falling"), .Select("low")) register_81 (
    .D(\数据 ), .en(and_90_out), .Q(register_81_q), .clk(CLK), .clr(RST));
  Comparator #(.width(4), .mode("unsigned")) comparator_155 (
    .a(A9), .b(register_73_q), .eq(comparator_155_eq));  // open: gt, lt
  Comparator #(.width(4), .mode("unsigned")) comparator_156 (
    .a(B9), .b(register_74_q), .eq(comparator_156_eq));  // open: gt, lt
  Comparator #(.width(4), .mode("unsigned")) comparator_157 (
    .a(C9), .b(register_75_q), .eq(comparator_157_eq));  // open: gt, lt
  Comparator #(.width(4), .mode("unsigned")) comparator_158 (
    .a(D9), .b(register_76_q), .eq(comparator_158_eq));  // open: gt, lt
  Comparator #(.width(4), .mode("unsigned")) comparator_159 (
    .a(E9), .b(register_77_q), .eq(comparator_159_eq));  // open: gt, lt
  Comparator #(.width(4), .mode("unsigned")) comparator_160 (
    .a(F9), .b(register_78_q), .eq(comparator_160_eq));  // open: gt, lt
  Comparator #(.width(4), .mode("unsigned")) comparator_161 (
    .a(G9), .b(register_79_q), .eq(comparator_161_eq));  // open: gt, lt
  Comparator #(.width(4), .mode("unsigned")) comparator_162 (
    .a(H9), .b(register_80_q), .eq(comparator_162_eq));  // open: gt, lt
  Comparator #(.width(4), .mode("unsigned")) comparator_163 (
    .a(I9), .b(register_81_q), .eq(comparator_163_eq));  // open: gt, lt
  and and_91 (\列9相等 , comparator_155_eq, comparator_156_eq, comparator_157_eq, comparator_158_eq, comparator_159_eq, comparator_160_eq, comparator_161_eq, comparator_162_eq, comparator_163_eq);
endmodule

// 宫格判断
module \判断坐标宫格  (
  input  [3:0] \X坐标 ,
  input  [3:0] \Y坐标 ,
  output \未选中宫格 ,
  output [3:0] \所属宫格位置_从左至右_从上至下_依次为0_8 ,
  output [3:0] \宫格内位置 
);

  wire and_7_out, and_8_out, and_9_out, and_10_out, and_11_out, and_12_out, and_13_out, and_14_out,
       and_15_out, comparator_1_lt, comparator_2_gt, comparator_3_lt, comparator_4_gt, comparator_5_lt,
       comparator_6_gt, comparator_7_lt, comparator_8_gt, comparator_9_lt, comparator_10_gt,
       comparator_11_lt, comparator_12_gt, \第一列 , \第一行 , \第三列 , \第三行 , \第二列 , \第二行 ;
  wire [3:0] adder_1_out, divider_1_rem, divider_2_rem, multiplier_1_out, priority_encoder_1_out,
       subtractor_1_out, subtractor_2_out;

  Comparator #(.width(4), .mode("unsigned")) comparator_1 (
    .a(4'b0000), .b(\X坐标 ), .lt(comparator_1_lt));  // open: gt, eq
  and and_1 (\第一列 , comparator_1_lt, comparator_2_gt);
  Comparator #(.width(4), .mode("unsigned")) comparator_2 (
    .a(4'b0100), .b(\X坐标 ), .gt(comparator_2_gt));  // open: eq, lt
  Comparator #(.width(4), .mode("unsigned")) comparator_3 (
    .a(4'b0011), .b(\X坐标 ), .lt(comparator_3_lt));  // open: gt, eq
  and and_2 (\第二列 , comparator_3_lt, comparator_4_gt);
  Comparator #(.width(4), .mode("unsigned")) comparator_4 (
    .a(4'b0111), .b(\X坐标 ), .gt(comparator_4_gt));  // open: eq, lt
  Comparator #(.width(4), .mode("unsigned")) comparator_5 (
    .a(4'b0110), .b(\X坐标 ), .lt(comparator_5_lt));  // open: gt, eq
  and and_3 (\第三列 , comparator_5_lt, comparator_6_gt);
  Comparator #(.width(4), .mode("unsigned")) comparator_6 (
    .a(4'b1010), .b(\X坐标 ), .gt(comparator_6_gt));  // open: eq, lt
  Comparator #(.width(4), .mode("unsigned")) comparator_7 (
    .a(4'b0000), .b(\Y坐标 ), .lt(comparator_7_lt));  // open: gt, eq
  and and_4 (\第一行 , comparator_7_lt, comparator_8_gt);
  Comparator #(.width(4), .mode("unsigned")) comparator_8 (
    .a(4'b0100), .b(\Y坐标 ), .gt(comparator_8_gt));  // open: eq, lt
  Comparator #(.width(4), .mode("unsigned")) comparator_9 (
    .a(4'b0011), .b(\Y坐标 ), .lt(comparator_9_lt));  // open: gt, eq
  and and_5 (\第二行 , comparator_9_lt, comparator_10_gt);
  Comparator #(.width(4), .mode("unsigned")) comparator_10 (
    .a(4'b0111), .b(\Y坐标 ), .gt(comparator_10_gt));  // open: eq, lt
  Comparator #(.width(4), .mode("unsigned")) comparator_11 (
    .a(4'b0110), .b(\Y坐标 ), .lt(comparator_11_lt));  // open: gt, eq
  and and_6 (\第三行 , comparator_11_lt, comparator_12_gt);
  Comparator #(.width(4), .mode("unsigned")) comparator_12 (
    .a(4'b1010), .b(\Y坐标 ), .gt(comparator_12_gt));  // open: eq, lt
  and and_7 (and_7_out, \第一列 , \第一行 );
  and and_8 (and_8_out, \第二列 , \第一行 );
  and and_9 (and_9_out, \第三列 , \第一行 );
  and and_10 (and_10_out, \第一列 , \第二行 );
  and and_11 (and_11_out, \第二列 , \第二行 );
  and and_12 (and_12_out, \第三列 , \第二行 );
  and and_13 (and_13_out, \第一列 , \第三行 );
  and and_14 (and_14_out, \第二列 , \第三行 );
  and and_15 (and_15_out, \第三列 , \第三行 );
  Subtractor #(.width(4)) subtractor_1 (.a(\X坐标 ), .b(4'b0001), .out(subtractor_1_out));  // open: bin, bout
  Divider #(.width(4)) divider_1 (.a(subtractor_1_out), .b(4'b0011), .rem(divider_1_rem));  // open: out, upper
  Adder #(.width(4)) adder_1 (.a(divider_1_rem), .b(4'b0001), .out(adder_1_out));  // open: cin, cout
  Priority_Encoder #(.select(4), .disabled("Z")) priority_encoder_1 (
    .in0(and_7_out), .in1(and_8_out), .in2(and_9_out), .in3(and_10_out), .in4(and_11_out), .in5(and_12_out),
    .in6(and_13_out), .in7(and_14_out), .in8(and_15_out), .out(priority_encoder_1_out), .en_out(\未选中宫格 ),
    .en_in(1'b1));  // open: in9, in10, in11, in12, in13, in14, in15, gs
  Subtractor #(.width(4)) subtractor_2 (.a(\Y坐标 ), .b(4'b0001), .out(subtractor_2_out));  // open: bin, bout
  Multiplexer #(.select(1), .width(4), .disabled("Z"), .enable("false")) multiplexer_1 (
    .in0(priority_encoder_1_out), .in1(4'b1010), .out(\所属宫格位置_从左至右_从上至下_依次为0_8 ), .sel(\未选中宫格 ));
  Divider #(.width(4)) divider_2 (.a(subtractor_2_out), .b(4'b0011), .rem(divider_2_rem));  // open: out, upper
  Multiplier #(.width(4)) multiplier_1 (.a(divider_2_rem), .b(4'b0011), .out(multiplier_1_out));  // open: cin, cout
  Adder #(.width(4)) adder_2 (.a(multiplier_1_out), .b(adder_1_out), .out(\宫格内位置 ));  // open: cin, cout
endmodule

// ALU
module ALU (
  input  [31:0] X,
  input  [31:0] Y,
  input  [3:0] AluOP,
  output out_4,
  output Equal,
  output out_6,
  output [31:0] Result,
  output [31:0] Result_2
);

  wire [0:0] comparator_1_lt, comparator_2_lt;
  wire [31:0] adder_1_out, AND_out, divider_1_out, divider_1_rem, multiplier_1_cout, multiplier_1_out,
       NOR_out, OR_out, shifter_1_out, shifter_2_out, shifter_3_out, subtractor_1_out, XOR_out;

  assign AND_out = X & Y;  // AND_Gate AND, 32 bits wide
  assign OR_out = X | Y;  // OR_Gate OR, 32 bits wide
  Shifter #(.width(32), .shift("ll")) shifter_1 (.in(X), .\dist (Y[4:0]), .out(shifter_1_out));
  Shifter #(.width(32), .shift("ar")) shifter_2 (.in(X), .\dist (Y[4:0]), .out(shifter_2_out));
  Shifter #(.width(32), .shift("lr")) shifter_3 (.in(X), .\dist (Y[4:0]), .out(shifter_3_out));
  Multiplier #(.width(32)) multiplier_1 (.a(X), .b(Y), .out(multiplier_1_out), .cout(multiplier_1_cout));  // open: cin
  Divider #(.width(32)) divider_1 (.a(X), .b(Y), .out(divider_1_out), .rem(divider_1_rem));  // open: upper
  Adder #(.width(32)) adder_1 (.a(X), .b(Y), .out(adder_1_out));  // open: cin, cout
  Subtractor #(.width(32)) subtractor_1 (.a(X), .b(Y), .out(subtractor_1_out));  // open: bin, bout
  assign XOR_out = X ^ Y;  // XOR_Gate XOR, 32 bits wide
  assign NOR_out = ~(X | Y);  // NOR_Gate NOR, 32 bits wide
  Comparator #(.width(32), .mode("twosComplement")) comparator_1 (
    .a(X), .b(Y), .eq(Equal), .lt(comparator_1_lt[0]));  // open: gt
  Comparator #(.width(32), .mode("unsigned")) comparator_2 (.a(X), .b(Y), .lt(comparator_2_lt[0]));  // open: gt, eq
  Multiplexer #(.select(4), .width(32), .disabled("Z"), .enable("false")) multiplexer_1 (
    .in0(shifter_1_out), .in1(shifter_2_out), .in2(shifter_3_out), .in3(multiplier_1_out),
    .in4(divider_1_out), .in5(adder_1_out), .in6(subtractor_1_out), .in7(AND_out), .in8(OR_out),
    .in9(XOR_out), .in10(NOR_out), .in11({{31{1'b0}}, comparator_1_lt[0]}),
    .in12({{31{1'b0}}, comparator_2_lt[0]}), .in13({32{1'b0}}), .in14({32{1'b0}}), .in15({32{1'b0}}),
    .out(Result), .sel(AluOP));
  Multiplexer #(.select(4), .width(32), .disabled("Z"), .enable("false")) multiplexer_2 (
    .in0({32{1'b0}}), .in1({32{1'b0}}), .in2({32{1'b0}}), .in3(multiplier_1_cout), .in4(divider_1_rem),
    .in5({32{1'b0}}), .in6({32{1'b0}}), .in7({32{1'b0}}), .in8({32{1'b0}}), .in9({32{1'b0}}),
    .in10({32{1'b0}}), .in11({32{1'b0}}), .in12({32{1'b0}}), .in13({32{1'b0}}), .in14({32{1'b0}}),
    .in15({32{1'b0}}), .out(Result_2), .sel(AluOP));
  Multiplexer #(.select(4), .width(1), .disabled("Z"), .enable("false")) multiplexer_3 (
    .in0(1'b0), .in1(1'b0), .in2(1'b0), .in3(1'b0), .in4(1'b0), .in5(1'b0), .in6(1'b0), .in7(1'b0),
    .in8(1'b0), .in9(1'b0), .in10(1'b0), .in11(comparator_1_lt[0]), .in12(comparator_2_lt[0]), .in13(1'b0),
    .in14(1'b0), .in15(1'b0), .out(out_6), .sel(AluOP));
  not not_1 (out_4, out_6);

  // Other names for the same wires on the sheet: Result2[31:0] = Result_2; S[3:0] = AluOP; tunnel = out_6;
  //   tunnel_t = out_4

  // Notes on the sheet:
  //   不要改变此引脚区域内容，也不要改变ALU封装形式
  //   输入引脚
  //   输出引脚
endmodule

module Regifile (
  input  [31:0] Din,
  input  Clk,
  input  WE,
  input  [4:0] R1_num,
  input  [4:0] W_num,
  input  [4:0] R2_num,
  output [31:0] R1,
  output [31:0] R2
);

  // RegisterFile registerfile_1: pin names not known; wires that end beside it: Din, Clk, WE, W_num, R1_num, R2_num, R1, R2
endmodule

// CPU
module \单周期CPU  (
  input  CLK,
  input  RST,
  input  \新游戏 ,
  output [31:0] LedData,
  output \数据产生 
);

  wire _0, _1, _2, _3, and_1_out, and_2_out, and_3_out, and_4_out, and_5_out, and_7_out, and_9_out,
       and_10_out, and_11_out, and_12_out, and_16_out, and_17_out, and_18_out, and_19_out, AUIPC, BEQ, BGE,
       BNE, ClearInt1, ClearInt2, ClearInt3, clock_1_out, comparator_1_eq, comparator_2_eq, comparator_2_lt,
       controlled_buffer_1_out, CSRRS, d_ff_2_q, d_ff_3_q, d_ff_4_q, d_ff_5_q, d_ff_6_q, decoder_1_out0,
       decoder_1_out1, decoder_1_out2, demultiplexer_1_out0, demultiplexer_1_out1, demultiplexer_1_out2,
       demultiplexer_1_out3, Go, halt, IE, INT, IR1, IR1_q, IR2, IR2_q, IR3, IR3_q, IRA, IRB, IRC, JAL, JALR,
       LBU, LUI, MemToReg, MemWrite, MUL, nand_1_out, not_1_out, not_2_out, not_3_out, or_9_out, or_10_out,
       or_11_out, RegWrite, REM, SW, tunnel, tunnel_t, undriven, undriven_2, URET, W1, W2, W3, \中断请求 ,
       \单周期硬布线控制器_1_alu_src , \无条件跳转 , \条件跳转 ;
  wire [1:0] priority_encoder_1_out, register_4_q, \中断号 ;
  wire [2:0] priority_encoder_2_out, select;
  wire [3:0] \单周期硬布线控制器_1_alu_op ;
  wire [4:0] multiplexer_7_out, multiplexer_8_out, multiplexer_9_out;
  wire [7:0] controlled_buffer_2_out, controlled_buffer_3_out, controlled_buffer_4_out,
       controlled_buffer_5_out, Din0, Din1, Din2, Din3, Dout0, Dout1, Dout2, Dout3;
  wire [11:0] multiplexer_10_out;
  wire [12:0] CNT_num;
  wire [31:0] alu_1_result, alu_1_result_2, Alu_Res, and_6_out, bit_extender_1_out, bit_extender_2_out,
       bit_extender_3_out, bit_extender_4_out, bit_extender_5_out, bit_extender_6_out, bit_extender_7_out,
       bit_extender_8_out, bit_extender_9_out, IR, MemData, mEPC, multiplexer_1_out, multiplexer_2_out,
       multiplexer_11_out, PC, PC_4, PC_INT, PC_JAL, PC_Next, PC_q, \PC_条件跳转 , R1, RDin, RDin_AUIPC,
       RDin_LUI, shifter_1_out, shifter_2_out, shifter_3_out, \总周期数 , \随机数 ;

  Button \u_继续运行  (.out(Go));
  // RiscV_Probe riscv_probe_1: pin names not known; wires that end beside it: IR
  and and_1 (and_1_out, \中断请求 , IE);
  Hex_Digit_Display hex_digit_display_1 (.value(LedData[31:28]));  // open: dp
  and and_2 (and_2_out, \中断请求 , IE);
  Register #(.width(32), .trigger("falling"), .Select("low")) register_1 (
    .D(PC_Next), .en(and_1_out), .Q(mEPC), .clk(CLK), .clr(RST));
  Multiplexer #(.select(1), .width(32), .disabled("Z"), .enable("false")) multiplexer_1 (
    .in0(Alu_Res), .in1(MemData), .out(multiplexer_1_out), .sel(MemToReg));
  and and_3 (and_3_out, BGE, tunnel_t);
  and and_4 (and_4_out, BEQ, tunnel);
  and and_5 (and_5_out, ~tunnel, BNE);  // AND_Gate
  Hex_Digit_Display hex_digit_display_2 (.value(LedData[27:24]));  // open: dp
  Hex_Digit_Display hex_digit_display_3 (.value(LedData[23:20]));  // open: dp
  Adder #(.width(32)) adder_1 (.a(PC), .b(32'h4), .out(PC_4));  // open: cin, cout
  Register #(.width(1), .trigger("rising"), .Select("low")) register_2 (
    .D(and_2_out), .Q(INT), .clk(CLK), .clr(RST));  // open: en
  Random #(.width(32), .seed(0), .trigger("rising")) random_1 (.clk(CLK), .next(1'b1), .out(\随机数 ));  // open: clr
  Comparator #(.width(32), .mode("unsigned")) comparator_1 (.a(R1), .b(32'h22), .eq(comparator_1_eq));  // open: gt, lt
  or or_1 (\条件跳转 , and_3_out, and_4_out, and_5_out);
  assign and_6_out = Alu_Res & 32'hfffffffe;  // AND_Gate and_6, 32 bits wide
  Hex_Digit_Display hex_digit_display_4 (.value(LedData[19:16]));  // open: dp
  Hex_Digit_Display hex_digit_display_5 (.value(LedData[15:12]));  // open: dp
  and and_7 (and_7_out, \数据产生 , comparator_1_eq);
  and and_8 (halt, \数据产生 , ~comparator_1_eq, ~Go);  // AND_Gate
  Multiplexer #(.select(2), .width(32), .disabled("Z"), .enable("false")) multiplexer_2 (
    .in0(PC_4), .in1(\PC_条件跳转 ), .in2(PC_JAL), .in3(and_6_out), .out(multiplexer_2_out),
    .sel(priority_encoder_1_out));
  Priority_Encoder #(.select(2), .disabled("Z")) priority_encoder_1 (
    .in0(1'b1), .in1(\条件跳转 ), .in2(JAL), .in3(JALR), .out(priority_encoder_1_out));  // open: gs, en_out, en_in
  Hex_Digit_Display hex_digit_display_6 (.value(LedData[11:8]));  // open: dp
  Hex_Digit_Display hex_digit_display_7 (.value(LedData[7:4]));  // open: dp
  // Probe on \总周期数 
  not not_1 (not_1_out, halt);
  Counter #(.width(32), .max('hffffffff), .ongoal("wrap"), .trigger("rising"), .behavior("new")) counter_1 (
    .count(not_1_out), .Q(\总周期数 ), .clk(CLK), .clr(RST));  // open: load, D, carry, preset, down
  Register #(.width(32), .trigger("rising"), .Select("low")) register_3 (
    .D({Din3, Din2, Din1, Din0}), .en(and_7_out), .Q(LedData), .clk(CLK), .clr(RST));
  Hex_Digit_Display hex_digit_display_8 (.value(LedData[3:0]));  // open: dp
  D_Flip_Flop #(.trigger("rising"), .Pre_Clr_Positions("LEGACY"), .NegatePresetClear("false"), .enable("true"), .NewFFLayout("false")) d_ff_1 (
    .clk(CLK), .D(and_9_out), .Qn(IE));  // open: Q, preset, en, reset
  and and_9 (and_9_out, ~URET, \中断请求 );  // AND_Gate
  Multiplexer #(.select(2), .width(32), .disabled("Z"), .enable("false")) multiplexer_3 (
    .in0(32'h30c0), .in1(32'h30c0), .in2(32'h30c0), .in3(32'h30c0), .out(PC_INT), .sel(\中断号 ));
  Priority_Encoder #(.select(3), .disabled("Z")) priority_encoder_2 (
    .in0(1'b1), .in1(\无条件跳转 ), .in2(AUIPC), .in3(LUI), .in4(LBU), .in5(CSRRS), .out(priority_encoder_2_out));  // open: in6, in7, gs, en_out, en_in
  or or_2 (\无条件跳转 , JAL, JALR);
  Multiplexer #(.select(1), .width(32), .disabled("Z"), .enable("false")) multiplexer_4 (
    .in0(multiplexer_2_out), .in1(mEPC), .out(PC_Next), .sel(URET));
  Multiplexer #(.select(3), .width(32), .disabled("Z"), .enable("false")) multiplexer_5 (
    .in0(multiplexer_1_out), .in1(PC_4), .in2(RDin_AUIPC), .in3(RDin_LUI), .in4(MemData), .in5(\随机数 ),
    .out(RDin), .sel(priority_encoder_2_out));  // open: in6, in7
  or or_3 (IR2, undriven, IRB);
  Button u__1 (.out(IRA));
  Button u__2 (.out(IRB));
  Button u__3 (.out(IRC));
  LED #(.active("true")) led_1 (.in(W1));
  LED #(.active("true")) led_2 (.in(W2));
  LED #(.active("true")) led_3 (.in(W3));
  D_Flip_Flop #(.trigger("high"), .Pre_Clr_Positions("ABOVE_BELOW"), .NegatePresetClear("false"), .enable("false"), .NewFFLayout("true")) d_ff_2 (
    .clk(CLK), .D(\新游戏 ), .Q(d_ff_2_q));  // open: Qn, preset, reset
  Register #(.width(32), .trigger("rising"), .Select("low")) u_PC (
    .D(PC_Next), .en(not_2_out), .Q(PC_q), .clk(CLK), .clr(RST));
  not not_2 (not_2_out, halt);
  or or_4 (IR3, undriven_2, IRC);
  or or_5 (IR1, d_ff_2_q, IRA);
  Multiplexer #(.select(1), .width(32), .disabled("Z"), .enable("false")) multiplexer_6 (
    .in0(PC_q), .in1(PC_INT), .out(PC), .sel(INT));
  ROM #(.addrWidth(10), .dataWidth(32), .Select("high")) rom_1 (.addr(PC[11:2]), .data(IR));
  or or_6 (W1, IR1_q, d_ff_3_q);
  or or_7 (W2, IR2_q, d_ff_4_q);
  or or_8 (W3, IR3_q, d_ff_5_q);
  D_Flip_Flop #(.trigger("rising"), .Pre_Clr_Positions("LEGACY"), .NegatePresetClear("false"), .enable("true"), .NewFFLayout("false")) d_ff_3 (
    .clk(IR1), .D(1'b1), .Q(d_ff_3_q), .reset(IR1_q));  // open: Qn, preset, en
  D_Flip_Flop #(.trigger("rising"), .Pre_Clr_Positions("LEGACY"), .NegatePresetClear("false"), .enable("true"), .NewFFLayout("false")) d_ff_4 (
    .clk(IR2), .D(1'b1), .Q(d_ff_4_q), .reset(IR2_q));  // open: Qn, preset, en
  D_Flip_Flop #(.trigger("rising"), .Pre_Clr_Positions("LEGACY"), .NegatePresetClear("false"), .enable("true"), .NewFFLayout("false")) d_ff_5 (
    .clk(IR3), .D(1'b1), .Q(d_ff_5_q), .reset(IR3_q));  // open: Qn, preset, en
  \单周期硬布线控制器  \u_单周期硬布线控制器_1  (
    .Funct({IR[30], IR[25], IR[14:12]}), .OP(IR[6:2]), .ALU_OP(\单周期硬布线控制器_1_alu_op ), .MemToReg(MemToReg),
    .MemWrite(MemWrite), .ALU_SRC(\单周期硬布线控制器_1_alu_src ), .RegWrite(RegWrite), .ecall(\数据产生 ), .S_type(SW),
    .Jalr(JALR), .Beq(BEQ), .JAL(JAL), .Bne(BNE), .in_3(IR[21]), .uret(URET), .BGE(BGE), .LUI(LUI),
    .AUIPC(AUIPC), .LBU(LBU), .REM(REM), .MUL(MUL), .CSRRS(CSRRS));
  Multiplexer #(.select(1), .width(5), .disabled("Z"), .enable("false")) multiplexer_7 (
    .in0(IR[19:15]), .in1(5'b10001), .out(multiplexer_7_out), .sel(\数据产生 ));
  Multiplexer #(.select(1), .width(5), .disabled("Z"), .enable("false")) multiplexer_8 (
    .in0(IR[24:20]), .in1(5'b01010), .out(multiplexer_8_out), .sel(\数据产生 ));
  Multiplexer #(.select(1), .width(5), .disabled("Z"), .enable("false")) multiplexer_9 (
    .in0(IR[11:7]), .in1(5'b01010), .out(multiplexer_9_out), .sel(CSRRS));
  Multiplexer #(.select(1), .width(12), .disabled("Z"), .enable("false")) multiplexer_10 (
    .in0(IR[31:20]), .in1({IR[31:25], IR[11:7]}), .out(multiplexer_10_out), .sel(SW));
  or or_9 (or_9_out, d_ff_3_q, IR1_q);
  or or_10 (or_10_out, d_ff_4_q, IR2_q);
  or or_11 (or_11_out, d_ff_5_q, IR3_q);
  assign bit_extender_1_out = {{20{multiplexer_10_out[11]}}, multiplexer_10_out};  // Bit_Extender bit_extender_1
  assign bit_extender_2_out = {{20{IR[31]}}, {IR[31], IR[7], IR[30:25], IR[11:8]}};  // Bit_Extender bit_extender_2
  assign bit_extender_3_out = {{12{IR[31]}}, {IR[31], IR[19:12], IR[20], IR[30:21]}};  // Bit_Extender bit_extender_3
  assign bit_extender_4_out = {{12{IR[31]}}, IR[31:12]};  // Bit_Extender bit_extender_4
  assign bit_extender_5_out = {{12{IR[31]}}, IR[31:12]};  // Bit_Extender bit_extender_5
  D_Flip_Flop #(.trigger("high"), .Pre_Clr_Positions("LEGACY"), .NegatePresetClear("false"), .enable("true"), .NewFFLayout("false")) d_ff_6 (.Q(d_ff_6_q));  // open: clk, D, Qn, preset, en, reset
  // Probe on 13'hb9
  D_Flip_Flop #(.trigger("rising"), .Pre_Clr_Positions("LEGACY"), .NegatePresetClear("false"), .enable("true"), .NewFFLayout("false")) u_IR1 (
    .clk(CLK), .D(and_10_out), .Q(IR1_q), .reset(RST));  // open: Qn, preset, en
  and and_10 (and_10_out, or_9_out, ~ClearInt1);  // AND_Gate
  D_Flip_Flop #(.trigger("rising"), .Pre_Clr_Positions("LEGACY"), .NegatePresetClear("false"), .enable("true"), .NewFFLayout("false")) u_IR2 (
    .clk(CLK), .D(and_11_out), .Q(IR2_q), .reset(RST));  // open: Qn, preset, en
  and and_11 (and_11_out, or_10_out, ~ClearInt2);  // AND_Gate
  D_Flip_Flop #(.trigger("rising"), .Pre_Clr_Positions("LEGACY"), .NegatePresetClear("false"), .enable("true"), .NewFFLayout("false")) u_IR3 (
    .clk(CLK), .D(and_12_out), .Q(IR3_q), .reset(RST));  // open: Qn, preset, en
  and and_12 (and_12_out, or_11_out, ~ClearInt3);  // AND_Gate
  Shifter #(.width(32), .shift("ll")) shifter_1 (.in(bit_extender_2_out), .\dist (5'b00001), .out(shifter_1_out));
  Shifter #(.width(32), .shift("ll")) shifter_2 (.in(bit_extender_3_out), .\dist (5'b00001), .out(shifter_2_out));
  Shifter #(.width(32), .shift("ll")) shifter_3 (.in(bit_extender_4_out), .\dist (5'b01100), .out(shifter_3_out));
  Shifter #(.width(32), .shift("ll")) shifter_4 (.in(bit_extender_5_out), .\dist (5'b01100), .out(RDin_LUI));
  Comparator #(.width(13), .mode("twosComplement")) comparator_2 (
    .a(CNT_num), .b(13'hb9), .eq(comparator_2_eq), .lt(comparator_2_lt));  // open: gt
  Clock #(.highDuration(1), .lowDuration(1)) clock_1 (.out(clock_1_out));
  Regifile regifile_1 (
    .Din(RDin), .Clk(CLK), .R1(R1), .R2({Din3, Din2, Din1, Din0}), .WE(RegWrite), .W_num(multiplexer_9_out),
    .R1_num(multiplexer_7_out), .R2_num(multiplexer_8_out));
  Adder #(.width(32)) adder_2 (.a(PC), .b(shifter_1_out), .out(\PC_条件跳转 ));  // open: cin, cout
  Adder #(.width(32)) adder_3 (.a(PC), .b(shifter_2_out), .out(PC_JAL));  // open: cin, cout
  Adder #(.width(32)) adder_4 (.a(PC), .b(shifter_3_out), .out(RDin_AUIPC));  // open: cin, cout
  Counter #(.width(13), .max('h1fff), .ongoal("stay"), .trigger("rising"), .behavior("old")) counter_2 (
    .count(comparator_2_lt), .Q(CNT_num), .clk(clock_1_out));  // open: load, D, carry, clr, preset
  Multiplexer #(.select(1), .width(32), .disabled("Z"), .enable("false")) multiplexer_11 (
    .in0({Din3, Din2, Din1, Din0}), .in1(bit_extender_1_out), .out(multiplexer_11_out),
    .sel(\单周期硬布线控制器_1_alu_src ));
  nand nand_1 (nand_1_out, d_ff_6_q, comparator_2_eq);
  Priority_Encoder #(.select(2), .disabled("Z")) priority_encoder_3 (
    .in0(IR1_q), .in1(IR2_q), .in2(IR3_q), .in3(1'b0), .out(\中断号 ), .gs(\中断请求 ));  // open: en_out, en_in
  ALU alu_1 (
    .X(R1), .Y(multiplexer_11_out), .AluOP(\单周期硬布线控制器_1_alu_op ), .Equal(tunnel), .Result(alu_1_result),
    .Result_2(alu_1_result_2), .out_4(tunnel_t));  // open: out_6
  assign controlled_buffer_1_out = nand_1_out ? clock_1_out : 1'bz;  // Controlled_Buffer controlled_buffer_1
  Pull_Resistor #(.pull(1)) pull_resistor_1 (.node(controlled_buffer_1_out));
  Multiplexer #(.select(1), .width(32), .disabled("Z"), .enable("false")) multiplexer_12 (
    .in0(alu_1_result), .in1(alu_1_result_2), .out(Alu_Res), .sel(REM));
  Register #(.width(2), .trigger("rising"), .Select("low")) register_4 (
    .D(\中断号 ), .en(INT), .Q(register_4_q), .clk(CLK), .clr(RST));
  Decoder #(.select(2), .tristate("false"), .disabled("Z"), .enable("false")) decoder_1 (
    .out0(decoder_1_out0), .out1(decoder_1_out1), .out2(decoder_1_out2), .sel(register_4_q));  // open: out3
  and and_13 (ClearInt1, decoder_1_out0, URET);
  and and_14 (ClearInt2, decoder_1_out1, URET);
  and and_15 (ClearInt3, decoder_1_out2, URET);
  assign controlled_buffer_2_out = and_16_out ? Din0 : 8'bz;  // Controlled_Buffer controlled_buffer_2
  and and_16 (and_16_out, MemWrite, _0);
  RAM #(.addrWidth(10), .dataWidth(8), .bus("separate"), .Select("high")) \u_数据存储器0  (
    .addr(Alu_Res[11:2]), .din(controlled_buffer_2_out), .data(Dout0), .str(and_16_out), .clk(CLK));  // open: sel, ld, clr
  assign controlled_buffer_3_out = and_17_out ? Din1 : 8'bz;  // Controlled_Buffer controlled_buffer_3
  assign bit_extender_6_out = {{24{1'b0}}, Dout0};  // Bit_Extender bit_extender_6
  assign bit_extender_7_out = {{24{1'b0}}, Dout1};  // Bit_Extender bit_extender_7
  assign bit_extender_8_out = {{24{1'b0}}, Dout2};  // Bit_Extender bit_extender_8
  assign bit_extender_9_out = {{24{1'b0}}, Dout3};  // Bit_Extender bit_extender_9
  and and_17 (and_17_out, MemWrite, _1);
  RAM #(.addrWidth(10), .dataWidth(8), .bus("separate"), .Select("high")) \u_数据存储器1  (
    .addr(Alu_Res[11:2]), .din(controlled_buffer_3_out), .data(Dout1), .str(and_17_out), .clk(CLK));  // open: sel, ld, clr
  Multiplexer #(.select(3), .width(32), .disabled(0), .enable("false")) multiplexer_13 (
    .in0({Dout3, Dout2, Dout1, Dout0}), .in1(bit_extender_6_out), .in2(bit_extender_7_out),
    .in3(bit_extender_8_out), .in4(bit_extender_9_out), .in5({32{1'b0}}), .in6({32{1'b0}}), .in7({32{1'b0}}),
    .out(MemData), .sel(select));
  assign controlled_buffer_4_out = and_18_out ? Din2 : 8'bz;  // Controlled_Buffer controlled_buffer_4
  and and_18 (and_18_out, MemWrite, _2);
  not not_3 (not_3_out, LBU);
  Demultiplexer #(.select(2), .width(1), .tristate("false"), .disabled(0), .enable("true")) demultiplexer_1 (
    .out0(demultiplexer_1_out0), .out1(demultiplexer_1_out1), .out2(demultiplexer_1_out2),
    .out3(demultiplexer_1_out3), .in(1'b1), .sel(Alu_Res[1:0]), .en(LBU));
  RAM #(.addrWidth(10), .dataWidth(8), .bus("separate"), .Select("high")) \u_数据存储器2  (
    .addr(Alu_Res[11:2]), .din(controlled_buffer_4_out), .data(Dout2), .str(and_18_out), .clk(CLK));  // open: sel, ld, clr
  assign controlled_buffer_5_out = and_19_out ? Din3 : 8'bz;  // Controlled_Buffer controlled_buffer_5
  Priority_Encoder #(.select(3), .disabled("Z")) priority_encoder_4 (
    .in0(not_3_out), .in1(demultiplexer_1_out0), .in2(demultiplexer_1_out1), .in3(demultiplexer_1_out2),
    .in4(demultiplexer_1_out3), .out(select));  // open: in5, in6, in7, gs, en_out, en_in
  and and_19 (and_19_out, MemWrite, _3);
  or or_12 (_0, not_3_out, demultiplexer_1_out0);
  or or_13 (_1, not_3_out, demultiplexer_1_out1);
  or or_14 (_2, not_3_out, demultiplexer_1_out2);
  or or_15 (_3, not_3_out, demultiplexer_1_out3);
  RAM #(.addrWidth(10), .dataWidth(8), .bus("separate"), .Select("high")) \u_数据存储器3  (
    .addr(Alu_Res[11:2]), .din(controlled_buffer_5_out), .data(Dout3), .str(and_19_out), .clk(CLK));  // open: sel, ld, clr

  // Other names for the same wires on the sheet: 片选信号[1:0] = Alu_Res[1:0]; 字地址[9:0] = Alu_Res[11:2]; ECALL = \数据产生 ;
  //   MDin[31:0] = {Din3, Din2, Din1, Din0}; R2[31:0] = {Din3, Din2, Din1, Din0}

  // Notes on the sheet:
  //   中断相关寄存器/变量
  //   RDin数据源
  //   ECALL指令
  //   PC数据源
  //   指令探针
  //   条件跳转/无条件跳转
  //   响应中断
  //   中断程序返回寄存器
  //   数码管输出
  //   总复位信号应将除ROM以外所有存储组件全部清零
  //   数码管输出应该用寄存器锁存，否则显示数据只能一闪而过
  //   中断使能寄存器
  //   中断源
  //   中断等待指示
  //   指令存储器
  //   contents of rom_1 (hex, n*v repeats v):
  //   ff010113 812623 1010413 fb3 6f ff010113 812623 1010413 13 c0102573 c12403 1010113 8067 fe010113
  //   112e23 812c23 2010413 317 fd0300e7 fea42623 fec42703 41c657b7 78793 e6d78793 2f70733 37b7 78793
  //   3978793 f707b3 fef42623 fec42783 41f7d693 10737 70713 fff70713 e6f733 f707b3 4107d793 f00733 87b7
  //   78793 fff78793 f777b3 f00533 1c12083 1812403 2010113 8067 fe010113 112e23 812c23 2010413 317
  //   f64300e7 a00733 a00793 2f767b3 fef42623 1c0006f 317 f48300e7 a00733 a00793 2f767b3 fef42623 fec42703
  //   fff702e3 fec42703 e00fb3 fe042423 340006f 5200713 fec42783 2f70733 fe842783 f707b3 7c783 f00533
  //   2200893 73 fe842783 178793 fef42423 fe842703 5000793 fce7d4e3 fe042223 13 13 73 3c0006f 5200713
  //   fec42783 2f70733 fe442783 f707b3 35c00713 f707b3 7c783 f00533 2200893 73 fe442783 178793 fef42223
  //   fe442703 5100793 fce7d0e3 13 13 1c12083 1812403 2010113 533 2200893 73 200073 e3dff06f
  //   为方便自动评测，需要输出PC，IR，寄存器堆写如数据RDin
  //   RAM写使能MemWrite、RAM写入数据MDin等信号
  //   REM
  //   MUL
  //   CSRRS
  //   JAL
  //   JALR
  //   AUIPC
  //   Bge
  //   Beq
  //   URET
  //   Bne
  //   LBU
  //   LUI
  //   MemToReg
  //   MemWrite
  //   AluOP
  //   AluSrcB
  //   RegWrite
  //   控制位
  //   暂停节拍，不能为0
  //   戳工具置1进入计数暂停模式，ctrl+k时钟自动运行到对应节拍暂停
  //   ctrl+k关闭时钟连续运行，将控制位置零，进入单步调试模式调试
  //   用这个时钟源需要去掉电路中的其他时钟源
  //   可计数暂停的时钟源
  //   如果不慎复位，请向4片RAM中分别加载"数据文件"文件夹中对应的data.hex
endmodule

// 控制信号生成
module \控制信号自动生成  (
  input  OP2,
  input  OP3,
  input  OP4,
  input  OP5,
  input  OP6,
  input  F12,
  input  F13,
  input  F14,
  input  F25,
  input  F30,
  output MemToReg,
  output MemWrite,
  output ALU_SRC,
  output RegWrite,
  output ecall,
  output S_Type,
  output BEQ,
  output BNE,
  output JALR,
  output JAL,
  output AUIPC,
  output LBU,
  output BGE,
  output LUI,
  output REM,
  output MUL,
  output CSRRS
);

  wire and_1_out, and_2_out, and_4_out, and_5_out, and_6_out, and_7_out, and_8_out, and_9_out, and_10_out,
       and_11_out, and_12_out, and_13_out, and_14_out, and_15_out, and_16_out, and_17_out, and_18_out,
       and_19_out, and_20_out, and_21_out, and_22_out, and_23_out, and_24_out, not_1_out, not_2_out,
       not_3_out, not_4_out, not_5_out, not_6_out, not_7_out, not_8_out, not_9_out, not_10_out, not_11_out,
       not_12_out, not_13_out, not_14_out, not_15_out, not_16_out, not_17_out, not_18_out, not_19_out,
       not_20_out, not_21_out, not_22_out, not_23_out, not_24_out, not_25_out, not_26_out, not_27_out,
       not_28_out, not_29_out, not_30_out, not_31_out, not_32_out, not_33_out, not_34_out, not_35_out,
       not_36_out, not_37_out, not_38_out, not_39_out, not_40_out, not_41_out, not_42_out, not_43_out,
       not_44_out, not_45_out, not_46_out, not_47_out, not_48_out, not_49_out, not_50_out, not_51_out,
       not_52_out, not_53_out, not_54_out, not_55_out, not_56_out, not_57_out, not_58_out, not_59_out,
       not_60_out, not_61_out, not_62_out, not_63_out, not_64_out, not_65_out, not_66_out, not_67_out,
       not_68_out, not_69_out, not_70_out, not_71_out, not_72_out, not_73_out, not_74_out, not_75_out,
       not_76_out, not_77_out, not_78_out, not_79_out, not_80_out, not_81_out, not_82_out, not_83_out,
       not_84_out, not_85_out, not_86_out, not_87_out, not_88_out, not_89_out, not_90_out, not_91_out,
       not_92_out, not_93_out, not_94_out, not_95_out, not_96_out, not_97_out, not_98_out, not_99_out,
       not_100_out, not_101_out, not_102_out, not_103_out, not_104_out, not_105_out, not_106_out,
       not_107_out, not_108_out, not_109_out, not_110_out, not_111_out, not_112_out, not_113_out,
       not_114_out, not_115_out, not_116_out, not_117_out, not_118_out, not_119_out, not_120_out,
       not_121_out, not_122_out, not_123_out, not_124_out, not_125_out, not_126_out, not_127_out,
       not_128_out, not_129_out, not_130_out, not_131_out, not_132_out, not_133_out, not_134_out,
       not_135_out, not_136_out, not_137_out, not_138_out, not_139_out, not_140_out, not_141_out,
       not_142_out, not_143_out, not_144_out, not_145_out, not_146_out, not_147_out, not_148_out,
       not_149_out, not_150_out, not_151_out, not_152_out, not_153_out, not_154_out, not_155_out,
       not_156_out, not_157_out, not_158_out, not_159_out, not_160_out, not_161_out, not_162_out,
       not_163_out, not_164_out, not_165_out, not_166_out, not_167_out, not_168_out, not_169_out,
       not_170_out, not_171_out, not_172_out, not_173_out, not_174_out, not_175_out, not_176_out,
       not_177_out, not_178_out;

  not not_1 (not_1_out, OP2);
  not not_2 (not_2_out, OP3);
  not not_3 (not_3_out, OP4);
  not not_4 (not_4_out, OP5);
  not not_5 (not_5_out, OP6);
  not not_6 (not_6_out, F12);
  not not_7 (not_7_out, F13);
  not not_8 (not_8_out, OP2);
  not not_9 (not_9_out, OP3);
  not not_10 (not_10_out, OP4);
  not not_11 (not_11_out, OP5);
  not not_12 (not_12_out, OP6);
  not not_13 (not_13_out, F12);
  not not_14 (not_14_out, F14);
  not not_15 (not_15_out, OP2);
  not not_16 (not_16_out, OP3);
  not not_17 (not_17_out, OP4);
  not not_18 (not_18_out, OP6);
  not not_19 (not_19_out, F12);
  not not_20 (not_20_out, F14);
  not not_21 (not_21_out, OP2);
  not not_22 (not_22_out, OP3);
  not not_23 (not_23_out, OP5);
  not not_24 (not_24_out, OP6);
  not not_25 (not_25_out, F12);
  not not_26 (not_26_out, F13);
  not not_27 (not_27_out, OP2);
  not not_28 (not_28_out, OP3);
  not not_29 (not_29_out, OP4);
  not not_30 (not_30_out, OP6);
  not not_31 (not_31_out, F12);
  not not_32 (not_32_out, F14);
  not not_33 (not_33_out, OP2);
  not not_34 (not_34_out, OP3);
  not not_35 (not_35_out, OP5);
  not not_36 (not_36_out, OP6);
  not not_37 (not_37_out, F12);
  not not_38 (not_38_out, OP2);
  not not_39 (not_39_out, OP3);
  not not_40 (not_40_out, OP5);
  not not_41 (not_41_out, OP6);
  not not_42 (not_42_out, F13);
  not not_43 (not_43_out, F25);
  not not_44 (not_44_out, F30);
  not not_45 (not_45_out, OP2);
  not not_46 (not_46_out, OP3);
  not not_47 (not_47_out, OP5);
  not not_48 (not_48_out, OP6);
  not not_49 (not_49_out, F25);
  not not_50 (not_50_out, OP2);
  not not_51 (not_51_out, OP3);
  not not_52 (not_52_out, OP5);
  not not_53 (not_53_out, OP6);
  not not_54 (not_54_out, OP3);
  not not_55 (not_55_out, OP4);
  not not_56 (not_56_out, F12);
  not not_57 (not_57_out, F13);
  not not_58 (not_58_out, F14);
  not not_59 (not_59_out, OP2);
  not not_60 (not_60_out, OP3);
  not not_61 (not_61_out, OP5);
  not not_62 (not_62_out, OP6);
  not not_63 (not_63_out, F12);
  not not_64 (not_64_out, F13);
  not not_65 (not_65_out, OP2);
  not not_66 (not_66_out, OP3);
  not not_67 (not_67_out, OP5);
  not not_68 (not_68_out, OP6);
  not not_69 (not_69_out, F12);
  not not_70 (not_70_out, F14);
  not not_71 (not_71_out, OP3);
  not not_72 (not_72_out, OP5);
  not not_73 (not_73_out, OP6);
  not not_74 (not_74_out, F12);
  not not_75 (not_75_out, OP3);
  not not_76 (not_76_out, OP5);
  not not_77 (not_77_out, OP6);
  not not_78 (not_78_out, F13);
  not not_79 (not_79_out, F25);
  not not_80 (not_80_out, F30);
  not not_81 (not_81_out, OP3);
  not not_82 (not_82_out, OP6);
  not not_83 (not_83_out, F12);
  not not_84 (not_84_out, F13);
  not not_85 (not_85_out, F14);
  not not_86 (not_86_out, F25);
  not not_87 (not_87_out, OP3);
  not not_88 (not_88_out, OP6);
  not not_89 (not_89_out, F12);
  not not_90 (not_90_out, F13);
  not not_91 (not_91_out, F14);
  not not_92 (not_92_out, F30);
  not not_93 (not_93_out, OP3);
  not not_94 (not_94_out, OP5);
  not not_95 (not_95_out, OP6);
  not not_96 (not_96_out, F25);
  not not_97 (not_97_out, OP3);
  not not_98 (not_98_out, OP5);
  not not_99 (not_99_out, OP6);
  not not_100 (not_100_out, OP3);
  not not_101 (not_101_out, OP6);
  not not_102 (not_102_out, F12);
  not not_103 (not_103_out, F30);
  not not_104 (not_104_out, OP3);
  not not_105 (not_105_out, OP6);
  not not_106 (not_106_out, F25);
  not not_107 (not_107_out, F30);
  not not_108 (not_108_out, OP2);
  not not_109 (not_109_out, OP3);
  not not_110 (not_110_out, F12);
  not not_111 (not_111_out, F14);
  not not_112 (not_112_out, OP4);
  not not_113 (not_113_out, F12);
  not not_114 (not_114_out, F13);
  not not_115 (not_115_out, F14);
  not not_116 (not_116_out, OP3);
  not not_117 (not_117_out, OP6);
  not not_118 (not_118_out, OP4);
  not not_119 (not_119_out, OP2);
  not not_120 (not_120_out, OP3);
  not not_121 (not_121_out, F12);
  not not_122 (not_122_out, F13);
  not not_123 (not_123_out, F14);
  not not_124 (not_124_out, OP2);
  not not_125 (not_125_out, OP3);
  not not_126 (not_126_out, OP4);
  not not_127 (not_127_out, OP6);
  not not_128 (not_128_out, F12);
  not not_129 (not_129_out, F14);
  not not_130 (not_130_out, OP2);
  not not_131 (not_131_out, OP3);
  not not_132 (not_132_out, OP4);
  not not_133 (not_133_out, F12);
  not not_134 (not_134_out, F13);
  not not_135 (not_135_out, F14);
  not not_136 (not_136_out, OP2);
  not not_137 (not_137_out, OP3);
  not not_138 (not_138_out, OP4);
  not not_139 (not_139_out, F13);
  not not_140 (not_140_out, F14);
  not not_141 (not_141_out, OP3);
  not not_142 (not_142_out, OP4);
  not not_143 (not_143_out, F12);
  not not_144 (not_144_out, F13);
  not not_145 (not_145_out, F14);
  not not_146 (not_146_out, OP4);
  not not_147 (not_147_out, OP3);
  not not_148 (not_148_out, OP5);
  not not_149 (not_149_out, OP6);
  not not_150 (not_150_out, OP2);
  not not_151 (not_151_out, OP3);
  not not_152 (not_152_out, OP4);
  not not_153 (not_153_out, OP5);
  not not_154 (not_154_out, OP6);
  not not_155 (not_155_out, F12);
  not not_156 (not_156_out, F13);
  not not_157 (not_157_out, OP2);
  not not_158 (not_158_out, OP3);
  not not_159 (not_159_out, OP4);
  not not_160 (not_160_out, F13);
  not not_161 (not_161_out, OP3);
  not not_162 (not_162_out, OP6);
  not not_163 (not_163_out, F30);
  not not_164 (not_164_out, F12);
  not not_165 (not_165_out, OP6);
  not not_166 (not_166_out, OP3);
  not not_167 (not_167_out, OP2);
  not not_168 (not_168_out, F30);
  not not_169 (not_169_out, F14);
  not not_170 (not_170_out, F13);
  not not_171 (not_171_out, F12);
  not not_172 (not_172_out, OP6);
  not not_173 (not_173_out, OP3);
  not not_174 (not_174_out, OP2);
  not not_175 (not_175_out, F14);
  not not_176 (not_176_out, F12);
  not not_177 (not_177_out, OP3);
  not not_178 (not_178_out, OP2);
  and and_1 (and_1_out, not_1_out, not_2_out, not_3_out, not_4_out, not_5_out, not_6_out, not_7_out, F14);
  and and_2 (and_2_out, not_8_out, not_9_out, not_10_out, not_11_out, not_12_out, not_13_out, F13, not_14_out);
  and and_3 (MemWrite, not_15_out, not_16_out, not_17_out, OP5, not_18_out, not_19_out, F13, not_20_out);
  and and_4 (and_4_out, not_21_out, not_22_out, not_23_out, not_24_out, not_25_out, not_26_out, F14);
  and and_5 (and_5_out, not_27_out, not_28_out, not_29_out, not_30_out, not_31_out, F13, not_32_out);
  and and_6 (and_6_out, not_33_out, not_34_out, OP4, not_35_out, not_36_out, not_37_out);
  and and_7 (and_7_out, not_38_out, not_39_out, OP4, not_40_out, not_41_out, not_42_out, not_43_out, not_44_out);
  and and_8 (and_8_out, not_45_out, not_46_out, OP4, not_47_out, not_48_out, F14, not_49_out);
  and and_9 (and_9_out, not_50_out, not_51_out, OP4, not_52_out, not_53_out, F13, F14);
  and and_10 (and_10_out, OP2, not_54_out, not_55_out, OP5, OP6, not_56_out, not_57_out, not_58_out);
  and and_11 (and_11_out, not_59_out, not_60_out, not_61_out, not_62_out, not_63_out, not_64_out, F14);
  and and_12 (and_12_out, not_65_out, not_66_out, not_67_out, not_68_out, not_69_out, F13, not_70_out);
  and and_13 (and_13_out, not_71_out, OP4, not_72_out, not_73_out, not_74_out);
  and and_14 (and_14_out, not_75_out, OP4, not_76_out, not_77_out, not_78_out, not_79_out, not_80_out);
  and and_15 (and_15_out, not_81_out, OP4, not_82_out, not_83_out, not_84_out, not_85_out, not_86_out);
  and and_16 (and_16_out, not_87_out, OP4, not_88_out, not_89_out, not_90_out, not_91_out, not_92_out);
  and and_17 (and_17_out, not_93_out, OP4, not_94_out, not_95_out, F14, not_96_out);
  and and_18 (and_18_out, not_97_out, OP4, not_98_out, not_99_out, F13, F14);
  and and_19 (and_19_out, not_100_out, OP4, not_101_out, not_102_out, F13, F14, not_103_out);
  and and_20 (and_20_out, not_104_out, OP4, OP5, not_105_out, F13, not_106_out, not_107_out);
  and and_21 (and_21_out, not_108_out, not_109_out, OP4, OP5, OP6, not_110_out, F13, not_111_out);
  and and_22 (and_22_out, OP2, not_112_out, OP5, OP6, not_113_out, not_114_out, not_115_out);
  and and_23 (and_23_out, OP2, not_116_out, OP4, not_117_out);
  and and_24 (and_24_out, OP2, OP3, not_118_out, OP5, OP6);
  and and_25 (ecall, not_119_out, not_120_out, OP4, OP5, OP6, not_121_out, not_122_out, not_123_out);
  and and_26 (S_Type, not_124_out, not_125_out, not_126_out, OP5, not_127_out, not_128_out, F13, not_129_out);
  and and_27 (BEQ, not_130_out, not_131_out, not_132_out, OP5, OP6, not_133_out, not_134_out, not_135_out);
  and and_28 (BNE, not_136_out, not_137_out, not_138_out, OP5, OP6, F12, not_139_out, not_140_out);
  and and_29 (JALR, OP2, not_141_out, not_142_out, OP5, OP6, not_143_out, not_144_out, not_145_out);
  and and_30 (JAL, OP2, OP3, not_146_out, OP5, OP6);
  and and_31 (AUIPC, OP2, not_147_out, OP4, not_148_out, not_149_out);
  and and_32 (LBU, not_150_out, not_151_out, not_152_out, not_153_out, not_154_out, not_155_out, not_156_out, F14);
  and and_33 (BGE, not_157_out, not_158_out, not_159_out, OP5, OP6, F12, not_160_out, F14);
  and and_34 (LUI, OP2, not_161_out, OP4, OP5, not_162_out);
  and and_35 (REM, not_163_out, F25, F14, F13, not_164_out, not_165_out, OP5, OP4, not_166_out, not_167_out);
  and and_36 (MUL, not_168_out, F25, not_169_out, not_170_out, not_171_out, not_172_out, OP5, OP4, not_173_out, not_174_out);
  and and_37 (CSRRS, not_175_out, F13, not_176_out, OP6, OP5, OP4, not_177_out, not_178_out);
  or or_1 (MemToReg, and_1_out, and_2_out);
  or or_2 (ALU_SRC, and_4_out, and_5_out, and_6_out, and_7_out, and_8_out, and_9_out, and_10_out);
  or or_3 (RegWrite, and_11_out, and_12_out, and_13_out, and_14_out, and_15_out, and_16_out, and_17_out, and_18_out, and_19_out, and_20_out, and_21_out, and_22_out, and_23_out, and_24_out);
endmodule

// 运算器控制器
module \运算控制器自动生成  (
  input  OP2,
  input  OP3,
  input  OP4,
  input  OP5,
  input  OP6,
  input  F12,
  input  F13,
  input  F14,
  input  F25,
  input  F30,
  output S0,
  output S1,
  output S2,
  output S3
);

  wire and_1_out, and_2_out, and_3_out, and_4_out, and_5_out, and_6_out, and_7_out, and_8_out, and_9_out,
       and_10_out, and_11_out, and_12_out, and_13_out, and_14_out, and_15_out, and_16_out, and_17_out,
       and_18_out, and_19_out, and_20_out, and_21_out, and_22_out, and_23_out, and_24_out, and_25_out,
       and_26_out, and_27_out, and_28_out, and_29_out, and_30_out, and_31_out, not_1_out, not_2_out,
       not_3_out, not_4_out, not_5_out, not_6_out, not_7_out, not_8_out, not_9_out, not_10_out, not_11_out,
       not_12_out, not_13_out, not_14_out, not_15_out, not_16_out, not_17_out, not_18_out, not_19_out,
       not_20_out, not_21_out, not_22_out, not_23_out, not_24_out, not_25_out, not_26_out, not_27_out,
       not_28_out, not_29_out, not_30_out, not_31_out, not_32_out, not_33_out, not_34_out, not_35_out,
       not_36_out, not_37_out, not_38_out, not_39_out, not_40_out, not_41_out, not_42_out, not_43_out,
       not_44_out, not_45_out, not_46_out, not_47_out, not_48_out, not_49_out, not_50_out, not_51_out,
       not_52_out, not_53_out, not_54_out, not_55_out, not_56_out, not_57_out, not_58_out, not_59_out,
       not_60_out, not_61_out, not_62_out, not_63_out, not_64_out, not_65_out, not_66_out, not_67_out,
       not_68_out, not_69_out, not_70_out, not_71_out, not_72_out, not_73_out, not_74_out, not_75_out,
       not_76_out, not_77_out, not_78_out, not_79_out, not_80_out, not_81_out, not_82_out, not_83_out,
       not_84_out, not_85_out, not_86_out, not_87_out, not_88_out, not_89_out, not_90_out, not_91_out,
       not_92_out, not_93_out, not_94_out, not_95_out, not_96_out, not_97_out, not_98_out, not_99_out,
       not_100_out, not_101_out, not_102_out, not_103_out, not_104_out, not_105_out, not_106_out,
       not_107_out, not_108_out, not_109_out, not_110_out, not_111_out, not_112_out, not_113_out,
       not_114_out, not_115_out, not_116_out, not_117_out, not_118_out, not_119_out, not_120_out,
       not_121_out, not_122_out, not_123_out, not_124_out, not_125_out, not_126_out, not_127_out,
       not_128_out, not_129_out, not_130_out, not_131_out, not_132_out, not_133_out, not_134_out,
       not_135_out, not_136_out, not_137_out, not_138_out, not_139_out, not_140_out, not_141_out,
       not_142_out, not_143_out, not_144_out, not_145_out, not_146_out, not_147_out, not_148_out,
       not_149_out, not_150_out, not_151_out, not_152_out, not_153_out, not_154_out, not_155_out,
       not_156_out, not_157_out, not_158_out, not_159_out, not_160_out, not_161_out, not_162_out,
       not_163_out, not_164_out, not_165_out, not_166_out, not_167_out, not_168_out, not_169_out,
       not_170_out, not_171_out, not_172_out, not_173_out, not_174_out;

  not not_1 (not_1_out, OP2);
  not not_2 (not_2_out, OP3);
  not not_3 (not_3_out, OP5);
  not not_4 (not_4_out, OP6);
  not not_5 (not_5_out, F12);
  not not_6 (not_6_out, F13);
  not not_7 (not_7_out, OP2);
  not not_8 (not_8_out, OP3);
  not not_9 (not_9_out, OP4);
  not not_10 (not_10_out, OP6);
  not not_11 (not_11_out, F12);
  not not_12 (not_12_out, F14);
  not not_13 (not_13_out, OP2);
  not not_14 (not_14_out, OP3);
  not not_15 (not_15_out, OP4);
  not not_16 (not_16_out, F13);
  not not_17 (not_17_out, OP2);
  not not_18 (not_18_out, OP3);
  not not_19 (not_19_out, OP5);
  not not_20 (not_20_out, OP6);
  not not_21 (not_21_out, F12);
  not not_22 (not_22_out, F14);
  not not_23 (not_23_out, OP2);
  not not_24 (not_24_out, OP3);
  not not_25 (not_25_out, OP6);
  not not_26 (not_26_out, F12);
  not not_27 (not_27_out, F13);
  not not_28 (not_28_out, F14);
  not not_29 (not_29_out, F30);
  not not_30 (not_30_out, OP2);
  not not_31 (not_31_out, OP3);
  not not_32 (not_32_out, OP6);
  not not_33 (not_33_out, F12);
  not not_34 (not_34_out, F14);
  not not_35 (not_35_out, F25);
  not not_36 (not_36_out, F30);
  not not_37 (not_37_out, OP2);
  not not_38 (not_38_out, OP3);
  not not_39 (not_39_out, OP5);
  not not_40 (not_40_out, OP6);
  not not_41 (not_41_out, F13);
  not not_42 (not_42_out, F25);
  not not_43 (not_43_out, OP2);
  not not_44 (not_44_out, OP3);
  not not_45 (not_45_out, OP5);
  not not_46 (not_46_out, OP6);
  not not_47 (not_47_out, OP2);
  not not_48 (not_48_out, OP3);
  not not_49 (not_49_out, OP6);
  not not_50 (not_50_out, F25);
  not not_51 (not_51_out, F30);
  not not_52 (not_52_out, OP3);
  not not_53 (not_53_out, OP4);
  not not_54 (not_54_out, F12);
  not not_55 (not_55_out, F13);
  not not_56 (not_56_out, F14);
  not not_57 (not_57_out, OP2);
  not not_58 (not_58_out, OP3);
  not not_59 (not_59_out, OP4);
  not not_60 (not_60_out, F13);
  not not_61 (not_61_out, OP2);
  not not_62 (not_62_out, OP3);
  not not_63 (not_63_out, OP5);
  not not_64 (not_64_out, OP6);
  not not_65 (not_65_out, F12);
  not not_66 (not_66_out, F14);
  not not_67 (not_67_out, OP2);
  not not_68 (not_68_out, OP3);
  not not_69 (not_69_out, OP6);
  not not_70 (not_70_out, F12);
  not not_71 (not_71_out, F14);
  not not_72 (not_72_out, F25);
  not not_73 (not_73_out, F30);
  not not_74 (not_74_out, OP2);
  not not_75 (not_75_out, OP3);
  not not_76 (not_76_out, OP5);
  not not_77 (not_77_out, OP6);
  not not_78 (not_78_out, F25);
  not not_79 (not_79_out, F30);
  not not_80 (not_80_out, OP2);
  not not_81 (not_81_out, OP3);
  not not_82 (not_82_out, OP5);
  not not_83 (not_83_out, OP6);
  not not_84 (not_84_out, OP2);
  not not_85 (not_85_out, OP3);
  not not_86 (not_86_out, OP6);
  not not_87 (not_87_out, F25);
  not not_88 (not_88_out, F30);
  not not_89 (not_89_out, OP2);
  not not_90 (not_90_out, OP3);
  not not_91 (not_91_out, OP6);
  not not_92 (not_92_out, F12);
  not not_93 (not_93_out, F13);
  not not_94 (not_94_out, F14);
  not not_95 (not_95_out, F25);
  not not_96 (not_96_out, OP2);
  not not_97 (not_97_out, OP3);
  not not_98 (not_98_out, OP6);
  not not_99 (not_99_out, F12);
  not not_100 (not_100_out, F13);
  not not_101 (not_101_out, F14);
  not not_102 (not_102_out, F30);
  not not_103 (not_103_out, OP2);
  not not_104 (not_104_out, OP3);
  not not_105 (not_105_out, OP4);
  not not_106 (not_106_out, OP5);
  not not_107 (not_107_out, OP6);
  not not_108 (not_108_out, F12);
  not not_109 (not_109_out, F13);
  not not_110 (not_110_out, OP2);
  not not_111 (not_111_out, OP3);
  not not_112 (not_112_out, OP4);
  not not_113 (not_113_out, OP6);
  not not_114 (not_114_out, F12);
  not not_115 (not_115_out, F14);
  not not_116 (not_116_out, OP2);
  not not_117 (not_117_out, OP3);
  not not_118 (not_118_out, OP5);
  not not_119 (not_119_out, OP6);
  not not_120 (not_120_out, F12);
  not not_121 (not_121_out, F13);
  not not_122 (not_122_out, F14);
  not not_123 (not_123_out, OP2);
  not not_124 (not_124_out, OP3);
  not not_125 (not_125_out, OP6);
  not not_126 (not_126_out, F12);
  not not_127 (not_127_out, F13);
  not not_128 (not_128_out, F14);
  not not_129 (not_129_out, F25);
  not not_130 (not_130_out, OP2);
  not not_131 (not_131_out, OP3);
  not not_132 (not_132_out, OP5);
  not not_133 (not_133_out, OP6);
  not not_134 (not_134_out, OP2);
  not not_135 (not_135_out, OP3);
  not not_136 (not_136_out, OP6);
  not not_137 (not_137_out, F12);
  not not_138 (not_138_out, F30);
  not not_139 (not_139_out, OP2);
  not not_140 (not_140_out, OP3);
  not not_141 (not_141_out, OP6);
  not not_142 (not_142_out, F25);
  not not_143 (not_143_out, F30);
  not not_144 (not_144_out, OP3);
  not not_145 (not_145_out, OP4);
  not not_146 (not_146_out, F12);
  not not_147 (not_147_out, F13);
  not not_148 (not_148_out, F14);
  not not_149 (not_149_out, OP2);
  not not_150 (not_150_out, OP3);
  not not_151 (not_151_out, OP4);
  not not_152 (not_152_out, F13);
  not not_153 (not_153_out, OP2);
  not not_154 (not_154_out, OP3);
  not not_155 (not_155_out, OP5);
  not not_156 (not_156_out, OP6);
  not not_157 (not_157_out, F12);
  not not_158 (not_158_out, OP2);
  not not_159 (not_159_out, OP3);
  not not_160 (not_160_out, OP5);
  not not_161 (not_161_out, OP6);
  not not_162 (not_162_out, F12);
  not not_163 (not_163_out, OP2);
  not not_164 (not_164_out, OP3);
  not not_165 (not_165_out, OP6);
  not not_166 (not_166_out, F12);
  not not_167 (not_167_out, F25);
  not not_168 (not_168_out, F30);
  not not_169 (not_169_out, OP2);
  not not_170 (not_170_out, OP3);
  not not_171 (not_171_out, OP6);
  not not_172 (not_172_out, F14);
  not not_173 (not_173_out, F25);
  not not_174 (not_174_out, F30);
  and and_1 (and_1_out, not_1_out, not_2_out, not_3_out, not_4_out, not_5_out, not_6_out, F14);
  and and_2 (and_2_out, not_7_out, not_8_out, not_9_out, not_10_out, not_11_out, F13, not_12_out);
  and and_3 (and_3_out, not_13_out, not_14_out, not_15_out, OP5, OP6, F12, not_16_out, F14);
  and and_4 (and_4_out, not_17_out, not_18_out, OP4, not_19_out, not_20_out, not_21_out, not_22_out);
  and and_5 (and_5_out, not_23_out, not_24_out, OP4, not_25_out, not_26_out, not_27_out, not_28_out, not_29_out);
  and and_6 (and_6_out, not_30_out, not_31_out, OP4, not_32_out, not_33_out, not_34_out, not_35_out, not_36_out);
  and and_7 (and_7_out, not_37_out, not_38_out, OP4, not_39_out, not_40_out, not_41_out, F14, not_42_out, F30);
  and and_8 (and_8_out, not_43_out, not_44_out, OP4, not_45_out, not_46_out, F12, F13, F14);
  and and_9 (and_9_out, not_47_out, not_48_out, OP4, not_49_out, F12, F13, F14, not_50_out, not_51_out);
  and and_10 (and_10_out, OP2, not_52_out, not_53_out, OP5, OP6, not_54_out, not_55_out, not_56_out);
  and and_11 (and_11_out, not_57_out, not_58_out, not_59_out, OP5, OP6, F12, not_60_out, F14);
  and and_12 (and_12_out, not_61_out, not_62_out, OP4, not_63_out, not_64_out, not_65_out, F13, not_66_out);
  and and_13 (and_13_out, not_67_out, not_68_out, OP4, not_69_out, not_70_out, F13, not_71_out, not_72_out, not_73_out);
  and and_14 (and_14_out, not_74_out, not_75_out, OP4, not_76_out, not_77_out, F12, F14, not_78_out, not_79_out);
  and and_15 (and_15_out, not_80_out, not_81_out, OP4, not_82_out, not_83_out, F12, F13, F14);
  and and_16 (and_16_out, not_84_out, not_85_out, OP4, not_86_out, F12, F13, F14, not_87_out, not_88_out);
  and and_17 (and_17_out, not_89_out, not_90_out, OP4, OP5, not_91_out, not_92_out, not_93_out, not_94_out, not_95_out, F30);
  and and_18 (and_18_out, not_96_out, not_97_out, OP4, OP5, not_98_out, not_99_out, not_100_out, not_101_out, F25, not_102_out);
  and and_19 (and_19_out, not_103_out, not_104_out, not_105_out, not_106_out, not_107_out, not_108_out, not_109_out, F14);
  and and_20 (and_20_out, not_110_out, not_111_out, not_112_out, not_113_out, not_114_out, F13, not_115_out);
  and and_21 (and_21_out, not_116_out, not_117_out, OP4, not_118_out, not_119_out, not_120_out, not_121_out, not_122_out);
  and and_22 (and_22_out, not_123_out, not_124_out, OP4, not_125_out, not_126_out, not_127_out, not_128_out, not_129_out);
  and and_23 (and_23_out, not_130_out, not_131_out, OP4, not_132_out, not_133_out, F12, F13, F14);
  and and_24 (and_24_out, not_134_out, not_135_out, OP4, OP5, not_136_out, not_137_out, F13, F14, F25, not_138_out);
  and and_25 (and_25_out, not_139_out, not_140_out, OP4, OP5, not_141_out, F12, F13, not_142_out, not_143_out);
  and and_26 (and_26_out, OP2, not_144_out, not_145_out, OP5, OP6, not_146_out, not_147_out, not_148_out);
  and and_27 (and_27_out, not_149_out, not_150_out, not_151_out, OP5, OP6, F12, not_152_out, F14);
  and and_28 (and_28_out, not_153_out, not_154_out, OP4, not_155_out, not_156_out, not_157_out, F14);
  and and_29 (and_29_out, not_158_out, not_159_out, OP4, not_160_out, not_161_out, not_162_out, F13);
  and and_30 (and_30_out, not_163_out, not_164_out, OP4, not_165_out, not_166_out, F13, not_167_out, not_168_out);
  and and_31 (and_31_out, not_169_out, not_170_out, OP4, OP5, not_171_out, F13, not_172_out, not_173_out, not_174_out);
  or or_1 (S3, and_27_out, and_28_out, and_29_out, and_30_out, and_31_out);
  or or_2 (S0, and_1_out, and_2_out, and_3_out, and_4_out, and_5_out, and_6_out, and_7_out, and_8_out, and_9_out, and_10_out);
  or or_3 (S1, and_11_out, and_12_out, and_13_out, and_14_out, and_15_out, and_16_out, and_17_out, and_18_out);
  or or_4 (S2, and_19_out, and_20_out, and_21_out, and_22_out, and_23_out, and_24_out, and_25_out, and_26_out);
endmodule

// 单周期硬布线控制器
module \单周期硬布线控制器  (
  input  [4:0] OP,
  input  [4:0] Funct,
  input  in_3,
  output [3:0] ALU_OP,
  output uret,
  output MemToReg,
  output ecall,
  output MemWrite,
  output ALU_SRC,
  output RegWrite,
  output S_type,
  output Beq,
  output Bne,
  output Jalr,
  output JAL,
  output AUIPC,
  output LBU,
  output BGE,
  output LUI,
  output REM,
  output MUL,
  output CSRRS
);

  wire \控制信号自动生成_1_ecall ;

  \运算控制器自动生成  \u_运算控制器自动生成_1  (
    .OP2(OP[0]), .OP3(OP[1]), .OP4(OP[2]), .OP5(OP[3]), .OP6(OP[4]), .F12(Funct[0]), .F13(Funct[1]),
    .F14(Funct[2]), .F25(Funct[3]), .F30(Funct[4]), .S0(ALU_OP[0]), .S1(ALU_OP[1]), .S2(ALU_OP[2]),
    .S3(ALU_OP[3]));
  \控制信号自动生成  \u_控制信号自动生成_1  (
    .OP2(OP[0]), .OP3(OP[1]), .OP4(OP[2]), .OP5(OP[3]), .OP6(OP[4]), .MemToReg(MemToReg), .F12(Funct[0]),
    .F13(Funct[1]), .F14(Funct[2]), .F25(Funct[3]), .F30(Funct[4]), .MemWrite(MemWrite), .ALU_SRC(ALU_SRC),
    .RegWrite(RegWrite), .ecall(\控制信号自动生成_1_ecall ), .S_Type(S_type), .BEQ(Beq), .BNE(Bne), .JALR(Jalr),
    .JAL(JAL), .AUIPC(AUIPC), .LBU(LBU), .BGE(BGE), .LUI(LUI), .REM(REM), .MUL(MUL), .CSRRS(CSRRS));
  and and_1 (uret, in_3, \控制信号自动生成_1_ecall );
  and and_2 (ecall, ~in_3, \控制信号自动生成_1_ecall );  // AND_Gate

  // Other names for the same wires on the sheet: IR21 = in_3; OP_CODE[4:0] = OP

  // Notes on the sheet:
  //   运算器控制器，根据指令生成运算器功能选择信号
  //   控制信号生成，产生数据通路需要的其他控制信号
endmodule
